// Logisim project 乘法器除法器.circ as structural Verilog: 10 circuits, main circuit main
module main (
  input  [3:0] in_1,
  input  [7:0] in_2,
  output [7:0] out_3
);

  wire [7:0] adder_1_out, adder_2_out, adder_3_out, adder_4_out, multiplexer_1_out, multiplexer_2_out,
       multiplexer_3_out, shifter_1_out, shifter_2_out, shifter_3_out;

  Adder adder_1 (.a({8{1'b0}}), .b(in_2), .out(adder_1_out));  // open: cin, cout
  Shifter shifter_1 (.in(in_2), .\dist (3'b001), .out(shifter_1_out));
  Multiplexer #(.width(8), .disabled(0), .enable("false")) multiplexer_1 (
    .in0({8{1'b0}}), .in1(adder_1_out), .out(multiplexer_1_out), .sel(in_1[0]));
  Adder adder_2 (.a(multiplexer_1_out), .b(shifter_1_out), .out(adder_2_out));  // open: cin, cout
  Shifter shifter_2 (.in(shifter_1_out), .\dist (3'b001), .out(shifter_2_out));
  Multiplexer #(.width(8), .disabled(0), .enable("false")) multiplexer_2 (
    .in0(multiplexer_1_out), .in1(adder_2_out), .out(multiplexer_2_out), .sel(in_1[1]));
  Adder adder_3 (.a(multiplexer_2_out), .b(shifter_2_out), .out(adder_3_out));  // open: cin, cout
  Shifter shifter_3 (.in(shifter_2_out), .\dist (3'b001), .out(shifter_3_out));
  Multiplexer #(.width(8), .disabled(0), .enable("false")) multiplexer_3 (
    .in0(multiplexer_2_out), .in1(adder_3_out), .out(multiplexer_3_out), .sel(in_1[2]));
  Adder adder_4 (.a(multiplexer_3_out), .b(shifter_3_out), .out(adder_4_out));  // open: cin, cout
  Multiplexer #(.width(8), .disabled(0), .enable("false")) multiplexer_4 (
    .in0(multiplexer_3_out), .in1(adder_4_out), .out(out_3), .sel(in_1[3]));
  Shifter shifter_4 (.in(shifter_3_out), .\dist (3'b001));  // open: out

  // Notes on the sheet:
  //      sh1
  //   sh1
  //   sh1  
  //      sh1
endmodule

module _32_4 (
  input  [3:0] in_1,
  input  [31:0] in_2,
  output [31:0] out_3
);

  wire [31:0] adder_1_out, adder_2_out, adder_3_out, adder_4_out, multiplexer_1_out, multiplexer_2_out,
       multiplexer_3_out, shifter_1_out, shifter_2_out, shifter_3_out;

  Adder #(.width(32)) adder_1 (.a({32{1'b0}}), .b(in_2), .out(adder_1_out));  // open: cin, cout
  Shifter #(.width(32)) shifter_1 (.in(in_2), .\dist (5'b00001), .out(shifter_1_out));
  Multiplexer #(.width(32), .disabled(0), .enable("false")) multiplexer_1 (
    .in0({32{1'b0}}), .in1(adder_1_out), .out(multiplexer_1_out), .sel(in_1[0]));
  Adder #(.width(32)) adder_2 (.a(multiplexer_1_out), .b(shifter_1_out), .out(adder_2_out));  // open: cin, cout
  Shifter #(.width(32)) shifter_2 (.in(shifter_1_out), .\dist (5'b00001), .out(shifter_2_out));
  Multiplexer #(.width(32), .disabled(0), .enable("false")) multiplexer_2 (
    .in0(multiplexer_1_out), .in1(adder_2_out), .out(multiplexer_2_out), .sel(in_1[1]));
  Adder #(.width(32)) adder_3 (.a(multiplexer_2_out), .b(shifter_2_out), .out(adder_3_out));  // open: cin, cout
  Shifter #(.width(32)) shifter_3 (.in(shifter_2_out), .\dist (5'b00001), .out(shifter_3_out));
  Multiplexer #(.width(32), .disabled(0), .enable("false")) multiplexer_3 (
    .in0(multiplexer_2_out), .in1(adder_3_out), .out(multiplexer_3_out), .sel(in_1[2]));
  Adder #(.width(32)) adder_4 (.a(multiplexer_3_out), .b(shifter_3_out), .out(adder_4_out));  // open: cin, cout
  Multiplexer #(.width(32), .disabled(0), .enable("false")) multiplexer_4 (
    .in0(multiplexer_3_out), .in1(adder_4_out), .out(out_3), .sel(in_1[3]));
  Shifter #(.width(32)) shifter_4 (.in(shifter_3_out), .\dist (5'b00001));  // open: out
endmodule

module _32_32 (
  input  [31:0] in_1,
  input  [31:0] in_2,
  output [31:0] out_3
);

  wire [31:0] adder_1_out, adder_2_out, adder_3_out, adder_4_out, adder_5_out, adder_6_out, n32_4_1_out_3,
       n32_4_2_out_3, n32_4_3_out_3, n32_4_4_out_3, n32_4_5_out_3, n32_4_6_out_3, n32_4_7_out_3,
       n32_4_8_out_3, shifter_1_out, shifter_2_out, shifter_3_out, shifter_4_out, shifter_5_out,
       shifter_6_out, shifter_7_out, shifter_8_out;

  _32_4 u_32_4_1 (.in_2(in_2), .out_3(n32_4_1_out_3), .in_1(in_1[31:28]));
  _32_4 u_32_4_2 (.in_2(in_2), .out_3(n32_4_2_out_3), .in_1(in_1[27:24]));
  _32_4 u_32_4_3 (.in_2(in_2), .out_3(n32_4_3_out_3), .in_1(in_1[23:20]));
  _32_4 u_32_4_4 (.in_2(in_2), .out_3(n32_4_4_out_3), .in_1(in_1[19:16]));
  Shifter #(.width(32)) shifter_1 (.in(n32_4_1_out_3), .\dist (5'b11100), .out(shifter_1_out));
  Shifter #(.width(32)) shifter_2 (.in(n32_4_2_out_3), .\dist (5'b11000), .out(shifter_2_out));
  Shifter #(.width(32)) shifter_3 (.in(n32_4_3_out_3), .\dist (5'b10100), .out(shifter_3_out));
  Shifter #(.width(32)) shifter_4 (.in(n32_4_4_out_3), .\dist (5'b10000), .out(shifter_4_out));
  _32_4 u_32_4_5 (.in_2(in_2), .out_3(n32_4_5_out_3), .in_1(in_1[15:12]));
  _32_4 u_32_4_6 (.in_2(in_2), .out_3(n32_4_6_out_3), .in_1(in_1[11:8]));
  _32_4 u_32_4_7 (.in_2(in_2), .out_3(n32_4_7_out_3), .in_1(in_1[7:4]));
  _32_4 u_32_4_8 (.in_2(in_2), .out_3(n32_4_8_out_3), .in_1(in_1[3:0]));
  Shifter #(.width(32)) shifter_5 (.in(n32_4_5_out_3), .\dist (5'b01100), .out(shifter_5_out));
  Shifter #(.width(32)) shifter_6 (.in(n32_4_6_out_3), .\dist (5'b01000), .out(shifter_6_out));
  Shifter #(.width(32)) shifter_7 (.in(n32_4_7_out_3), .\dist (5'b00100), .out(shifter_7_out));
  Shifter #(.width(32)) shifter_8 (.in(n32_4_8_out_3), .\dist ({5{1'b0}}), .out(shifter_8_out));
  Adder #(.width(32)) adder_1 (.a(shifter_1_out), .b(shifter_2_out), .out(adder_1_out));  // open: cin, cout
  Adder #(.width(32)) adder_2 (.a(shifter_5_out), .b(shifter_6_out), .out(adder_2_out));  // open: cin, cout
  Adder #(.width(32)) adder_3 (.a(shifter_7_out), .b(shifter_8_out), .out(adder_3_out));  // open: cin, cout
  Adder #(.width(32)) adder_4 (.a(shifter_3_out), .b(shifter_4_out), .out(adder_4_out));  // open: cin, cout
  Adder #(.width(32)) adder_5 (.a(adder_1_out), .b(adder_2_out), .out(adder_5_out));  // open: cin, cout
  Adder #(.width(32)) adder_6 (.a(adder_3_out), .b(adder_4_out), .out(adder_6_out));  // open: cin, cout
  Adder #(.width(32)) adder_7 (.a(adder_5_out), .b(adder_6_out), .out(out_3));  // open: cin, cout

  // Notes on the sheet:
  //   b
  //   P
endmodule

module \_32_32封装  (
  input  [31:0] in_1,
  input  [31:0] in_2,
  output [31:0] out_3
);

  _32_32 u_32_32_1 (.in_2(in_2), .out_3(out_3), .in_1(in_1));
endmodule

module \四位除法器  (
  input  [3:0] d,
  input  [3:0] n2,
  output [3:0] \余数 ,
  output [3:0] \商 
);

  wire comparator_1_eq, comparator_1_lt, comparator_2_eq, comparator_2_lt, comparator_3_eq, comparator_3_lt,
       comparator_4_eq, comparator_4_lt, or_1_out, or_2_out, or_3_out, or_4_out;
  wire [0:0] multiplexer_2_out, multiplexer_6_out;
  wire [3:0] multiplexer_1_out, multiplexer_3_out, multiplexer_4_out, multiplexer_5_out, subtractor_1_out,
       subtractor_2_out, subtractor_3_out, subtractor_4_out;
  wire [7:0] shifter_1_out, shifter_2_out, shifter_3_out, shifter_4_out;

  Shifter shifter_1 (.in({4'b0000, n2}), .\dist (3'b001), .out(shifter_1_out));
  Comparator #(.width(4), .mode("unsigned")) comparator_1 (
    .a(d), .b(shifter_1_out[7:4]), .eq(comparator_1_eq), .lt(comparator_1_lt));  // open: gt
  Subtractor #(.width(4)) subtractor_1 (.a(shifter_1_out[7:4]), .b(d), .out(subtractor_1_out));  // open: bin, bout
  Multiplexer #(.width(4), .enable("false")) multiplexer_1 (
    .in0(shifter_1_out[7:4]), .in1(subtractor_1_out), .out(multiplexer_1_out), .sel(or_1_out));
  or or_1 (or_1_out, comparator_1_eq, comparator_1_lt);
  Multiplexer #(.enable("false")) multiplexer_2 (
    .in0(shifter_1_out[0]), .in1(1'b1), .out(multiplexer_2_out[0]), .sel(or_1_out));
  Shifter shifter_2 (
    .in({multiplexer_1_out, shifter_1_out[3:1], multiplexer_2_out[0]}), .\dist (3'b001),
    .out({shifter_2_out[7:4], multiplexer_4_out[3:1], shifter_2_out[0]}));
  Comparator #(.width(4), .mode("unsigned")) comparator_2 (
    .a(d), .b(shifter_2_out[7:4]), .eq(comparator_2_eq), .lt(comparator_2_lt));  // open: gt
  Subtractor #(.width(4)) subtractor_2 (.a(shifter_2_out[7:4]), .b(d), .out(subtractor_2_out));  // open: bin, bout
  Multiplexer #(.width(4), .enable("false")) multiplexer_3 (
    .in0(shifter_2_out[7:4]), .in1(subtractor_2_out), .out(multiplexer_3_out), .sel(or_2_out));
  or or_2 (or_2_out, comparator_2_eq, comparator_2_lt);
  Multiplexer #(.enable("false")) multiplexer_4 (
    .in0(shifter_2_out[0]), .in1(1'b1), .out(multiplexer_4_out[0]), .sel(or_2_out));
  Shifter shifter_3 (.in({multiplexer_3_out, multiplexer_4_out}), .\dist (3'b001), .out(shifter_3_out));
  Comparator #(.width(4), .mode("unsigned")) comparator_3 (
    .a(d), .b(shifter_3_out[7:4]), .eq(comparator_3_eq), .lt(comparator_3_lt));  // open: gt
  Subtractor #(.width(4)) subtractor_3 (.a(shifter_3_out[7:4]), .b(d), .out(subtractor_3_out));  // open: bin, bout
  Multiplexer #(.width(4), .enable("false")) multiplexer_5 (
    .in0(shifter_3_out[7:4]), .in1(subtractor_3_out), .out(multiplexer_5_out), .sel(or_3_out));
  or or_3 (or_3_out, comparator_3_eq, comparator_3_lt);
  Multiplexer #(.enable("false")) multiplexer_6 (
    .in0(shifter_3_out[0]), .in1(1'b1), .out(multiplexer_6_out[0]), .sel(or_3_out));
  Shifter shifter_4 (
    .in({multiplexer_5_out, shifter_3_out[3:1], multiplexer_6_out[0]}), .\dist (3'b001),
    .out({shifter_4_out[7:4], \商 [3:1], shifter_4_out[0]}));
  Comparator #(.width(4), .mode("unsigned")) comparator_4 (
    .a(d), .b(shifter_4_out[7:4]), .eq(comparator_4_eq), .lt(comparator_4_lt));  // open: gt
  Subtractor #(.width(4)) subtractor_4 (.a(shifter_4_out[7:4]), .b(d), .out(subtractor_4_out));  // open: bin, bout
  or or_4 (or_4_out, comparator_4_eq, comparator_4_lt);
  Multiplexer #(.width(4), .enable("false")) multiplexer_7 (
    .in0(shifter_4_out[7:4]), .in1(subtractor_4_out), .out(\余数 ), .sel(or_4_out));
  Multiplexer #(.enable("false")) multiplexer_8 (.in0(shifter_4_out[0]), .in1(1'b1), .out(\商 [0]), .sel(or_4_out));

  // Notes on the sheet:
  //   n1
endmodule

module \封装  (
  input  [3:0] in_1,
  input  [3:0] in_2,
  output [3:0] out_3,
  output [3:0] out_4
);

  \四位除法器  \u_四位除法器_1  (.d(in_1), .n2(in_2), .\余数 (out_3), .\商 (out_4));
endmodule

module \_32_32除法器  (
  input  [31:0] d,
  input  [31:0] n1,
  input  [31:0] n2,
  output [31:0] out_4,
  output [31:0] out_5
);

  wire comparator_1_eq, comparator_1_lt, or_1_out;
  wire [0:0] \n64位移位器_1_out_4 ;
  wire [31:0] \n64位移位器_1_out_3 , subtractor_1_out;

  \_64位移位器  \u_64位移位器_1  (.in_1(n1), .in_2(n2), .out_3(\n64位移位器_1_out_3 ), .out_4({out_5[31:1], \n64位移位器_1_out_4 [0]}));
  Subtractor #(.width(32)) subtractor_1 (.a(\n64位移位器_1_out_3 ), .b(d), .out(subtractor_1_out));  // open: bin, bout
  Comparator #(.width(32), .mode("unsigned")) comparator_1 (
    .a(d), .b(\n64位移位器_1_out_3 ), .eq(comparator_1_eq), .lt(comparator_1_lt));  // open: gt
  Multiplexer #(.width(32), .enable("false")) multiplexer_1 (
    .in0(\n64位移位器_1_out_3 ), .in1(subtractor_1_out), .out(out_4), .sel(or_1_out));
  or or_1 (or_1_out, comparator_1_eq, comparator_1_lt);
  Multiplexer #(.enable("false")) multiplexer_2 (
    .in0(\n64位移位器_1_out_4 [0]), .in1(1'b1), .out(out_5[0]), .sel(or_1_out));
endmodule

module \_64位移位器  (
  input  [31:0] in_1,
  input  [31:0] in_2,
  output [31:0] out_3,
  output [31:0] out_4
);


  assign out_3 = {in_1[30:0], in_2[31]};
  assign out_4 = {in_2[30:0], 1'b0};
endmodule

module \_32_32除法器完整版  (
  input  [31:0] d,
  input  [31:0] n2,
  output [31:0] out_3,
  output [31:0] out_4
);

  wire [31:0] \n32_32除法器_1_out_4 , \n32_32除法器_1_out_5 , \n32_32除法器_2_out_4 , \n32_32除法器_2_out_5 ,
       \n32_32除法器_3_out_4 , \n32_32除法器_3_out_5 , \n32_32除法器_4_out_4 , \n32_32除法器_4_out_5 ,
       \n32_32除法器_5_out_4 , \n32_32除法器_5_out_5 , \n32_32除法器_6_out_4 , \n32_32除法器_6_out_5 ,
       \n32_32除法器_7_out_4 , \n32_32除法器_7_out_5 , \n32_32除法器_8_out_4 , \n32_32除法器_8_out_5 ,
       \n32_32除法器_9_out_4 , \n32_32除法器_9_out_5 , \n32_32除法器_10_out_4 , \n32_32除法器_10_out_5 ,
       \n32_32除法器_11_out_4 , \n32_32除法器_11_out_5 , \n32_32除法器_12_out_4 , \n32_32除法器_12_out_5 ,
       \n32_32除法器_13_out_4 , \n32_32除法器_13_out_5 , \n32_32除法器_14_out_4 , \n32_32除法器_14_out_5 ,
       \n32_32除法器_15_out_4 , \n32_32除法器_15_out_5 , \n32_32除法器_16_out_4 , \n32_32除法器_16_out_5 ,
       \n32_32除法器_17_out_4 , \n32_32除法器_17_out_5 , \n32_32除法器_18_out_4 , \n32_32除法器_18_out_5 ,
       \n32_32除法器_19_out_4 , \n32_32除法器_19_out_5 , \n32_32除法器_20_out_4 , \n32_32除法器_20_out_5 ,
       \n32_32除法器_21_out_4 , \n32_32除法器_21_out_5 , \n32_32除法器_22_out_4 , \n32_32除法器_22_out_5 ,
       \n32_32除法器_23_out_4 , \n32_32除法器_23_out_5 , \n32_32除法器_24_out_4 , \n32_32除法器_24_out_5 ,
       \n32_32除法器_25_out_4 , \n32_32除法器_25_out_5 , \n32_32除法器_26_out_4 , \n32_32除法器_26_out_5 ,
       \n32_32除法器_27_out_4 , \n32_32除法器_27_out_5 , \n32_32除法器_28_out_4 , \n32_32除法器_28_out_5 ,
       \n32_32除法器_29_out_4 , \n32_32除法器_29_out_5 , \n32_32除法器_30_out_4 , \n32_32除法器_30_out_5 ,
       \n32_32除法器_31_out_4 , \n32_32除法器_31_out_5 ;

  \_32_32除法器  \u_32_32除法器_1  (
    .d(d), .n2(n2), .out_4(\n32_32除法器_1_out_4 ), .out_5(\n32_32除法器_1_out_5 ), .n1({32{1'b0}}));
  \_32_32除法器  \u_32_32除法器_2  (
    .d(d), .n2(\n32_32除法器_25_out_5 ), .out_4(\n32_32除法器_2_out_4 ), .out_5(\n32_32除法器_2_out_5 ),
    .n1(\n32_32除法器_25_out_4 ));
  \_32_32除法器  \u_32_32除法器_3  (
    .d(d), .n2(\n32_32除法器_26_out_5 ), .out_4(\n32_32除法器_3_out_4 ), .out_5(\n32_32除法器_3_out_5 ),
    .n1(\n32_32除法器_26_out_4 ));
  \_32_32除法器  \u_32_32除法器_4  (
    .d(d), .n2(\n32_32除法器_27_out_5 ), .out_4(\n32_32除法器_4_out_4 ), .out_5(\n32_32除法器_4_out_5 ),
    .n1(\n32_32除法器_27_out_4 ));
  \_32_32除法器  \u_32_32除法器_5  (
    .d(d), .n2(\n32_32除法器_28_out_5 ), .out_4(\n32_32除法器_5_out_4 ), .out_5(\n32_32除法器_5_out_5 ),
    .n1(\n32_32除法器_28_out_4 ));
  \_32_32除法器  \u_32_32除法器_6  (
    .d(d), .n2(\n32_32除法器_29_out_5 ), .out_4(\n32_32除法器_6_out_4 ), .out_5(\n32_32除法器_6_out_5 ),
    .n1(\n32_32除法器_29_out_4 ));
  \_32_32除法器  \u_32_32除法器_7  (
    .d(d), .n2(\n32_32除法器_30_out_5 ), .out_4(\n32_32除法器_7_out_4 ), .out_5(\n32_32除法器_7_out_5 ),
    .n1(\n32_32除法器_30_out_4 ));
  \_32_32除法器  \u_32_32除法器_8  (
    .d(d), .n2(\n32_32除法器_31_out_5 ), .out_4(\n32_32除法器_8_out_4 ), .out_5(\n32_32除法器_8_out_5 ),
    .n1(\n32_32除法器_31_out_4 ));
  \_32_32除法器  \u_32_32除法器_9  (
    .d(d), .n2(\n32_32除法器_1_out_5 ), .out_4(\n32_32除法器_9_out_4 ), .out_5(\n32_32除法器_9_out_5 ),
    .n1(\n32_32除法器_1_out_4 ));
  \_32_32除法器  \u_32_32除法器_10  (
    .d(d), .n2(\n32_32除法器_2_out_5 ), .out_4(\n32_32除法器_10_out_4 ), .out_5(\n32_32除法器_10_out_5 ),
    .n1(\n32_32除法器_2_out_4 ));
  \_32_32除法器  \u_32_32除法器_11  (
    .d(d), .n2(\n32_32除法器_3_out_5 ), .out_4(\n32_32除法器_11_out_4 ), .out_5(\n32_32除法器_11_out_5 ),
    .n1(\n32_32除法器_3_out_4 ));
  \_32_32除法器  \u_32_32除法器_12  (
    .d(d), .n2(\n32_32除法器_4_out_5 ), .out_4(\n32_32除法器_12_out_4 ), .out_5(\n32_32除法器_12_out_5 ),
    .n1(\n32_32除法器_4_out_4 ));
  \_32_32除法器  \u_32_32除法器_13  (
    .d(d), .n2(\n32_32除法器_5_out_5 ), .out_4(\n32_32除法器_13_out_4 ), .out_5(\n32_32除法器_13_out_5 ),
    .n1(\n32_32除法器_5_out_4 ));
  \_32_32除法器  \u_32_32除法器_14  (
    .d(d), .n2(\n32_32除法器_6_out_5 ), .out_4(\n32_32除法器_14_out_4 ), .out_5(\n32_32除法器_14_out_5 ),
    .n1(\n32_32除法器_6_out_4 ));
  \_32_32除法器  \u_32_32除法器_15  (
    .d(d), .n2(\n32_32除法器_7_out_5 ), .out_4(\n32_32除法器_15_out_4 ), .out_5(\n32_32除法器_15_out_5 ),
    .n1(\n32_32除法器_7_out_4 ));
  \_32_32除法器  \u_32_32除法器_16  (
    .d(d), .n2(\n32_32除法器_8_out_5 ), .out_4(\n32_32除法器_16_out_4 ), .out_5(\n32_32除法器_16_out_5 ),
    .n1(\n32_32除法器_8_out_4 ));
  \_32_32除法器  \u_32_32除法器_17  (
    .d(d), .n2(\n32_32除法器_9_out_5 ), .out_4(\n32_32除法器_17_out_4 ), .out_5(\n32_32除法器_17_out_5 ),
    .n1(\n32_32除法器_9_out_4 ));
  \_32_32除法器  \u_32_32除法器_18  (
    .d(d), .n2(\n32_32除法器_10_out_5 ), .out_4(\n32_32除法器_18_out_4 ), .out_5(\n32_32除法器_18_out_5 ),
    .n1(\n32_32除法器_10_out_4 ));
  \_32_32除法器  \u_32_32除法器_19  (
    .d(d), .n2(\n32_32除法器_11_out_5 ), .out_4(\n32_32除法器_19_out_4 ), .out_5(\n32_32除法器_19_out_5 ),
    .n1(\n32_32除法器_11_out_4 ));
  \_32_32除法器  \u_32_32除法器_20  (
    .d(d), .n2(\n32_32除法器_12_out_5 ), .out_4(\n32_32除法器_20_out_4 ), .out_5(\n32_32除法器_20_out_5 ),
    .n1(\n32_32除法器_12_out_4 ));
  \_32_32除法器  \u_32_32除法器_21  (
    .d(d), .n2(\n32_32除法器_13_out_5 ), .out_4(\n32_32除法器_21_out_4 ), .out_5(\n32_32除法器_21_out_5 ),
    .n1(\n32_32除法器_13_out_4 ));
  \_32_32除法器  \u_32_32除法器_22  (
    .d(d), .n2(\n32_32除法器_14_out_5 ), .out_4(\n32_32除法器_22_out_4 ), .out_5(\n32_32除法器_22_out_5 ),
    .n1(\n32_32除法器_14_out_4 ));
  \_32_32除法器  \u_32_32除法器_23  (
    .d(d), .n2(\n32_32除法器_15_out_5 ), .out_4(\n32_32除法器_23_out_4 ), .out_5(\n32_32除法器_23_out_5 ),
    .n1(\n32_32除法器_15_out_4 ));
  \_32_32除法器  \u_32_32除法器_24  (
    .d(d), .n2(\n32_32除法器_16_out_5 ), .out_4(\n32_32除法器_24_out_4 ), .out_5(\n32_32除法器_24_out_5 ),
    .n1(\n32_32除法器_16_out_4 ));
  \_32_32除法器  \u_32_32除法器_25  (
    .d(d), .n2(\n32_32除法器_17_out_5 ), .out_4(\n32_32除法器_25_out_4 ), .out_5(\n32_32除法器_25_out_5 ),
    .n1(\n32_32除法器_17_out_4 ));
  \_32_32除法器  \u_32_32除法器_26  (
    .d(d), .n2(\n32_32除法器_18_out_5 ), .out_4(\n32_32除法器_26_out_4 ), .out_5(\n32_32除法器_26_out_5 ),
    .n1(\n32_32除法器_18_out_4 ));
  \_32_32除法器  \u_32_32除法器_27  (
    .d(d), .n2(\n32_32除法器_19_out_5 ), .out_4(\n32_32除法器_27_out_4 ), .out_5(\n32_32除法器_27_out_5 ),
    .n1(\n32_32除法器_19_out_4 ));
  \_32_32除法器  \u_32_32除法器_28  (
    .d(d), .n2(\n32_32除法器_20_out_5 ), .out_4(\n32_32除法器_28_out_4 ), .out_5(\n32_32除法器_28_out_5 ),
    .n1(\n32_32除法器_20_out_4 ));
  \_32_32除法器  \u_32_32除法器_29  (
    .d(d), .n2(\n32_32除法器_21_out_5 ), .out_4(\n32_32除法器_29_out_4 ), .out_5(\n32_32除法器_29_out_5 ),
    .n1(\n32_32除法器_21_out_4 ));
  \_32_32除法器  \u_32_32除法器_30  (
    .d(d), .n2(\n32_32除法器_22_out_5 ), .out_4(\n32_32除法器_30_out_4 ), .out_5(\n32_32除法器_30_out_5 ),
    .n1(\n32_32除法器_22_out_4 ));
  \_32_32除法器  \u_32_32除法器_31  (
    .d(d), .n2(\n32_32除法器_23_out_5 ), .out_4(\n32_32除法器_31_out_4 ), .out_5(\n32_32除法器_31_out_5 ),
    .n1(\n32_32除法器_23_out_4 ));
  \_32_32除法器  \u_32_32除法器_32  (
    .d(d), .n2(\n32_32除法器_24_out_5 ), .out_4(out_3), .out_5(out_4), .n1(\n32_32除法器_24_out_4 ));
endmodule

module \_32_32除法器封装  (
  input  [31:0] in_1,
  input  [31:0] in_2,
  output [31:0] out_3,
  output [31:0] out_4
);

  \_32_32除法器完整版  \u_32_32除法器完整版_1  (.d(in_1), .n2(in_2), .out_3(out_3), .out_4(out_4));
endmodule
