// Logisim project 斐波拉契数列.circ as structural Verilog: 6 circuits, main circuit main
module main (
  input  [5:0] in_1
);

  wire button_1_out, clock_1_out, controller_1_clear, controller_1_clk_2, controller_1_n_i_1,
       controller_1_start;
  wire [3:0] display_1_a0, display_1_a1, display_1_a2, display_1_a3, display_1_a4, display_1_a5,
       display_1_a6, display_1_a7, display_1_a8, display_1_a9;
  wire [31:0] fibo_1_fi;

  Button button_1 (.out(button_1_out));
  Clock clock_1 (.out(clock_1_out));
  Controller controller_1 (
    .n(in_1), .clr(button_1_out), .clk(clock_1_out), .start(controller_1_start), .clear(controller_1_clear),
    .n_i_1(controller_1_n_i_1), .clk_2(controller_1_clk_2));
  Fibo fibo_1 (
    .start(controller_1_start), .clk(controller_1_clk_2), .clr(controller_1_clear),
    .n_i_1(controller_1_n_i_1), .Fi(fibo_1_fi));
  Hex_Digit_Display hex_digit_display_1 (.value(display_1_a9));  // open: dp
  Display display_1 (
    .in_1(fibo_1_fi), .a0(display_1_a0), .a1(display_1_a1), .a2(display_1_a2), .a3(display_1_a3),
    .a4(display_1_a4), .a5(display_1_a5), .a6(display_1_a6), .a7(display_1_a7), .a8(display_1_a8),
    .a9(display_1_a9));
  Hex_Digit_Display hex_digit_display_2 (.value(display_1_a7));  // open: dp
  Hex_Digit_Display hex_digit_display_3 (.value(display_1_a8));  // open: dp
  Hex_Digit_Display hex_digit_display_4 (.value(display_1_a5));  // open: dp
  Hex_Digit_Display hex_digit_display_5 (.value(display_1_a6));  // open: dp
  Hex_Digit_Display hex_digit_display_6 (.value(display_1_a4));  // open: dp
  Hex_Digit_Display hex_digit_display_7 (.value(display_1_a3));  // open: dp
  Hex_Digit_Display hex_digit_display_8 (.value(display_1_a2));  // open: dp
  Hex_Digit_Display hex_digit_display_9 (.value(display_1_a1));  // open: dp
  Hex_Digit_Display hex_digit_display_10 (.value(display_1_a0));  // open: dp
endmodule

module sqrX (
  input  [31:0] a,
  input  [31:0] b,
  input  [31:0] c,
  input  [31:0] d,
  output [31:0] a_prime,
  output [31:0] b_prime,
  output [31:0] c_prime,
  output [31:0] d_prime
);

  wire [31:0] multiplier_1_out, multiplier_2_out, multiplier_3_out, multiplier_4_out, multiplier_5_out,
       multiplier_6_out, multiplier_7_out, multiplier_8_out;

  Multiplier #(.width(32)) multiplier_1 (.a(a), .b(a), .out(multiplier_1_out));  // open: cin, cout
  Multiplier #(.width(32)) multiplier_2 (.a(b), .b(c), .out(multiplier_2_out));  // open: cin, cout
  Multiplier #(.width(32)) multiplier_3 (.a(a), .b(b), .out(multiplier_3_out));  // open: cin, cout
  Multiplier #(.width(32)) multiplier_4 (.a(b), .b(d), .out(multiplier_4_out));  // open: cin, cout
  Multiplier #(.width(32)) multiplier_5 (.a(a), .b(c), .out(multiplier_5_out));  // open: cin, cout
  Multiplier #(.width(32)) multiplier_6 (.a(c), .b(d), .out(multiplier_6_out));  // open: cin, cout
  Multiplier #(.width(32)) multiplier_7 (.a(b), .b(c), .out(multiplier_7_out));  // open: cin, cout
  Multiplier #(.width(32)) multiplier_8 (.a(d), .b(d), .out(multiplier_8_out));  // open: cin, cout
  Adder #(.width(32)) adder_1 (.a(multiplier_1_out), .b(multiplier_2_out), .out(a_prime));  // open: cin, cout
  Adder #(.width(32)) adder_2 (.a(multiplier_3_out), .b(multiplier_4_out), .out(b_prime));  // open: cin, cout
  Adder #(.width(32)) adder_3 (.a(multiplier_5_out), .b(multiplier_6_out), .out(c_prime));  // open: cin, cout
  Adder #(.width(32)) adder_4 (.a(multiplier_7_out), .b(multiplier_8_out), .out(d_prime));  // open: cin, cout
endmodule

module sqrX_A (
  input  [31:0] a,
  input  [31:0] b,
  input  [31:0] c,
  input  [31:0] d,
  output [31:0] a_prime_prime,
  output [31:0] b_prime_prime,
  output [31:0] c_prime_prime,
  output [31:0] d_prime_prime
);

  wire [31:0] adder_2_out, adder_4_out, multiplier_1_out, multiplier_2_out, multiplier_3_out,
       multiplier_4_out, multiplier_5_out, multiplier_6_out, multiplier_7_out;

  Multiplier #(.width(32)) multiplier_1 (.a(a), .b(b), .out(multiplier_1_out));  // open: cin, cout
  Multiplier #(.width(32)) multiplier_2 (.a(b), .b(d), .out(multiplier_2_out));  // open: cin, cout
  Multiplier #(.width(32)) multiplier_3 (.a(a), .b(a), .out(multiplier_3_out));  // open: cin, cout
  Multiplier #(.width(32)) multiplier_4 (.a(b), .b(c), .out(multiplier_4_out));  // open: cin, cout
  Multiplier #(.width(32)) multiplier_5 (.a(d), .b(d), .out(multiplier_5_out));  // open: cin, cout
  Multiplier #(.width(32)) multiplier_6 (.a(a), .b(c), .out(multiplier_6_out));  // open: cin, cout
  Multiplier #(.width(32)) multiplier_7 (.a(c), .b(d), .out(multiplier_7_out));  // open: cin, cout
  Adder #(.width(32)) adder_1 (.a(multiplier_1_out), .b(multiplier_2_out), .out(a_prime_prime));  // open: cin, cout
  Adder #(.width(32)) adder_2 (.a(multiplier_3_out), .b(multiplier_4_out), .out(adder_2_out));  // open: cin, cout
  Adder #(.width(32)) adder_3 (.a(multiplier_4_out), .b(multiplier_5_out), .out(c_prime_prime));  // open: cin, cout
  Adder #(.width(32)) adder_4 (.a(multiplier_6_out), .b(multiplier_7_out), .out(adder_4_out));  // open: cin, cout
  Adder #(.width(32)) adder_5 (.a(adder_2_out), .b(a_prime_prime), .out(b_prime_prime));  // open: cin, cout
  Adder #(.width(32)) adder_6 (.a(adder_4_out), .b(c_prime_prime), .out(d_prime_prime));  // open: cin, cout
endmodule

module Fibo (
  input  start,
  input  clk,
  input  clr,
  input  n_i_1,
  output [31:0] Fi
);

  wire [31:0] multiplexer_1_out, multiplexer_2_out, multiplexer_3_out, multiplexer_4_out, multiplexer_5_out,
       multiplexer_6_out, multiplexer_7_out, multiplexer_8_out, register_1_q, register_2_q, register_4_q,
       sqrx_1_a_prime, sqrx_1_b_prime, sqrx_1_c_prime, sqrx_1_d_prime, sqrx_a_1_a_prime_prime,
       sqrx_a_1_b_prime_prime, sqrx_a_1_c_prime_prime, sqrx_a_1_d_prime_prime;

  Multiplexer #(.width(32)) multiplexer_1 (
    .in0({32{1'b0}}), .in1(multiplexer_5_out), .out(multiplexer_1_out), .sel(start));  // open: en
  Multiplexer #(.width(32)) multiplexer_2 (
    .in0(32'h1), .in1(multiplexer_6_out), .out(multiplexer_2_out), .sel(start));  // open: en
  Multiplexer #(.width(32)) multiplexer_3 (
    .in0(32'h1), .in1(multiplexer_7_out), .out(multiplexer_3_out), .sel(start));  // open: en
  Multiplexer #(.width(32)) multiplexer_4 (
    .in0(32'h1), .in1(multiplexer_8_out), .out(multiplexer_4_out), .sel(start));  // open: en
  Register #(.width(32)) register_1 (.D(multiplexer_1_out), .Q(register_1_q), .clk(clk), .clr(clr));  // open: en
  Register #(.width(32)) register_2 (.D(multiplexer_3_out), .Q(register_2_q), .clk(clk), .clr(clr));  // open: en
  Register #(.width(32)) register_3 (.D(multiplexer_2_out), .Q(Fi), .clk(clk), .clr(clr));  // open: en
  Register #(.width(32)) register_4 (.D(multiplexer_4_out), .Q(register_4_q), .clk(clk), .clr(clr));  // open: en
  sqrX sqrx_1 (
    .a(register_1_q), .b(Fi), .c(register_2_q), .d(register_4_q), .a_prime(sqrx_1_a_prime),
    .b_prime(sqrx_1_b_prime), .c_prime(sqrx_1_c_prime), .d_prime(sqrx_1_d_prime));
  sqrX_A sqrx_a_1 (
    .a(register_1_q), .b(Fi), .c(register_2_q), .d(register_4_q), .a_prime_prime(sqrx_a_1_a_prime_prime),
    .b_prime_prime(sqrx_a_1_b_prime_prime), .c_prime_prime(sqrx_a_1_c_prime_prime),
    .d_prime_prime(sqrx_a_1_d_prime_prime));
  Multiplexer #(.width(32)) multiplexer_5 (
    .in0(sqrx_1_a_prime), .in1(sqrx_a_1_a_prime_prime), .out(multiplexer_5_out), .sel(n_i_1));  // open: en
  Multiplexer #(.width(32)) multiplexer_6 (
    .in0(sqrx_1_b_prime), .in1(sqrx_a_1_b_prime_prime), .out(multiplexer_6_out), .sel(n_i_1));  // open: en
  Multiplexer #(.width(32)) multiplexer_7 (
    .in0(sqrx_1_c_prime), .in1(sqrx_a_1_c_prime_prime), .out(multiplexer_7_out), .sel(n_i_1));  // open: en
  Multiplexer #(.width(32)) multiplexer_8 (
    .in0(sqrx_1_d_prime), .in1(sqrx_a_1_d_prime_prime), .out(multiplexer_8_out), .sel(n_i_1));  // open: en
endmodule

module Controller (
  input  [5:0] n,
  input  clr,
  input  clk,
  output start,
  output clear,
  output n_i_1,
  output clk_2
);

  wire comparator_1_eq, d_ff_1_qn, not_1_out, not_2_out, shift_register_1_out;
  wire [7:0] counter_1_q;

  not not_1 (not_1_out, comparator_1_eq);
  not not_2 (not_2_out, clr);
  and and_1 (clk_2, clk, not_1_out);
  Shift_Register #(.length(7)) shift_register_1 (
    .shift(not_2_out), .clk(clk_2), .out(shift_register_1_out), .load(clr), .d0(n[0]), .d1(n[1]), .d2(n[2]),
    .d3(n[3]), .d4(n[4]), .d5(n[5]), .q5(n_i_1), .d6(1'b0));  // open: in, clr, q0, q1, q2, q3, q4, q6
  Counter counter_1 (.count(not_1_out), .Q(counter_1_q), .clk(clk), .clr(clr));  // open: load, D, carry
  Comparator comparator_1 (.a(counter_1_q), .b(8'h6), .eq(comparator_1_eq));  // open: gt, lt
  D_Flip_Flop #(.trigger("falling")) d_ff_1 (
    .clk(clk), .D(shift_register_1_out), .Q(start), .Qn(d_ff_1_qn), .en(d_ff_1_qn), .reset(clr));  // open: preset

  assign clear = clr;
endmodule

module Display (
  input  [31:0] in_1,
  output [3:0] a0,
  output [3:0] a1,
  output [3:0] a2,
  output [3:0] a3,
  output [3:0] a4,
  output [3:0] a5,
  output [3:0] a6,
  output [3:0] a7,
  output [3:0] a8,
  output [3:0] a9
);

  wire [31:0] divider_1_out, divider_2_out, divider_3_out, divider_4_out, divider_5_out, divider_6_out,
       divider_7_out, divider_8_out, divider_9_out;
  wire [31:4] divider_1_rem, divider_2_rem, divider_3_rem, divider_4_rem, divider_5_rem, divider_6_rem,
       divider_7_rem, divider_8_rem, divider_9_rem, divider_10_rem;

  Divider #(.width(32)) divider_1 (.a(in_1), .b(32'ha), .out(divider_1_out), .rem({divider_1_rem, a0}));  // open: upper
  Divider #(.width(32)) divider_2 (
    .a(divider_1_out), .b(32'ha), .out(divider_2_out), .rem({divider_2_rem, a1}));  // open: upper
  Divider #(.width(32)) divider_3 (
    .a(divider_2_out), .b(32'ha), .out(divider_3_out), .rem({divider_3_rem, a2}));  // open: upper
  Divider #(.width(32)) divider_4 (
    .a(divider_3_out), .b(32'ha), .out(divider_4_out), .rem({divider_4_rem, a3}));  // open: upper
  Divider #(.width(32)) divider_5 (
    .a(divider_4_out), .b(32'ha), .out(divider_5_out), .rem({divider_5_rem, a4}));  // open: upper
  Divider #(.width(32)) divider_6 (
    .a(divider_5_out), .b(32'ha), .out(divider_6_out), .rem({divider_6_rem, a5}));  // open: upper
  Divider #(.width(32)) divider_7 (
    .a(divider_6_out), .b(32'ha), .out(divider_7_out), .rem({divider_7_rem, a6}));  // open: upper
  Divider #(.width(32)) divider_8 (
    .a(divider_7_out), .b(32'ha), .out(divider_8_out), .rem({divider_8_rem, a7}));  // open: upper
  Divider #(.width(32)) divider_9 (
    .a(divider_8_out), .b(32'ha), .out(divider_9_out), .rem({divider_9_rem, a8}));  // open: upper
  Divider #(.width(32)) divider_10 (.a(divider_9_out), .b(32'ha), .rem({divider_10_rem, a9}));  // open: out, upper
endmodule
