// Logisim project 时钟.circ as structural Verilog: 10 circuits, main circuit 主电路
module \四位二进制可逆计数器  (
  input  CPU,
  input  CPD,
  input  CLR,
  output Q0,
  output Q1,
  output Q2,
  output Q3
);

  wire and_1_out, and_2_out, and_3_out, and_4_out, and_5_out, and_6_out, and_7_out, and_8_out, and_9_out,
       and_10_out, and_11_out, d_ff_1_qn, d_ff_2_qn, d_ff_3_qn, d_ff_4_qn, nor_1_out, nor_2_out, nor_3_out,
       nor_4_out, not_1_out, or_1_out, or_2_out, or_3_out, or_4_out, or_5_out, or_6_out, or_7_out, or_8_out;

  or or_1 (or_1_out, CPU, CPD);
  and and_1 (and_1_out, Q0, CPU);
  and and_2 (and_2_out, d_ff_1_qn, CPD);
  and and_3 (and_3_out, Q1, Q0, CPU);
  and and_4 (and_4_out, d_ff_2_qn, d_ff_1_qn, CPD);
  and and_5 (and_5_out, Q2, Q1, Q0, CPU);
  and and_6 (and_6_out, d_ff_3_qn, d_ff_2_qn, d_ff_1_qn, CPD);
  D_Flip_Flop #(.trigger("falling")) d_ff_1 (
    .clk(or_1_out), .D(d_ff_1_qn), .Q(Q0), .Qn(d_ff_1_qn), .preset(and_8_out), .reset(or_5_out));  // open: en
  or or_2 (or_2_out, and_1_out, and_2_out);
  or or_3 (or_3_out, and_3_out, and_4_out);
  or or_4 (or_4_out, and_5_out, and_6_out);
  D_Flip_Flop #(.trigger("falling")) d_ff_2 (
    .clk(or_2_out), .D(d_ff_2_qn), .Q(Q1), .Qn(d_ff_2_qn), .preset(and_9_out), .reset(or_6_out));  // open: en
  D_Flip_Flop #(.trigger("falling")) d_ff_3 (
    .clk(or_3_out), .D(d_ff_3_qn), .Q(Q2), .Qn(d_ff_3_qn), .preset(and_10_out), .reset(or_7_out));  // open: en
  D_Flip_Flop #(.trigger("falling")) d_ff_4 (
    .clk(or_4_out), .D(d_ff_4_qn), .Q(Q3), .Qn(d_ff_4_qn), .preset(and_11_out), .reset(or_8_out));  // open: en
  or or_5 (or_5_out, CLR, nor_1_out);
  or or_6 (or_6_out, CLR, nor_2_out);
  or or_7 (or_7_out, CLR, nor_4_out);
  or or_8 (or_8_out, CLR, nor_3_out);
  and and_7 (and_7_out, Q0, Q1, Q3, Q2);
  not not_1 (not_1_out, and_7_out);
  and and_8 (and_8_out, and_7_out, 1'b1);
  nor nor_1 (nor_1_out, not_1_out, 1'b1);
  and and_9 (and_9_out, and_7_out, 1'b0);
  nor nor_2 (nor_2_out, not_1_out, 1'b0);
  and and_10 (and_10_out, and_7_out, 1'b0);
  and and_11 (and_11_out, and_7_out, 1'b1);
  nor nor_3 (nor_3_out, not_1_out, 1'b1);
  nor nor_4 (nor_4_out, 1'b0, not_1_out);
endmodule

module \显示上午下午的电路  (
  input  SET,
  input  AM_PM,
  output [4:0] out_3,
  output [4:0] out_4,
  output [4:0] out_5,
  output [4:0] out_6
);

  Multiplexer #(.width(5)) multiplexer_1 (.in0(5'b10000), .in1(5'b00001), .out(out_3), .sel(AM_PM), .en(SET));
  Multiplexer #(.width(5)) multiplexer_2 (.in0(5'b10100), .in1(5'b00101), .out(out_5), .sel(AM_PM), .en(SET));
  Multiplexer #(.width(5)) multiplexer_3 (.in0({5{1'b1}}), .in1({5{1'b1}}), .out(out_4), .sel(AM_PM), .en(SET));
  Multiplexer #(.width(5)) multiplexer_4 (.in0(5'b10000), .in1(5'b00001), .out(out_6), .sel(AM_PM), .en(SET));
endmodule

module \秒钟时脉冲产生电路  (
  input  in_1,
  output out_2
);

  wire d_ff_1_q, d_ff_1_qn, d_ff_2_q, d_ff_2_qn, d_ff_3_qn;

  D_Flip_Flop d_ff_1 (.clk(in_1), .D(d_ff_1_qn), .Q(d_ff_1_q), .Qn(d_ff_1_qn));  // open: preset, en, reset
  D_Flip_Flop d_ff_2 (.clk(d_ff_1_q), .D(d_ff_2_qn), .Q(d_ff_2_q), .Qn(d_ff_2_qn));  // open: preset, en, reset
  D_Flip_Flop d_ff_3 (.clk(d_ff_2_q), .D(d_ff_3_qn), .Q(out_2), .Qn(d_ff_3_qn));  // open: preset, en, reset
endmodule

module \六十进制计数器  (
  input  CPu,
  input  CLR,
  input  Adj,
  input  CPD,
  output Q1D,
  output out_6,
  output out_7,
  output out_8,
  output Q0D,
  output out_10,
  output out_11,
  output out_12,
  output Qcc
);

  wire and_1_out, and_2_out, and_3_out, and_4_out, and_5_out, and_6_out, nor_1_out, not_1_out, not_2_out,
       not_3_out, not_4_out, not_5_out, or_1_out, or_2_out, or_3_out, or_4_out, or_5_out;

  and and_1 (and_1_out, Adj, CPD);
  or or_1 (or_1_out, CLR, and_4_out);
  and and_2 (and_2_out, Adj, and_1_out, or_3_out);
  and and_3 (and_3_out, and_1_out, and_5_out);
  \四位二进制可逆计数器  \u_四位二进制可逆计数器_1  (
    .CPU(CPu), .CPD(and_2_out), .CLR(or_1_out), .Q0(out_12), .Q1(out_11), .Q2(out_10), .Q3(Q0D));
  or or_2 (or_2_out, and_6_out, and_3_out);
  not not_1 (not_1_out, out_12);
  and and_4 (and_4_out, Q0D, not_1_out, out_11);
  and and_5 (and_5_out, out_8, not_2_out, nor_1_out, not_3_out, not_4_out);
  or or_3 (or_3_out, Q0D, out_11, or_5_out, out_10, out_12);
  and and_6 (and_6_out, nor_1_out, and_1_out, or_5_out);
  not not_2 (not_2_out, out_7);
  not not_3 (not_3_out, out_6);
  not not_4 (not_4_out, Q1D);
  nor nor_1 (nor_1_out, Q0D, out_11, out_10, out_12);
  or or_4 (or_4_out, CLR, Qcc);
  \四位二进制可逆计数器  \u_四位二进制可逆计数器_2  (
    .CPU(and_4_out), .CPD(or_2_out), .CLR(or_4_out), .Q0(out_8), .Q1(out_7), .Q2(out_6), .Q3(Q1D));
  and and_7 (Qcc, out_6, out_7, not_5_out);
  not not_5 (not_5_out, out_8);
  or or_5 (or_5_out, out_6, out_7, out_8, Q1D);

  // Notes on the sheet:
  //   个位输出
  //   十位输出
endmodule

module \显示上午下午封装测试  (
  input  in_1,
  input  in_2
);

  wire [4:0] \显示上午下午的电路_1_out_3 , \显示上午下午的电路_1_out_4 , \显示上午下午的电路_1_out_5 , \显示上午下午的电路_1_out_6 ;

  DotMatrix #(.matrixcols(4), .matrixrows(5)) dotmatrix_1 (
    .col0(\显示上午下午的电路_1_out_3 ), .col1(\显示上午下午的电路_1_out_4 ), .col2(\显示上午下午的电路_1_out_5 ),
    .col3(\显示上午下午的电路_1_out_6 ));
  \显示上午下午的电路  \u_显示上午下午的电路_1  (
    .out_3(\显示上午下午的电路_1_out_3 ), .out_4(\显示上午下午的电路_1_out_4 ), .out_5(\显示上午下午的电路_1_out_5 ),
    .out_6(\显示上午下午的电路_1_out_6 ), .SET(in_2), .AM_PM(in_1));
endmodule

module \整点报时电路  (
  input  in_1,
  input  in_2,
  input  in_3,
  input  in_4,
  input  in_5,
  input  in_6,
  input  in_7,
  input  in_8,
  input  in_9,
  input  in_10,
  input  in_11,
  input  in_12,
  input  in_13,
  input  in_14,
  input  in_15,
  input  in_16,
  input  in_17,
  output out_18
);

  wire comparator_1_gt, not_1_out;

  Comparator #(.width(16), .mode("unsigned")) comparator_1 (
    .a(16'h5950),
    .b({in_10, in_11, in_12, in_13, in_14, in_15, in_16, in_17, in_2, in_3, in_4, in_5, in_6, in_7, in_8, in_9}),
    .gt(comparator_1_gt));  // open: eq, lt
  not not_1 (not_1_out, comparator_1_gt);
  and and_1 (out_18, in_1, not_1_out);
endmodule

module \测试  (
  input  in_1,
  input  in_2,
  input  in_3,
  input  in_4
);

  wire button_1_out, button_2_out, clock_1_out, \主电路_1_out_10 ;
  wire [3:0] \主电路_1_out_8 , \主电路_1_out_9 , \主电路_1_out_11 , \主电路_1_out_12 , \主电路_1_out_13 , \主电路_1_out_15 ;
  wire [4:0] \主电路_1_out_14 , \主电路_1_out_16 , \主电路_1_out_17 , \主电路_1_out_18 ;

  DotMatrix #(.matrixcols(4), .matrixrows(5)) dotmatrix_1 (
    .col0(\主电路_1_out_14 ), .col1(\主电路_1_out_16 ), .col2(\主电路_1_out_17 ), .col3(\主电路_1_out_18 ));
  Clock clock_1 (.out(clock_1_out));
  Hex_Digit_Display hex_digit_display_1 (.value(\主电路_1_out_13 ));  // open: dp
  Button button_1 (.out(button_1_out));
  Button button_2 (.out(button_2_out));
  Hex_Digit_Display hex_digit_display_2 (.value(\主电路_1_out_15 ));  // open: dp
  Hex_Digit_Display hex_digit_display_3 (.value(\主电路_1_out_12 ));  // open: dp
  \主电路  \u_主电路_1  (
    .clk(clock_1_out), .adj1(in_2), .cpu(button_1_out), .adj0(in_1), .set(in_3), .clr(in_4),
    .cpd(button_2_out), .out_10(\主电路_1_out_10 ), .out_8(\主电路_1_out_8 ), .out_9(\主电路_1_out_9 ),
    .out_15(\主电路_1_out_15 ), .out_11(\主电路_1_out_11 ), .out_13(\主电路_1_out_13 ), .out_12(\主电路_1_out_12 ),
    .out_14(\主电路_1_out_14 ), .out_16(\主电路_1_out_16 ), .out_17(\主电路_1_out_17 ), .out_18(\主电路_1_out_18 ));
  Hex_Digit_Display hex_digit_display_4 (.value(\主电路_1_out_11 ));  // open: dp
  Hex_Digit_Display hex_digit_display_5 (.value(\主电路_1_out_8 ));  // open: dp
  LED led_1 (.in(\主电路_1_out_10 ));
  Hex_Digit_Display hex_digit_display_6 (.value(\主电路_1_out_9 ));  // open: dp
endmodule

module \六十进制测试电路  (
  input  \加 ,
  input  \调整 ,
  input  \减 ,
  input  \清零 ,
  output out_5,
  output out_6,
  output out_7,
  output out_8,
  output out_9,
  output out_10,
  output out_11,
  output out_12,
  output \进位 
);

  \六十进制计数器  \u_六十进制计数器_1  (
    .CPu(\加 ), .CLR(\清零 ), .Adj(\调整 ), .CPD(\减 ), .Qcc(\进位 ), .Q0D(out_9), .out_10(out_10), .out_11(out_11),
    .out_12(out_12), .Q1D(out_5), .out_6(out_6), .out_7(out_7), .out_8(out_8));
endmodule

module \十二二十四进制  (
  input  SET,
  input  in_2,
  input  in_3,
  input  in_4,
  input  in_5,
  output out_6,
  output out_7,
  output out_8,
  output out_9,
  output out_10,
  output out_11,
  output out_12,
  output out_13,
  output out_14
);

  wire and_2_out, comparator_1_gt, d_ff_1_q, d_ff_1_qn, not_1_out, or_1_out;
  wire [3:0] adder_1_out, adder_2_out, multiplexer_2_out, subtractor_1_out, \六十进制计数器_1_out_8 ,
       \六十进制计数器_1_out_12 ;

  Adder #(.width(4)) adder_1 (.a(\六十进制计数器_1_out_8 ), .b(4'b0001), .out(adder_1_out), .cin(not_1_out));  // open: cout
  \六十进制计数器  \u_六十进制计数器_1  (
    .CPu(in_2), .CLR(or_1_out), .Adj(in_3), .CPD(in_4), .Q0D(\六十进制计数器_1_out_12 [3]),
    .out_10(\六十进制计数器_1_out_12 [2]), .out_11(\六十进制计数器_1_out_12 [1]), .out_12(\六十进制计数器_1_out_12 [0]),
    .Q1D(\六十进制计数器_1_out_8 [3]), .out_6(\六十进制计数器_1_out_8 [2]), .out_7(\六十进制计数器_1_out_8 [1]),
    .out_8(\六十进制计数器_1_out_8 [0]));  // open: Qcc
  Multiplexer #(.width(4), .enable("false")) multiplexer_1 (
    .in0(\六十进制计数器_1_out_8 ), .in1(adder_1_out), .out({out_6, out_7, out_8, out_9}), .sel(and_2_out));
  Adder #(.width(4)) adder_2 (.a(4'b0010), .b(\六十进制计数器_1_out_12 ), .out(adder_2_out));  // open: cin, cout
  // Probe on \六十进制计数器_1_out_12 
  and and_1 (out_14, \六十进制计数器_1_out_8 [0], \六十进制计数器_1_out_12 [1]);
  not not_1 (not_1_out, comparator_1_gt);
  Subtractor #(.width(4)) subtractor_1 (.a(adder_2_out), .b(4'b1010), .out(subtractor_1_out));  // open: bin, bout
  Comparator #(.width(4), .mode("unsigned")) comparator_1 (
    .a(4'b1010), .b(adder_2_out), .gt(comparator_1_gt));  // open: eq, lt
  or or_1 (or_1_out, out_14, in_5);
  Multiplexer #(.width(4), .enable("false")) multiplexer_2 (
    .in0(subtractor_1_out), .in1(adder_2_out), .out(multiplexer_2_out), .sel(comparator_1_gt));
  Multiplexer #(.width(4), .enable("false")) multiplexer_3 (
    .in0(\六十进制计数器_1_out_12 ), .in1(multiplexer_2_out), .out({out_10, out_11, out_12, out_13}), .sel(and_2_out));
  and and_2 (and_2_out, SET, d_ff_1_q);
  D_Flip_Flop d_ff_1 (.clk(out_14), .D(d_ff_1_qn), .Q(d_ff_1_q), .Qn(d_ff_1_qn));  // open: preset, en, reset
  // Probe on {out_10, out_11, out_12, out_13}
endmodule

module \主电路  (
  input  clk,
  input  adj1,
  input  cpu,
  input  adj0,
  input  set,
  input  clr,
  input  cpd,
  output [3:0] out_8,
  output [3:0] out_9,
  output out_10,
  output [3:0] out_11,
  output [3:0] out_12,
  output [3:0] out_13,
  output [4:0] out_14,
  output [3:0] out_15,
  output [4:0] out_16,
  output [4:0] out_17,
  output [4:0] out_18
);

  wire and_1_out, and_2_out, d_ff_1_q, d_ff_1_qn, not_1_out, not_2_out, or_1_out, or_2_out, \六十进制计数器_1_qcc ,
       \六十进制计数器_2_qcc , \十二二十四进制_1_out_14 , \秒钟时脉冲产生电路_1_out_2 ;

  \秒钟时脉冲产生电路  \u_秒钟时脉冲产生电路_1  (.in_1(clk), .out_2(\秒钟时脉冲产生电路_1_out_2 ));
  \六十进制计数器  \u_六十进制计数器_1  (
    .CPu(\秒钟时脉冲产生电路_1_out_2 ), .CLR(clr), .Adj(1'b0), .CPD(1'b0), .Qcc(\六十进制计数器_1_qcc ), .Q0D(out_9[3]),
    .out_10(out_9[2]), .out_11(out_9[1]), .out_12(out_9[0]), .Q1D(out_8[3]), .out_6(out_8[2]),
    .out_7(out_8[1]), .out_8(out_8[0]));
  and and_1 (and_1_out, adj1, cpu);
  or or_1 (or_1_out, \六十进制计数器_1_qcc , and_1_out);
  \整点报时电路  \u_整点报时电路_1  (
    .out_18(out_10), .in_10(out_15[3]), .in_11(out_15[2]), .in_12(out_15[1]), .in_13(out_15[0]),
    .in_14(out_11[3]), .in_2(out_8[3]), .in_15(out_11[2]), .in_3(out_8[2]), .in_16(out_11[1]),
    .in_4(out_8[1]), .in_17(out_11[0]), .in_5(out_8[0]), .in_6(out_9[3]), .in_7(out_9[2]), .in_8(out_9[1]),
    .in_9(out_9[0]), .in_1(out_9[0]));
  \六十进制计数器  \u_六十进制计数器_2  (
    .CPu(or_1_out), .CLR(clr), .Adj(adj1), .CPD(cpd), .Qcc(\六十进制计数器_2_qcc ), .Q0D(out_11[3]),
    .out_10(out_11[2]), .out_11(out_11[1]), .out_12(out_11[0]), .Q1D(out_15[3]), .out_6(out_15[2]),
    .out_7(out_15[1]), .out_8(out_15[0]));
  and and_2 (and_2_out, cpu, adj0);
  or or_2 (or_2_out, \六十进制计数器_2_qcc , and_2_out);
  \十二二十四进制  \u_十二二十四进制_1  (
    .SET(set), .in_2(or_2_out), .in_3(adj0), .in_4(cpd), .out_14(\十二二十四进制_1_out_14 ), .in_5(clr),
    .out_6(out_13[3]), .out_7(out_13[2]), .out_8(out_13[1]), .out_9(out_13[0]), .out_10(out_12[3]),
    .out_11(out_12[2]), .out_12(out_12[1]), .out_13(out_12[0]));
  \显示上午下午的电路  \u_显示上午下午的电路_1  (
    .out_3(out_14), .out_4(out_16), .out_5(out_17), .out_6(out_18), .SET(not_2_out), .AM_PM(not_1_out));
  not not_1 (not_1_out, d_ff_1_q);
  D_Flip_Flop d_ff_1 (
    .clk(\十二二十四进制_1_out_14 ), .D(d_ff_1_qn), .Q(d_ff_1_q), .Qn(d_ff_1_qn));  // open: preset, en, reset
  not not_2 (not_2_out, set);
endmodule
