// Logisim project 门禁系统.circ as structural Verilog: 14 circuits, main circuit 封装
module main (
  input  A,
  input  B,
  input  Ci,
  output Co,
  output S
);

  wire and_1_out, and_2_out, xor_2_out;

  xor xor_1 (S, xor_2_out, Ci);
  xor xor_2 (xor_2_out, A, B);
  or or_1 (Co, and_1_out, and_2_out);
  and and_1 (and_1_out, xor_2_out, Ci);
  and and_2 (and_2_out, A, B);
endmodule

module \一位二进制半加器  (
  input  A,
  input  B,
  output C,
  output S
);

  and and_1 (C, A, B);
  xor xor_1 (S, B, A);
endmodule

module \四位二进制并行加法器  (
  input  C0,
  input  A3,
  input  B3,
  input  A2,
  input  B2,
  input  A1,
  input  in_7,
  input  A,
  input  B0,
  output S3,
  output S2,
  output S1,
  output S0,
  output C4
);

  wire main_2_co, main_3_co, main_4_co;

  main main_1 (.S(S3), .Co(C4), .A(A3), .B(B3), .Ci(main_2_co));
  main main_2 (.S(S2), .Co(main_2_co), .A(A2), .B(B2), .Ci(main_3_co));
  main main_3 (.S(S1), .Co(main_3_co), .A(A1), .B(in_7), .Ci(main_4_co));
  main main_4 (.S(S0), .Co(main_4_co), .A(A), .B(B0), .Ci(C0));
endmodule

module \先行进位的四位二进制并行加法器  (
  input  C0,
  input  A4,
  input  B4,
  input  A3,
  input  B3,
  input  A2,
  input  B2,
  input  A1,
  input  B1,
  output C4,
  output S3,
  output S1,
  output S2,
  output S0
);

  wire and_1_out, and_2_out, and_3_out, and_4_out, and_5_out, and_6_out, and_7_out, and_8_out, and_9_out,
       and_10_out, C1_out, C2_out, C3_out, G1_out, G2_out, G3_out, G4_out, P1_out, P2_out, P3_out, P4_out;

  and and_1 (and_1_out, P4_out, P3_out, P2_out, P1_out, C0);
  and G4 (G4_out, A4, B4);
  or u_C4 (C4, and_1_out, and_3_out, and_2_out, and_4_out, G4_out);
  and and_2 (and_2_out, P4_out, P3_out, G2_out);
  and and_3 (and_3_out, P4_out, P3_out, P2_out, G1_out);
  and G3 (G3_out, A3, B3);
  and and_4 (and_4_out, P4_out, G3_out);
  and G2 (G2_out, A2, B2);
  and and_5 (and_5_out, P3_out, P1_out, C0, P2_out);
  and G1 (G1_out, A1, B1);
  or C3 (C3_out, and_5_out, and_6_out, G3_out, and_7_out);
  and and_6 (and_6_out, P3_out, P2_out, G1_out);
  and and_7 (and_7_out, P3_out, G2_out);
  xor P4 (P4_out, A4, B4);
  xor u_S3 (S3, P4_out, C3_out);
  or C2 (C2_out, and_8_out, G2_out, and_9_out);
  and and_8 (and_8_out, C0, P1_out, P2_out);
  xor P3 (P3_out, A3, B3);
  xor u_S2 (S2, P3_out, C2_out);
  and and_9 (and_9_out, G1_out, P2_out);
  xor P2 (P2_out, A2, B2);
  xor u_S1 (S1, P2_out, C1_out);
  or C1 (C1_out, G1_out, and_10_out);
  xor P1 (P1_out, A1, B1);
  xor u_S0 (S0, P1_out, C0);
  and and_10 (and_10_out, P1_out, C0);
endmodule

module \封装  (
  input  C0,
  input  A3,
  input  A2,
  input  A1,
  input  A0,
  input  B3,
  input  B2,
  input  B1,
  input  B0,
  output S3,
  output S2,
  output S1,
  output S0,
  output C4
);

  \先行进位的四位二进制并行加法器  \u_先行进位的四位二进制并行加法器_1  (
    .A4(A3), .B4(B3), .A3(A2), .B3(B2), .A2(A1), .B2(B1), .A1(A0), .B1(B0), .C0(C0), .C4(C4), .S3(S3),
    .S2(S2), .S1(S1), .S0(S0));
endmodule

module \四位二进制可逆计数器  (
  input  \置0 ,
  input  CPU,
  input  CPD,
  output Q3,
  output Q2,
  output Q1,
  output Q0
);

  wire and_1_out, and_2_out, and_3_out, and_4_out, and_5_out, and_6_out, D0_qn, D1_qn, D2_qn, D3_qn,
       or_1_out, or_2_out, or_3_out, or_4_out;

  and and_1 (and_1_out, Q2, Q1, Q0, CPU);
  D_Flip_Flop #(.trigger("falling")) D3 (
    .clk(or_1_out), .D(D3_qn), .Q(Q3), .Qn(D3_qn), .reset(\置0 ));  // open: preset, en
  or or_1 (or_1_out, and_1_out, and_2_out);
  and and_2 (and_2_out, D2_qn, D1_qn, D0_qn, CPD);
  or or_2 (or_2_out, and_3_out, and_4_out);
  and and_3 (and_3_out, Q1, Q0, CPU);
  D_Flip_Flop #(.trigger("falling")) D2 (
    .clk(or_2_out), .D(D2_qn), .Q(Q2), .Qn(D2_qn), .reset(\置0 ));  // open: preset, en
  and and_4 (and_4_out, D1_qn, D0_qn, CPD);
  and and_5 (and_5_out, CPD, D0_qn);
  D_Flip_Flop #(.trigger("falling")) D1 (
    .clk(or_3_out), .D(D1_qn), .Q(Q1), .Qn(D1_qn), .reset(\置0 ));  // open: preset, en
  or or_3 (or_3_out, and_5_out, and_6_out);
  and and_6 (and_6_out, CPU, Q0);
  or or_4 (or_4_out, CPD, CPU);
  D_Flip_Flop #(.trigger("falling")) D0 (
    .clk(or_4_out), .D(D0_qn), .Q(Q0), .Qn(D0_qn), .reset(\置0 ));  // open: preset, en
endmodule

module \可逆计数器封装  (
  input  in_1,
  input  in_2,
  input  in_3,
  output out_4,
  output out_5,
  output out_6,
  output out_7
);

  \四位二进制可逆计数器  \u_四位二进制可逆计数器_1  (.Q3(out_4), .Q2(out_5), .Q1(out_6), .Q0(out_7), .\置0 (in_2), .CPU(in_1), .CPD(in_3));
endmodule

module \四位二进制数转8421码  (
  input  A3,
  input  A2,
  input  A1,
  input  A0,
  output S80,
  output S40,
  output S20,
  output S10,
  output S8,
  output S4,
  output S2,
  output S1
);

  wire and_1_out, or_1_out;

  \先行进位的四位二进制并行加法器  \u_先行进位的四位二进制并行加法器_1  (
    .A4(A3), .B4(1'b0), .A3(A2), .B3(and_1_out), .A2(A1), .B2(and_1_out), .A1(A0), .B1(1'b0), .C0(1'b0),
    .C4(S10), .S3(S8), .S2(S4), .S1(S2), .S0(S1));
  or or_1 (or_1_out, A1, A2);
  and and_1 (and_1_out, A3, or_1_out);

  assign S20 = 1'b0;
  assign S40 = 1'b0;
  assign S80 = 1'b0;

  // Notes on the sheet:
  //   十位
  //   个位
endmodule

module \四位二进制数转8421码封装  (
  input  A4,
  input  A3,
  input  A2,
  input  A1,
  output out_5,
  output out_6,
  output out_7,
  output out_8,
  output out_9,
  output \个位 ,
  output out_11,
  output out_12
);

  \四位二进制数转8421码  \u_四位二进制数转8421码_1  (
    .S80(out_5), .S40(out_6), .S20(out_7), .S10(out_8), .S8(out_9), .S4(\个位 ), .S2(out_11), .S1(out_12),
    .A3(A4), .A2(A3), .A1(A2), .A0(A1));

  // Notes on the sheet:
  //   十位
endmodule

module \七段译码器  (
  input  A3,
  input  A2,
  input  A1,
  input  A0,
  output a,
  output b,
  output c,
  output d,
  output e,
  output f,
  output g
);

  wire and_1_out, and_2_out, and_3_out, and_4_out, and_5_out, and_6_out, and_7_out, and_8_out, and_9_out,
       and_10_out, and_11_out, and_12_out, and_13_out, and_14_out, and_15_out, and_16_out, and_17_out,
       and_18_out, and_19_out, and_20_out, and_21_out, not_1_out, not_2_out, not_3_out, not_4_out;

  not not_1 (not_1_out, A3);
  not not_2 (not_2_out, A2);
  not not_3 (not_3_out, A1);
  not not_4 (not_4_out, A0);
  and and_1 (and_1_out, not_2_out, not_3_out, not_4_out);
  and and_2 (and_2_out, not_1_out, not_2_out, A1);
  and and_3 (and_3_out, not_1_out, A2, A0);
  and and_4 (and_4_out, A3, A0, not_3_out);
  and and_5 (and_5_out, not_1_out, not_2_out);
  and and_6 (and_6_out, not_3_out, not_4_out);
  and and_7 (and_7_out, not_2_out, not_3_out);
  and and_8 (and_8_out, not_1_out, A1, A0);
  and and_9 (and_9_out, not_1_out, A2);
  and and_10 (and_10_out, not_2_out, A0);
  and and_11 (and_11_out, A2, not_3_out, A0);
  and and_12 (and_12_out, not_2_out, not_4_out);
  and and_13 (and_13_out, not_2_out, A1, A0);
  and and_14 (and_14_out, A2, A1, not_4_out);
  and and_15 (and_15_out, A1, not_4_out);
  and and_16 (and_16_out, not_3_out, not_4_out);
  and and_17 (and_17_out, A2, not_3_out);
  and and_18 (and_18_out, A3, not_2_out, not_3_out);
  and and_19 (and_19_out, A2, not_4_out);
  and and_20 (and_20_out, A3, not_2_out);
  and and_21 (and_21_out, not_2_out, A1);
  or or_1 (a, and_1_out, and_2_out, and_3_out, and_4_out);
  or or_2 (b, and_5_out, and_6_out, and_7_out, and_8_out);
  or or_3 (c, and_7_out, and_9_out, and_10_out);
  or or_4 (d, and_11_out, and_12_out, and_13_out, and_14_out);
  or or_5 (e, and_12_out, and_15_out);
  or or_6 (f, and_16_out, and_17_out, and_18_out, and_19_out);
  or or_7 (g, and_17_out, and_15_out, and_20_out, and_21_out);
endmodule

module \_7段数码显示管  (
  input  in_1,
  input  in_2,
  input  in_3,
  input  in_4
);

  wire \七段译码器_1_a , \七段译码器_1_b , \七段译码器_1_c , \七段译码器_1_d , \七段译码器_1_e , \七段译码器_1_f , \七段译码器_1_g ,
       \七段译码器_2_a , \七段译码器_2_b , \七段译码器_2_c , \七段译码器_2_d , \七段译码器_2_e , \七段译码器_2_f , \七段译码器_2_g ,
       \四位二进制数转8421码_1_s1 , \四位二进制数转8421码_1_s2 , \四位二进制数转8421码_1_s4 , \四位二进制数转8421码_1_s8 ,
       \四位二进制数转8421码_1_s10 , \四位二进制数转8421码_1_s20 , \四位二进制数转8421码_1_s40 , \四位二进制数转8421码_1_s80 ;

  \七段译码器  \u_七段译码器_1  (
    .A3(\四位二进制数转8421码_1_s80 ), .A2(\四位二进制数转8421码_1_s40 ), .A1(\四位二进制数转8421码_1_s20 ),
    .A0(\四位二进制数转8421码_1_s10 ), .a(\七段译码器_1_a ), .b(\七段译码器_1_b ), .c(\七段译码器_1_c ), .d(\七段译码器_1_d ),
    .e(\七段译码器_1_e ), .f(\七段译码器_1_f ), .g(\七段译码器_1_g ));
  _7_Segment_Display u_7_segment_display_1 (
    .g(\七段译码器_1_g ), .f(\七段译码器_1_f ), .a(\七段译码器_1_a ), .b(\七段译码器_1_b ), .e(\七段译码器_1_e ), .d(\七段译码器_1_d ),
    .c(\七段译码器_1_c ));  // open: dp
  \四位二进制数转8421码  \u_四位二进制数转8421码_1  (
    .S80(\四位二进制数转8421码_1_s80 ), .S40(\四位二进制数转8421码_1_s40 ), .S20(\四位二进制数转8421码_1_s20 ),
    .S10(\四位二进制数转8421码_1_s10 ), .S8(\四位二进制数转8421码_1_s8 ), .S4(\四位二进制数转8421码_1_s4 ), .S2(\四位二进制数转8421码_1_s2 ),
    .S1(\四位二进制数转8421码_1_s1 ), .A3(in_1), .A2(in_2), .A1(in_3), .A0(in_4));
  \七段译码器  \u_七段译码器_2  (
    .A3(\四位二进制数转8421码_1_s8 ), .A2(\四位二进制数转8421码_1_s4 ), .A1(\四位二进制数转8421码_1_s2 ), .A0(\四位二进制数转8421码_1_s1 ),
    .a(\七段译码器_2_a ), .b(\七段译码器_2_b ), .c(\七段译码器_2_c ), .d(\七段译码器_2_d ), .e(\七段译码器_2_e ), .f(\七段译码器_2_f ),
    .g(\七段译码器_2_g ));
  _7_Segment_Display u_7_segment_display_2 (
    .g(\七段译码器_2_g ), .f(\七段译码器_2_f ), .a(\七段译码器_2_a ), .b(\七段译码器_2_b ), .e(\七段译码器_2_e ), .d(\七段译码器_2_d ),
    .c(\七段译码器_2_c ));  // open: dp
endmodule

module \报警电路  (
  input  U,
  input  CLR,
  input  D,
  output out_4,
  output out_5,
  output out_6,
  output out_7
);

  wire and_1_out, and_2_out, not_1_out, \报警_out , \无人_out , \满员_out ;

  LED led_1 (.in(\报警_out ));
  and \u_报警  (\报警_out , U, \满员_out );
  and and_1 (and_1_out, U, not_1_out);
  and and_2 (and_2_out, \无人_out , D);
  or \u_无人  (\无人_out , out_7, out_6, out_5, out_4);
  not not_1 (not_1_out, \满员_out );
  and \u_满员  (\满员_out , out_7, out_6, out_5, out_4);
  \四位二进制可逆计数器  \u_四位二进制可逆计数器_1  (
    .Q3(out_4), .Q2(out_5), .Q1(out_6), .Q0(out_7), .\置0 (CLR), .CPU(and_1_out), .CPD(and_2_out));
endmodule

module \小型实验室门禁系统  (
  input  U,
  input  CLR,
  input  D,
  output a1,
  output b1,
  output c1,
  output d1,
  output e1,
  output f1,
  output g1,
  output a0,
  output b0,
  output c1_2,
  output d0,
  output e0,
  output f0,
  output g0,
  output Z
);

  wire and_1_out, and_2_out, not_1_out, \四位二进制可逆计数器_1_q0 , \四位二进制可逆计数器_1_q1 , \四位二进制可逆计数器_1_q2 ,
       \四位二进制可逆计数器_1_q3 , \四位二进制数转8421码_1_s1 , \四位二进制数转8421码_1_s2 , \四位二进制数转8421码_1_s4 , \四位二进制数转8421码_1_s8 ,
       \四位二进制数转8421码_1_s10 , \四位二进制数转8421码_1_s20 , \四位二进制数转8421码_1_s40 , \四位二进制数转8421码_1_s80 , \无人_out ,
       \满员_out ;

  and \u_报警  (Z, U, \满员_out );
  and and_1 (and_1_out, U, not_1_out);
  and and_2 (and_2_out, \无人_out , D);
  \七段译码器  \u_七段译码器_1  (
    .A3(\四位二进制数转8421码_1_s80 ), .A2(\四位二进制数转8421码_1_s40 ), .A1(\四位二进制数转8421码_1_s20 ),
    .A0(\四位二进制数转8421码_1_s10 ), .a(a1), .b(b1), .c(c1), .d(d1), .e(e1), .f(f1), .g(g1));
  or \u_无人  (\无人_out , \四位二进制可逆计数器_1_q0 , \四位二进制可逆计数器_1_q1 , \四位二进制可逆计数器_1_q2 , \四位二进制可逆计数器_1_q3 );
  not not_1 (not_1_out, \满员_out );
  and \u_满员  (\满员_out , \四位二进制可逆计数器_1_q0 , \四位二进制可逆计数器_1_q1 , \四位二进制可逆计数器_1_q2 , \四位二进制可逆计数器_1_q3 );
  \四位二进制数转8421码  \u_四位二进制数转8421码_1  (
    .S80(\四位二进制数转8421码_1_s80 ), .S40(\四位二进制数转8421码_1_s40 ), .S20(\四位二进制数转8421码_1_s20 ),
    .S10(\四位二进制数转8421码_1_s10 ), .S8(\四位二进制数转8421码_1_s8 ), .S4(\四位二进制数转8421码_1_s4 ), .S2(\四位二进制数转8421码_1_s2 ),
    .S1(\四位二进制数转8421码_1_s1 ), .A3(\四位二进制可逆计数器_1_q3 ), .A2(\四位二进制可逆计数器_1_q2 ), .A1(\四位二进制可逆计数器_1_q1 ),
    .A0(\四位二进制可逆计数器_1_q0 ));
  \四位二进制可逆计数器  \u_四位二进制可逆计数器_1  (
    .Q3(\四位二进制可逆计数器_1_q3 ), .Q2(\四位二进制可逆计数器_1_q2 ), .Q1(\四位二进制可逆计数器_1_q1 ), .Q0(\四位二进制可逆计数器_1_q0 ),
    .\置0 (CLR), .CPU(and_1_out), .CPD(and_2_out));
  \七段译码器  \u_七段译码器_2  (
    .A3(\四位二进制数转8421码_1_s8 ), .A2(\四位二进制数转8421码_1_s4 ), .A1(\四位二进制数转8421码_1_s2 ), .A0(\四位二进制数转8421码_1_s1 ),
    .a(a0), .b(b0), .c(c1_2), .d(d0), .e(e0), .f(f0), .g(g0));
endmodule

module \门禁系统封装  (
  input  in_1,
  input  in_2,
  input  in_3
);

  wire \小型实验室门禁系统_1_a0 , \小型实验室门禁系统_1_a1 , \小型实验室门禁系统_1_b0 , \小型实验室门禁系统_1_b1 , \小型实验室门禁系统_1_c1 ,
       \小型实验室门禁系统_1_c1_2 , \小型实验室门禁系统_1_d0 , \小型实验室门禁系统_1_d1 , \小型实验室门禁系统_1_e0 , \小型实验室门禁系统_1_e1 ,
       \小型实验室门禁系统_1_f0 , \小型实验室门禁系统_1_f1 , \小型实验室门禁系统_1_g0 , \小型实验室门禁系统_1_g1 , \小型实验室门禁系统_1_z ;

  \小型实验室门禁系统  \u_小型实验室门禁系统_1  (
    .U(in_1), .CLR(in_2), .D(in_3), .a1(\小型实验室门禁系统_1_a1 ), .b1(\小型实验室门禁系统_1_b1 ), .c1(\小型实验室门禁系统_1_c1 ),
    .d1(\小型实验室门禁系统_1_d1 ), .e1(\小型实验室门禁系统_1_e1 ), .f1(\小型实验室门禁系统_1_f1 ), .g1(\小型实验室门禁系统_1_g1 ),
    .a0(\小型实验室门禁系统_1_a0 ), .b0(\小型实验室门禁系统_1_b0 ), .c1_2(\小型实验室门禁系统_1_c1_2 ), .d0(\小型实验室门禁系统_1_d0 ),
    .e0(\小型实验室门禁系统_1_e0 ), .f0(\小型实验室门禁系统_1_f0 ), .g0(\小型实验室门禁系统_1_g0 ), .Z(\小型实验室门禁系统_1_z ));
  _7_Segment_Display u_7_segment_display_1 (
    .g(\小型实验室门禁系统_1_g1 ), .f(\小型实验室门禁系统_1_f1 ), .a(\小型实验室门禁系统_1_a1 ), .b(\小型实验室门禁系统_1_b1 ),
    .e(\小型实验室门禁系统_1_e1 ), .d(\小型实验室门禁系统_1_d1 ), .c(\小型实验室门禁系统_1_c1 ));  // open: dp
  _7_Segment_Display u_7_segment_display_2 (
    .g(\小型实验室门禁系统_1_g0 ), .f(\小型实验室门禁系统_1_f0 ), .a(\小型实验室门禁系统_1_a0 ), .b(\小型实验室门禁系统_1_b0 ),
    .e(\小型实验室门禁系统_1_e0 ), .d(\小型实验室门禁系统_1_d0 ), .c(\小型实验室门禁系统_1_c1_2 ));  // open: dp
  LED led_1 (.in(\小型实验室门禁系统_1_z ));
endmodule
