// Logisim project 梁一飞_CS1706_U201714762(团队项目电路）.circ as structural Verilog: 18 circuits, main circuit ◇单周期MIPS
module \单周期MIPS  (
  input  IR1,
  input  IR2,
  input  IR3,
  output RegWrite,
  output MemWrite,
  output [31:0] PC,
  output [31:0] IR,
  output [31:0] RDin,
  output [31:0] MDin,
  output [31:0] LedData,
  output [31:0] OUT
);

  wire and_1_out, and_2_out, and_3_out, and_4_out, and_5_out, and_6_out, Byte, C0, C1, C2, C3, C4, C5, C6,
       C7, C8, C9, C10, C11, C12, C13, C14, C15, C16, C17, C18, C19, C20, C21, C22, C23, C24, C25, C26, C27,
       C28, C29, C30, C31, CLK, comparator_1_eq, comparator_2_eq, Go, IR1_t, IR2_t, IR3_t, IRA, IRB, IRC,
       mips_alu_1_equal, MTR, not_1_out, not_2_out, not_3_out, not_4_out, or_1_out, RST, SignedExt, W1, W2,
       W3, \单周期硬布线控制器_1_alu_src , \单周期硬布线控制器_1_beq , \单周期硬布线控制器_1_blez , \单周期硬布线控制器_1_bne ,
       \单周期硬布线控制器_1_jal , \单周期硬布线控制器_1_jmp , \单周期硬布线控制器_1_jr , \单周期硬布线控制器_1_regdst , \单周期硬布线控制器_1_syscall ;
  wire [1:0] bytePlace;
  wire [3:0] \单周期硬布线控制器_1_alu_op ;
  wire [4:0] multiplexer_4_out, multiplexer_5_out, multiplexer_6_out, multiplexer_7_out;
  wire [5:0] counter_2_q;
  wire [15:0] \总周期数 ;
  wire [31:0] _0, _1, _2, _3, _4, _5, _6, _7, _8, _9, _10, _11, _12, _13, _14, _15, _16, _17, _18, _19, _20,
       _21, _22, _23, _24, _25, _26, _27, _28, _29, _30, _31, adder_1_out, adder_2_out, bit_extender_1_out,
       bit_extender_2_out, bit_extender_3_out, bit_extender_4_out, bit_extender_5_out, bit_extender_6_out,
       mips_regifile_1_r1, multiplexer_1_out, multiplexer_2_out, multiplexer_3_out, multiplexer_8_out,
       multiplexer_10_out, multiplexer_11_out, multiplexer_12_out, multiplexer_13_out, O0, O1, O2, O3, O4,
       O5, O6, O7, O8, O9, O10, O11, O12, O13, O14, O15, O16, O17, O18, O19, O20, O21, O22, O23, O24, O25,
       O26, O27, O28, O29, O30, O31, ram_1_data, shifter_1_out;
  wire [31:2] mips_alu_1_result;

  Clock clock_1 (.out(CLK));
  Button u__1 (.out(IRA));
  Button u__2 (.out(IRB));
  Button u__3 (.out(IRC));
  Button \u_继续运行  (.out(Go));
  LED led_1 (.in(W1));
  LED led_2 (.in(W2));
  LED led_3 (.in(W3));
  Multiplexer #(.width(32), .enable("false")) multiplexer_1 (
    .in0(adder_1_out), .in1(adder_2_out), .out(multiplexer_1_out), .sel(or_1_out));
  Multiplexer #(.width(32), .enable("false")) multiplexer_2 (
    .in0(multiplexer_1_out), .in1({IR[31:28], IR[25:0], 2'b00}), .out(multiplexer_2_out),
    .sel(\单周期硬布线控制器_1_jmp ));
  Hex_Digit_Display hex_digit_display_1 (.value(LedData[31:28]));  // open: dp
  Multiplexer #(.width(32), .enable("false")) multiplexer_3 (
    .in0(multiplexer_2_out), .in1(mips_regifile_1_r1), .out(multiplexer_3_out), .sel(\单周期硬布线控制器_1_jr ));
  Hex_Digit_Display hex_digit_display_2 (.value(LedData[23:20]));  // open: dp
  Hex_Digit_Display hex_digit_display_3 (.value(LedData[27:24]));  // open: dp
  Register #(.width(32)) u_PC (.D(multiplexer_3_out), .en(not_4_out), .Q(PC), .clk(CLK), .clr(RST));
  Hex_Digit_Display hex_digit_display_4 (.value(LedData[19:16]));  // open: dp
  Hex_Digit_Display hex_digit_display_5 (.value(LedData[15:12]));  // open: dp
  Counter #(.width(16), .max('hffff)) counter_1 (
    .count(not_4_out), .Q(\总周期数 ), .clk(CLK), .clr(RST));  // open: load, D, carry
  Counter #(.width(6), .max('h3f)) counter_2 (
    .Q(counter_2_q), .clk(MTR), .clr(comparator_1_eq));  // open: load, D, count, carry
  Hex_Digit_Display hex_digit_display_6 (.value(LedData[7:4]));  // open: dp
  Hex_Digit_Display hex_digit_display_7 (.value(LedData[11:8]));  // open: dp
  // Probe on \总周期数 
  or or_1 (or_1_out, and_3_out, and_1_out, and_2_out);
  Adder #(.width(32)) adder_1 (.a(PC), .b(32'h4), .out(adder_1_out));  // open: cin, cout
  Button button_1 (.out(RST));
  Comparator #(.width(6), .mode("unsigned")) comparator_1 (
    .a(counter_2_q), .b(6'b100000), .eq(comparator_1_eq));  // open: gt, lt
  Hex_Digit_Display hex_digit_display_8 (.value(LedData[3:0]));  // open: dp
  // Mips_Probe mips_probe_1: pin names not known; wires that end beside it: IR
  ROM #(.addrWidth(10), .dataWidth(32)) rom_1 (.addr(PC[11:2]), .data(IR));  // open: sel
  Demultiplexer #(.select(5), .width(32), .enable("false")) demultiplexer_1 (
    .out0(O0), .out1(O1), .out2(O2), .out3(O3), .out4(O4), .out5(O5), .out6(O6), .out7(O7), .out8(O8),
    .out9(O9), .out10(O10), .out11(O11), .out12(O12), .out13(O13), .out14(O14), .out15(O15), .out16(O16),
    .out17(O17), .out18(O18), .out19(O19), .out20(O20), .out21(O21), .out22(O22), .out23(O23), .out24(O24),
    .out25(O25), .out26(O26), .out27(O27), .out28(O28), .out29(O29), .out30(O30), .out31(O31), .in(OUT),
    .sel(counter_2_q[4:0]));
  or or_2 (IR1_t, IR1, IRA);
  \单周期硬布线控制器  \u_单周期硬布线控制器_1  (
    .Func(IR[5:0]), .OP(IR[31:26]), .ALU_OP(\单周期硬布线控制器_1_alu_op ), .MemToReg(MTR), .MemWrite(MemWrite),
    .ALU_SRC(\单周期硬布线控制器_1_alu_src ), .RegWrite(RegWrite), .SysCALL(\单周期硬布线控制器_1_syscall ),
    .SignedExt(SignedExt), .RegDst(\单周期硬布线控制器_1_regdst ), .JR(\单周期硬布线控制器_1_jr ), .JMP(\单周期硬布线控制器_1_jmp ),
    .Beq(\单周期硬布线控制器_1_beq ), .JAL(\单周期硬布线控制器_1_jal ), .Bne(\单周期硬布线控制器_1_bne ), .BLEZ(\单周期硬布线控制器_1_blez ),
    .Byte(Byte));  // open: R1, R2
  Multiplexer #(.width(5), .enable("false")) multiplexer_4 (
    .in0(IR[25:21]), .in1(5'b00010), .out(multiplexer_4_out), .sel(\单周期硬布线控制器_1_syscall ));
  Multiplexer #(.width(5), .enable("false")) multiplexer_5 (
    .in0(IR[20:16]), .in1(5'b00100), .out(multiplexer_5_out), .sel(\单周期硬布线控制器_1_syscall ));
  assign bit_extender_1_out = {{16{1'b0}}, IR[15:0]};  // Bit_Extender bit_extender_1
  assign bit_extender_2_out = {{16{IR[15]}}, IR[15:0]};  // Bit_Extender bit_extender_2
  Decoder #(.select(5), .enable("false")) decoder_1 (
    .out0(C0), .out1(C1), .out2(C2), .out3(C3), .out4(C4), .out5(C5), .out6(C6), .out7(C7), .out8(C8),
    .out9(C9), .out10(C10), .out11(C11), .out12(C12), .out13(C13), .out14(C14), .out15(C15), .out16(C16),
    .out17(C17), .out18(C18), .out19(C19), .out20(C20), .out21(C21), .out22(C22), .out23(C23), .out24(C24),
    .out25(C25), .out26(C26), .out27(C27), .out28(C28), .out29(C29), .out30(C30), .out31(C31),
    .sel(counter_2_q[4:0]));
  or or_3 (IR2_t, IR2, IRB);
  Multiplexer #(.width(5), .enable("false")) multiplexer_6 (
    .in0(IR[20:16]), .in1(IR[15:11]), .out(multiplexer_6_out), .sel(\单周期硬布线控制器_1_regdst ));
  Multiplexer #(.width(5), .enable("false")) multiplexer_7 (
    .in0(multiplexer_6_out), .in1({5{1'b1}}), .out(multiplexer_7_out), .sel(\单周期硬布线控制器_1_jal ));
  Multiplexer #(.width(32), .enable("false")) multiplexer_8 (
    .in0(bit_extender_1_out), .in1(bit_extender_2_out), .out(multiplexer_8_out), .sel(SignedExt));
  Multiplexer #(.width(32), .enable("false")) multiplexer_9 (
    .in0(multiplexer_10_out), .in1(multiplexer_12_out), .out(RDin), .sel(Byte));
  Register #(.width(32), .trigger("high")) register_1 (.D(O0), .Q(_0), .clk(C0), .clr(RST));  // open: en
  Register #(.width(32), .trigger("high")) register_2 (.D(O4), .Q(_4), .clk(C4), .clr(RST));  // open: en
  Register #(.width(32), .trigger("high")) register_3 (.D(O8), .Q(_8), .clk(C8), .clr(RST));  // open: en
  Register #(.width(32), .trigger("high")) register_4 (.D(O12), .Q(_12), .clk(C12), .clr(RST));  // open: en
  Register #(.width(32), .trigger("high")) register_5 (.D(O16), .Q(_16), .clk(C16), .clr(RST));  // open: en
  Register #(.width(32), .trigger("high")) register_6 (.D(O20), .Q(_20), .clk(C20), .clr(RST));  // open: en
  Register #(.width(32), .trigger("high")) register_7 (.D(O24), .Q(_24), .clk(C24), .clr(RST));  // open: en
  Register #(.width(32), .trigger("high")) register_8 (.D(O28), .Q(_28), .clk(C28), .clr(RST));  // open: en
  or or_4 (IR3_t, IR3, IRC);
  Button button_2 (.out(RST));
  MIPS_Regifile mips_regifile_1 (
    .Din(RDin), .Clk(CLK), .R1(mips_regifile_1_r1), .R2(MDin), .WE(RegWrite), .W_num(multiplexer_7_out),
    .R1_num(multiplexer_4_out), .R2_num(multiplexer_5_out));
  Multiplexer #(.width(32), .enable("false")) multiplexer_10 (
    .in0(multiplexer_13_out), .in1(adder_1_out), .out(multiplexer_10_out), .sel(\单周期硬布线控制器_1_jal ));
  Shifter #(.width(32)) shifter_1 (.in(bit_extender_2_out), .\dist (5'b00010), .out(shifter_1_out));
  Register #(.width(32), .trigger("high")) register_9 (.D(O1), .Q(_1), .clk(C1), .clr(RST));  // open: en
  Register #(.width(32), .trigger("high")) register_10 (.D(O5), .Q(_5), .clk(C5), .clr(RST));  // open: en
  Register #(.width(32), .trigger("high")) register_11 (.D(O9), .Q(_9), .clk(C9), .clr(RST));  // open: en
  Register #(.width(32), .trigger("high")) register_12 (.D(O13), .Q(_13), .clk(C13), .clr(RST));  // open: en
  Register #(.width(32), .trigger("high")) register_13 (.D(O17), .Q(_17), .clk(C17), .clr(RST));  // open: en
  Register #(.width(32), .trigger("high")) register_14 (.D(O21), .Q(_21), .clk(C21), .clr(RST));  // open: en
  Register #(.width(32), .trigger("high")) register_15 (.D(O25), .Q(_25), .clk(C25), .clr(RST));  // open: en
  Register #(.width(32), .trigger("high")) register_16 (.D(O29), .Q(_29), .clk(C29), .clr(RST));  // open: en
  Multiplexer #(.width(32), .enable("false")) multiplexer_11 (
    .in0(MDin), .in1(multiplexer_8_out), .out(multiplexer_11_out), .sel(\单周期硬布线控制器_1_alu_src ));
  Adder #(.width(32)) adder_2 (.a(shifter_1_out), .b(adder_1_out), .out(adder_2_out));  // open: cin, cout
  not not_1 (not_1_out, mips_alu_1_equal);
  MIPS_ALU mips_alu_1 (
    .X(mips_regifile_1_r1), .Y(multiplexer_11_out), .AluOP(\单周期硬布线控制器_1_alu_op ), .Equal(mips_alu_1_equal),
    .Result({mips_alu_1_result, bytePlace}), .shamt(IR[10:6]));  // open: Result_2
  Register #(.width(32), .trigger("high")) register_17 (.D(O2), .Q(_2), .clk(C2), .clr(RST));  // open: en
  Register #(.width(32), .trigger("high")) register_18 (.D(O6), .Q(_6), .clk(C6), .clr(RST));  // open: en
  Register #(.width(32), .trigger("high")) register_19 (.D(O10), .Q(_10), .clk(C10), .clr(RST));  // open: en
  Register #(.width(32), .trigger("high")) register_20 (.D(O14), .Q(_14), .clk(C14), .clr(RST));  // open: en
  Register #(.width(32), .trigger("high")) register_21 (.D(O18), .Q(_18), .clk(C18), .clr(RST));  // open: en
  Register #(.width(32), .trigger("high")) register_22 (.D(O22), .Q(_22), .clk(C22), .clr(RST));  // open: en
  Register #(.width(32), .trigger("high")) register_23 (.D(O26), .Q(_26), .clk(C26), .clr(RST));  // open: en
  Register #(.width(32), .trigger("high")) register_24 (.D(O30), .Q(_30), .clk(C30), .clr(RST));  // open: en
  and and_1 (and_1_out, \单周期硬布线控制器_1_blez , not_2_out);
  and and_2 (and_2_out, mips_alu_1_equal, \单周期硬布线控制器_1_beq );
  and and_3 (and_3_out, not_1_out, \单周期硬布线控制器_1_bne );
  Register #(.width(32), .trigger("high")) register_25 (.D(O3), .Q(_3), .clk(C3), .clr(RST));  // open: en
  Register #(.width(32), .trigger("high")) register_26 (.D(O7), .Q(_7), .clk(C7), .clr(RST));  // open: en
  Register #(.width(32), .trigger("high")) register_27 (.D(O11), .Q(_11), .clk(C11), .clr(RST));  // open: en
  Register #(.width(32), .trigger("high")) register_28 (.D(O15), .Q(_15), .clk(C15), .clr(RST));  // open: en
  Register #(.width(32), .trigger("high")) register_29 (.D(O19), .Q(_19), .clk(C19), .clr(RST));  // open: en
  Register #(.width(32), .trigger("high")) register_30 (.D(O23), .Q(_23), .clk(C23), .clr(RST));  // open: en
  Register #(.width(32), .trigger("high")) register_31 (.D(O27), .Q(_27), .clk(C27), .clr(RST));  // open: en
  Register #(.width(32), .trigger("high")) register_32 (.D(O31), .Q(_31), .clk(C31), .clr(RST));  // open: en
  and and_4 (and_4_out, ~bytePlace[0], ~mips_alu_1_equal);  // AND_Gate
  not not_2 (not_2_out, and_4_out);
  Multiplexer #(.select(2), .width(32), .enable("false")) multiplexer_12 (
    .in0(bit_extender_3_out), .in1(bit_extender_4_out), .in2(bit_extender_5_out), .in3(bit_extender_6_out),
    .out(multiplexer_12_out), .sel(bytePlace));
  RAM #(.addrWidth(24), .dataWidth(32), .bus("separate")) ram_1 (
    .addr(mips_alu_1_result[25:2]), .din(MDin), .data(ram_1_data), .str(MemWrite), .clk(CLK));  // open: sel, ld, clr
  not not_3 (not_3_out, comparator_2_eq);
  Comparator #(.width(32)) comparator_2 (.a(32'h22), .b(mips_regifile_1_r1), .eq(comparator_2_eq));  // open: gt, lt
  Multiplexer #(.width(32), .enable("false")) multiplexer_13 (
    .in0({mips_alu_1_result, bytePlace}), .in1(ram_1_data), .out(multiplexer_13_out), .sel(MTR));
  and and_5 (and_5_out, \单周期硬布线控制器_1_syscall , not_3_out);
  not not_4 (not_4_out, and_5_out);
  and and_6 (and_6_out, \单周期硬布线控制器_1_syscall , comparator_2_eq);
  assign bit_extender_3_out = {{24{1'b0}}, multiplexer_13_out[7:0]};  // Bit_Extender bit_extender_3
  assign bit_extender_4_out = {{24{1'b0}}, multiplexer_13_out[15:8]};  // Bit_Extender bit_extender_4
  assign bit_extender_5_out = {{24{1'b0}}, multiplexer_13_out[23:16]};  // Bit_Extender bit_extender_5
  assign bit_extender_6_out = {{24{1'b0}}, multiplexer_13_out[31:24]};  // Bit_Extender bit_extender_6
  Register #(.width(32)) register_33 (.D(MDin), .en(and_6_out), .Q(LedData), .clk(CLK), .clr(RST));
  Register #(.width(32)) register_34 (.D(ram_1_data), .Q(OUT), .clk(MTR), .clr(RST));  // open: en
  DotMatrix #(.inputtype("row"), .matrixcols(32), .matrixrows(32)) dotmatrix_1 (
    .row0(_0), .row1(_1), .row2(_2), .row3(_3), .row4(_4), .row5(_5), .row6(_6), .row7(_7), .row8(_8),
    .row9(_9), .row10(_10), .row11(_11), .row12(_12), .row13(_13), .row14(_14), .row15(_15), .row16(_16),
    .row17(_17), .row18(_18), .row19(_19), .row20(_20), .row21(_21), .row22(_22), .row23(_23), .row24(_24),
    .row25(_25), .row26(_26), .row27(_27), .row28(_28), .row29(_29), .row30(_30), .row31(_31));

  // Other names for the same wires on the sheet: sign6_10[4:0] = IR[10:6]

  // Notes on the sheet:
  //   中断源
  //   中断等待指示
  //   总复位信号应将除ROM以外所有存储组件全部清零
  //   数码管输出
  //   数码管输出应该用寄存器锁存，否则显示数据只能一闪而过
  //   指令存储器
  //   指令字
  //   contents of rom_1 (hex, n*v repeats v):
  //   20110000 20121106 129140 112020 8e260000 22310004 8100003 c
  //   OP
  //   Func
  //   rs
  //   rt
  //   rd
  //   Beq
  //   JMP
  //   JR
  //   Bne
  //   OP
  //   JAL
  //   Func
  //   Syscall
  //   MemToReg
  //   MemWrite
  //   AluOP
  //   AluSrcB
  //   RegWrite
  //   RegDst
  //   为方便自动评测，需要输出PC，IR，寄存器堆写如数据RDin
  //   RAM写使能MemWrite、RAM写入数据MDin等信号
endmodule

// 单周期硬布线控制器
module \单周期硬布线控制器  (
  input  [5:0] OP,
  input  [5:0] Func,
  output [3:0] ALU_OP,
  output MemToReg,
  output MemWrite,
  output ALU_SRC,
  output RegWrite,
  output SysCALL,
  output SignedExt,
  output RegDst,
  output Beq,
  output Bne,
  output JR,
  output JMP,
  output JAL,
  output BLEZ,
  output Byte,
  output R1,
  output R2
);

  \运算控制器自动生成  \u_运算控制器自动生成_1  (
    .OP0(OP[0]), .OP1(OP[1]), .OP2(OP[2]), .OP3(OP[3]), .OP4(OP[4]), .OP5(OP[5]), .F0(Func[0]), .F1(Func[1]),
    .F2(Func[2]), .F3(Func[3]), .F4(Func[4]), .F5(Func[5]), .S0(ALU_OP[0]), .S1(ALU_OP[1]), .S2(ALU_OP[2]),
    .S3(ALU_OP[3]));
  \控制信号自动生成  \u_控制信号自动生成_1  (
    .OP0(OP[0]), .OP1(OP[1]), .OP2(OP[2]), .OP3(OP[3]), .OP4(OP[4]), .OP5(OP[5]), .F0(Func[0]), .F1(Func[1]),
    .F2(Func[2]), .F3(Func[3]), .F4(Func[4]), .F5(Func[5]), .MemToReg(MemToReg), .MemWrite(MemWrite),
    .ALU_SRC(ALU_SRC), .RegWrite(RegWrite), .SysCALL(SysCALL), .SignedExt(SignedExt), .RegDst(RegDst),
    .BEQ(Beq), .BNE(Bne), .JR(JR), .JUMP(JMP), .JAL(JAL), .BLEZ(BLEZ), .UNSIGN(Byte), .R1Used(R1), .R2Used(R2));

  // Other names for the same wires on the sheet: OP_CODE[5:0] = OP

  // Notes on the sheet:
  //   控制信号生成，产生数据通路需要的其他控制信号
  //   运算器控制器，根据指令生成运算器功能选择信号
endmodule

// 运算器控制器
module \运算控制器自动生成  (
  input  OP0,
  input  OP1,
  input  OP2,
  input  OP3,
  input  OP4,
  input  OP5,
  input  F0,
  input  F1,
  input  F2,
  input  F3,
  input  F4,
  input  F5,
  output S0,
  output S1,
  output S2,
  output S3
);

  wire and_1_out, and_2_out, and_3_out, and_4_out, and_5_out, and_6_out, and_7_out, and_8_out, and_9_out,
       and_10_out, and_11_out, and_12_out, and_13_out, and_14_out, and_15_out, and_16_out, and_17_out,
       and_18_out, and_19_out, and_20_out, and_21_out, and_22_out, and_23_out, and_24_out, and_25_out,
       and_26_out, and_27_out, and_28_out, and_29_out, and_30_out, and_31_out, and_32_out, and_33_out,
       and_34_out, and_35_out, and_36_out, and_37_out, and_38_out, and_39_out, and_40_out, and_41_out,
       and_42_out, and_43_out, not_1_out, not_2_out, not_3_out, not_4_out, not_5_out, not_6_out, not_7_out,
       not_8_out, not_9_out, not_10_out, not_11_out, not_12_out, not_13_out, not_14_out, not_15_out,
       not_16_out, not_17_out, not_18_out, not_19_out, not_20_out, not_21_out, not_22_out, not_23_out,
       not_24_out, not_25_out, not_26_out, not_27_out, not_28_out, not_29_out, not_30_out, not_31_out,
       not_32_out, not_33_out, not_34_out, not_35_out, not_36_out, not_37_out, not_38_out, not_39_out,
       not_40_out, not_41_out, not_42_out, not_43_out, not_44_out, not_45_out, not_46_out, not_47_out,
       not_48_out, not_49_out, not_50_out, not_51_out, not_52_out, not_53_out, not_54_out, not_55_out,
       not_56_out, not_57_out, not_58_out, not_59_out, not_60_out, not_61_out, not_62_out, not_63_out,
       not_64_out, not_65_out, not_66_out, not_67_out, not_68_out, not_69_out, not_70_out, not_71_out,
       not_72_out, not_73_out, not_74_out, not_75_out, not_76_out, not_77_out, not_78_out, not_79_out,
       not_80_out, not_81_out, not_82_out, not_83_out, not_84_out, not_85_out, not_86_out, not_87_out,
       not_88_out, not_89_out, not_90_out, not_91_out, not_92_out, not_93_out, not_94_out, not_95_out,
       not_96_out, not_97_out, not_98_out, not_99_out, not_100_out, not_101_out, not_102_out, not_103_out,
       not_104_out, not_105_out, not_106_out, not_107_out, not_108_out, not_109_out, not_110_out,
       not_111_out, not_112_out, not_113_out, not_114_out, not_115_out, not_116_out, not_117_out,
       not_118_out, not_119_out, not_120_out, not_121_out, not_122_out, not_123_out, not_124_out,
       not_125_out, not_126_out, not_127_out, not_128_out, not_129_out, not_130_out, not_131_out,
       not_132_out, not_133_out, not_134_out, not_135_out, not_136_out, not_137_out, not_138_out,
       not_139_out, not_140_out, not_141_out, not_142_out, not_143_out, not_144_out, not_145_out,
       not_146_out, not_147_out, not_148_out, not_149_out, not_150_out, not_151_out, not_152_out,
       not_153_out, not_154_out, not_155_out, not_156_out, not_157_out, not_158_out, not_159_out,
       not_160_out, not_161_out, not_162_out, not_163_out, not_164_out, not_165_out, not_166_out,
       not_167_out, not_168_out, not_169_out, not_170_out, not_171_out, not_172_out, not_173_out,
       not_174_out, not_175_out, not_176_out, not_177_out, not_178_out, not_179_out, not_180_out,
       not_181_out, not_182_out, not_183_out, not_184_out, not_185_out, not_186_out, not_187_out,
       not_188_out, not_189_out, not_190_out, not_191_out, not_192_out, not_193_out, not_194_out,
       not_195_out, not_196_out, not_197_out, not_198_out, not_199_out, not_200_out, not_201_out,
       not_202_out, not_203_out, not_204_out, not_205_out, not_206_out, not_207_out, not_208_out,
       not_209_out, not_210_out, not_211_out, not_212_out, not_213_out, not_214_out, not_215_out,
       not_216_out, not_217_out, not_218_out, not_219_out, not_220_out, not_221_out, not_222_out,
       not_223_out, not_224_out, not_225_out, not_226_out, not_227_out, not_228_out, not_229_out,
       not_230_out, not_231_out, not_232_out, not_233_out, not_234_out, not_235_out, not_236_out,
       not_237_out, not_238_out, not_239_out, not_240_out, not_241_out, not_242_out, not_243_out,
       not_244_out, not_245_out, not_246_out, not_247_out, not_248_out, not_249_out, not_250_out,
       not_251_out, not_252_out, not_253_out, not_254_out, not_255_out, not_256_out, not_257_out,
       not_258_out, not_259_out, not_260_out, not_261_out, not_262_out, not_263_out, not_264_out,
       not_265_out, not_266_out, not_267_out, not_268_out, not_269_out, not_270_out, not_271_out,
       not_272_out, not_273_out, not_274_out, not_275_out, not_276_out, not_277_out, not_278_out,
       not_279_out, not_280_out;

  not not_1 (not_1_out, OP5);
  not not_2 (not_2_out, OP4);
  not not_3 (not_3_out, OP3);
  not not_4 (not_4_out, OP2);
  not not_5 (not_5_out, OP1);
  not not_6 (not_6_out, OP0);
  not not_7 (not_7_out, F5);
  not not_8 (not_8_out, F4);
  not not_9 (not_9_out, F3);
  not not_10 (not_10_out, F2);
  not not_11 (not_11_out, OP5);
  not not_12 (not_12_out, OP4);
  not not_13 (not_13_out, OP3);
  not not_14 (not_14_out, OP2);
  not not_15 (not_15_out, OP1);
  not not_16 (not_16_out, OP0);
  not not_17 (not_17_out, F4);
  not not_18 (not_18_out, F3);
  not not_19 (not_19_out, F2);
  not not_20 (not_20_out, F1);
  not not_21 (not_21_out, F0);
  not not_22 (not_22_out, OP5);
  not not_23 (not_23_out, OP4);
  not not_24 (not_24_out, OP3);
  not not_25 (not_25_out, OP2);
  not not_26 (not_26_out, OP1);
  not not_27 (not_27_out, OP0);
  not not_28 (not_28_out, F4);
  not not_29 (not_29_out, F3);
  not not_30 (not_30_out, F2);
  not not_31 (not_31_out, F1);
  not not_32 (not_32_out, OP5);
  not not_33 (not_33_out, OP4);
  not not_34 (not_34_out, OP3);
  not not_35 (not_35_out, OP2);
  not not_36 (not_36_out, OP1);
  not not_37 (not_37_out, OP0);
  not not_38 (not_38_out, F4);
  not not_39 (not_39_out, F3);
  not not_40 (not_40_out, F1);
  not not_41 (not_41_out, F0);
  not not_42 (not_42_out, OP5);
  not not_43 (not_43_out, OP4);
  not not_44 (not_44_out, OP3);
  not not_45 (not_45_out, OP2);
  not not_46 (not_46_out, OP1);
  not not_47 (not_47_out, OP0);
  not not_48 (not_48_out, F4);
  not not_49 (not_49_out, F2);
  not not_50 (not_50_out, F0);
  not not_51 (not_51_out, OP5);
  not not_52 (not_52_out, OP4);
  not not_53 (not_53_out, OP2);
  not not_54 (not_54_out, OP1);
  not not_55 (not_55_out, OP0);
  not not_56 (not_56_out, OP5);
  not not_57 (not_57_out, OP4);
  not not_58 (not_58_out, OP1);
  not not_59 (not_59_out, OP0);
  not not_60 (not_60_out, OP5);
  not not_61 (not_61_out, OP4);
  not not_62 (not_62_out, OP2);
  not not_63 (not_63_out, OP1);
  not not_64 (not_64_out, OP5);
  not not_65 (not_65_out, OP4);
  not not_66 (not_66_out, OP2);
  not not_67 (not_67_out, OP0);
  not not_68 (not_68_out, OP4);
  not not_69 (not_69_out, OP3);
  not not_70 (not_70_out, OP2);
  not not_71 (not_71_out, OP4);
  not not_72 (not_72_out, OP2);
  not not_73 (not_73_out, OP5);
  not not_74 (not_74_out, OP4);
  not not_75 (not_75_out, OP0);
  not not_76 (not_76_out, OP4);
  not not_77 (not_77_out, OP3);
  not not_78 (not_78_out, OP1);
  not not_79 (not_79_out, OP0);
  not not_80 (not_80_out, OP5);
  not not_81 (not_81_out, OP4);
  not not_82 (not_82_out, OP3);
  not not_83 (not_83_out, OP0);
  not not_84 (not_84_out, OP5);
  not not_85 (not_85_out, OP4);
  not not_86 (not_86_out, OP3);
  not not_87 (not_87_out, OP2);
  not not_88 (not_88_out, OP1);
  not not_89 (not_89_out, OP0);
  not not_90 (not_90_out, F5);
  not not_91 (not_91_out, F4);
  not not_92 (not_92_out, F3);
  not not_93 (not_93_out, F2);
  not not_94 (not_94_out, F0);
  not not_95 (not_95_out, OP5);
  not not_96 (not_96_out, OP4);
  not not_97 (not_97_out, OP3);
  not not_98 (not_98_out, OP2);
  not not_99 (not_99_out, OP1);
  not not_100 (not_100_out, OP0);
  not not_101 (not_101_out, F4);
  not not_102 (not_102_out, F3);
  not not_103 (not_103_out, F2);
  not not_104 (not_104_out, F0);
  not not_105 (not_105_out, OP5);
  not not_106 (not_106_out, OP4);
  not not_107 (not_107_out, OP3);
  not not_108 (not_108_out, OP2);
  not not_109 (not_109_out, OP1);
  not not_110 (not_110_out, OP0);
  not not_111 (not_111_out, F4);
  not not_112 (not_112_out, F3);
  not not_113 (not_113_out, F1);
  not not_114 (not_114_out, F0);
  not not_115 (not_115_out, OP5);
  not not_116 (not_116_out, OP4);
  not not_117 (not_117_out, OP3);
  not not_118 (not_118_out, OP2);
  not not_119 (not_119_out, OP1);
  not not_120 (not_120_out, OP0);
  not not_121 (not_121_out, F4);
  not not_122 (not_122_out, F3);
  not not_123 (not_123_out, OP5);
  not not_124 (not_124_out, OP4);
  not not_125 (not_125_out, OP3);
  not not_126 (not_126_out, OP2);
  not not_127 (not_127_out, OP1);
  not not_128 (not_128_out, OP0);
  not not_129 (not_129_out, F4);
  not not_130 (not_130_out, F2);
  not not_131 (not_131_out, F0);
  not not_132 (not_132_out, OP5);
  not not_133 (not_133_out, OP4);
  not not_134 (not_134_out, OP1);
  not not_135 (not_135_out, OP0);
  not not_136 (not_136_out, OP5);
  not not_137 (not_137_out, OP4);
  not not_138 (not_138_out, OP2);
  not not_139 (not_139_out, OP0);
  not not_140 (not_140_out, OP5);
  not not_141 (not_141_out, OP4);
  not not_142 (not_142_out, OP3);
  not not_143 (not_143_out, OP2);
  not not_144 (not_144_out, OP1);
  not not_145 (not_145_out, OP0);
  not not_146 (not_146_out, F4);
  not not_147 (not_147_out, F3);
  not not_148 (not_148_out, F2);
  not not_149 (not_149_out, OP5);
  not not_150 (not_150_out, OP4);
  not not_151 (not_151_out, OP3);
  not not_152 (not_152_out, OP0);
  not not_153 (not_153_out, OP5);
  not not_154 (not_154_out, OP4);
  not not_155 (not_155_out, OP3);
  not not_156 (not_156_out, OP2);
  not not_157 (not_157_out, OP1);
  not not_158 (not_158_out, OP0);
  not not_159 (not_159_out, F4);
  not not_160 (not_160_out, F3);
  not not_161 (not_161_out, F2);
  not not_162 (not_162_out, F1);
  not not_163 (not_163_out, F0);
  not not_164 (not_164_out, OP5);
  not not_165 (not_165_out, OP4);
  not not_166 (not_166_out, OP3);
  not not_167 (not_167_out, OP2);
  not not_168 (not_168_out, OP1);
  not not_169 (not_169_out, OP0);
  not not_170 (not_170_out, F4);
  not not_171 (not_171_out, F3);
  not not_172 (not_172_out, F2);
  not not_173 (not_173_out, F1);
  not not_174 (not_174_out, OP5);
  not not_175 (not_175_out, OP4);
  not not_176 (not_176_out, OP3);
  not not_177 (not_177_out, OP2);
  not not_178 (not_178_out, OP1);
  not not_179 (not_179_out, OP0);
  not not_180 (not_180_out, F4);
  not not_181 (not_181_out, F3);
  not not_182 (not_182_out, F2);
  not not_183 (not_183_out, F0);
  not not_184 (not_184_out, OP5);
  not not_185 (not_185_out, OP4);
  not not_186 (not_186_out, OP3);
  not not_187 (not_187_out, OP2);
  not not_188 (not_188_out, OP1);
  not not_189 (not_189_out, OP0);
  not not_190 (not_190_out, F4);
  not not_191 (not_191_out, F3);
  not not_192 (not_192_out, F1);
  not not_193 (not_193_out, F0);
  not not_194 (not_194_out, OP5);
  not not_195 (not_195_out, OP4);
  not not_196 (not_196_out, OP3);
  not not_197 (not_197_out, OP2);
  not not_198 (not_198_out, OP1);
  not not_199 (not_199_out, OP0);
  not not_200 (not_200_out, F4);
  not not_201 (not_201_out, F2);
  not not_202 (not_202_out, OP5);
  not not_203 (not_203_out, OP4);
  not not_204 (not_204_out, OP2);
  not not_205 (not_205_out, OP1);
  not not_206 (not_206_out, OP0);
  not not_207 (not_207_out, OP5);
  not not_208 (not_208_out, OP4);
  not not_209 (not_209_out, OP1);
  not not_210 (not_210_out, OP0);
  not not_211 (not_211_out, OP5);
  not not_212 (not_212_out, OP4);
  not not_213 (not_213_out, OP2);
  not not_214 (not_214_out, OP1);
  not not_215 (not_215_out, OP4);
  not not_216 (not_216_out, OP3);
  not not_217 (not_217_out, OP2);
  not not_218 (not_218_out, OP4);
  not not_219 (not_219_out, OP2);
  not not_220 (not_220_out, OP5);
  not not_221 (not_221_out, OP4);
  not not_222 (not_222_out, OP3);
  not not_223 (not_223_out, OP2);
  not not_224 (not_224_out, OP1);
  not not_225 (not_225_out, OP0);
  not not_226 (not_226_out, F4);
  not not_227 (not_227_out, F3);
  not not_228 (not_228_out, F2);
  not not_229 (not_229_out, OP4);
  not not_230 (not_230_out, OP3);
  not not_231 (not_231_out, OP1);
  not not_232 (not_232_out, OP0);
  not not_233 (not_233_out, OP5);
  not not_234 (not_234_out, OP4);
  not not_235 (not_235_out, OP3);
  not not_236 (not_236_out, OP2);
  not not_237 (not_237_out, OP1);
  not not_238 (not_238_out, OP0);
  not not_239 (not_239_out, F4);
  not not_240 (not_240_out, F3);
  not not_241 (not_241_out, F1);
  not not_242 (not_242_out, OP5);
  not not_243 (not_243_out, OP4);
  not not_244 (not_244_out, OP3);
  not not_245 (not_245_out, OP2);
  not not_246 (not_246_out, OP1);
  not not_247 (not_247_out, OP0);
  not not_248 (not_248_out, F4);
  not not_249 (not_249_out, F3);
  not not_250 (not_250_out, OP5);
  not not_251 (not_251_out, OP4);
  not not_252 (not_252_out, OP3);
  not not_253 (not_253_out, OP2);
  not not_254 (not_254_out, OP1);
  not not_255 (not_255_out, OP0);
  not not_256 (not_256_out, F4);
  not not_257 (not_257_out, F2);
  not not_258 (not_258_out, F0);
  not not_259 (not_259_out, OP5);
  not not_260 (not_260_out, OP4);
  not not_261 (not_261_out, OP3);
  not not_262 (not_262_out, OP2);
  not not_263 (not_263_out, OP1);
  not not_264 (not_264_out, OP0);
  not not_265 (not_265_out, F4);
  not not_266 (not_266_out, F2);
  not not_267 (not_267_out, OP5);
  not not_268 (not_268_out, OP4);
  not not_269 (not_269_out, OP2);
  not not_270 (not_270_out, OP0);
  not not_271 (not_271_out, OP5);
  not not_272 (not_272_out, OP4);
  not not_273 (not_273_out, OP1);
  not not_274 (not_274_out, OP5);
  not not_275 (not_275_out, OP4);
  not not_276 (not_276_out, OP0);
  not not_277 (not_277_out, OP5);
  not not_278 (not_278_out, OP4);
  not not_279 (not_279_out, OP3);
  not not_280 (not_280_out, OP0);
  and and_1 (and_1_out, not_1_out, not_2_out, not_3_out, not_4_out, not_5_out, not_6_out, not_7_out, not_8_out, not_9_out, not_10_out, F1, F0);
  and and_2 (and_2_out, not_11_out, not_12_out, not_13_out, not_14_out, not_15_out, not_16_out, F5, not_17_out, not_18_out, not_19_out, not_20_out, not_21_out);
  and and_3 (and_3_out, not_22_out, not_23_out, not_24_out, not_25_out, not_26_out, not_27_out, F5, not_28_out, not_29_out, not_30_out, not_31_out, F0);
  and and_4 (and_4_out, not_32_out, not_33_out, not_34_out, not_35_out, not_36_out, not_37_out, F5, not_38_out, not_39_out, F2, not_40_out, not_41_out);
  and and_5 (and_5_out, not_42_out, not_43_out, not_44_out, not_45_out, not_46_out, not_47_out, F5, not_48_out, F3, not_49_out, F1, not_50_out);
  and and_6 (and_6_out, not_51_out, not_52_out, OP3, not_53_out, not_54_out, not_55_out);
  and and_7 (and_7_out, not_56_out, not_57_out, OP3, OP2, not_58_out, not_59_out);
  and and_8 (and_8_out, not_60_out, not_61_out, OP3, not_62_out, not_63_out, OP0);
  and and_9 (and_9_out, not_64_out, not_65_out, OP3, not_66_out, OP1, not_67_out);
  and and_10 (and_10_out, OP5, not_68_out, not_69_out, not_70_out, OP1, OP0);
  and and_11 (and_11_out, OP5, not_71_out, OP3, not_72_out, OP1, OP0);
  and and_12 (and_12_out, not_73_out, not_74_out, OP3, OP2, OP1, not_75_out);
  and and_13 (and_13_out, OP5, not_76_out, not_77_out, OP2, not_78_out, not_79_out);
  and and_14 (and_14_out, not_80_out, not_81_out, not_82_out, OP2, OP1, not_83_out);
  and and_15 (and_15_out, not_84_out, not_85_out, not_86_out, not_87_out, not_88_out, not_89_out, not_90_out, not_91_out, not_92_out, not_93_out, F1, not_94_out);
  and and_16 (and_16_out, not_95_out, not_96_out, not_97_out, not_98_out, not_99_out, not_100_out, F5, not_101_out, not_102_out, not_103_out, F1, not_104_out);
  and and_17 (and_17_out, not_105_out, not_106_out, not_107_out, not_108_out, not_109_out, not_110_out, F5, not_111_out, not_112_out, F2, not_113_out, not_114_out);
  and and_18 (and_18_out, not_115_out, not_116_out, not_117_out, not_118_out, not_119_out, not_120_out, F5, not_121_out, not_122_out, F2, F1, F0);
  and and_19 (and_19_out, not_123_out, not_124_out, not_125_out, not_126_out, not_127_out, not_128_out, F5, not_129_out, F3, not_130_out, F1, not_131_out);
  and and_20 (and_20_out, not_132_out, not_133_out, OP3, OP2, not_134_out, not_135_out);
  and and_21 (and_21_out, not_136_out, not_137_out, OP3, not_138_out, OP1, not_139_out);
  and and_22 (and_22_out, not_140_out, not_141_out, not_142_out, not_143_out, not_144_out, not_145_out, F5, not_146_out, not_147_out, not_148_out, F1, F0);
  and and_23 (and_23_out, not_149_out, not_150_out, not_151_out, OP2, OP1, not_152_out);
  and and_24 (and_24_out, not_153_out, not_154_out, not_155_out, not_156_out, not_157_out, not_158_out, F5, not_159_out, not_160_out, not_161_out, not_162_out, not_163_out);
  and and_25 (and_25_out, not_164_out, not_165_out, not_166_out, not_167_out, not_168_out, not_169_out, F5, not_170_out, not_171_out, not_172_out, not_173_out, F0);
  and and_26 (and_26_out, not_174_out, not_175_out, not_176_out, not_177_out, not_178_out, not_179_out, F5, not_180_out, not_181_out, not_182_out, F1, not_183_out);
  and and_27 (and_27_out, not_184_out, not_185_out, not_186_out, not_187_out, not_188_out, not_189_out, F5, not_190_out, not_191_out, F2, not_192_out, not_193_out);
  and and_28 (and_28_out, not_194_out, not_195_out, not_196_out, not_197_out, not_198_out, not_199_out, F5, not_200_out, F3, not_201_out, F1, F0);
  and and_29 (and_29_out, not_202_out, not_203_out, OP3, not_204_out, not_205_out, not_206_out);
  and and_30 (and_30_out, not_207_out, not_208_out, OP3, OP2, not_209_out, not_210_out);
  and and_31 (and_31_out, not_211_out, not_212_out, OP3, not_213_out, not_214_out, OP0);
  and and_32 (and_32_out, OP5, not_215_out, not_216_out, not_217_out, OP1, OP0);
  and and_33 (and_33_out, OP5, not_218_out, OP3, not_219_out, OP1, OP0);
  and and_34 (and_34_out, not_220_out, not_221_out, not_222_out, not_223_out, not_224_out, not_225_out, F5, not_226_out, not_227_out, not_228_out, F1, F0);
  and and_35 (and_35_out, OP5, not_229_out, not_230_out, OP2, not_231_out, not_232_out);
  and and_36 (and_36_out, not_233_out, not_234_out, not_235_out, not_236_out, not_237_out, not_238_out, F5, not_239_out, not_240_out, F2, not_241_out, F0);
  and and_37 (and_37_out, not_242_out, not_243_out, not_244_out, not_245_out, not_246_out, not_247_out, F5, not_248_out, not_249_out, F2, F1, F0);
  and and_38 (and_38_out, not_250_out, not_251_out, not_252_out, not_253_out, not_254_out, not_255_out, F5, not_256_out, F3, not_257_out, F1, not_258_out);
  and and_39 (and_39_out, not_259_out, not_260_out, not_261_out, not_262_out, not_263_out, not_264_out, F5, not_265_out, F3, not_266_out, F1, F0);
  and and_40 (and_40_out, not_267_out, not_268_out, OP3, not_269_out, OP1, not_270_out);
  and and_41 (and_41_out, not_271_out, not_272_out, OP3, OP2, not_273_out, OP0);
  and and_42 (and_42_out, not_274_out, not_275_out, OP3, OP2, OP1, not_276_out);
  and and_43 (and_43_out, not_277_out, not_278_out, not_279_out, OP2, OP1, not_280_out);
  or or_1 (S1, and_15_out, and_16_out, and_17_out, and_18_out, and_19_out, and_20_out, and_21_out, and_22_out, and_23_out);
  or or_2 (S3, and_36_out, and_37_out, and_38_out, and_39_out, and_40_out, and_41_out, and_42_out, and_43_out);
  or or_3 (S0, and_1_out, and_2_out, and_3_out, and_4_out, and_5_out, and_6_out, and_7_out, and_8_out, and_9_out, and_10_out, and_11_out, and_12_out, and_13_out, and_14_out);
  or or_4 (S2, and_24_out, and_25_out, and_26_out, and_27_out, and_28_out, and_29_out, and_30_out, and_31_out, and_32_out, and_33_out, and_34_out, and_35_out);
endmodule

// 控制信号生成
module \控制信号自动生成  (
  input  OP0,
  input  OP1,
  input  OP2,
  input  OP3,
  input  OP4,
  input  OP5,
  input  F0,
  input  F1,
  input  F2,
  input  F3,
  input  F4,
  input  F5,
  output MemToReg,
  output MemWrite,
  output ALU_SRC,
  output RegWrite,
  output SysCALL,
  output SignedExt,
  output RegDst,
  output BEQ,
  output BNE,
  output JR,
  output JUMP,
  output JAL,
  output BLEZ,
  output UNSIGN,
  output R1Used,
  output R2Used
);

  wire and_1_out, and_2_out, and_4_out, and_5_out, and_6_out, and_7_out, and_8_out, and_9_out, and_10_out,
       and_11_out, and_12_out, and_13_out, and_14_out, and_15_out, and_16_out, and_17_out, and_18_out,
       and_19_out, and_20_out, and_21_out, and_22_out, and_23_out, and_24_out, and_25_out, and_26_out,
       and_27_out, and_28_out, and_29_out, and_30_out, and_31_out, and_32_out, and_33_out, and_35_out,
       and_36_out, and_37_out, and_38_out, and_39_out, and_40_out, and_41_out, and_42_out, and_43_out,
       and_44_out, and_45_out, and_46_out, and_47_out, and_48_out, and_49_out, and_50_out, and_51_out,
       and_55_out, and_56_out, and_57_out, and_61_out, and_62_out, and_63_out, and_64_out, and_65_out,
       and_66_out, and_67_out, and_68_out, and_69_out, and_70_out, and_71_out, and_72_out, and_73_out,
       and_74_out, and_75_out, and_76_out, and_77_out, and_78_out, and_79_out, not_1_out, not_2_out,
       not_3_out, not_4_out, not_5_out, not_6_out, not_7_out, not_8_out, not_9_out, not_10_out, not_11_out,
       not_12_out, not_13_out, not_14_out, not_15_out, not_16_out, not_17_out, not_18_out, not_19_out,
       not_20_out, not_21_out, not_22_out, not_23_out, not_24_out, not_25_out, not_26_out, not_27_out,
       not_28_out, not_29_out, not_30_out, not_31_out, not_32_out, not_33_out, not_34_out, not_35_out,
       not_36_out, not_37_out, not_38_out, not_39_out, not_40_out, not_41_out, not_42_out, not_43_out,
       not_44_out, not_45_out, not_46_out, not_47_out, not_48_out, not_49_out, not_50_out, not_51_out,
       not_52_out, not_53_out, not_54_out, not_55_out, not_56_out, not_57_out, not_58_out, not_59_out,
       not_60_out, not_61_out, not_62_out, not_63_out, not_64_out, not_65_out, not_66_out, not_67_out,
       not_68_out, not_69_out, not_70_out, not_71_out, not_72_out, not_73_out, not_74_out, not_75_out,
       not_76_out, not_77_out, not_78_out, not_79_out, not_80_out, not_81_out, not_82_out, not_83_out,
       not_84_out, not_85_out, not_86_out, not_87_out, not_88_out, not_89_out, not_90_out, not_91_out,
       not_92_out, not_93_out, not_94_out, not_95_out, not_96_out, not_97_out, not_98_out, not_99_out,
       not_100_out, not_101_out, not_102_out, not_103_out, not_104_out, not_105_out, not_106_out,
       not_107_out, not_108_out, not_109_out, not_110_out, not_111_out, not_112_out, not_113_out,
       not_114_out, not_115_out, not_116_out, not_117_out, not_118_out, not_119_out, not_120_out,
       not_121_out, not_122_out, not_123_out, not_124_out, not_125_out, not_126_out, not_127_out,
       not_128_out, not_129_out, not_130_out, not_131_out, not_132_out, not_133_out, not_134_out,
       not_135_out, not_136_out, not_137_out, not_138_out, not_139_out, not_140_out, not_141_out,
       not_142_out, not_143_out, not_144_out, not_145_out, not_146_out, not_147_out, not_148_out,
       not_149_out, not_150_out, not_151_out, not_152_out, not_153_out, not_154_out, not_155_out,
       not_156_out, not_157_out, not_158_out, not_159_out, not_160_out, not_161_out, not_162_out,
       not_163_out, not_164_out, not_165_out, not_166_out, not_167_out, not_168_out, not_169_out,
       not_170_out, not_171_out, not_172_out, not_173_out, not_174_out, not_175_out, not_176_out,
       not_177_out, not_178_out, not_179_out, not_180_out, not_181_out, not_182_out, not_183_out,
       not_184_out, not_185_out, not_186_out, not_187_out, not_188_out, not_189_out, not_190_out,
       not_191_out, not_192_out, not_193_out, not_194_out, not_195_out, not_196_out, not_197_out,
       not_198_out, not_199_out, not_200_out, not_201_out, not_202_out, not_203_out, not_204_out,
       not_205_out, not_206_out, not_207_out, not_208_out, not_209_out, not_210_out, not_211_out,
       not_212_out, not_213_out, not_214_out, not_215_out, not_216_out, not_217_out, not_218_out,
       not_219_out, not_220_out, not_221_out, not_222_out, not_223_out, not_224_out, not_225_out,
       not_226_out, not_227_out, not_228_out, not_229_out, not_230_out, not_231_out, not_232_out,
       not_233_out, not_234_out, not_235_out, not_236_out, not_237_out, not_238_out, not_239_out,
       not_240_out, not_241_out, not_242_out, not_243_out, not_244_out, not_245_out, not_246_out,
       not_247_out, not_248_out, not_249_out, not_250_out, not_251_out, not_252_out, not_253_out,
       not_254_out, not_255_out, not_256_out, not_257_out, not_258_out, not_259_out, not_260_out,
       not_261_out, not_262_out, not_263_out, not_264_out, not_265_out, not_266_out, not_267_out,
       not_268_out, not_269_out, not_270_out, not_271_out, not_272_out, not_273_out, not_274_out,
       not_275_out, not_276_out, not_277_out, not_278_out, not_279_out, not_280_out, not_281_out,
       not_282_out, not_283_out, not_284_out, not_285_out, not_286_out, not_287_out, not_288_out,
       not_289_out, not_290_out, not_291_out, not_292_out, not_293_out, not_294_out, not_295_out,
       not_296_out, not_297_out, not_298_out, not_299_out, not_300_out, not_301_out, not_302_out,
       not_303_out, not_304_out, not_305_out, not_306_out, not_307_out, not_308_out, not_309_out,
       not_310_out, not_311_out, not_312_out, not_313_out, not_314_out, not_315_out, not_316_out,
       not_317_out, not_318_out, not_319_out, not_320_out, not_321_out, not_322_out, not_323_out,
       not_324_out, not_325_out, not_326_out, not_327_out, not_328_out, not_329_out, not_330_out,
       not_331_out, not_332_out, not_333_out, not_334_out, not_335_out, not_336_out, not_337_out,
       not_338_out, not_339_out, not_340_out, not_341_out, not_342_out, not_343_out, not_344_out,
       not_345_out, not_346_out, not_347_out, not_348_out, not_349_out, not_350_out, not_351_out,
       not_352_out, not_353_out, not_354_out, not_355_out, not_356_out, not_357_out, not_358_out,
       not_359_out, not_360_out, not_361_out, not_362_out, not_363_out, not_364_out, not_365_out,
       not_366_out, not_367_out, not_368_out, not_369_out, not_370_out, not_371_out, not_372_out,
       not_373_out, not_374_out, not_375_out, not_376_out, not_377_out, not_378_out, not_379_out,
       not_380_out, not_381_out, not_382_out, not_383_out, not_384_out, not_385_out, not_386_out,
       not_387_out, not_388_out, not_389_out, not_390_out, not_391_out, not_392_out, not_393_out,
       not_394_out, not_395_out, not_396_out, not_397_out, not_398_out, not_399_out, not_400_out,
       not_401_out, not_402_out, not_403_out, not_404_out, not_405_out, not_406_out, not_407_out,
       not_408_out, not_409_out, not_410_out, not_411_out, not_412_out, not_413_out, not_414_out,
       not_415_out, not_416_out, not_417_out, not_418_out, not_419_out, not_420_out, not_421_out,
       not_422_out, not_423_out, not_424_out, not_425_out, not_426_out, not_427_out, not_428_out,
       not_429_out, not_430_out, not_431_out, not_432_out, not_433_out, not_434_out, not_435_out,
       not_436_out, not_437_out, not_438_out, not_439_out, not_440_out, not_441_out, not_442_out,
       not_443_out, not_444_out, not_445_out, not_446_out, not_447_out, not_448_out, not_449_out,
       not_450_out, not_451_out, not_452_out, not_453_out, not_454_out, not_455_out, not_456_out,
       not_457_out, not_458_out, not_459_out, not_460_out, not_461_out, not_462_out, not_463_out,
       not_464_out, not_465_out, not_466_out, not_467_out, not_468_out, not_469_out, not_470_out,
       not_471_out, not_472_out, not_473_out, not_474_out, not_475_out, not_476_out, not_477_out,
       not_478_out, not_479_out, not_480_out, not_481_out, not_482_out, not_483_out, not_484_out,
       not_485_out, not_486_out, not_487_out, not_488_out, not_489_out, not_490_out, not_491_out,
       not_492_out, not_493_out, not_494_out, not_495_out, not_496_out, not_497_out, not_498_out,
       not_499_out, not_500_out, not_501_out, not_502_out;

  not not_1 (not_1_out, OP4);
  not not_2 (not_2_out, OP3);
  not not_3 (not_3_out, OP2);
  not not_4 (not_4_out, OP4);
  not not_5 (not_5_out, OP3);
  not not_6 (not_6_out, OP1);
  not not_7 (not_7_out, OP0);
  not not_8 (not_8_out, OP4);
  not not_9 (not_9_out, OP2);
  not not_10 (not_10_out, OP5);
  not not_11 (not_11_out, OP4);
  not not_12 (not_12_out, OP2);
  not not_13 (not_13_out, OP1);
  not not_14 (not_14_out, OP0);
  not not_15 (not_15_out, OP5);
  not not_16 (not_16_out, OP4);
  not not_17 (not_17_out, OP1);
  not not_18 (not_18_out, OP0);
  not not_19 (not_19_out, OP5);
  not not_20 (not_20_out, OP4);
  not not_21 (not_21_out, OP2);
  not not_22 (not_22_out, OP1);
  not not_23 (not_23_out, OP5);
  not not_24 (not_24_out, OP4);
  not not_25 (not_25_out, OP2);
  not not_26 (not_26_out, OP0);
  not not_27 (not_27_out, OP5);
  not not_28 (not_28_out, OP4);
  not not_29 (not_29_out, OP1);
  not not_30 (not_30_out, OP4);
  not not_31 (not_31_out, OP3);
  not not_32 (not_32_out, OP2);
  not not_33 (not_33_out, OP4);
  not not_34 (not_34_out, OP2);
  not not_35 (not_35_out, OP5);
  not not_36 (not_36_out, OP4);
  not not_37 (not_37_out, OP0);
  not not_38 (not_38_out, OP4);
  not not_39 (not_39_out, OP3);
  not not_40 (not_40_out, OP1);
  not not_41 (not_41_out, OP0);
  not not_42 (not_42_out, OP5);
  not not_43 (not_43_out, OP4);
  not not_44 (not_44_out, OP3);
  not not_45 (not_45_out, OP2);
  not not_46 (not_46_out, OP1);
  not not_47 (not_47_out, OP0);
  not not_48 (not_48_out, F5);
  not not_49 (not_49_out, F4);
  not not_50 (not_50_out, F3);
  not not_51 (not_51_out, F2);
  not not_52 (not_52_out, F1);
  not not_53 (not_53_out, F0);
  not not_54 (not_54_out, OP5);
  not not_55 (not_55_out, OP4);
  not not_56 (not_56_out, OP3);
  not not_57 (not_57_out, OP2);
  not not_58 (not_58_out, OP1);
  not not_59 (not_59_out, OP0);
  not not_60 (not_60_out, F5);
  not not_61 (not_61_out, F4);
  not not_62 (not_62_out, F3);
  not not_63 (not_63_out, F2);
  not not_64 (not_64_out, OP5);
  not not_65 (not_65_out, OP4);
  not not_66 (not_66_out, OP3);
  not not_67 (not_67_out, OP2);
  not not_68 (not_68_out, OP1);
  not not_69 (not_69_out, OP0);
  not not_70 (not_70_out, F5);
  not not_71 (not_71_out, F4);
  not not_72 (not_72_out, F3);
  not not_73 (not_73_out, F2);
  not not_74 (not_74_out, F0);
  not not_75 (not_75_out, OP5);
  not not_76 (not_76_out, OP4);
  not not_77 (not_77_out, OP3);
  not not_78 (not_78_out, OP2);
  not not_79 (not_79_out, OP1);
  not not_80 (not_80_out, OP0);
  not not_81 (not_81_out, F4);
  not not_82 (not_82_out, F3);
  not not_83 (not_83_out, F2);
  not not_84 (not_84_out, F1);
  not not_85 (not_85_out, F0);
  not not_86 (not_86_out, OP5);
  not not_87 (not_87_out, OP4);
  not not_88 (not_88_out, OP3);
  not not_89 (not_89_out, OP2);
  not not_90 (not_90_out, OP1);
  not not_91 (not_91_out, OP0);
  not not_92 (not_92_out, F4);
  not not_93 (not_93_out, F3);
  not not_94 (not_94_out, F2);
  not not_95 (not_95_out, F1);
  not not_96 (not_96_out, OP5);
  not not_97 (not_97_out, OP4);
  not not_98 (not_98_out, OP3);
  not not_99 (not_99_out, OP2);
  not not_100 (not_100_out, OP1);
  not not_101 (not_101_out, OP0);
  not not_102 (not_102_out, F4);
  not not_103 (not_103_out, F3);
  not not_104 (not_104_out, F2);
  not not_105 (not_105_out, F0);
  not not_106 (not_106_out, OP5);
  not not_107 (not_107_out, OP4);
  not not_108 (not_108_out, OP3);
  not not_109 (not_109_out, OP2);
  not not_110 (not_110_out, OP1);
  not not_111 (not_111_out, OP0);
  not not_112 (not_112_out, F4);
  not not_113 (not_113_out, F3);
  not not_114 (not_114_out, F1);
  not not_115 (not_115_out, F0);
  not not_116 (not_116_out, OP5);
  not not_117 (not_117_out, OP4);
  not not_118 (not_118_out, OP3);
  not not_119 (not_119_out, OP2);
  not not_120 (not_120_out, OP1);
  not not_121 (not_121_out, OP0);
  not not_122 (not_122_out, F4);
  not not_123 (not_123_out, F3);
  not not_124 (not_124_out, F1);
  not not_125 (not_125_out, OP5);
  not not_126 (not_126_out, OP4);
  not not_127 (not_127_out, OP3);
  not not_128 (not_128_out, OP2);
  not not_129 (not_129_out, OP1);
  not not_130 (not_130_out, OP0);
  not not_131 (not_131_out, F4);
  not not_132 (not_132_out, F3);
  not not_133 (not_133_out, OP5);
  not not_134 (not_134_out, OP4);
  not not_135 (not_135_out, OP3);
  not not_136 (not_136_out, OP2);
  not not_137 (not_137_out, OP1);
  not not_138 (not_138_out, OP0);
  not not_139 (not_139_out, F4);
  not not_140 (not_140_out, F2);
  not not_141 (not_141_out, F0);
  not not_142 (not_142_out, OP5);
  not not_143 (not_143_out, OP4);
  not not_144 (not_144_out, OP3);
  not not_145 (not_145_out, OP2);
  not not_146 (not_146_out, OP1);
  not not_147 (not_147_out, OP0);
  not not_148 (not_148_out, F4);
  not not_149 (not_149_out, F2);
  not not_150 (not_150_out, OP5);
  not not_151 (not_151_out, OP4);
  not not_152 (not_152_out, OP3);
  not not_153 (not_153_out, OP2);
  not not_154 (not_154_out, OP5);
  not not_155 (not_155_out, OP4);
  not not_156 (not_156_out, OP2);
  not not_157 (not_157_out, OP1);
  not not_158 (not_158_out, OP0);
  not not_159 (not_159_out, OP5);
  not not_160 (not_160_out, OP4);
  not not_161 (not_161_out, OP1);
  not not_162 (not_162_out, OP0);
  not not_163 (not_163_out, OP5);
  not not_164 (not_164_out, OP4);
  not not_165 (not_165_out, OP2);
  not not_166 (not_166_out, OP1);
  not not_167 (not_167_out, OP5);
  not not_168 (not_168_out, OP4);
  not not_169 (not_169_out, OP2);
  not not_170 (not_170_out, OP0);
  not not_171 (not_171_out, OP5);
  not not_172 (not_172_out, OP4);
  not not_173 (not_173_out, OP1);
  not not_174 (not_174_out, OP4);
  not not_175 (not_175_out, OP3);
  not not_176 (not_176_out, OP2);
  not not_177 (not_177_out, OP5);
  not not_178 (not_178_out, OP4);
  not not_179 (not_179_out, OP0);
  not not_180 (not_180_out, OP5);
  not not_181 (not_181_out, OP4);
  not not_182 (not_182_out, OP3);
  not not_183 (not_183_out, OP2);
  not not_184 (not_184_out, OP1);
  not not_185 (not_185_out, OP0);
  not not_186 (not_186_out, F4);
  not not_187 (not_187_out, F3);
  not not_188 (not_188_out, F2);
  not not_189 (not_189_out, OP4);
  not not_190 (not_190_out, OP3);
  not not_191 (not_191_out, OP1);
  not not_192 (not_192_out, OP0);
  not not_193 (not_193_out, OP5);
  not not_194 (not_194_out, OP4);
  not not_195 (not_195_out, OP3);
  not not_196 (not_196_out, OP2);
  not not_197 (not_197_out, OP1);
  not not_198 (not_198_out, OP0);
  not not_199 (not_199_out, F5);
  not not_200 (not_200_out, F4);
  not not_201 (not_201_out, F1);
  not not_202 (not_202_out, F0);
  not not_203 (not_203_out, OP5);
  not not_204 (not_204_out, OP4);
  not not_205 (not_205_out, OP2);
  not not_206 (not_206_out, OP1);
  not not_207 (not_207_out, OP0);
  not not_208 (not_208_out, OP5);
  not not_209 (not_209_out, OP4);
  not not_210 (not_210_out, OP2);
  not not_211 (not_211_out, OP1);
  not not_212 (not_212_out, OP5);
  not not_213 (not_213_out, OP4);
  not not_214 (not_214_out, OP2);
  not not_215 (not_215_out, OP0);
  not not_216 (not_216_out, OP4);
  not not_217 (not_217_out, OP3);
  not not_218 (not_218_out, OP2);
  not not_219 (not_219_out, OP4);
  not not_220 (not_220_out, OP2);
  not not_221 (not_221_out, OP5);
  not not_222 (not_222_out, OP4);
  not not_223 (not_223_out, OP3);
  not not_224 (not_224_out, OP2);
  not not_225 (not_225_out, OP1);
  not not_226 (not_226_out, OP0);
  not not_227 (not_227_out, F5);
  not not_228 (not_228_out, F4);
  not not_229 (not_229_out, F3);
  not not_230 (not_230_out, F2);
  not not_231 (not_231_out, F1);
  not not_232 (not_232_out, F0);
  not not_233 (not_233_out, OP5);
  not not_234 (not_234_out, OP4);
  not not_235 (not_235_out, OP3);
  not not_236 (not_236_out, OP2);
  not not_237 (not_237_out, OP1);
  not not_238 (not_238_out, OP0);
  not not_239 (not_239_out, F5);
  not not_240 (not_240_out, F4);
  not not_241 (not_241_out, F3);
  not not_242 (not_242_out, F2);
  not not_243 (not_243_out, OP5);
  not not_244 (not_244_out, OP4);
  not not_245 (not_245_out, OP3);
  not not_246 (not_246_out, OP2);
  not not_247 (not_247_out, OP1);
  not not_248 (not_248_out, OP0);
  not not_249 (not_249_out, F5);
  not not_250 (not_250_out, F4);
  not not_251 (not_251_out, F3);
  not not_252 (not_252_out, F2);
  not not_253 (not_253_out, F0);
  not not_254 (not_254_out, OP5);
  not not_255 (not_255_out, OP4);
  not not_256 (not_256_out, OP3);
  not not_257 (not_257_out, OP2);
  not not_258 (not_258_out, OP1);
  not not_259 (not_259_out, OP0);
  not not_260 (not_260_out, F4);
  not not_261 (not_261_out, F3);
  not not_262 (not_262_out, F2);
  not not_263 (not_263_out, F1);
  not not_264 (not_264_out, F0);
  not not_265 (not_265_out, OP5);
  not not_266 (not_266_out, OP4);
  not not_267 (not_267_out, OP3);
  not not_268 (not_268_out, OP2);
  not not_269 (not_269_out, OP1);
  not not_270 (not_270_out, OP0);
  not not_271 (not_271_out, F4);
  not not_272 (not_272_out, F3);
  not not_273 (not_273_out, F2);
  not not_274 (not_274_out, F1);
  not not_275 (not_275_out, OP5);
  not not_276 (not_276_out, OP4);
  not not_277 (not_277_out, OP3);
  not not_278 (not_278_out, OP2);
  not not_279 (not_279_out, OP1);
  not not_280 (not_280_out, OP0);
  not not_281 (not_281_out, F4);
  not not_282 (not_282_out, F3);
  not not_283 (not_283_out, F2);
  not not_284 (not_284_out, F0);
  not not_285 (not_285_out, OP5);
  not not_286 (not_286_out, OP4);
  not not_287 (not_287_out, OP3);
  not not_288 (not_288_out, OP2);
  not not_289 (not_289_out, OP1);
  not not_290 (not_290_out, OP0);
  not not_291 (not_291_out, F4);
  not not_292 (not_292_out, F3);
  not not_293 (not_293_out, F1);
  not not_294 (not_294_out, F0);
  not not_295 (not_295_out, OP5);
  not not_296 (not_296_out, OP4);
  not not_297 (not_297_out, OP3);
  not not_298 (not_298_out, OP2);
  not not_299 (not_299_out, OP1);
  not not_300 (not_300_out, OP0);
  not not_301 (not_301_out, F4);
  not not_302 (not_302_out, F3);
  not not_303 (not_303_out, F1);
  not not_304 (not_304_out, OP5);
  not not_305 (not_305_out, OP4);
  not not_306 (not_306_out, OP3);
  not not_307 (not_307_out, OP2);
  not not_308 (not_308_out, OP1);
  not not_309 (not_309_out, OP0);
  not not_310 (not_310_out, F4);
  not not_311 (not_311_out, F3);
  not not_312 (not_312_out, OP5);
  not not_313 (not_313_out, OP4);
  not not_314 (not_314_out, OP3);
  not not_315 (not_315_out, OP2);
  not not_316 (not_316_out, OP1);
  not not_317 (not_317_out, OP0);
  not not_318 (not_318_out, F4);
  not not_319 (not_319_out, F2);
  not not_320 (not_320_out, F0);
  not not_321 (not_321_out, OP5);
  not not_322 (not_322_out, OP4);
  not not_323 (not_323_out, OP3);
  not not_324 (not_324_out, OP2);
  not not_325 (not_325_out, OP1);
  not not_326 (not_326_out, OP0);
  not not_327 (not_327_out, F4);
  not not_328 (not_328_out, F2);
  not not_329 (not_329_out, OP5);
  not not_330 (not_330_out, OP4);
  not not_331 (not_331_out, OP3);
  not not_332 (not_332_out, OP2);
  not not_333 (not_333_out, OP1);
  not not_334 (not_334_out, OP0);
  not not_335 (not_335_out, F4);
  not not_336 (not_336_out, F3);
  not not_337 (not_337_out, F2);
  not not_338 (not_338_out, OP5);
  not not_339 (not_339_out, OP4);
  not not_340 (not_340_out, OP3);
  not not_341 (not_341_out, OP1);
  not not_342 (not_342_out, OP0);
  not not_343 (not_343_out, OP5);
  not not_344 (not_344_out, OP4);
  not not_345 (not_345_out, OP3);
  not not_346 (not_346_out, OP1);
  not not_347 (not_347_out, OP5);
  not not_348 (not_348_out, OP4);
  not not_349 (not_349_out, OP3);
  not not_350 (not_350_out, OP2);
  not not_351 (not_351_out, OP1);
  not not_352 (not_352_out, OP0);
  not not_353 (not_353_out, F5);
  not not_354 (not_354_out, F4);
  not not_355 (not_355_out, F2);
  not not_356 (not_356_out, F1);
  not not_357 (not_357_out, F0);
  not not_358 (not_358_out, OP5);
  not not_359 (not_359_out, OP4);
  not not_360 (not_360_out, OP3);
  not not_361 (not_361_out, OP2);
  not not_362 (not_362_out, OP1);
  not not_363 (not_363_out, OP0);
  not not_364 (not_364_out, F5);
  not not_365 (not_365_out, F4);
  not not_366 (not_366_out, F2);
  not not_367 (not_367_out, F1);
  not not_368 (not_368_out, F0);
  not not_369 (not_369_out, OP5);
  not not_370 (not_370_out, OP4);
  not not_371 (not_371_out, OP3);
  not not_372 (not_372_out, OP2);
  not not_373 (not_373_out, OP0);
  not not_374 (not_374_out, OP5);
  not not_375 (not_375_out, OP4);
  not not_376 (not_376_out, OP3);
  not not_377 (not_377_out, OP2);
  not not_378 (not_378_out, OP5);
  not not_379 (not_379_out, OP4);
  not not_380 (not_380_out, OP3);
  not not_381 (not_381_out, OP2);
  not not_382 (not_382_out, OP0);
  not not_383 (not_383_out, OP3);
  not not_384 (not_384_out, OP4);
  not not_385 (not_385_out, OP5);
  not not_386 (not_386_out, OP0);
  not not_387 (not_387_out, OP1);
  not not_388 (not_388_out, OP3);
  not not_389 (not_389_out, OP4);
  not not_390 (not_390_out, OP0);
  not not_391 (not_391_out, OP1);
  not not_392 (not_392_out, OP4);
  not not_393 (not_393_out, OP5);
  not not_394 (not_394_out, F0);
  not not_395 (not_395_out, F2);
  not not_396 (not_396_out, F3);
  not not_397 (not_397_out, F4);
  not not_398 (not_398_out, OP0);
  not not_399 (not_399_out, OP1);
  not not_400 (not_400_out, OP4);
  not not_401 (not_401_out, OP5);
  not not_402 (not_402_out, F1);
  not not_403 (not_403_out, F3);
  not not_404 (not_404_out, F4);
  not not_405 (not_405_out, OP0);
  not not_406 (not_406_out, OP1);
  not not_407 (not_407_out, OP4);
  not not_408 (not_408_out, OP5);
  not not_409 (not_409_out, F0);
  not not_410 (not_410_out, F1);
  not not_411 (not_411_out, F4);
  not not_412 (not_412_out, F5);
  not not_413 (not_413_out, OP0);
  not not_414 (not_414_out, OP1);
  not not_415 (not_415_out, OP4);
  not not_416 (not_416_out, OP5);
  not not_417 (not_417_out, F2);
  not not_418 (not_418_out, F4);
  not not_419 (not_419_out, OP0);
  not not_420 (not_420_out, OP1);
  not not_421 (not_421_out, OP4);
  not not_422 (not_422_out, OP5);
  not not_423 (not_423_out, F3);
  not not_424 (not_424_out, F4);
  not not_425 (not_425_out, F5);
  not not_426 (not_426_out, OP0);
  not not_427 (not_427_out, OP1);
  not not_428 (not_428_out, OP4);
  not not_429 (not_429_out, OP5);
  not not_430 (not_430_out, F3);
  not not_431 (not_431_out, F4);
  not not_432 (not_432_out, OP0);
  not not_433 (not_433_out, OP1);
  not not_434 (not_434_out, OP2);
  not not_435 (not_435_out, OP3);
  not not_436 (not_436_out, OP4);
  not not_437 (not_437_out, OP2);
  not not_438 (not_438_out, OP4);
  not not_439 (not_439_out, OP5);
  not not_440 (not_440_out, OP0);
  not not_441 (not_441_out, OP3);
  not not_442 (not_442_out, OP4);
  not not_443 (not_443_out, OP5);
  not not_444 (not_444_out, OP1);
  not not_445 (not_445_out, OP4);
  not not_446 (not_446_out, OP5);
  not not_447 (not_447_out, OP2);
  not not_448 (not_448_out, OP4);
  not not_449 (not_449_out, OP0);
  not not_450 (not_450_out, OP1);
  not not_451 (not_451_out, OP3);
  not not_452 (not_452_out, OP4);
  not not_453 (not_453_out, OP5);
  not not_454 (not_454_out, F0);
  not not_455 (not_455_out, F2);
  not not_456 (not_456_out, F3);
  not not_457 (not_457_out, F4);
  not not_458 (not_458_out, OP0);
  not not_459 (not_459_out, OP1);
  not not_460 (not_460_out, OP3);
  not not_461 (not_461_out, OP4);
  not not_462 (not_462_out, OP5);
  not not_463 (not_463_out, F1);
  not not_464 (not_464_out, F3);
  not not_465 (not_465_out, F4);
  not not_466 (not_466_out, OP0);
  not not_467 (not_467_out, OP1);
  not not_468 (not_468_out, OP3);
  not not_469 (not_469_out, OP4);
  not not_470 (not_470_out, OP5);
  not not_471 (not_471_out, F0);
  not not_472 (not_472_out, F1);
  not not_473 (not_473_out, F4);
  not not_474 (not_474_out, F5);
  not not_475 (not_475_out, OP0);
  not not_476 (not_476_out, OP1);
  not not_477 (not_477_out, OP3);
  not not_478 (not_478_out, OP4);
  not not_479 (not_479_out, OP5);
  not not_480 (not_480_out, F2);
  not not_481 (not_481_out, F4);
  not not_482 (not_482_out, OP0);
  not not_483 (not_483_out, OP1);
  not not_484 (not_484_out, OP3);
  not not_485 (not_485_out, OP4);
  not not_486 (not_486_out, OP5);
  not not_487 (not_487_out, F3);
  not not_488 (not_488_out, F4);
  not not_489 (not_489_out, F5);
  not not_490 (not_490_out, OP0);
  not not_491 (not_491_out, OP1);
  not not_492 (not_492_out, OP3);
  not not_493 (not_493_out, OP4);
  not not_494 (not_494_out, OP5);
  not not_495 (not_495_out, F3);
  not not_496 (not_496_out, F4);
  not not_497 (not_497_out, OP1);
  not not_498 (not_498_out, OP3);
  not not_499 (not_499_out, OP4);
  not not_500 (not_500_out, OP5);
  not not_501 (not_501_out, OP2);
  not not_502 (not_502_out, OP4);
  and and_1 (and_1_out, OP5, not_1_out, not_2_out, not_3_out, OP1, OP0);
  and and_2 (and_2_out, OP5, not_4_out, not_5_out, OP2, not_6_out, not_7_out);
  and and_3 (MemWrite, OP5, not_8_out, OP3, not_9_out, OP1, OP0);
  and and_4 (and_4_out, not_10_out, not_11_out, OP3, not_12_out, not_13_out, not_14_out);
  and and_5 (and_5_out, not_15_out, not_16_out, OP3, OP2, not_17_out, not_18_out);
  and and_6 (and_6_out, not_19_out, not_20_out, OP3, not_21_out, not_22_out, OP0);
  and and_7 (and_7_out, not_23_out, not_24_out, OP3, not_25_out, OP1, not_26_out);
  and and_8 (and_8_out, not_27_out, not_28_out, OP3, OP2, not_29_out, OP0);
  and and_9 (and_9_out, OP5, not_30_out, not_31_out, not_32_out, OP1, OP0);
  and and_10 (and_10_out, OP5, not_33_out, OP3, not_34_out, OP1, OP0);
  and and_11 (and_11_out, not_35_out, not_36_out, OP3, OP2, OP1, not_37_out);
  and and_12 (and_12_out, OP5, not_38_out, not_39_out, OP2, not_40_out, not_41_out);
  and and_13 (and_13_out, not_42_out, not_43_out, not_44_out, not_45_out, not_46_out, not_47_out, not_48_out, not_49_out, not_50_out, not_51_out, not_52_out, not_53_out);
  and and_14 (and_14_out, not_54_out, not_55_out, not_56_out, not_57_out, not_58_out, not_59_out, not_60_out, not_61_out, not_62_out, not_63_out, F1, F0);
  and and_15 (and_15_out, not_64_out, not_65_out, not_66_out, not_67_out, not_68_out, not_69_out, not_70_out, not_71_out, not_72_out, not_73_out, F1, not_74_out);
  and and_16 (and_16_out, not_75_out, not_76_out, not_77_out, not_78_out, not_79_out, not_80_out, F5, not_81_out, not_82_out, not_83_out, not_84_out, not_85_out);
  and and_17 (and_17_out, not_86_out, not_87_out, not_88_out, not_89_out, not_90_out, not_91_out, F5, not_92_out, not_93_out, not_94_out, not_95_out, F0);
  and and_18 (and_18_out, not_96_out, not_97_out, not_98_out, not_99_out, not_100_out, not_101_out, F5, not_102_out, not_103_out, not_104_out, F1, not_105_out);
  and and_19 (and_19_out, not_106_out, not_107_out, not_108_out, not_109_out, not_110_out, not_111_out, F5, not_112_out, not_113_out, F2, not_114_out, not_115_out);
  and and_20 (and_20_out, not_116_out, not_117_out, not_118_out, not_119_out, not_120_out, not_121_out, F5, not_122_out, not_123_out, F2, not_124_out, F0);
  and and_21 (and_21_out, not_125_out, not_126_out, not_127_out, not_128_out, not_129_out, not_130_out, F5, not_131_out, not_132_out, F2, F1, F0);
  and and_22 (and_22_out, not_133_out, not_134_out, not_135_out, not_136_out, not_137_out, not_138_out, F5, not_139_out, F3, not_140_out, F1, not_141_out);
  and and_23 (and_23_out, not_142_out, not_143_out, not_144_out, not_145_out, not_146_out, not_147_out, F5, not_148_out, F3, not_149_out, F1, F0);
  and and_24 (and_24_out, not_150_out, not_151_out, not_152_out, not_153_out, OP1, OP0);
  and and_25 (and_25_out, not_154_out, not_155_out, OP3, not_156_out, not_157_out, not_158_out);
  and and_26 (and_26_out, not_159_out, not_160_out, OP3, OP2, not_161_out, not_162_out);
  and and_27 (and_27_out, not_163_out, not_164_out, OP3, not_165_out, not_166_out, OP0);
  and and_28 (and_28_out, not_167_out, not_168_out, OP3, not_169_out, OP1, not_170_out);
  and and_29 (and_29_out, not_171_out, not_172_out, OP3, OP2, not_173_out, OP0);
  and and_30 (and_30_out, OP5, not_174_out, not_175_out, not_176_out, OP1, OP0);
  and and_31 (and_31_out, not_177_out, not_178_out, OP3, OP2, OP1, not_179_out);
  and and_32 (and_32_out, not_180_out, not_181_out, not_182_out, not_183_out, not_184_out, not_185_out, F5, not_186_out, not_187_out, not_188_out, F1, F0);
  and and_33 (and_33_out, OP5, not_189_out, not_190_out, OP2, not_191_out, not_192_out);
  and and_34 (SysCALL, not_193_out, not_194_out, not_195_out, not_196_out, not_197_out, not_198_out, not_199_out, not_200_out, F3, F2, not_201_out, not_202_out);
  and and_35 (and_35_out, not_203_out, not_204_out, OP3, not_205_out, not_206_out, not_207_out);
  and and_36 (and_36_out, not_208_out, not_209_out, OP3, not_210_out, not_211_out, OP0);
  and and_37 (and_37_out, not_212_out, not_213_out, OP3, not_214_out, OP1, not_215_out);
  and and_38 (and_38_out, OP5, not_216_out, not_217_out, not_218_out, OP1, OP0);
  and and_39 (and_39_out, OP5, not_219_out, OP3, not_220_out, OP1, OP0);
  and and_40 (and_40_out, not_221_out, not_222_out, not_223_out, not_224_out, not_225_out, not_226_out, not_227_out, not_228_out, not_229_out, not_230_out, not_231_out, not_232_out);
  and and_41 (and_41_out, not_233_out, not_234_out, not_235_out, not_236_out, not_237_out, not_238_out, not_239_out, not_240_out, not_241_out, not_242_out, F1, F0);
  and and_42 (and_42_out, not_243_out, not_244_out, not_245_out, not_246_out, not_247_out, not_248_out, not_249_out, not_250_out, not_251_out, not_252_out, F1, not_253_out);
  and and_43 (and_43_out, not_254_out, not_255_out, not_256_out, not_257_out, not_258_out, not_259_out, F5, not_260_out, not_261_out, not_262_out, not_263_out, not_264_out);
  and and_44 (and_44_out, not_265_out, not_266_out, not_267_out, not_268_out, not_269_out, not_270_out, F5, not_271_out, not_272_out, not_273_out, not_274_out, F0);
  and and_45 (and_45_out, not_275_out, not_276_out, not_277_out, not_278_out, not_279_out, not_280_out, F5, not_281_out, not_282_out, not_283_out, F1, not_284_out);
  and and_46 (and_46_out, not_285_out, not_286_out, not_287_out, not_288_out, not_289_out, not_290_out, F5, not_291_out, not_292_out, F2, not_293_out, not_294_out);
  and and_47 (and_47_out, not_295_out, not_296_out, not_297_out, not_298_out, not_299_out, not_300_out, F5, not_301_out, not_302_out, F2, not_303_out, F0);
  and and_48 (and_48_out, not_304_out, not_305_out, not_306_out, not_307_out, not_308_out, not_309_out, F5, not_310_out, not_311_out, F2, F1, F0);
  and and_49 (and_49_out, not_312_out, not_313_out, not_314_out, not_315_out, not_316_out, not_317_out, F5, not_318_out, F3, not_319_out, F1, not_320_out);
  and and_50 (and_50_out, not_321_out, not_322_out, not_323_out, not_324_out, not_325_out, not_326_out, F5, not_327_out, F3, not_328_out, F1, F0);
  and and_51 (and_51_out, not_329_out, not_330_out, not_331_out, not_332_out, not_333_out, not_334_out, F5, not_335_out, not_336_out, not_337_out, F1, F0);
  and and_52 (BEQ, not_338_out, not_339_out, not_340_out, OP2, not_341_out, not_342_out);
  and and_53 (BNE, not_343_out, not_344_out, not_345_out, OP2, not_346_out, OP0);
  and and_54 (JR, not_347_out, not_348_out, not_349_out, not_350_out, not_351_out, not_352_out, not_353_out, not_354_out, F3, not_355_out, not_356_out, not_357_out);
  and and_55 (and_55_out, not_358_out, not_359_out, not_360_out, not_361_out, not_362_out, not_363_out, not_364_out, not_365_out, F3, not_366_out, not_367_out, not_368_out);
  and and_56 (and_56_out, not_369_out, not_370_out, not_371_out, not_372_out, OP1, not_373_out);
  and and_57 (and_57_out, not_374_out, not_375_out, not_376_out, not_377_out, OP1, OP0);
  and and_58 (JAL, not_378_out, not_379_out, not_380_out, not_381_out, OP1, OP0);
  and and_59 (BLEZ, not_382_out, OP1, OP2, not_383_out, not_384_out, not_385_out);
  and and_60 (UNSIGN, not_386_out, not_387_out, OP2, not_388_out, not_389_out, OP5);
  and and_61 (and_61_out, not_390_out, not_391_out, not_392_out, not_393_out, not_394_out, not_395_out, not_396_out, not_397_out);
  and and_62 (and_62_out, not_398_out, not_399_out, not_400_out, not_401_out, not_402_out, not_403_out, not_404_out, F5);
  and and_63 (and_63_out, not_405_out, not_406_out, not_407_out, not_408_out, not_409_out, not_410_out, F3, not_411_out, not_412_out);
  and and_64 (and_64_out, not_413_out, not_414_out, not_415_out, not_416_out, F1, not_417_out, F3, not_418_out, F5);
  and and_65 (and_65_out, not_419_out, not_420_out, not_421_out, not_422_out, F0, F1, not_423_out, not_424_out, not_425_out);
  and and_66 (and_66_out, not_426_out, not_427_out, not_428_out, not_429_out, F0, F1, F2, not_430_out, not_431_out);
  and and_67 (and_67_out, not_432_out, not_433_out, not_434_out, not_435_out, not_436_out, OP5);
  and and_68 (and_68_out, not_437_out, OP3, not_438_out, not_439_out);
  and and_69 (and_69_out, not_440_out, OP2, not_441_out, not_442_out, not_443_out);
  and and_70 (and_70_out, not_444_out, OP2, not_445_out, not_446_out);
  and and_71 (and_71_out, OP0, OP1, not_447_out, not_448_out, OP5);
  and and_72 (and_72_out, not_449_out, not_450_out, not_451_out, not_452_out, not_453_out, not_454_out, not_455_out, not_456_out, not_457_out);
  and and_73 (and_73_out, not_458_out, not_459_out, not_460_out, not_461_out, not_462_out, not_463_out, not_464_out, not_465_out, F5);
  and and_74 (and_74_out, not_466_out, not_467_out, not_468_out, not_469_out, not_470_out, not_471_out, not_472_out, F2, F3, not_473_out, not_474_out);
  and and_75 (and_75_out, not_475_out, not_476_out, not_477_out, not_478_out, not_479_out, F1, not_480_out, F3, not_481_out, F5);
  and and_76 (and_76_out, not_482_out, not_483_out, not_484_out, not_485_out, not_486_out, F0, F1, not_487_out, not_488_out, not_489_out);
  and and_77 (and_77_out, not_490_out, not_491_out, not_492_out, not_493_out, not_494_out, F0, F1, F2, not_495_out, not_496_out);
  and and_78 (and_78_out, not_497_out, OP2, not_498_out, not_499_out, not_500_out);
  and and_79 (and_79_out, OP0, OP1, not_501_out, OP3, not_502_out, OP5);
  or or_1 (MemToReg, and_1_out, and_2_out);
  or or_2 (ALU_SRC, and_4_out, and_5_out, and_6_out, and_7_out, and_8_out, and_9_out, and_10_out, and_11_out, and_12_out);
  or or_3 (SignedExt, and_35_out, and_36_out, and_37_out, and_38_out, and_39_out);
  or or_4 (JUMP, and_55_out, and_56_out, and_57_out);
  or or_5 (R1Used, and_61_out, and_62_out, and_63_out, and_64_out, and_65_out, and_66_out, and_67_out, and_68_out, and_69_out, and_70_out, and_71_out);
  or or_6 (R2Used, and_72_out, and_73_out, and_74_out, and_75_out, and_76_out, and_77_out, and_78_out, and_79_out);
  or or_7 (RegWrite, and_13_out, and_14_out, and_15_out, and_16_out, and_17_out, and_18_out, and_19_out, and_20_out, and_21_out, and_22_out, and_23_out, and_24_out, and_25_out, and_26_out, and_27_out, and_28_out, and_29_out, and_30_out, and_31_out, and_32_out, and_33_out);
  or or_8 (RegDst, and_40_out, and_41_out, and_42_out, and_43_out, and_44_out, and_45_out, and_46_out, and_47_out, and_48_out, and_49_out, and_50_out, and_51_out);
endmodule

// ALU
module MIPS_ALU (
  input  [4:0] shamt,
  input  [31:0] X,
  input  [31:0] Y,
  input  [3:0] AluOP,
  output Equal,
  output [31:0] Result,
  output [31:0] Result_2
);

  wire [0:0] comparator_1_lt, comparator_2_lt;
  wire [31:0] adder_1_out, AND_out, divider_1_out, divider_1_rem, multiplier_1_cout, multiplier_1_out,
       NOR_out, OR_out, shifter_1_out, shifter_2_out, shifter_3_out, subtractor_1_out, XOR_out;

  assign AND_out = X & Y;  // AND_Gate AND, 32 bits wide
  assign OR_out = X | Y;  // OR_Gate OR, 32 bits wide
  Shifter #(.width(32)) shifter_1 (.in(Y), .\dist (shamt), .out(shifter_1_out));
  Shifter #(.width(32), .shift("ar")) shifter_2 (.in(Y), .\dist (shamt), .out(shifter_2_out));
  Shifter #(.width(32), .shift("lr")) shifter_3 (.in(Y), .\dist (shamt), .out(shifter_3_out));
  Multiplier #(.width(32)) multiplier_1 (.a(X), .b(Y), .out(multiplier_1_out), .cout(multiplier_1_cout));  // open: cin
  Divider #(.width(32)) divider_1 (.a(X), .b(Y), .out(divider_1_out), .rem(divider_1_rem));  // open: upper
  Adder #(.width(32)) adder_1 (.a(X), .b(Y), .out(adder_1_out));  // open: cin, cout
  Subtractor #(.width(32)) subtractor_1 (.a(X), .b(Y), .out(subtractor_1_out));  // open: bin, bout
  assign XOR_out = X ^ Y;  // XOR_Gate XOR, 32 bits wide
  assign NOR_out = ~(X | Y);  // NOR_Gate NOR, 32 bits wide
  Comparator #(.width(32)) comparator_1 (.a(X), .b(Y), .eq(Equal), .lt(comparator_1_lt[0]));  // open: gt
  Comparator #(.width(32), .mode("unsigned")) comparator_2 (.a(X), .b(Y), .lt(comparator_2_lt[0]));  // open: gt, eq
  Multiplexer #(.select(4), .width(32), .enable("false")) multiplexer_1 (
    .in0(shifter_1_out), .in1(shifter_2_out), .in2(shifter_3_out), .in3(multiplier_1_out),
    .in4(divider_1_out), .in5(adder_1_out), .in6(subtractor_1_out), .in7(AND_out), .in8(OR_out),
    .in9(XOR_out), .in10(NOR_out), .in11({{31{1'b0}}, comparator_1_lt[0]}),
    .in12({{31{1'b0}}, comparator_2_lt[0]}), .in13({32{1'b0}}), .in14({32{1'b0}}), .in15({32{1'b0}}),
    .out(Result), .sel(AluOP));
  Multiplexer #(.select(4), .width(32), .enable("false")) multiplexer_2 (
    .in0({32{1'b0}}), .in1({32{1'b0}}), .in2({32{1'b0}}), .in3(multiplier_1_cout), .in4(divider_1_rem),
    .in5({32{1'b0}}), .in6({32{1'b0}}), .in7({32{1'b0}}), .in8({32{1'b0}}), .in9({32{1'b0}}),
    .in10({32{1'b0}}), .in11({32{1'b0}}), .in12({32{1'b0}}), .in13({32{1'b0}}), .in14({32{1'b0}}),
    .in15({32{1'b0}}), .out(Result_2), .sel(AluOP));

  // Other names for the same wires on the sheet: Result2[31:0] = Result_2; S[3:0] = AluOP

  // Notes on the sheet:
  //   不要改变此引脚区域内容，也不要改变ALU封装形式
  //   输入引脚
  //   输出引脚
endmodule

module MIPS_Regifile (
  input  [31:0] Din,
  input  Clk,
  input  WE,
  input  [4:0] R1_num,
  input  [4:0] W_num,
  input  [4:0] R2_num,
  output [31:0] R1,
  output [31:0] R2
);

  // RegisterFile registerfile_1: pin names not known; wires that end beside it: Din, Clk, WE, W_num, R1_num, R2_num, R1, R2
endmodule

module \理想流水线  (
  output RegWrite,
  output MemWrite,
  output [31:0] IF_PC,
  output [31:0] ID_PC,
  output [31:0] EX_PC,
  output [31:0] M_PC,
  output [31:0] WB_PC,
  output [31:0] RDin,
  output [31:0] MDin,
  output [31:0] LedData
);

  wire and_1_out, and_2_out, and_3_out, and_4_out, and_5_out, and_6_out, and_7_out, Byte, CLK,
       comparator_1_eq, ex_mem_1_p12, ex_mem_1_p15, Go, id_ex_1_out_24, IR1, IR2, IR3, mem_wb_1_out_22,
       mips_alu_1_equal, not_1_out, not_2_out, not_3_out, not_4_out, not_5_out, or_1_out, register_5_q,
       register_6_q, RST, SignedExt, W1, W2, W3, \单周期硬布线控制器_1_blez , \单周期硬布线控制器_1_byte , \单周期硬布线控制器_1_jal ,
       \单周期硬布线控制器_1_jmp , \单周期硬布线控制器_1_jr , \单周期硬布线控制器_1_regdst ;
  wire [0:0] mem_wb_1_out_17;
  wire [1:0] bytePlace;
  wire [3:0] \单周期硬布线控制器_1_alu_op ;
  wire [4:0] multiplexer_4_out, multiplexer_5_out, multiplexer_6_out, multiplexer_7_out, W;
  wire [9:0] ex_mem_1_p11;
  wire [11:1] \单周期硬布线控制器_1_beq ;
  wire [15:0] id_ex_1_out_23, \LoadUse次数 , \总周期数 , \插入气泡数 , \无条件分支数 , \条件分支成功数 ;
  wire [16:0] id_ex_1_out_18;
  wire [27:26] if_id_1_out_8_2;
  wire [31:0] adder_1_out, adder_2_out, bit_extender_1_out, bit_extender_2_out, bit_extender_3_out,
       bit_extender_4_out, bit_extender_5_out, bit_extender_6_out, EX_IR, id_ex_1_out_21, id_ex_1_out_22,
       ID_IR, IF_IR, MEM_IR, mem_wb_1_out_18, mem_wb_1_out_19, mips_alu_1_result, mips_regifile_1_r1,
       mips_regifile_1_r2, multiplexer_1_out, multiplexer_2_out, multiplexer_3_out, multiplexer_9_out,
       multiplexer_10_out, multiplexer_11_out, multiplexer_13_out, OUT, ram_1_data, shifter_1_out, WB_IR;
  wire [31:2] ex_mem_1_p13, if_id_1_out_8;

  Button \u_总复位  (.out(RST));
  Button _1 (.out(IR1));
  Button _2 (.out(IR2));
  Button _3 (.out(IR3));
  // Probe on \总周期数 
  // Probe on \总周期数 
  Multiplexer #(.width(32), .enable("false")) multiplexer_1 (
    .in0(adder_1_out), .in1(adder_2_out), .out(multiplexer_1_out), .sel(or_1_out));
  Button \u_继续运行  (.out(Go));
  LED led_1 (.in(W1));
  LED led_2 (.in(W2));
  LED led_3 (.in(W3));
  Multiplexer #(.width(32), .enable("false")) multiplexer_2 (
    .in0(multiplexer_1_out), .in1({if_id_1_out_8, 2'b00}), .out(multiplexer_2_out), .sel(\单周期硬布线控制器_1_jmp ));
  Multiplexer #(.width(32), .enable("false")) multiplexer_3 (
    .in0(multiplexer_2_out), .in1(mips_regifile_1_r1), .out(multiplexer_3_out), .sel(\单周期硬布线控制器_1_jr ));
  Hex_Digit_Display hex_digit_display_1 (.value(LedData[31:28]));  // open: dp
  // Probe on IF_PC[19:0]
  // Mips_Probe mips_probe_1: pin names not known; wires that end beside it: IF_IR
  Register #(.width(32)) register_1 (.D(IF_IR), .Q(ID_IR), .clk(CLK));  // open: en, clr
  Register #(.width(32)) PC (.D(multiplexer_3_out), .en(not_1_out), .Q(IF_PC), .clk(CLK), .clr(RST));
  not not_1 (not_1_out, mem_wb_1_out_22);
  // Probe on multiplexer_3_out
  Hex_Digit_Display hex_digit_display_2 (.value(LedData[27:24]));  // open: dp
  Hex_Digit_Display hex_digit_display_3 (.value(LedData[23:20]));  // open: dp
  // Probe on ID_PC[19:0]
  // Mips_Probe mips_probe_2: pin names not known; wires that end beside it: ID_IR
  Counter #(.width(16), .max('hffff)) counter_1 (
    .count(not_1_out), .Q(\总周期数 ), .clk(CLK), .clr(RST));  // open: load, D, carry
  Hex_Digit_Display hex_digit_display_4 (.value(LedData[15:12]));  // open: dp
  Hex_Digit_Display hex_digit_display_5 (.value(LedData[19:16]));  // open: dp
  Register #(.width(32)) register_2 (.D(ID_IR), .Q(EX_IR), .clk(CLK));  // open: en, clr
  or or_1 (or_1_out, and_7_out, and_3_out, and_6_out);
  Adder #(.width(32)) adder_1 (.a(IF_PC), .b(32'h4), .out(adder_1_out));  // open: cin, cout
  Hex_Digit_Display hex_digit_display_6 (.value(LedData[11:8]));  // open: dp
  Hex_Digit_Display hex_digit_display_7 (.value(LedData[7:4]));  // open: dp
  Clock clock_1 (.out(CLK));
  // Probe on EX_PC[19:0]
  // Mips_Probe mips_probe_3: pin names not known; wires that end beside it: EX_IR
  ROM #(.addrWidth(10), .dataWidth(32)) rom_1 (.addr(IF_PC[11:2]), .data(IF_IR));  // open: sel
  Hex_Digit_Display hex_digit_display_8 (.value(LedData[3:0]));  // open: dp
  Register #(.width(32)) register_3 (.D(EX_IR), .Q(MEM_IR), .clk(CLK));  // open: en, clr
  // Probe on \总周期数 
  // Probe on M_PC[19:0]
  // Mips_Probe mips_probe_4: pin names not known; wires that end beside it: MEM_IR
  // Probe on {if_id_1_out_8[31:28], if_id_1_out_8_2, if_id_1_out_8[27:2]}
  IF_ID if_id_1 (
    .in_2(IF_IR), .in_3(adder_1_out), .out_8({if_id_1_out_8[31:28], if_id_1_out_8_2, if_id_1_out_8[27:2]}),
    .in_5(CLK), .in_7(RST), .\使能 (mem_wb_1_out_22), .in_4(1'b1), .in_6(1'b0));  // open: out_9, out_10
  // Probe on adder_1_out
  // Probe on \总周期数 
  // Probe on \无条件分支数 
  // Probe on \条件分支成功数 
  // Probe on \插入气泡数 
  // Probe on \LoadUse次数 
  Register #(.width(32)) register_4 (.D(MEM_IR), .Q(WB_IR), .clk(CLK));  // open: en, clr
  // Mips_Probe mips_probe_5: pin names not known; wires that end beside it: {if_id_1_out_8[31:28], if_id_1_out_8_2, if_id_1_out_8[27:2]}
  // Probe on IF_PC[11:0]
  // Probe on WB_PC[19:0]
  // Mips_Probe mips_probe_6: pin names not known; wires that end beside it: WB_IR
  // Probe on EX_PC[11:0]
  // Probe on ID_PC[11:0]
  // Probe on M_PC[11:0]
  \单周期硬布线控制器  \u_单周期硬布线控制器_1  (
    .Func(if_id_1_out_8[7:2]), .OP({if_id_1_out_8[31:28], if_id_1_out_8_2}), .ALU_OP(\单周期硬布线控制器_1_alu_op ),
    .MemToReg(\单周期硬布线控制器_1_beq [3]), .MemWrite(\单周期硬布线控制器_1_beq [4]), .ALU_SRC(\单周期硬布线控制器_1_beq [9]),
    .RegWrite(\单周期硬布线控制器_1_beq [10]), .SysCALL(\单周期硬布线控制器_1_beq [11]), .SignedExt(SignedExt),
    .RegDst(\单周期硬布线控制器_1_regdst ), .JR(\单周期硬布线控制器_1_jr ), .JMP(\单周期硬布线控制器_1_jmp ),
    .Beq(\单周期硬布线控制器_1_beq [1]), .JAL(\单周期硬布线控制器_1_jal ), .Bne(\单周期硬布线控制器_1_beq [2]),
    .BLEZ(\单周期硬布线控制器_1_blez ), .Byte(\单周期硬布线控制器_1_byte ));  // open: R1, R2
  Multiplexer #(.width(5), .enable("false")) multiplexer_4 (
    .in0(if_id_1_out_8[27:23]), .in1(5'b00010), .out(multiplexer_4_out), .sel(\单周期硬布线控制器_1_beq [11]));
  Multiplexer #(.width(5), .enable("false")) multiplexer_5 (
    .in0(if_id_1_out_8[22:18]), .in1(5'b00100), .out(multiplexer_5_out), .sel(\单周期硬布线控制器_1_beq [11]));
  Multiplexer #(.width(5), .enable("false")) multiplexer_6 (
    .in0(if_id_1_out_8[22:18]), .in1(if_id_1_out_8[17:13]), .out(multiplexer_6_out),
    .sel(\单周期硬布线控制器_1_regdst ));
  Multiplexer #(.width(5), .enable("false")) multiplexer_7 (
    .in0(multiplexer_6_out), .in1({5{1'b1}}), .out(multiplexer_7_out), .sel(\单周期硬布线控制器_1_jal ));
  // Probe on WB_PC[11:0]
  Multiplexer #(.width(32), .enable("false")) multiplexer_8 (
    .in0(multiplexer_9_out), .in1(OUT), .out(RDin), .sel(Byte));
  // Probe on mips_regifile_1_r1
  MIPS_Regifile mips_regifile_1 (
    .Din(RDin), .Clk(CLK), .R1(mips_regifile_1_r1), .R2(mips_regifile_1_r2), .WE(RegWrite), .W_num(W),
    .R1_num(multiplexer_4_out), .R2_num(multiplexer_5_out));
  // Probe on mips_regifile_1_r2
  Multiplexer #(.width(32), .enable("false")) multiplexer_9 (
    .in0(multiplexer_13_out), .in1(adder_1_out), .out(multiplexer_9_out), .sel(\单周期硬布线控制器_1_jal ));
  Shifter #(.width(32)) shifter_1 (.in(bit_extender_2_out), .\dist (5'b00010), .out(shifter_1_out));
  Adder #(.width(32)) adder_2 (.a(shifter_1_out), .b(adder_1_out), .out(adder_2_out));  // open: cin, cout
  Register #(.width(1)) register_5 (.D(\单周期硬布线控制器_1_blez ), .Q(register_5_q), .clk(CLK), .clr(RST));  // open: en
  Register #(.width(1)) register_6 (.D(\单周期硬布线控制器_1_byte ), .Q(register_6_q), .clk(CLK), .clr(RST));  // open: en
  ID_EX id_ex_1 (
    .in_5({multiplexer_7_out, \单周期硬布线控制器_1_beq [11:9], \单周期硬布线控制器_1_alu_op , \单周期硬布线控制器_1_beq [4:1], SignedExt}),
    .in_8(mips_regifile_1_r1), .in_9(mips_regifile_1_r2), .in_10(if_id_1_out_8[17:2]),
    .out_18(id_ex_1_out_18), .out_21(id_ex_1_out_21), .out_22(id_ex_1_out_22), .out_23(id_ex_1_out_23),
    .in_13(CLK), .\异步清零 (RST), .\锁定 (mem_wb_1_out_22), .in_11(1'b1), .out_24(id_ex_1_out_24), .\同步清零 (1'b0));  // open: in_6, in_7, out_19, out_20, in_3, out_16, in_2, out_15, in_4, out_17
  Register #(.width(32)) register_7 (.D(IF_PC), .Q(ID_PC), .clk(CLK));  // open: en, clr
  // Probe on id_ex_1_out_22
  Register #(.width(1)) register_8 (.D(register_6_q), .Q(Byte), .clk(CLK), .clr(RST));  // open: en
  // Probe on id_ex_1_out_18
  Multiplexer #(.width(32), .enable("false")) multiplexer_10 (
    .in0(id_ex_1_out_22), .in1(multiplexer_11_out), .out(multiplexer_10_out), .sel(id_ex_1_out_18[9]));
  assign bit_extender_1_out = {{16{1'b0}}, id_ex_1_out_23};  // Bit_Extender bit_extender_1
  assign bit_extender_2_out = {{16{id_ex_1_out_23[15]}}, id_ex_1_out_23};  // Bit_Extender bit_extender_2
  // Probe on id_ex_1_out_23
  Register #(.width(32)) register_9 (.D(ID_PC), .Q(EX_PC), .clk(CLK));  // open: en, clr
  not not_2 (not_2_out, comparator_1_eq);
  Comparator #(.width(32)) comparator_1 (.a(32'h22), .b(id_ex_1_out_21), .eq(comparator_1_eq));  // open: gt, lt
  // Probe on id_ex_1_out_21
  MIPS_ALU mips_alu_1 (
    .X(id_ex_1_out_21), .Y(multiplexer_10_out), .AluOP(id_ex_1_out_18[8:5]), .Equal(mips_alu_1_equal),
    .Result(mips_alu_1_result), .shamt(id_ex_1_out_23[10:6]));  // open: Result_2
  Multiplexer #(.width(32), .enable("false")) multiplexer_11 (
    .in0(bit_extender_1_out), .in1(bit_extender_2_out), .out(multiplexer_11_out), .sel(id_ex_1_out_18[0]));
  Register #(.width(32)) register_10 (.D(EX_PC), .Q(M_PC), .clk(CLK));  // open: en, clr
  and and_1 (and_1_out, id_ex_1_out_18[11], not_2_out);
  and and_2 (and_2_out, id_ex_1_out_18[11], comparator_1_eq);
  and and_3 (and_3_out, register_5_q, not_4_out);
  not not_3 (not_3_out, and_4_out);
  and and_4 (and_4_out, id_ex_1_out_24, ~mem_wb_1_out_22);  // AND_Gate
  Register #(.width(32)) register_11 (.D(id_ex_1_out_22), .en(and_2_out), .Q(LedData), .clk(CLK), .clr(RST));
  not not_4 (not_4_out, and_5_out);
  and and_5 (and_5_out, ~mips_alu_1_equal, ~mips_alu_1_result[0]);  // AND_Gate
  // EX_MEM ex_mem_1: pin names not known; wires that end beside it: {id_ex_1_out_18[16:12], id_ex_1_out_18[10], id_ex_1_out_18[4:1]}, mips_alu_1_equal, mips_alu_1_result, id_ex_1_out_22, and_1_out, id_ex_1_out_24, RST, 1'b0, not_3_out, CLK, {ex_mem_1_p11[9:4], MemWrite, ex_mem_1_p11[2:0]}, ex_mem_1_p12, {ex_mem_1_p13, bytePlace}, MDin, ex_mem_1_p15
  // Probe on MDin
  Register #(.width(32)) register_12 (.D(M_PC), .Q(WB_PC), .clk(CLK));  // open: en, clr
  // Probe on {ex_mem_1_p13, bytePlace}
  not not_5 (not_5_out, ex_mem_1_p12);
  Multiplexer #(.select(2), .width(32), .enable("false")) multiplexer_12 (
    .in0(bit_extender_3_out), .in1(bit_extender_4_out), .in2(bit_extender_5_out), .in3(bit_extender_6_out),
    .out(OUT), .sel(bytePlace));
  and and_6 (and_6_out, ex_mem_1_p12, ex_mem_1_p11[0]);
  and and_7 (and_7_out, not_5_out, ex_mem_1_p11[1]);
  RAM #(.addrWidth(10), .dataWidth(32), .bus("separate")) ram_1 (
    .addr(ex_mem_1_p13[11:2]), .din(MDin), .data(ram_1_data), .str(MemWrite), .clk(CLK), .clr(RST));  // open: sel, ld
  MEM_WB mem_wb_1 (
    .in_4({ex_mem_1_p11[9:4], ex_mem_1_p11[2]}), .in_5({ex_mem_1_p13, bytePlace}), .in_6(ram_1_data),
    .out_17({W, RegWrite, mem_wb_1_out_17[0]}), .out_18(mem_wb_1_out_18), .out_19(mem_wb_1_out_19),
    .in_12(CLK), .in_14(RST), .in_1(mem_wb_1_out_22), .in_9(ex_mem_1_p15), .out_22(mem_wb_1_out_22),
    .in_11(1'b1), .in_13(1'b0));  // open: out_23, in_7, out_20, in_8, out_21, in_10, in_2, out_15, in_3, out_16
  // Probe on mem_wb_1_out_19
  // Probe on mem_wb_1_out_18
  assign bit_extender_3_out = {{24{1'b0}}, ram_1_data[7:0]};  // Bit_Extender bit_extender_3
  assign bit_extender_4_out = {{24{1'b0}}, ram_1_data[15:8]};  // Bit_Extender bit_extender_4
  assign bit_extender_5_out = {{24{1'b0}}, ram_1_data[23:16]};  // Bit_Extender bit_extender_5
  assign bit_extender_6_out = {{24{1'b0}}, ram_1_data[31:24]};  // Bit_Extender bit_extender_6
  Multiplexer #(.width(32), .enable("false")) multiplexer_13 (
    .in0(mem_wb_1_out_18), .in1(mem_wb_1_out_19), .out(multiplexer_13_out), .sel(mem_wb_1_out_17[0]));

  // Other names for the same wires on the sheet: IR[31:0] = IF_IR; MEM_PC[31:0] = M_PC; PC[31:0] = IF_PC

  // Notes on the sheet:
  //   中断源
  //   时空图监测，可删除
  //   中断等待指示
  //   总复位信号应将除ROM以外所有存储组件全部清零
  //   数码管输出
  //   指令存储器
  //   contents of rom_1 (hex, n*v repeats v):
  //   20110001 8000c05 20110001 20120002 20130003 8000c09 20110001 20120002 20130003 8000c0d 20110001
  //   20120002 20130003 8000c11 20110001 20120002 20130003 c000cb8 20100001 20110001 118fc0 112020
  //   20020022 c 118882 12200001 8000c15 112020 20020022 c 20110001 118880 112020 20020022 c 12200001
  //   8000c1f 20110001 118fc0 112020 20020022 c 1188c3 112020 20020022 c 118903 112020 20020022 c 118903
  //   112020 20020022 c 118903 112020 20020022 c 118903 112020 20020022 c 118903 112020 20020022 c 118903
  //   112020 20020022 c 118903 112020 20020022 c 20100001 109fc0 139fc3 8021 2012000c 24160003 26100001
  //   3210000f 20080008 20090001 139900 2709825 132020 20020022 c 1094022 1500fff9 22100001 2018000f
  //   2188024 108700 20080008 20090001 139902 2709825 132021 20020022 c 1094022 1500fff9 108702 2c9b022
  //   12c00001 8000c50 4020 1084027 84400 3508ffff 82021 20020022 c 2010ffff 20110000 ae300000 22100001
  //   22310004 ae300000 22100001 22310004 ae300000 22100001 22310004 ae300000 22100001 22310004 ae300000
  //   22100001 22310004 ae300000 22100001 22310004 ae300000 22100001 22310004 ae300000 22100001 22310004
  //   ae300000 22100001 22310004 ae300000 22100001 22310004 ae300000 22100001 22310004 ae300000 22100001
  //   22310004 ae300000 22100001 22310004 ae300000 22100001 22310004 ae300000 22100001 22310004 ae300000
  //   22100001 22310004 22100001 8020 2011003c 8e130000 8e340000 274402a 11000002 ae330000 ae140000
  //   2231fffc 1611fff8 102020 20020022 c 22100004 2011003c 1611fff2 20020032 c 20100000 22100001 102020
  //   20020022 c 22100002 102020 20020022 c 22100003 102020 20020022 c 22100004 102020 20020022 c 22100005
  //   102020 20020022 c 22100006 102020 20020022 c 22100007 102020 20020022 c 22100008 102020 20020022
  //   20020022 c 3e00008
  //   数码管输出应该用寄存器锁存，否则显示数据只能一闪而过
  //   指令字
  //   OP
  //   Func
  //   rs
  //   rt
  //   rd
  //   JMP
  //   JR
  //   OP
  //   Func
  //   Syscall
  //   流水调试日志用
  //   Beq
  //   Bne
  //   MemToReg
  //   MemWrite
  //   AluOP
  //   AluSrcB
  //   RegWrite
  //   JAL
  //   RegDst
  //   Syscall
  //   为方便自动评测，需要输出流水线各段保存的PC值，注意是PC不是PC+4，另外ID段寄存器写入信息，Mem段内存写入信息也要输出
endmodule
module \气泡流水线  (
  output RegWrite,
  output MemWrite,
  output [31:0] IF_PC,
  output [31:0] ID_PC,
  output [31:0] EX_PC,
  output [31:0] M_PC,
  output [31:0] WB_PC,
  output [31:0] RDin,
  output [31:0] MDin,
  output [31:0] LedData
);

  wire and_1_out, and_2_out, and_11_out, and_12_out, and_13_out, and_14_out, and_15_out, and_16_out,
       and_17_out, and_18_out, and_19_out, and_20_out, and_21_out, and_22_out, Beq, Bne, Byte, CLK,
       comparator_1_eq, comparator_2_eq, comparator_3_eq, comparator_4_eq, comparator_5_eq, comparator_6_eq,
       comparator_8_eq, comparator_9_eq, comparator_10_eq, comparator_11_eq, comparator_12_eq,
       comparator_13_eq, comparator_14_eq, comparator_15_eq, comparator_17_eq, comparator_18_eq,
       comparator_19_eq, comparator_20_eq, comparator_21_eq, comparator_22_eq, comparator_23_eq,
       comparator_24_eq, comparator_25_eq, comparator_26_eq, comparator_27_eq, comparator_28_eq,
       comparator_29_eq, comparator_30_eq, comparator_31_eq, comparator_32_eq, comparator_33_eq,
       comparator_34_eq, comparator_35_eq, comparator_36_eq, comparator_37_eq, comparator_38_eq,
       comparator_39_eq, comparator_39_lt, ex_mem_1_p15, ex_mem_1_p16, ex_mem_1_p18, ex_mem_1_p23, Go,
       id_ex_1_out_24, IR1, IR2, IR3, J, Jal, Jout, Jr, JUMP, mem_wb_1_out_22, mips_alu_1_equal,
       multiplexer_12_out, multiplexer_13_out, multiplexer_16_out, multiplexer_17_out, multiplexer_18_out,
       multiplexer_19_out, multiplexer_20_out, multiplexer_21_out, not_1_out, not_2_out, not_3_out,
       not_4_out, not_5_out, not_6_out, not_7_out, not_8_out, not_9_out, not_10_out, not_11_out, not_12_out,
       not_13_out, not_14_out, not_15_out, not_16_out, not_17_out, not_18_out, or_1_out, or_2_out, or_3_out,
       or_4_out, or_5_out, or_6_out, or_7_out, or_8_out, or_9_out, or_10_out, or_11_out, or_12_out,
       or_13_out, or_15_out, register_1_q, register_2_q, register_4_q, RST, SignedExt, Stall, W1, W2, W3,
       \单周期硬布线控制器_1_blez , \单周期硬布线控制器_1_byte , \单周期硬布线控制器_1_jal , \单周期硬布线控制器_1_jmp , \单周期硬布线控制器_1_jr ,
       \单周期硬布线控制器_1_regdst ;
  wire [0:0] mem_wb_1_out_17;
  wire [1:0] and_3_out, and_6_out, bytePlace, comparator_7_eq, comparator_16_eq;
  wire [4:0] multiplexer_4_out, multiplexer_5_out, multiplexer_6_out, multiplexer_7_out, multiplexer_10_out,
       multiplexer_11_out, W;
  wire [9:0] ex_mem_1_p17;
  wire [11:1] \单周期硬布线控制器_1_beq ;
  wire [15:0] id_ex_1_out_23, \LoadUse次数 , \总周期数 , \插入气泡数 , \无条件分支数 , \条件分支成功数 ;
  wire [16:0] id_ex_1_out_18;
  wire [31:0] adder_1_out, adder_2_out, adder_3_out, adder_4_out, bit_extender_1_out, bit_extender_2_out,
       bit_extender_3_out, bit_extender_4_out, bit_extender_5_out, bit_extender_6_out, EX_IR, ex_mem_1_p20,
       id_ex_1_out_21, id_ex_1_out_22, ID_IR, ID_R1, IF_IR, MEM_IR, mem_wb_1_out_18, mem_wb_1_out_19,
       mips_alu_1_result, mips_regifile_1_r2, multiplexer_1_out, multiplexer_2_out, multiplexer_3_out,
       multiplexer_9_out, multiplexer_14_out, multiplexer_15_out, multiplexer_23_out, OUT, ram_1_data,
       register_3_q, shifter_1_out, WB_IR;

  Button \u_总复位  (.out(RST));
  Button _1 (.out(IR1));
  Button _2 (.out(IR2));
  Button _3 (.out(IR3));
  // Probe on \总周期数 
  // Probe on \总周期数 
  Clock clock_1 (.out(CLK));
  Button \u_继续运行  (.out(Go));
  LED led_1 (.in(W1));
  LED led_2 (.in(W2));
  LED led_3 (.in(W3));
  Comparator #(.width(16), .mode("unsigned")) comparator_1 (
    .a(\总周期数 ), .b(16'h9b), .eq(comparator_1_eq));  // open: gt, lt
  Multiplexer #(.width(32), .enable("false")) multiplexer_1 (
    .in0(adder_1_out), .in1(adder_4_out), .out(multiplexer_1_out), .sel(or_6_out));
  Multiplexer #(.width(32), .enable("false")) multiplexer_2 (
    .in0(register_3_q), .in1(id_ex_1_out_21), .out(multiplexer_2_out), .sel(Jr));
  Hex_Digit_Display hex_digit_display_1 (.value(LedData[31:28]));  // open: dp
  // Probe on IF_PC[19:0]
  // Mips_Probe mips_probe_1: pin names not known; wires that end beside it: comparator_1_eq, CLK, IF_IR
  // Probe on ID_IR
  // Probe on RDin
  not not_1 (not_1_out, mem_wb_1_out_22);
  Multiplexer #(.width(32), .enable("false")) multiplexer_3 (
    .in0(multiplexer_1_out), .in1(multiplexer_2_out), .out(multiplexer_3_out), .sel(J));
  not not_2 (not_2_out, or_1_out);
  or or_1 (or_1_out, Stall, mem_wb_1_out_22);
  Hex_Digit_Display hex_digit_display_2 (.value(LedData[27:24]));  // open: dp
  Hex_Digit_Display hex_digit_display_3 (.value(LedData[23:20]));  // open: dp
  // Probe on ID_PC[19:0]
  // Mips_Probe mips_probe_2: pin names not known; wires that end beside it: ID_IR
  Register #(.width(32)) PC (.D(multiplexer_3_out), .en(not_2_out), .Q(IF_PC), .clk(CLK), .clr(RST));
  Hex_Digit_Display hex_digit_display_4 (.value(LedData[15:12]));  // open: dp
  Hex_Digit_Display hex_digit_display_5 (.value(LedData[19:16]));  // open: dp
  LED led_4 (.in(Stall));
  Counter #(.width(16), .max('hffff)) counter_1 (
    .count(not_1_out), .Q(\总周期数 ), .clk(CLK), .clr(RST));  // open: load, D, carry
  Hex_Digit_Display hex_digit_display_6 (.value(LedData[11:8]));  // open: dp
  Hex_Digit_Display hex_digit_display_7 (.value(LedData[7:4]));  // open: dp
  // Probe on EX_PC[19:0]
  // Mips_Probe mips_probe_3: pin names not known; wires that end beside it: EX_IR
  // Probe on bytePlace
  ROM #(.addrWidth(10), .dataWidth(32)) rom_1 (.addr(IF_PC[11:2]), .data(IF_IR));  // open: sel
  Adder #(.width(32)) adder_1 (.a(IF_PC), .b(32'h4), .out(adder_1_out));  // open: cin, cout
  Hex_Digit_Display hex_digit_display_8 (.value(LedData[3:0]));  // open: dp
  // Probe on \总周期数 
  // Probe on M_PC[19:0]
  // Mips_Probe mips_probe_4: pin names not known; wires that end beside it: MEM_IR
  Counter #(.width(16), .max('hffff), .ongoal("stay")) counter_2 (
    .Q(\插入气泡数 ), .clk(Stall));  // open: load, D, count, carry, clr
  IF_ID if_id_1 (
    .in_2(IF_IR), .in_3(IF_PC), .out_8(ID_IR), .out_9(ID_PC), .in_5(CLK), .in_7(RST), .\使能 (or_1_out),
    .in_4(1'b1), .in_6(JUMP));  // open: out_10
  // Probe on \总周期数 
  // Probe on \无条件分支数 
  // Probe on \条件分支成功数 
  // Probe on \插入气泡数 
  // Probe on \LoadUse次数 
  // Probe on ID_IR
  // Probe on IF_PC[11:0]
  // Probe on WB_PC[19:0]
  // Mips_Probe mips_probe_5: pin names not known; wires that end beside it: WB_IR
  // Mips_Probe mips_probe_6: pin names not known; wires that end beside it: ID_IR
  Adder #(.width(32)) adder_2 (.a(EX_PC), .b(32'h4), .out(adder_2_out));  // open: cin, cout
  // Probe on ID_PC[11:0]
  // Probe on EX_PC[11:0]
  // Probe on M_PC[11:0]
  \单周期硬布线控制器  \u_单周期硬布线控制器_1  (
    .Func(ID_IR[5:0]), .OP(ID_IR[31:26]), .ALU_OP(\单周期硬布线控制器_1_beq [8:5]), .MemToReg(\单周期硬布线控制器_1_beq [3]),
    .MemWrite(\单周期硬布线控制器_1_beq [4]), .ALU_SRC(\单周期硬布线控制器_1_beq [9]), .RegWrite(\单周期硬布线控制器_1_beq [10]),
    .SysCALL(\单周期硬布线控制器_1_beq [11]), .SignedExt(SignedExt), .RegDst(\单周期硬布线控制器_1_regdst ),
    .JR(\单周期硬布线控制器_1_jr ), .JMP(\单周期硬布线控制器_1_jmp ), .Beq(\单周期硬布线控制器_1_beq [1]), .JAL(\单周期硬布线控制器_1_jal ),
    .Bne(\单周期硬布线控制器_1_beq [2]), .BLEZ(\单周期硬布线控制器_1_blez ), .Byte(\单周期硬布线控制器_1_byte ));  // open: R1, R2
  Multiplexer #(.width(5), .enable("false")) multiplexer_4 (
    .in0(ID_IR[25:21]), .in1(5'b00010), .out(multiplexer_4_out), .sel(\单周期硬布线控制器_1_beq [11]));
  Multiplexer #(.width(5), .enable("false")) multiplexer_5 (
    .in0(ID_IR[20:16]), .in1(5'b00100), .out(multiplexer_5_out), .sel(\单周期硬布线控制器_1_beq [11]));
  Multiplexer #(.width(5), .enable("false")) multiplexer_6 (
    .in0(ID_IR[20:16]), .in1(ID_IR[15:11]), .out(multiplexer_6_out), .sel(\单周期硬布线控制器_1_regdst ));
  Adder #(.width(32)) adder_3 (.a(WB_PC), .b(32'h4), .out(adder_3_out));  // open: cin, cout
  Comparator #(.width(6)) comparator_2 (.a(ID_IR[31:26]), .b({6{1'b0}}), .eq(comparator_2_eq));  // open: gt, lt
  Comparator #(.width(6)) comparator_3 (.a(ID_IR[31:26]), .b(6'b000010), .eq(comparator_3_eq));  // open: gt, lt
  Comparator #(.width(6)) comparator_4 (.a(ID_IR[31:26]), .b(6'b000011), .eq(comparator_4_eq));  // open: gt, lt
  Comparator #(.width(6)) comparator_5 (.a(ID_IR[31:26]), .b({6{1'b0}}), .eq(comparator_5_eq));  // open: gt, lt
  Comparator #(.width(26)) comparator_6 (.a(ID_IR[25:0]), .b(26'hc), .eq(comparator_6_eq));  // open: gt, lt
  Comparator #(.width(6)) comparator_7 (.a(EX_IR[31:26]), .b({6{1'b0}}), .eq(comparator_7_eq[0]));  // open: gt, lt
  Comparator #(.width(6)) comparator_8 (.a(EX_IR[31:26]), .b(6'b000010), .eq(comparator_8_eq));  // open: gt, lt
  Comparator #(.width(6)) comparator_9 (.a(EX_IR[31:26]), .b(6'b000011), .eq(comparator_9_eq));  // open: gt, lt
  Comparator #(.width(6)) comparator_10 (.a(EX_IR[31:26]), .b(6'b101011), .eq(comparator_10_eq));  // open: gt, lt
  Comparator #(.width(6)) comparator_11 (.a(ID_IR[31:26]), .b({6{1'b0}}), .eq(comparator_11_eq));  // open: gt, lt
  Comparator #(.width(6)) comparator_12 (.a(ID_IR[31:26]), .b(6'b000010), .eq(comparator_12_eq));  // open: gt, lt
  Comparator #(.width(6)) comparator_13 (.a(ID_IR[31:26]), .b(6'b000011), .eq(comparator_13_eq));  // open: gt, lt
  Comparator #(.width(6)) comparator_14 (.a(ID_IR[31:26]), .b({6{1'b0}}), .eq(comparator_14_eq));  // open: gt, lt
  Comparator #(.width(26)) comparator_15 (.a(ID_IR[25:0]), .b(26'hc), .eq(comparator_15_eq));  // open: gt, lt
  Comparator #(.width(6)) comparator_16 (.a(MEM_IR[31:26]), .b({6{1'b0}}), .eq(comparator_16_eq[0]));  // open: gt, lt
  Comparator #(.width(6)) comparator_17 (.a(MEM_IR[31:26]), .b(6'b000010), .eq(comparator_17_eq));  // open: gt, lt
  Comparator #(.width(6)) comparator_18 (.a(MEM_IR[31:26]), .b(6'b000011), .eq(comparator_18_eq));  // open: gt, lt
  Comparator #(.width(6)) comparator_19 (.a(MEM_IR[31:26]), .b(6'b101011), .eq(comparator_19_eq));  // open: gt, lt
  // Probe on WB_PC[11:0]
  Multiplexer #(.width(5), .enable("false")) multiplexer_7 (
    .in0(multiplexer_6_out), .in1({5{1'b1}}), .out(multiplexer_7_out), .sel(\单周期硬布线控制器_1_jal ));
  Multiplexer #(.width(32), .enable("false")) multiplexer_8 (
    .in0(multiplexer_9_out), .in1(OUT), .out(RDin), .sel(Byte));
  not not_3 (not_3_out, comparator_2_eq);
  not not_4 (not_4_out, comparator_3_eq);
  not not_5 (not_5_out, comparator_4_eq);
  and and_1 (and_1_out, comparator_5_eq, comparator_6_eq);
  not not_6 (not_6_out, comparator_7_eq[0]);
  not not_7 (not_7_out, comparator_8_eq);
  not not_8 (not_8_out, comparator_9_eq);
  not not_9 (not_9_out, comparator_11_eq);
  not not_10 (not_10_out, comparator_12_eq);
  not not_11 (not_11_out, comparator_13_eq);
  and and_2 (and_2_out, comparator_14_eq, comparator_15_eq);
  not not_12 (not_12_out, comparator_16_eq[0]);
  not not_13 (not_13_out, comparator_17_eq);
  not not_14 (not_14_out, comparator_18_eq);
  Multiplexer #(.width(32), .enable("false")) multiplexer_9 (
    .in0(multiplexer_23_out), .in1(adder_3_out), .out(multiplexer_9_out), .sel(Jout));
  Shifter #(.width(32)) shifter_1 (.in(bit_extender_2_out), .\dist (5'b00010), .out(shifter_1_out));
  and and_3 (and_3_out[0], comparator_2_eq, ~and_1_out);  // AND_Gate
  or or_2 (or_2_out, comparator_3_eq, comparator_4_eq, and_1_out);
  and and_4 (and_3_out[1], not_3_out, not_4_out, not_5_out);
  or or_3 (or_3_out, comparator_8_eq, comparator_9_eq);
  and and_5 (comparator_7_eq[1], not_6_out, not_7_out, not_8_out);
  and and_6 (and_6_out[0], comparator_11_eq, ~and_2_out);  // AND_Gate
  or or_4 (or_4_out, comparator_12_eq, comparator_13_eq, and_2_out);
  and and_7 (and_6_out[1], not_9_out, not_10_out, not_11_out);
  or or_5 (or_5_out, comparator_17_eq, comparator_18_eq);
  and and_8 (comparator_16_eq[1], not_12_out, not_13_out, not_14_out);
  or or_6 (or_6_out, Bne, and_16_out, Beq);
  MIPS_Regifile mips_regifile_1 (
    .Din(RDin), .Clk(CLK), .R1(ID_R1), .R2(mips_regifile_1_r2), .WE(RegWrite), .W_num(W),
    .R1_num(multiplexer_4_out), .R2_num(multiplexer_5_out));
  Adder #(.width(32)) adder_4 (.a(shifter_1_out), .b(adder_2_out), .out(adder_4_out));  // open: cin, cout
  Multiplexer #(.select(2), .width(5), .enable("false")) multiplexer_10 (
    .in0({5{1'b0}}), .in1(EX_IR[15:11]), .in2(EX_IR[20:16]), .in3({5{1'b0}}), .out(multiplexer_10_out),
    .sel(comparator_7_eq));
  Multiplexer #(.select(2), .width(5), .enable("false")) multiplexer_11 (
    .in0({5{1'b0}}), .in1(MEM_IR[15:11]), .in2(MEM_IR[20:16]), .in3({5{1'b0}}), .out(multiplexer_11_out),
    .sel(comparator_16_eq));
  Register #(.width(1)) register_1 (.D(\单周期硬布线控制器_1_blez ), .Q(register_1_q), .clk(CLK), .clr(RST));  // open: en
  Register #(.width(1)) register_2 (.D(\单周期硬布线控制器_1_byte ), .Q(register_2_q), .clk(CLK), .clr(RST));  // open: en
  ID_EX id_ex_1 (
    .in_5({multiplexer_7_out, \单周期硬布线控制器_1_beq , SignedExt}), .in_6(ID_IR), .in_7(ID_PC), .in_8(ID_R1),
    .in_9(mips_regifile_1_r2), .in_10(ID_IR[15:0]), .out_18(id_ex_1_out_18), .out_19(EX_IR), .out_20(EX_PC),
    .out_21(id_ex_1_out_21), .out_22(id_ex_1_out_22), .out_23(id_ex_1_out_23), .in_13(CLK), .\异步清零 (RST),
    .\锁定 (mem_wb_1_out_22), .in_11(1'b1), .out_24(id_ex_1_out_24), .\同步清零 (or_7_out),
    .in_3(\单周期硬布线控制器_1_jal ), .out_16(Jal), .in_2(\单周期硬布线控制器_1_jmp ), .out_15(J), .in_4(\单周期硬布线控制器_1_jr ),
    .out_17(Jr));
  Register #(.width(32)) register_3 (
    .D({ID_IR[31:28], ID_IR[25:0], 2'b00}), .Q(register_3_q), .clk(CLK));  // open: en, clr
  or or_7 (or_7_out, JUMP, Stall);
  and and_9 (Bne, id_ex_1_out_18[2], ~mips_alu_1_equal);  // AND_Gate
  assign bit_extender_1_out = {{16{1'b0}}, id_ex_1_out_23};  // Bit_Extender bit_extender_1
  assign bit_extender_2_out = {{16{id_ex_1_out_23[15]}}, id_ex_1_out_23};  // Bit_Extender bit_extender_2
  Comparator #(.width(5)) comparator_20 (.a({5{1'b0}}), .b(ID_IR[20:16]), .eq(comparator_20_eq));  // open: gt, lt
  Comparator #(.width(5)) comparator_21 (
    .a(ID_IR[20:16]), .b(multiplexer_10_out), .eq(comparator_21_eq));  // open: gt, lt
  Multiplexer #(.enable("false")) multiplexer_12 (
    .in0(comparator_21_eq), .in1(1'b0), .out(multiplexer_12_out), .sel(comparator_20_eq));
  Comparator #(.width(5)) comparator_22 (.a({5{1'b0}}), .b(ID_IR[25:21]), .eq(comparator_22_eq));  // open: gt, lt
  Comparator #(.width(5)) comparator_23 (
    .a(ID_IR[25:21]), .b(multiplexer_10_out), .eq(comparator_23_eq));  // open: gt, lt
  Multiplexer #(.enable("false")) multiplexer_13 (
    .in0(comparator_23_eq), .in1(1'b0), .out(multiplexer_13_out), .sel(comparator_22_eq));
  Comparator #(.width(5)) comparator_24 (.a(multiplexer_10_out), .b(5'b00010), .eq(comparator_24_eq));  // open: gt, lt
  or or_8 (or_8_out, comparator_24_eq, comparator_25_eq);
  Comparator #(.width(5)) comparator_25 (.a(multiplexer_10_out), .b(5'b00100), .eq(comparator_25_eq));  // open: gt, lt
  Comparator #(.width(5)) comparator_26 (.a({5{1'b0}}), .b(ID_IR[20:16]), .eq(comparator_26_eq));  // open: gt, lt
  Comparator #(.width(5)) comparator_27 (
    .a(ID_IR[20:16]), .b(multiplexer_11_out), .eq(comparator_27_eq));  // open: gt, lt
  Comparator #(.width(5)) comparator_28 (.a({5{1'b0}}), .b(ID_IR[25:21]), .eq(comparator_28_eq));  // open: gt, lt
  Comparator #(.width(5)) comparator_29 (
    .a(ID_IR[25:21]), .b(multiplexer_11_out), .eq(comparator_29_eq));  // open: gt, lt
  Comparator #(.width(5)) comparator_30 (.a(multiplexer_11_out), .b(5'b00010), .eq(comparator_30_eq));  // open: gt, lt
  or or_9 (or_9_out, comparator_30_eq, comparator_31_eq);
  Comparator #(.width(5)) comparator_31 (.a(multiplexer_11_out), .b(5'b00100), .eq(comparator_31_eq));  // open: gt, lt
  Register #(.width(1)) register_4 (.D(register_2_q), .Q(register_4_q), .clk(CLK), .clr(RST));  // open: en
  Register #(.width(1)) register_5 (.D(register_4_q), .Q(Byte), .clk(CLK), .clr(RST));  // open: en
  Comparator #(.width(32)) comparator_32 (.a(32'h22), .b(id_ex_1_out_21), .eq(comparator_32_eq));  // open: gt, lt
  and and_10 (Beq, id_ex_1_out_18[1], mips_alu_1_equal);
  Multiplexer #(.width(32), .enable("false")) multiplexer_14 (
    .in0(id_ex_1_out_22), .in1(multiplexer_15_out), .out(multiplexer_14_out), .sel(id_ex_1_out_18[9]));
  Multiplexer #(.width(32), .enable("false")) multiplexer_15 (
    .in0(bit_extender_1_out), .in1(bit_extender_2_out), .out(multiplexer_15_out), .sel(id_ex_1_out_18[0]));
  Comparator #(.width(6)) comparator_33 (.a(ID_IR[31:26]), .b(6'b101011), .eq(comparator_33_eq));  // open: gt, lt
  Comparator #(.width(6)) comparator_34 (.a(ID_IR[31:26]), .b(6'b000100), .eq(comparator_34_eq));  // open: gt, lt
  Comparator #(.width(6)) comparator_35 (.a(6'b000101), .b(ID_IR[31:26]), .eq(comparator_35_eq));  // open: gt, lt
  or or_10 (or_10_out, multiplexer_12_out, multiplexer_13_out);
  and and_11 (and_11_out, or_8_out, and_1_out);
  Comparator #(.width(6)) comparator_36 (.a(ID_IR[31:26]), .b(6'b101011), .eq(comparator_36_eq));  // open: gt, lt
  Comparator #(.width(6)) comparator_37 (.a(ID_IR[31:26]), .b(6'b000100), .eq(comparator_37_eq));  // open: gt, lt
  Comparator #(.width(6)) comparator_38 (.a(6'b000101), .b(ID_IR[31:26]), .eq(comparator_38_eq));  // open: gt, lt
  Multiplexer #(.enable("false")) multiplexer_16 (
    .in0(comparator_27_eq), .in1(1'b0), .out(multiplexer_16_out), .sel(comparator_26_eq));
  or or_11 (or_11_out, multiplexer_16_out, multiplexer_17_out);
  Multiplexer #(.enable("false")) multiplexer_17 (
    .in0(comparator_29_eq), .in1(1'b0), .out(multiplexer_17_out), .sel(comparator_28_eq));
  and and_12 (and_12_out, or_9_out, and_2_out);
  and and_13 (and_13_out, id_ex_1_out_18[11], not_15_out);
  not not_15 (not_15_out, comparator_32_eq);
  and and_14 (and_14_out, id_ex_1_out_18[11], comparator_32_eq);
  MIPS_ALU mips_alu_1 (
    .X(id_ex_1_out_21), .Y(multiplexer_14_out), .AluOP(id_ex_1_out_18[8:5]), .Equal(mips_alu_1_equal),
    .Result(mips_alu_1_result), .shamt(id_ex_1_out_23[10:6]));  // open: Result_2
  not not_16 (not_16_out, and_15_out);
  and and_15 (and_15_out, id_ex_1_out_24, ~mem_wb_1_out_22);  // AND_Gate
  or or_12 (or_12_out, comparator_35_eq, comparator_34_eq, comparator_33_eq);
  Multiplexer #(.enable("false")) multiplexer_18 (
    .in0(multiplexer_13_out), .in1(or_10_out), .out(multiplexer_18_out), .sel(or_12_out));
  or or_13 (or_13_out, comparator_38_eq, comparator_37_eq, comparator_36_eq);
  Multiplexer #(.enable("false")) multiplexer_19 (
    .in0(multiplexer_17_out), .in1(or_11_out), .out(multiplexer_19_out), .sel(or_13_out));
  Register #(.width(32)) register_6 (.D(id_ex_1_out_22), .en(and_14_out), .Q(LedData), .clk(CLK), .clr(RST));
  and and_16 (and_16_out, and_18_out, not_17_out);
  and and_17 (and_17_out, ~mips_alu_1_equal, ~mips_alu_1_result[0]);  // AND_Gate
  not not_17 (not_17_out, and_17_out);
  // EX_MEM ex_mem_1: pin names not known; wires that end beside it: J, Jal, {id_ex_1_out_18[16:12], id_ex_1_out_18[10], id_ex_1_out_18[4:1]}, mips_alu_1_equal, EX_PC, mips_alu_1_result, EX_IR, id_ex_1_out_22, and_13_out, id_ex_1_out_24, RST, 1'b0, not_16_out, CLK, ex_mem_1_p15, ex_mem_1_p16, {ex_mem_1_p17[9:4], MemWrite, ex_mem_1_p17[2:0]}, ex_mem_1_p18, M_PC, ex_mem_1_p20, MEM_IR, MDin, ex_mem_1_p23
  Multiplexer #(.select(2), .enable("false")) multiplexer_20 (
    .in0(1'b0), .in1(or_10_out), .in2(multiplexer_18_out), .in3(1'b0), .out(multiplexer_20_out),
    .sel(and_3_out));
  Multiplexer #(.select(2), .enable("false")) multiplexer_21 (
    .in0(1'b0), .in1(or_11_out), .in2(multiplexer_19_out), .in3(1'b0), .out(multiplexer_21_out),
    .sel(and_6_out));
  and and_18 (and_18_out, register_1_q, or_15_out);
  and and_19 (and_19_out, multiplexer_20_out, ~comparator_10_eq);  // AND_Gate
  and and_20 (and_20_out, multiplexer_21_out, ~comparator_19_eq);  // AND_Gate
  or or_14 (JUMP, Beq, Bne, Jal, J);
  or or_15 (or_15_out, comparator_39_lt, comparator_39_eq);
  Comparator #(.width(32)) comparator_39 (
    .a(ID_R1), .b({32{1'b0}}), .eq(comparator_39_eq), .lt(comparator_39_lt));  // open: gt
  // Probe on ID_R1
  // OR_Gate or_16 has open pins: in0=and_22_out, in1=and_21_out, out=open
  not not_18 (not_18_out, ex_mem_1_p18);
  or or_17 (Stall, and_19_out, and_11_out, and_20_out, and_12_out);
  and and_21 (and_21_out, ex_mem_1_p18, ex_mem_1_p17[0]);
  and and_22 (and_22_out, not_18_out, ex_mem_1_p17[1]);
  // Probe on ex_mem_1_p20
  RAM #(.addrWidth(10), .dataWidth(32), .bus("separate")) ram_1 (
    .addr(ex_mem_1_p20[11:2]), .din(MDin), .data(ram_1_data), .str(MemWrite), .clk(CLK), .clr(RST));  // open: sel, ld
  Multiplexer #(.select(2), .width(32), .enable("false")) multiplexer_22 (
    .in0(bit_extender_3_out), .in1(bit_extender_4_out), .in2(bit_extender_5_out), .in3(bit_extender_6_out),
    .out(OUT), .sel(bytePlace));
  Register #(.width(2)) register_7 (.D(ex_mem_1_p20[1:0]), .Q(bytePlace), .clk(CLK), .clr(RST));  // open: en
  MEM_WB mem_wb_1 (
    .in_4({ex_mem_1_p17[9:4], ex_mem_1_p17[2]}), .in_5(ex_mem_1_p20), .in_6(ram_1_data),
    .out_17({W, RegWrite, mem_wb_1_out_17[0]}), .out_18(mem_wb_1_out_18), .out_19(mem_wb_1_out_19),
    .in_12(CLK), .in_14(RST), .in_1(mem_wb_1_out_22), .in_9(ex_mem_1_p23), .out_22(mem_wb_1_out_22),
    .in_11(1'b1), .in_7(M_PC), .out_20(WB_PC), .in_8(MEM_IR), .out_21(WB_IR), .in_10(Go), .in_13(1'b0),
    .in_2(ex_mem_1_p15), .in_3(ex_mem_1_p16), .out_16(Jout));  // open: out_23, out_15
  Multiplexer #(.width(32), .enable("false")) multiplexer_23 (
    .in0(mem_wb_1_out_18), .in1(mem_wb_1_out_19), .out(multiplexer_23_out), .sel(mem_wb_1_out_17[0]));
  // Probe on mem_wb_1_out_18
  assign bit_extender_3_out = {{24{1'b0}}, mem_wb_1_out_19[7:0]};  // Bit_Extender bit_extender_3
  assign bit_extender_4_out = {{24{1'b0}}, mem_wb_1_out_19[15:8]};  // Bit_Extender bit_extender_4
  assign bit_extender_5_out = {{24{1'b0}}, mem_wb_1_out_19[23:16]};  // Bit_Extender bit_extender_5
  assign bit_extender_6_out = {{24{1'b0}}, mem_wb_1_out_19[31:24]};  // Bit_Extender bit_extender_6

  // Other names for the same wires on the sheet: IR_NOW[31:0] = ID_IR; IR[31:0] = IF_IR; IR_NEXT[31:0] = EX_IR;
  //   MEM_NOW[31:0] = MEM_IR; MEM_PC[31:0] = M_PC; PC[31:0] = IF_PC

  // Notes on the sheet:
  //   中断源
  //   时空图监测，可删除
  //   中断等待指示
  //   数码管输出
  //   指令存储器
  //   contents of rom_1 (hex, n*v repeats v):
  //   2011fff1 112020 20020022 c 22310001 1a20fffb 2002000a c
  //   OP
  //   Func
  //   rs
  //   指令字
  //   rt
  //   rd
  //   JMP
  //   JR
  //   OP
  //   Func
  //   Syscall
  //   rd
  //   rt
  //   rd
  //   rt
  //   流水调试日志用
  //   Beq
  //   Bne
  //   MemToReg
  //   MemWrite
  //   AluOP
  //   AluSrcB
  //   RegWrite
  //   JAL
  //   RegDst
  //   R?
  //   j?
  //   jal?
  //   Syscall
  //   R?
  //   j?
  //   jal?
  //   sw?
  //   R?
  //   j?
  //   jal?
  //   R?
  //   j?
  //   jal?
  //   Syscall
  //   J?
  //   I?
  //   rt
  //   J?
  //   I?
  //   J?
  //   I?
  //   J?
  //   I?
  //   rs
  //   v0
  //   a0
  //   rt
  //   rs
  //   v0
  //   a0
  //   Syscall
  //   sw
  //   beq
  //   bne
  //   sw
  //   beq
  //   bne
  //   为方便自动评测，需要输出流水线各段保存的PC值，注意是PC不是PC+4，另外ID段寄存器写入信息，Mem段内存写入信息也要输出
endmodule

module \重定向流水线  (
  output RegWrite,
  output MemWrite,
  output [31:0] IF_PC,
  output [31:0] ID_PC,
  output [31:0] EX_PC,
  output [31:0] M_PC,
  output [31:0] WB_PC,
  output [31:0] RDin,
  output [31:0] MDin,
  output [31:0] LedData
);

  wire and_1_out, and_2_out, and_9_out, and_10_out, and_11_out, and_12_out, and_13_out, and_14_out,
       and_15_out, and_16_out, and_17_out, Beq, Bne, Byte, CLK, comparator_1_eq, comparator_2_eq,
       comparator_3_eq, comparator_4_eq, comparator_5_eq, comparator_6_eq, comparator_7_eq, comparator_8_eq,
       comparator_9_eq, comparator_10_eq, comparator_11_eq, comparator_12_eq, comparator_13_eq,
       comparator_14_eq, comparator_15_eq, comparator_16_eq, comparator_17_eq, comparator_18_eq,
       comparator_19_eq, ex_mem_1_p15, ex_mem_1_p16, ex_mem_1_p18, ex_mem_1_p23, EX_MEMTOREG, EX_R1Used,
       EX_R2Used, Go, id_ex_1_out_24, ID_R1Used, ID_R2Used, IR1, IR2, IR3, J, Jal, Jout, Jr, JUMP, LoadUse,
       MEM_REGWRITE, mem_wb_1_out_22, mips_alu_1_equal, mips_probe_6_p1, multiplexer_14_out,
       multiplexer_15_out, not_1_out, not_2_out, not_3_out, not_4_out, not_5_out, not_6_out, or_2_out,
       or_3_out, register_1_q, register_2_q, RST, SignedExt, W1, W2, W3, \单周期硬布线控制器_1_blez ,
       \单周期硬布线控制器_1_byte , \单周期硬布线控制器_1_jal , \单周期硬布线控制器_1_jr , \单周期硬布线控制器_1_regdst ;
  wire [0:0] mem_wb_1_out_17;
  wire [1:0] bytePlace, SignalR1, SignalR2;
  wire [2:0] ex_mem_1_p17;
  wire [3:0] \单周期硬布线控制器_1_alu_op ;
  wire [4:0] EX_R1_num, EX_R2_num, EX_RD, ID_R1_num, ID_R2_num, MEM_RD, multiplexer_8_out, multiplexer_9_out,
       multiplexer_12_out, multiplexer_13_out, W;
  wire [7:0] ram_1_data, ram_1_data_2, ram_1_data_3, ram_1_data_4;
  wire [11:0] id_ex_1_out_18;
  wire [11:1] \单周期硬布线控制器_1_beq ;
  wire [15:0] id_ex_1_out_23, \LoadUse次数 , \总周期数 , \插入气泡数 , \无条件分支数 , \条件分支成功数 ;
  wire [31:0] adder_1_out, adder_2_out, adder_3_out, adder_4_out, bit_extender_1_out, bit_extender_2_out,
       bit_extender_3_out, bit_extender_4_out, bit_extender_5_out, bit_extender_6_out, EX_IR, EX_R1, EX_R2,
       ID_IR, IF_IR, MEM_IR, mem_wb_1_out_19, mips_alu_1_result, mips_regifile_1_r1, mips_regifile_1_r2,
       multiplexer_1_out, multiplexer_2_out, multiplexer_3_out, multiplexer_11_out, multiplexer_16_out,
       multiplexer_17_out, OUT, R1, R2, register_8_q, shifter_1_out, WB_ALURes, WB_IR, WB_ReadData;
  wire [31:2] MEM_ALURes;

  Button \u_总复位  (.out(RST));
  Button _1 (.out(IR1));
  Button _2 (.out(IR2));
  Button _3 (.out(IR3));
  // Probe on \总周期数 
  // Probe on \总周期数 
  Button \u_继续运行  (.out(Go));
  LED led_1 (.in(W1));
  LED led_2 (.in(W2));
  LED led_3 (.in(W3));
  Hex_Digit_Display hex_digit_display_1 (.value(LedData[31:28]));  // open: dp
  // Probe on IF_PC[19:0]
  // Mips_Probe mips_probe_1: pin names not known; wires that end beside it: IF_IR
  Hex_Digit_Display hex_digit_display_2 (.value(LedData[23:20]));  // open: dp
  Hex_Digit_Display hex_digit_display_3 (.value(LedData[27:24]));  // open: dp
  // Probe on ID_PC[19:0]
  // Mips_Probe mips_probe_2: pin names not known; wires that end beside it: ID_IR
  Hex_Digit_Display hex_digit_display_4 (.value(LedData[15:12]));  // open: dp
  Hex_Digit_Display hex_digit_display_5 (.value(LedData[19:16]));  // open: dp
  Hex_Digit_Display hex_digit_display_6 (.value(LedData[7:4]));  // open: dp
  Hex_Digit_Display hex_digit_display_7 (.value(LedData[11:8]));  // open: dp
  Clock clock_1 (.out(CLK));
  // Probe on EX_PC[19:0]
  // Mips_Probe mips_probe_3: pin names not known; wires that end beside it: RDin, EX_IR
  // Probe on RDin
  Hex_Digit_Display hex_digit_display_8 (.value(LedData[3:0]));  // open: dp
  // Probe on \总周期数 
  // Probe on M_PC[19:0]
  // Mips_Probe mips_probe_4: pin names not known; wires that end beside it: MEM_IR
  // Probe on \总周期数 
  // Probe on \无条件分支数 
  // Probe on \条件分支成功数 
  // Probe on \插入气泡数 
  // Probe on \LoadUse次数 
  // Probe on IF_PC[11:0]
  // Probe on WB_PC[19:0]
  // Mips_Probe mips_probe_5: pin names not known; wires that end beside it: WB_IR
  // Probe on EX_PC[11:0]
  // Probe on ID_PC[11:0]
  // Probe on M_PC[11:0]
  // Probe on \总周期数 
  // Probe on \总周期数 
  Multiplexer #(.width(32), .enable("false")) multiplexer_1 (
    .in0(adder_1_out), .in1(adder_4_out), .out(multiplexer_1_out), .sel(or_2_out));
  // Probe on WB_PC[11:0]
  // Probe on IF_PC[19:0]
  // Mips_Probe mips_probe_6: pin names not known; wires that end beside it: mips_probe_6_p1, IF_IR
  // Probe on ID_IR
  Multiplexer #(.width(32), .enable("false")) multiplexer_2 (
    .in0(register_8_q), .in1(EX_R1), .out(multiplexer_2_out), .sel(Jr));
  // Probe on RDin
  not not_1 (not_1_out, mem_wb_1_out_22);
  Multiplexer #(.width(32), .enable("false")) multiplexer_3 (
    .in0(multiplexer_1_out), .in1(multiplexer_2_out), .out(multiplexer_3_out), .sel(J));
  and and_1 (and_1_out, ~LoadUse, ~mem_wb_1_out_22);  // AND_Gate
  // OR_Gate or_1 has open pins: in0=1'b0, in1=mem_wb_1_out_22, out=open
  // Probe on ID_PC[19:0]
  // Mips_Probe mips_probe_7: pin names not known; wires that end beside it: ID_IR
  Counter #(.width(16), .max('hffff)) counter_1 (
    .count(not_1_out), .Q(\总周期数 ), .clk(CLK), .clr(RST));  // open: load, D, carry
  Register #(.width(32)) PC (.D(multiplexer_3_out), .en(and_1_out), .Q(IF_PC), .clk(CLK), .clr(RST));
  LED led_4 (.in(1'b0));
  and and_2 (and_2_out, ~mem_wb_1_out_22, ~LoadUse);  // AND_Gate
  not not_2 (not_2_out, and_2_out);
  // Probe on EX_PC[19:0]
  // Mips_Probe mips_probe_8: pin names not known; wires that end beside it: EX_IR
  ROM #(.addrWidth(10), .dataWidth(32)) rom_1 (.addr(IF_PC[11:2]), .data(IF_IR));  // open: sel
  Adder #(.width(32)) adder_1 (.a(IF_PC), .b(32'h4), .out(adder_1_out));  // open: cin, cout
  // Probe on M_PC[19:0]
  // Mips_Probe mips_probe_9: pin names not known; wires that end beside it: MEM_IR
  Counter #(.width(16), .max('hffff), .ongoal("stay")) counter_2 (
    .Q(\插入气泡数 ), .clk(1'b0));  // open: load, D, count, carry, clr
  IF_ID if_id_1 (
    .in_2(IF_IR), .in_3(IF_PC), .out_8(ID_IR), .out_9(ID_PC), .in_5(CLK), .in_7(RST), .\使能 (not_2_out),
    .in_4(1'b1), .in_6(JUMP));  // open: out_10
  Multiplexer #(.select(2), .width(32), .enable("false")) multiplexer_4 (
    .in0(R1), .in1({MEM_ALURes, bytePlace}), .in2(WB_ReadData), .in3({MEM_ALURes, bytePlace}), .out(EX_R1),
    .sel(SignalR1));
  Multiplexer #(.select(2), .width(32), .enable("false")) multiplexer_5 (
    .in0(R2), .in1({MEM_ALURes, bytePlace}), .in2(WB_ReadData), .in3({MEM_ALURes, bytePlace}), .out(EX_R2),
    .sel(SignalR2));
  // Probe on WB_PC[19:0]
  // Mips_Probe mips_probe_10: pin names not known; wires that end beside it: WB_IR
  // Probe on ID_IR
  // Probe on EX_R1
  // Probe on EX_R2
  // Mips_Probe mips_probe_11: pin names not known; wires that end beside it: ID_IR
  Adder #(.width(32)) adder_2 (.a(EX_PC), .b(32'h4), .out(adder_2_out));  // open: cin, cout
  // Probe on \总周期数 
  // Probe on \总周期数 
  // Probe on ID_IR[20:16]
  // Probe on SignalR1
  // Probe on SignalR2
  // Probe on EX_R1_num
  // Probe on EX_R2_num
  \单周期硬布线控制器  \u_单周期硬布线控制器_1  (
    .Func(ID_IR[5:0]), .OP(ID_IR[31:26]), .ALU_OP(\单周期硬布线控制器_1_alu_op ), .MemToReg(\单周期硬布线控制器_1_beq [3]),
    .MemWrite(\单周期硬布线控制器_1_beq [4]), .ALU_SRC(\单周期硬布线控制器_1_beq [9]), .RegWrite(\单周期硬布线控制器_1_beq [10]),
    .SysCALL(\单周期硬布线控制器_1_beq [11]), .SignedExt(SignedExt), .RegDst(\单周期硬布线控制器_1_regdst ),
    .JR(\单周期硬布线控制器_1_jr ), .JMP(mips_probe_6_p1), .Beq(\单周期硬布线控制器_1_beq [1]), .JAL(\单周期硬布线控制器_1_jal ),
    .Bne(\单周期硬布线控制器_1_beq [2]), .BLEZ(\单周期硬布线控制器_1_blez ), .Byte(\单周期硬布线控制器_1_byte ), .R1(ID_R1Used),
    .R2(ID_R2Used));
  Multiplexer #(.width(5), .enable("false")) multiplexer_6 (
    .in0(ID_IR[25:21]), .in1(5'b00100), .out(ID_R1_num), .sel(\单周期硬布线控制器_1_beq [11]));
  Multiplexer #(.width(5), .enable("false")) multiplexer_7 (
    .in0(ID_IR[20:16]), .in1(5'b00010), .out(ID_R2_num), .sel(\单周期硬布线控制器_1_beq [11]));
  Multiplexer #(.width(5), .enable("false")) multiplexer_8 (
    .in0(ID_IR[20:16]), .in1(ID_IR[15:11]), .out(multiplexer_8_out), .sel(\单周期硬布线控制器_1_regdst ));
  Multiplexer #(.width(5), .enable("false")) multiplexer_9 (
    .in0(multiplexer_8_out), .in1({5{1'b1}}), .out(multiplexer_9_out), .sel(\单周期硬布线控制器_1_jal ));
  Adder #(.width(32)) adder_3 (.a(WB_PC), .b(32'h4), .out(adder_3_out));  // open: cin, cout
  Register #(.width(1)) register_1 (.D(\单周期硬布线控制器_1_blez ), .Q(register_1_q), .clk(CLK), .clr(RST));  // open: en
  Register #(.width(1)) register_2 (.D(\单周期硬布线控制器_1_byte ), .Q(register_2_q), .clk(CLK), .clr(RST));  // open: en
  Multiplexer #(.width(32), .enable("false")) multiplexer_10 (
    .in0(multiplexer_11_out), .in1(OUT), .out(RDin), .sel(Byte));
  // Probe on ID_R1_num
  // Probe on ID_R2_num
  Comparator #(.width(5)) comparator_1 (.a(EX_R1_num), .b(MEM_RD), .eq(comparator_1_eq));  // open: gt, lt
  Comparator #(.width(5)) comparator_2 (.a(EX_R1_num), .b({5{1'b0}}), .eq(comparator_2_eq));  // open: gt, lt
  Comparator #(.width(5)) comparator_3 (.a(MEM_RD), .b({5{1'b0}}), .eq(comparator_3_eq));  // open: gt, lt
  Comparator #(.width(5)) comparator_4 (.a(EX_R2_num), .b(MEM_RD), .eq(comparator_4_eq));  // open: gt, lt
  Comparator #(.width(5)) comparator_5 (.a(EX_R2_num), .b({5{1'b0}}), .eq(comparator_5_eq));  // open: gt, lt
  Comparator #(.width(5)) comparator_6 (.a(MEM_RD), .b({5{1'b0}}), .eq(comparator_6_eq));  // open: gt, lt
  Comparator #(.width(5)) comparator_7 (.a(EX_R1_num), .b(W), .eq(comparator_7_eq));  // open: gt, lt
  Comparator #(.width(5)) comparator_8 (.a(EX_R1_num), .b({5{1'b0}}), .eq(comparator_8_eq));  // open: gt, lt
  Comparator #(.width(5)) comparator_9 (.a(W), .b({5{1'b0}}), .eq(comparator_9_eq));  // open: gt, lt
  Comparator #(.width(5)) comparator_10 (.a(EX_R2_num), .b(W), .eq(comparator_10_eq));  // open: gt, lt
  Comparator #(.width(5)) comparator_11 (.a(EX_R2_num), .b({5{1'b0}}), .eq(comparator_11_eq));  // open: gt, lt
  Comparator #(.width(5)) comparator_12 (.a(W), .b({5{1'b0}}), .eq(comparator_12_eq));  // open: gt, lt
  Register #(.width(1)) register_3 (.D(register_2_q), .Q(Byte), .clk(CLK), .clr(RST));  // open: en
  MIPS_Regifile mips_regifile_1 (
    .Din(RDin), .Clk(CLK), .R1(mips_regifile_1_r1), .R2(mips_regifile_1_r2), .WE(RegWrite), .W_num(W),
    .R1_num(ID_R1_num), .R2_num(ID_R2_num));
  Multiplexer #(.width(32), .enable("false")) multiplexer_11 (
    .in0(WB_ReadData), .in1(adder_3_out), .out(multiplexer_11_out), .sel(Jout));
  Shifter #(.width(32)) shifter_1 (.in(bit_extender_2_out), .\dist (5'b00010), .out(shifter_1_out));
  Multiplexer #(.width(5), .enable("false")) multiplexer_12 (
    .in0(ID_R1_num), .in1({5{1'b0}}), .out(multiplexer_12_out), .sel(or_3_out));
  Multiplexer #(.width(5), .enable("false")) multiplexer_13 (
    .in0(ID_R2_num), .in1({5{1'b0}}), .out(multiplexer_13_out), .sel(or_3_out));
  Multiplexer #(.enable("false")) multiplexer_14 (
    .in0(ID_R1Used), .in1(1'b0), .out(multiplexer_14_out), .sel(or_3_out));
  Multiplexer #(.enable("false")) multiplexer_15 (
    .in0(ID_R2Used), .in1(1'b0), .out(multiplexer_15_out), .sel(or_3_out));
  or or_2 (or_2_out, Bne, and_12_out, Beq);
  Adder #(.width(32)) adder_4 (.a(shifter_1_out), .b(adder_2_out), .out(adder_4_out));  // open: cin, cout
  or or_3 (or_3_out, JUMP, LoadUse, 1'b0);
  Register #(.width(5)) register_4 (.D(multiplexer_12_out), .Q(EX_R1_num), .clk(CLK), .clr(RST));  // open: en
  Register #(.width(5)) register_5 (.D(multiplexer_13_out), .Q(EX_R2_num), .clk(CLK), .clr(RST));  // open: en
  Register #(.width(1)) register_6 (.D(multiplexer_14_out), .Q(EX_R1Used), .clk(CLK), .clr(RST));  // open: en
  Register #(.width(1)) register_7 (.D(multiplexer_15_out), .Q(EX_R2Used), .clk(CLK), .clr(RST));  // open: en
  and and_3 (SignalR1[0], MEM_REGWRITE, EX_R1Used, comparator_1_eq, ~comparator_3_eq, ~comparator_2_eq);  // AND_Gate
  and and_4 (SignalR2[0], MEM_REGWRITE, EX_R2Used, comparator_4_eq, ~comparator_6_eq, ~comparator_5_eq);  // AND_Gate
  and and_5 (SignalR1[1], RegWrite, EX_R1Used, comparator_7_eq, ~comparator_9_eq, ~comparator_8_eq);  // AND_Gate
  and and_6 (SignalR2[1], RegWrite, EX_R2Used, comparator_10_eq, ~comparator_12_eq, ~comparator_11_eq);  // AND_Gate
  ID_EX id_ex_1 (
    .in_5({multiplexer_9_out, \单周期硬布线控制器_1_beq [11:9], \单周期硬布线控制器_1_alu_op , \单周期硬布线控制器_1_beq [4:1], SignedExt}),
    .in_6(ID_IR), .in_7(ID_PC), .in_8(mips_regifile_1_r1), .in_9(mips_regifile_1_r2), .in_10(ID_IR[15:0]),
    .out_18({EX_RD, id_ex_1_out_18[11:4], EX_MEMTOREG, id_ex_1_out_18[2:0]}), .out_19(EX_IR), .out_20(EX_PC),
    .out_21(R1), .out_22(R2), .out_23(id_ex_1_out_23), .in_13(CLK), .\异步清零 (RST), .\锁定 (mem_wb_1_out_22),
    .in_11(1'b1), .out_24(id_ex_1_out_24), .\同步清零 (or_3_out), .in_3(\单周期硬布线控制器_1_jal ), .out_16(Jal),
    .in_2(mips_probe_6_p1), .out_15(J), .in_4(\单周期硬布线控制器_1_jr ), .out_17(Jr));
  Register #(.width(32)) register_8 (
    .D({ID_IR[31:28], ID_IR[25:0], 2'b00}), .Q(register_8_q), .clk(CLK));  // open: en, clr
  and and_7 (Bne, id_ex_1_out_18[2], ~mips_alu_1_equal);  // AND_Gate
  Multiplexer #(.width(32), .enable("false")) multiplexer_16 (
    .in0(EX_R2), .in1(multiplexer_17_out), .out(multiplexer_16_out), .sel(id_ex_1_out_18[9]));
  assign bit_extender_1_out = {{16{1'b0}}, id_ex_1_out_23};  // Bit_Extender bit_extender_1
  assign bit_extender_2_out = {{16{id_ex_1_out_23[15]}}, id_ex_1_out_23};  // Bit_Extender bit_extender_2
  not not_3 (not_3_out, comparator_13_eq);
  Comparator #(.width(32)) comparator_13 (.a(32'h22), .b(EX_R2), .eq(comparator_13_eq));  // open: gt, lt
  and and_8 (Beq, id_ex_1_out_18[1], mips_alu_1_equal);
  MIPS_ALU mips_alu_1 (
    .X(EX_R1), .Y(multiplexer_16_out), .AluOP(id_ex_1_out_18[8:5]), .Equal(mips_alu_1_equal),
    .Result(mips_alu_1_result), .shamt(id_ex_1_out_23[10:6]));  // open: Result_2
  Multiplexer #(.width(32), .enable("false")) multiplexer_17 (
    .in0(bit_extender_1_out), .in1(bit_extender_2_out), .out(multiplexer_17_out), .sel(id_ex_1_out_18[0]));
  or or_4 (JUMP, Beq, Bne, J);
  and and_9 (and_9_out, id_ex_1_out_18[11], not_3_out);
  and and_10 (and_10_out, id_ex_1_out_18[11], comparator_13_eq);
  // Probe on id_ex_1_out_18[8:5]
  and and_11 (and_11_out, id_ex_1_out_24, ~mem_wb_1_out_22);  // AND_Gate
  not not_4 (not_4_out, and_11_out);
  and and_12 (and_12_out, register_1_q, not_5_out);
  not not_5 (not_5_out, and_13_out);
  Register #(.width(32)) register_9 (.D(EX_R1), .en(and_10_out), .Q(LedData), .clk(CLK), .clr(RST));
  // EX_MEM ex_mem_1: pin names not known; wires that end beside it: J, Jal, {EX_RD, id_ex_1_out_18[10], id_ex_1_out_18[4], EX_MEMTOREG, id_ex_1_out_18[2:1]}, mips_alu_1_equal, EX_PC, mips_alu_1_result, EX_IR, EX_R2, and_9_out, id_ex_1_out_24, RST, 1'b0, not_4_out, CLK, ex_mem_1_p15, ex_mem_1_p16, {MEM_RD, MEM_REGWRITE, MemWrite, ex_mem_1_p17}, ex_mem_1_p18, M_PC, {MEM_ALURes, bytePlace}, MEM_IR, MDin, ex_mem_1_p23
  and and_13 (and_13_out, ~mips_alu_1_equal, ~mips_alu_1_result[0]);  // AND_Gate
  Multiplexer #(.select(2), .width(32), .enable("false")) multiplexer_18 (
    .in0(bit_extender_3_out), .in1(bit_extender_4_out), .in2(bit_extender_5_out), .in3(bit_extender_6_out),
    .out(OUT), .sel(bytePlace));
  Comparator #(.width(5)) comparator_14 (.a(ID_R1_num), .b(EX_RD), .eq(comparator_14_eq));  // open: gt, lt
  Comparator #(.width(5)) comparator_15 (.a(ID_R1_num), .b({5{1'b0}}), .eq(comparator_15_eq));  // open: gt, lt
  Comparator #(.width(5)) comparator_16 (.a(EX_RD), .b({5{1'b0}}), .eq(comparator_16_eq));  // open: gt, lt
  Comparator #(.width(5)) comparator_17 (.a(ID_R2_num), .b(EX_RD), .eq(comparator_17_eq));  // open: gt, lt
  Comparator #(.width(5)) comparator_18 (.a(ID_R2_num), .b({5{1'b0}}), .eq(comparator_18_eq));  // open: gt, lt
  Comparator #(.width(5)) comparator_19 (.a(EX_RD), .b({5{1'b0}}), .eq(comparator_19_eq));  // open: gt, lt
  // OR_Gate or_5 has open pins: in0=and_15_out, in1=and_14_out, out=open
  and and_14 (and_14_out, ex_mem_1_p18, ex_mem_1_p17[0]);
  not not_6 (not_6_out, ex_mem_1_p18);
  and and_15 (and_15_out, not_6_out, ex_mem_1_p17[1]);
  // Probe on {MEM_ALURes, bytePlace}
  // Probe on \总周期数 
  // Probe on \总周期数 
  // Probe on {ram_1_data_4, ram_1_data_3, ram_1_data_2, ram_1_data}
  RAM #(.addrWidth(10), .dataWidth(32), .bus("separate")) ram_1 (
    .addr(MEM_ALURes[11:2]), .din(MDin), .data({ram_1_data_4, ram_1_data_3, ram_1_data_2, ram_1_data}),
    .str(MemWrite), .clk(CLK), .clr(RST));  // open: sel, ld
  and and_16 (and_16_out, EX_MEMTOREG, ID_R1Used, comparator_14_eq, ~comparator_16_eq, ~comparator_15_eq);  // AND_Gate
  and and_17 (and_17_out, EX_MEMTOREG, ID_R2Used, comparator_17_eq, ~comparator_19_eq, ~comparator_18_eq);  // AND_Gate
  MEM_WB mem_wb_1 (
    .in_4({MEM_RD, MEM_REGWRITE, ex_mem_1_p17[2]}), .in_5({MEM_ALURes, bytePlace}),
    .in_6({ram_1_data_4, ram_1_data_3, ram_1_data_2, ram_1_data}),
    .out_17({W, RegWrite, mem_wb_1_out_17[0]}), .out_18(WB_ALURes), .out_19(mem_wb_1_out_19), .in_12(CLK),
    .in_14(RST), .in_1(mem_wb_1_out_22), .in_9(ex_mem_1_p23), .out_22(mem_wb_1_out_22), .in_11(1'b1),
    .in_7(M_PC), .out_20(WB_PC), .in_8(MEM_IR), .out_21(WB_IR), .in_10(Go), .in_13(1'b0),
    .in_2(ex_mem_1_p15), .in_3(ex_mem_1_p16), .out_16(Jout));  // open: out_23, out_15
  assign bit_extender_3_out = {{24{1'b0}}, ram_1_data};  // Bit_Extender bit_extender_3
  assign bit_extender_4_out = {{24{1'b0}}, ram_1_data_2};  // Bit_Extender bit_extender_4
  assign bit_extender_5_out = {{24{1'b0}}, ram_1_data_3};  // Bit_Extender bit_extender_5
  assign bit_extender_6_out = {{24{1'b0}}, ram_1_data_4};  // Bit_Extender bit_extender_6
  or or_6 (LoadUse, and_16_out, and_17_out);
  // Probe on WB_ALURes
  Multiplexer #(.width(32), .enable("false")) multiplexer_19 (
    .in0(WB_ALURes), .in1(mem_wb_1_out_19), .out(WB_ReadData), .sel(mem_wb_1_out_17[0]));
  Counter #(.width(16), .max('hffff)) counter_3 (
    .count(LoadUse), .Q(\LoadUse次数 ), .clk(CLK));  // open: load, D, carry, clr
  // Probe on WB_ReadData

  // Other names for the same wires on the sheet: IR_NOW[31:0] = ID_IR; WB_REGWRITE = RegWrite; WB_RD[4:0] = W;
  //   IR[31:0] = IF_IR; IR_NEXT[31:0] = EX_IR; MEM_ALURes[1:0] = bytePlace; MEM_NOW[31:0] = MEM_IR;
  //   MEM_PC[31:0] = M_PC; PC[31:0] = IF_PC

  // Notes on the sheet:
  //   中断源
  //   时空图监测，可删除
  //   中断等待指示
  //   数码管输出
  //   流水调试日志用
  //   时空图监测，可删除
  //   指令存储器
  //   contents of rom_1 (hex, n*v repeats v):
  //   20110001 8000c05 20110001 20120002 20130003 8000c09 20110001 20120002 20130003 8000c0d 20110001
  //   20120002 20130003 8000c11 20110001 20120002 20130003 c000cb8 20100001 20110001 118fc0 112020
  //   20020022 c 118882 12200001 8000c15 112020 20020022 c 20110001 118880 112020 20020022 c 12200001
  //   8000c1f 20110001 118fc0 112020 20020022 c 1188c3 112020 20020022 c 118903 112020 20020022 c 118903
  //   112020 20020022 c 118903 112020 20020022 c 118903 112020 20020022 c 118903 112020 20020022 c 118903
  //   112020 20020022 c 118903 112020 20020022 c 20100001 109fc0 139fc3 8021 2012000c 24160003 26100001
  //   3210000f 20080008 20090001 139900 2709825 132020 20020022 c 1094022 1500fff9 22100001 2018000f
  //   2188024 108700 20080008 20090001 139902 2709825 132021 20020022 c 1094022 1500fff9 108702 2c9b022
  //   12c00001 8000c50 4020 1084027 84400 3508ffff 82021 20020022 c 2010ffff 20110000 ae300000 22100001
  //   22310004 ae300000 22100001 22310004 ae300000 22100001 22310004 ae300000 22100001 22310004 ae300000
  //   22100001 22310004 ae300000 22100001 22310004 ae300000 22100001 22310004 ae300000 22100001 22310004
  //   ae300000 22100001 22310004 ae300000 22100001 22310004 ae300000 22100001 22310004 ae300000 22100001
  //   22310004 ae300000 22100001 22310004 ae300000 22100001 22310004 ae300000 22100001 22310004 ae300000
  //   22100001 22310004 22100001 8020 2011003c 8e130000 8e340000 274402a 11000002 ae330000 ae140000
  //   2231fffc 1611fff8 102020 20020022 c 22100004 2011003c 1611fff2 20020032 c 20100000 22100001 102020
  //   20020022 c 22100002 102020 20020022 c 22100003 102020 20020022 c 22100004 102020 20020022 c 22100005
  //   102020 20020022 c 22100006 102020 20020022 c 22100007 102020 20020022 c 22100008 102020 20020022
  //   20020022 c 3e00008
  //   GeneratedInID
  //   为方便自动评测，需要输出流水线各段保存的PC值，注意是PC不是PC+4，另外ID段寄存器写入信息，Mem段内存写入信息也要输出
  //   GeneratedInID
  //   指令字
  //   OP
  //   Func
  //   rs
  //   rt
  //   rd
  //   LoadUse判断
  //   JMP
  //   JR
  //   OP
  //   Func
  //   Syscall
  //   Beq
  //   Bne
  //   MemToReg
  //   MemWrite
  //   AluOP
  //   AluSrcB
  //   RegWrite
  //   JAL
  //   RegDst
  //   Syscall
endmodule

module \中断按键参考电路  (
  input  \同步清零信号 ,
  output \与中断屏蔽位与 
);

  wire \_1号中断_out , and_1_out, clock_1_out, d_ff_1_q, or_1_out, or_2_out;

  Clock clock_1 (.out(clock_1_out));
  Button \_1号中断  (.out(\_1号中断_out ));
  or or_1 (or_1_out, \与中断屏蔽位与 , d_ff_1_q);
  LED \_1号中断等待指示灯  (.in(or_1_out));
  D_Flip_Flop d_ff_1 (.clk(\_1号中断_out ), .D(1'b1), .Q(d_ff_1_q), .reset(\与中断屏蔽位与 ));  // open: Qn, preset, en
  or or_2 (or_2_out, d_ff_1_q, \与中断屏蔽位与 );
  and and_1 (and_1_out, or_2_out, ~\同步清零信号 );  // AND_Gate
  D_Flip_Flop IR1 (.clk(clock_1_out), .D(and_1_out), .Q(\与中断屏蔽位与 ));  // open: Qn, preset, en, reset
  \单周期硬布线控制器  \u_单周期硬布线控制器_1  ();  // open: Func, OP, ALU_OP, MemToReg, MemWrite, ALU_SRC, RegWrite, SysCALL, SignedExt, RegDst, JR, JMP, Beq, JAL, Bne, BLEZ, Byte, R1, R2

  // Notes on the sheet:
  //   中断信号采样参考电路
  //   Reset 
endmodule

module \单周期MIPS_单级中断  (
  input  IR1,
  input  IR2,
  input  IR3,
  output RegWrite,
  output MemWrite,
  output [31:0] PC,
  output [31:0] IR,
  output [31:0] RDin,
  output [31:0] MDin,
  output [31:0] LedData
);

  wire and_1_out, and_2_out, and_3_out, and_4_out, and_5_out, and_6_out, Byte, CLK, comparator_1_eq, Go,
       IR1_t, IR2_t, IR3_t, IRA, IRB, IRC, mips_alu_1_equal, not_1_out, not_2_out, not_3_out, not_4_out,
       or_1_out, RST, SignedExt, W1, W2, W3, \单周期硬布线控制器_1_alu_src , \单周期硬布线控制器_1_beq , \单周期硬布线控制器_1_blez ,
       \单周期硬布线控制器_1_bne , \单周期硬布线控制器_1_jal , \单周期硬布线控制器_1_jmp , \单周期硬布线控制器_1_jr , \单周期硬布线控制器_1_memtoreg ,
       \单周期硬布线控制器_1_regdst , \单周期硬布线控制器_1_syscall ;
  wire [1:0] bytePlace;
  wire [3:0] \单周期硬布线控制器_1_alu_op ;
  wire [4:0] multiplexer_4_out, multiplexer_5_out, multiplexer_6_out, multiplexer_7_out;
  wire [7:0] multiplexer_13_out, multiplexer_13_out_2, multiplexer_13_out_3, multiplexer_13_out_4;
  wire [15:0] \总周期数 ;
  wire [31:0] adder_1_out, adder_2_out, bit_extender_1_out, bit_extender_2_out, bit_extender_3_out,
       bit_extender_4_out, bit_extender_5_out, bit_extender_6_out, mips_regifile_1_r1, multiplexer_1_out,
       multiplexer_2_out, multiplexer_3_out, multiplexer_8_out, multiplexer_10_out, multiplexer_11_out,
       multiplexer_12_out, ram_1_data, shifter_1_out;
  wire [31:2] mips_alu_1_result;

  Clock clock_1 (.out(CLK));
  Button _1 (.out(IRA));
  Button _2 (.out(IRB));
  Button _3 (.out(IRC));
  Button \u_继续运行  (.out(Go));
  LED led_1 (.in(W1));
  LED led_2 (.in(W2));
  LED led_3 (.in(W3));
  Multiplexer #(.width(32), .enable("false")) multiplexer_1 (
    .in0(adder_1_out), .in1(adder_2_out), .out(multiplexer_1_out), .sel(or_1_out));
  Multiplexer #(.width(32), .enable("false")) multiplexer_2 (
    .in0(multiplexer_1_out), .in1({IR[31:28], IR[25:0], 2'b00}), .out(multiplexer_2_out),
    .sel(\单周期硬布线控制器_1_jmp ));
  Hex_Digit_Display hex_digit_display_1 (.value(LedData[31:28]));  // open: dp
  Multiplexer #(.width(32), .enable("false")) multiplexer_3 (
    .in0(multiplexer_2_out), .in1(mips_regifile_1_r1), .out(multiplexer_3_out), .sel(\单周期硬布线控制器_1_jr ));
  Hex_Digit_Display hex_digit_display_2 (.value(LedData[23:20]));  // open: dp
  Hex_Digit_Display hex_digit_display_3 (.value(LedData[27:24]));  // open: dp
  Hex_Digit_Display hex_digit_display_4 (.value(LedData[15:12]));  // open: dp
  Hex_Digit_Display hex_digit_display_5 (.value(LedData[19:16]));  // open: dp
  Counter #(.width(16), .max('hffff)) counter_1 (
    .count(not_4_out), .Q(\总周期数 ), .clk(CLK), .clr(RST));  // open: load, D, carry
  Register #(.width(32)) u_PC (.D(multiplexer_3_out), .en(not_4_out), .Q(PC), .clk(CLK), .clr(RST));
  Hex_Digit_Display hex_digit_display_6 (.value(LedData[7:4]));  // open: dp
  Hex_Digit_Display hex_digit_display_7 (.value(LedData[11:8]));  // open: dp
  // Probe on \总周期数 
  or or_1 (or_1_out, and_3_out, and_1_out, and_2_out);
  Hex_Digit_Display hex_digit_display_8 (.value(LedData[3:0]));  // open: dp
  // Mips_Probe mips_probe_1: pin names not known; wires that end beside it: IR
  ROM #(.addrWidth(10), .dataWidth(32)) rom_1 (.addr(PC[11:2]), .data(IR));  // open: sel
  Adder #(.width(32)) adder_1 (.a(PC), .b(32'h4), .out(adder_1_out));  // open: cin, cout
  or or_2 (IR1_t, IR1, IRA);
  \单周期硬布线控制器  \u_单周期硬布线控制器_1  (
    .Func(IR[5:0]), .OP(IR[31:26]), .ALU_OP(\单周期硬布线控制器_1_alu_op ), .MemToReg(\单周期硬布线控制器_1_memtoreg ),
    .MemWrite(MemWrite), .ALU_SRC(\单周期硬布线控制器_1_alu_src ), .RegWrite(RegWrite),
    .SysCALL(\单周期硬布线控制器_1_syscall ), .SignedExt(SignedExt), .RegDst(\单周期硬布线控制器_1_regdst ),
    .JR(\单周期硬布线控制器_1_jr ), .JMP(\单周期硬布线控制器_1_jmp ), .Beq(\单周期硬布线控制器_1_beq ), .JAL(\单周期硬布线控制器_1_jal ),
    .Bne(\单周期硬布线控制器_1_bne ), .BLEZ(\单周期硬布线控制器_1_blez ), .Byte(Byte));  // open: R1, R2
  Multiplexer #(.width(5), .enable("false")) multiplexer_4 (
    .in0(IR[25:21]), .in1(5'b00010), .out(multiplexer_4_out), .sel(\单周期硬布线控制器_1_syscall ));
  Multiplexer #(.width(5), .enable("false")) multiplexer_5 (
    .in0(IR[20:16]), .in1(5'b00100), .out(multiplexer_5_out), .sel(\单周期硬布线控制器_1_syscall ));
  assign bit_extender_1_out = {{16{1'b0}}, IR[15:0]};  // Bit_Extender bit_extender_1
  assign bit_extender_2_out = {{16{IR[15]}}, IR[15:0]};  // Bit_Extender bit_extender_2
  or or_3 (IR2_t, IR2, IRB);
  Multiplexer #(.width(5), .enable("false")) multiplexer_6 (
    .in0(IR[20:16]), .in1(IR[15:11]), .out(multiplexer_6_out), .sel(\单周期硬布线控制器_1_regdst ));
  Multiplexer #(.width(5), .enable("false")) multiplexer_7 (
    .in0(multiplexer_6_out), .in1({5{1'b1}}), .out(multiplexer_7_out), .sel(\单周期硬布线控制器_1_jal ));
  Multiplexer #(.width(32), .enable("false")) multiplexer_8 (
    .in0(bit_extender_1_out), .in1(bit_extender_2_out), .out(multiplexer_8_out), .sel(SignedExt));
  Button button_1 (.out(RST));
  Multiplexer #(.width(32), .enable("false")) multiplexer_9 (
    .in0(multiplexer_11_out), .in1(multiplexer_12_out), .out(RDin), .sel(Byte));
  or or_4 (IR3_t, IR3, IRC);
  MIPS_Regifile mips_regifile_1 (
    .Din(RDin), .Clk(CLK), .R1(mips_regifile_1_r1), .R2(MDin), .WE(RegWrite), .W_num(multiplexer_7_out),
    .R1_num(multiplexer_4_out), .R2_num(multiplexer_5_out));
  Multiplexer #(.width(32), .enable("false")) multiplexer_10 (
    .in0(MDin), .in1(multiplexer_8_out), .out(multiplexer_10_out), .sel(\单周期硬布线控制器_1_alu_src ));
  Multiplexer #(.width(32), .enable("false")) multiplexer_11 (
    .in0({multiplexer_13_out_4, multiplexer_13_out_3, multiplexer_13_out_2, multiplexer_13_out}),
    .in1(adder_1_out), .out(multiplexer_11_out), .sel(\单周期硬布线控制器_1_jal ));
  Shifter #(.width(32)) shifter_1 (.in(bit_extender_2_out), .\dist (5'b00010), .out(shifter_1_out));
  Adder #(.width(32)) adder_2 (.a(shifter_1_out), .b(adder_1_out), .out(adder_2_out));  // open: cin, cout
  not not_1 (not_1_out, mips_alu_1_equal);
  MIPS_ALU mips_alu_1 (
    .X(mips_regifile_1_r1), .Y(multiplexer_10_out), .AluOP(\单周期硬布线控制器_1_alu_op ), .Equal(mips_alu_1_equal),
    .Result({mips_alu_1_result, bytePlace}), .shamt(IR[10:6]));  // open: Result_2
  and and_1 (and_1_out, \单周期硬布线控制器_1_blez , not_2_out);
  and and_2 (and_2_out, mips_alu_1_equal, \单周期硬布线控制器_1_beq );
  and and_3 (and_3_out, not_1_out, \单周期硬布线控制器_1_bne );
  not not_2 (not_2_out, and_4_out);
  and and_4 (and_4_out, ~bytePlace[0], ~mips_alu_1_equal);  // AND_Gate
  Multiplexer #(.select(2), .width(32), .enable("false")) multiplexer_12 (
    .in0(bit_extender_3_out), .in1(bit_extender_4_out), .in2(bit_extender_5_out), .in3(bit_extender_6_out),
    .out(multiplexer_12_out), .sel(bytePlace));
  RAM #(.addrWidth(10), .dataWidth(32), .bus("separate")) ram_1 (
    .addr(mips_alu_1_result[11:2]), .din(MDin), .data(ram_1_data), .str(MemWrite), .clk(CLK), .clr(RST));  // open: sel, ld
  Comparator #(.width(32)) comparator_1 (.a(32'h22), .b(mips_regifile_1_r1), .eq(comparator_1_eq));  // open: gt, lt
  Multiplexer #(.width(32), .enable("false")) multiplexer_13 (
    .in0({mips_alu_1_result, bytePlace}), .in1(ram_1_data),
    .out({multiplexer_13_out_4, multiplexer_13_out_3, multiplexer_13_out_2, multiplexer_13_out}),
    .sel(\单周期硬布线控制器_1_memtoreg ));
  and and_5 (and_5_out, \单周期硬布线控制器_1_syscall , not_3_out);
  not not_3 (not_3_out, comparator_1_eq);
  and and_6 (and_6_out, \单周期硬布线控制器_1_syscall , comparator_1_eq);
  assign bit_extender_3_out = {{24{1'b0}}, multiplexer_13_out};  // Bit_Extender bit_extender_3
  assign bit_extender_4_out = {{24{1'b0}}, multiplexer_13_out_2};  // Bit_Extender bit_extender_4
  assign bit_extender_5_out = {{24{1'b0}}, multiplexer_13_out_3};  // Bit_Extender bit_extender_5
  assign bit_extender_6_out = {{24{1'b0}}, multiplexer_13_out_4};  // Bit_Extender bit_extender_6
  not not_4 (not_4_out, and_5_out);
  Register #(.width(32)) register_1 (.D(MDin), .en(and_6_out), .Q(LedData), .clk(CLK), .clr(RST));

  // Other names for the same wires on the sheet: sign6_10[4:0] = IR[10:6]

  // Notes on the sheet:
  //   中断源
  //   中断等待指示
  //   总复位信号应将除ROM以外所有存储组件全部清零
  //   数码管输出
  //   数码管输出应该用寄存器锁存，否则显示数据只能一闪而过
  //   指令存储器
  //   指令字
  //   contents of rom_1 (hex, n*v repeats v):
  //   20110001 8000c05 20110001 20120002 20130003 8000c09 20110001 20120002 20130003 8000c0d 20110001
  //   20120002 20130003 8000c11 20110001 20120002 20130003 c000cb8 20100001 20110001 118fc0 112020
  //   20020022 c 118882 12200001 8000c15 112020 20020022 c 20110001 118880 112020 20020022 c 12200001
  //   8000c1f 20110001 118fc0 112020 20020022 c 1188c3 112020 20020022 c 118903 112020 20020022 c 118903
  //   112020 20020022 c 118903 112020 20020022 c 118903 112020 20020022 c 118903 112020 20020022 c 118903
  //   112020 20020022 c 118903 112020 20020022 c 20100001 109fc0 139fc3 8021 2012000c 24160003 26100001
  //   3210000f 20080008 20090001 139900 2709825 132020 20020022 c 1094022 1500fff9 22100001 2018000f
  //   2188024 108700 20080008 20090001 139902 2709825 132021 20020022 c 1094022 1500fff9 108702 2c9b022
  //   12c00001 8000c50 4020 1084027 84400 3508ffff 82021 20020022 c 2010ffff 20110000 ae300000 22100001
  //   22310004 ae300000 22100001 22310004 ae300000 22100001 22310004 ae300000 22100001 22310004 ae300000
  //   22100001 22310004 ae300000 22100001 22310004 ae300000 22100001 22310004 ae300000 22100001 22310004
  //   ae300000 22100001 22310004 ae300000 22100001 22310004 ae300000 22100001 22310004 ae300000 22100001
  //   22310004 ae300000 22100001 22310004 ae300000 22100001 22310004 ae300000 22100001 22310004 ae300000
  //   22100001 22310004 22100001 8020 2011003c 8e130000 8e340000 274402a 11000002 ae330000 ae140000
  //   2231fffc 1611fff8 102020 20020022 c 22100004 2011003c 1611fff2 2002000a c 20100000 22100001 102020
  //   20020022 c 22100002 102020 20020022 c 22100003 102020 20020022 c 22100004 102020 20020022 c 22100005
  //   102020 20020022 c 22100006 102020 20020022 c 22100007 102020 20020022 c 22100008 102020 20020022
  //   20020022 c 3e00008
  //   OP
  //   Func
  //   rs
  //   rt
  //   rd
  //   JMP
  //   JR
  //   OP
  //   Func
  //   Syscall
  //   Beq
  //   Bne
  //   MemToReg
  //   MemWrite
  //   AluOP
  //   AluSrcB
  //   RegWrite
  //   JAL
  //   RegDst
  //   为方便自动评测，需要输出PC，IR，寄存器堆写如数据RDin
  //   RAM写使能MemWrite、RAM写入数据MDin等信号
endmodule

module \单周期MIPS_多级中断  (
  input  IR1,
  input  IR2,
  input  IR3,
  output RegWrite,
  output MemWrite,
  output [31:0] PC,
  output [31:0] IR,
  output [31:0] RDin,
  output [31:0] MDin,
  output [31:0] LedData
);

  wire CLK, Go, IR1_t, IR2_t, IR3_t, IRA, IRB, IRC, SignedExt, W1, W2, W3, \单周期硬布线控制器_1_alu_src ,
       \单周期硬布线控制器_1_beq , \单周期硬布线控制器_1_bne , \单周期硬布线控制器_1_jal , \单周期硬布线控制器_1_jmp , \单周期硬布线控制器_1_jr ,
       \单周期硬布线控制器_1_memtoreg , \单周期硬布线控制器_1_memwrite , \单周期硬布线控制器_1_regdst , \单周期硬布线控制器_1_regwrite ,
       \单周期硬布线控制器_1_syscall ;
  wire [3:0] \单周期硬布线控制器_1_alu_op ;
  wire [5:0] undriven, undriven_2;
  wire [15:0] \总周期数 ;
  wire [31:0] rom_1_data;

  Clock clock_1 (.out(CLK));
  Button _1 (.out(IRA));
  Button _2 (.out(IRB));
  Button _3 (.out(IRC));
  Register #(.width(32)) u_PC ();  // open: D, en, Q, clk, clr
  Button \u_继续运行  (.out(Go));
  LED led_1 (.in(W1));
  LED led_2 (.in(W2));
  LED led_3 (.in(W3));
  Hex_Digit_Display hex_digit_display_1 (.value(LedData[31:28]));  // open: dp
  ROM #(.addrWidth(10), .dataWidth(32)) rom_1 (.data(rom_1_data));  // open: addr, sel
  Hex_Digit_Display hex_digit_display_2 (.value(LedData[27:24]));  // open: dp
  Hex_Digit_Display hex_digit_display_3 (.value(LedData[23:20]));  // open: dp
  // Mips_Probe mips_probe_1: pin names not known; wires that end beside it: rom_1_data
  Hex_Digit_Display hex_digit_display_4 (.value(LedData[15:12]));  // open: dp
  Hex_Digit_Display hex_digit_display_5 (.value(LedData[19:16]));  // open: dp
  Hex_Digit_Display hex_digit_display_6 (.value(LedData[11:8]));  // open: dp
  Hex_Digit_Display hex_digit_display_7 (.value(LedData[7:4]));  // open: dp
  // Probe on \总周期数 
  MIPS_Regifile mips_regifile_1 ();  // open: Din, Clk, R1, R2, WE, W_num, R1_num, R2_num
  Hex_Digit_Display hex_digit_display_8 (.value(LedData[3:0]));  // open: dp
  MIPS_ALU mips_alu_1 ();  // open: X, Y, AluOP, Equal, Result, Result_2, shamt
  or or_1 (IR1_t, IR1, IRA);
  or or_2 (IR2_t, IR2, IRB);
  RAM #(.addrWidth(10), .dataWidth(32), .bus("separate")) ram_1 ();  // open: addr, din, data, str, sel, clk, ld, clr
  \单周期硬布线控制器  \u_单周期硬布线控制器_1  (
    .Func(undriven_2), .OP(undriven), .ALU_OP(\单周期硬布线控制器_1_alu_op ), .MemToReg(\单周期硬布线控制器_1_memtoreg ),
    .MemWrite(\单周期硬布线控制器_1_memwrite ), .ALU_SRC(\单周期硬布线控制器_1_alu_src ), .RegWrite(\单周期硬布线控制器_1_regwrite ),
    .SysCALL(\单周期硬布线控制器_1_syscall ), .SignedExt(SignedExt), .RegDst(\单周期硬布线控制器_1_regdst ),
    .JR(\单周期硬布线控制器_1_jr ), .JMP(\单周期硬布线控制器_1_jmp ), .Beq(\单周期硬布线控制器_1_beq ), .JAL(\单周期硬布线控制器_1_jal ),
    .Bne(\单周期硬布线控制器_1_bne ));  // open: BLEZ, Byte, R1, R2
  or or_3 (IR3_t, IR3, IRC);

  // Notes on the sheet:
  //   中断源
  //   中断等待指示
  //   总复位信号应将除ROM以外所有存储组件全部清零
  //   指令存储器
  //   contents of rom_1 (hex, n*v repeats v):
  //   20110001 8000c05 20110001 20120002 20130003 8000c09 20110001 20120002 20130003 8000c0d 20110001
  //   20120002 20130003 8000c11 20110001 20120002 20130003 c000cb8 20100001 20110001 118fc0 112020
  //   20020022 c 118882 12200001 8000c15 112020 20020022 c 20110001 118880 112020 20020022 c 12200001
  //   8000c1f 20110001 118fc0 112020 20020022 c 1188c3 112020 20020022 c 118903 112020 20020022 c 118903
  //   112020 20020022 c 118903 112020 20020022 c 118903 112020 20020022 c 118903 112020 20020022 c 118903
  //   112020 20020022 c 118903 112020 20020022 c 20100001 109fc0 139fc3 8021 2012000c 24160003 26100001
  //   3210000f 20080008 20090001 139900 2709825 132020 20020022 c 1094022 1500fff9 22100001 2018000f
  //   2188024 108700 20080008 20090001 139902 2709825 132021 20020022 c 1094022 1500fff9 108702 2c9b022
  //   12c00001 8000c50 4020 1084027 84400 3508ffff 82021 20020022 c 2010ffff 20110000 ae300000 22100001
  //   22310004 ae300000 22100001 22310004 ae300000 22100001 22310004 ae300000 22100001 22310004 ae300000
  //   22100001 22310004 ae300000 22100001 22310004 ae300000 22100001 22310004 ae300000 22100001 22310004
  //   ae300000 22100001 22310004 ae300000 22100001 22310004 ae300000 22100001 22310004 ae300000 22100001
  //   22310004 ae300000 22100001 22310004 ae300000 22100001 22310004 ae300000 22100001 22310004 ae300000
  //   22100001 22310004 22100001 8020 2011003c 8e130000 8e340000 274402a 11000002 ae330000 ae140000
  //   2231fffc 1611fff8 102020 20020022 c 22100004 2011003c 1611fff2 2002000a c 20100000 22100001 102020
  //   20020022 c 22100002 102020 20020022 c 22100003 102020 20020022 c 22100004 102020 20020022 c 22100005
  //   102020 20020022 c 22100006 102020 20020022 c 22100007 102020 20020022 c 22100008 102020 20020022
  //   20020022 c 3e00008
  //   OP
  //   Func
  //   rs
  //   指令字
  //   rt
  //   rd
  //   数码管输出
  //   数码管输出应该用寄存器锁存，否则显示数据只能一闪而过
  //   JMP
  //   JR
  //   OP
  //   Func
  //   Syscall
  //   Beq
  //   Bne
  //   MemToReg
  //   MemWrite
  //   AluOP
  //   AluSrcB
  //   RegWrite
  //   JAL
  //   RegDst
  //   为方便自动评测，需要输出PC，IR，寄存器堆写如数据RDin
  //   RAM写使能MemWrite、RAM写入数据MDin等信号
endmodule

module \封装正确性测试  (
);

  wire IR1, IR2, IR3, MemW, RegW;
  wire [31:0] EX_PC, ID_PC, IF_PC, IR, LED, MDin, MDinr, MEM_PC, PC, RDin, RDinr, WB_PC;

  \单周期MIPS  \u_单周期mips_1  (
    .RegWrite(RegW), .MemWrite(MemW), .PC(PC), .IR(IR), .RDin(RDin), .MDin(MDin), .LedData(LED));  // open: IR1, IR2, IR3, OUT
  \气泡流水线  \u_气泡流水线_1  (
    .RegWrite(RegW), .MemWrite(MemW), .IF_PC(IF_PC), .ID_PC(ID_PC), .EX_PC(EX_PC), .M_PC(MEM_PC),
    .WB_PC(WB_PC), .RDin(RDinr), .MDin(MDinr), .LedData(LED));
  \单周期MIPS_单级中断  \u_单周期mips_单级中断_1  (
    .IR1(IR1), .IR2(IR2), .IR3(IR3), .RegWrite(RegW), .MemWrite(MemW), .PC(PC), .IR(IR), .RDin(RDin),
    .MDin(MDin), .LedData(LED));
  \理想流水线  \u_理想流水线_1  (
    .RegWrite(RegW), .MemWrite(MemW), .IF_PC(IF_PC), .ID_PC(ID_PC), .EX_PC(EX_PC), .M_PC(MEM_PC),
    .WB_PC(WB_PC), .RDin(RDinr), .MDin(MDinr), .LedData(LED));
  \气泡流水线  \u_气泡流水线_2  (
    .RegWrite(RegW), .MemWrite(MemW), .IF_PC(IF_PC), .ID_PC(ID_PC), .EX_PC(EX_PC), .M_PC(MEM_PC),
    .WB_PC(WB_PC), .RDin(RDinr), .MDin(MDinr), .LedData(LED));
  \单周期MIPS_多级中断  \u_单周期mips_多级中断_1  (
    .IR1(IR1), .IR2(IR2), .IR3(IR3), .RegWrite(RegW), .MemWrite(MemW), .PC(PC), .IR(IR), .RDin(RDin),
    .MDin(MDin), .LedData(LED));

  // Notes on the sheet:
  //   单周期封装测试
  //   气泡流水封装测试
  //   单周期+单级中断封装测试
  //   请检查上面封装有无位宽不匹配，引脚标签是否和连接的标签相对应，否则无法在educoder平台上正确测试
  //   理想流水封装测试
  //   重定向流水封装测试
  //   单周期+多级中断封装测试
endmodule

module IF_ID (
  input  \使能 ,
  input  [31:0] in_2,
  input  [31:0] in_3,
  input  in_4,
  input  in_5,
  input  in_6,
  input  in_7,
  output [31:0] out_8,
  output [31:0] out_9,
  output out_10
);

  wire multiplexer_3_out, not_1_out;
  wire [31:0] multiplexer_1_out, multiplexer_2_out;

  Multiplexer #(.width(32), .enable("false")) multiplexer_1 (
    .in0(in_2), .in1({32{1'b0}}), .out(multiplexer_1_out), .sel(in_6));
  Multiplexer #(.width(32), .enable("false")) multiplexer_2 (
    .in0(in_3), .in1({32{1'b0}}), .out(multiplexer_2_out), .sel(in_6));
  Multiplexer #(.enable("false")) multiplexer_3 (.in0(in_4), .in1(1'b0), .out(multiplexer_3_out), .sel(in_6));
  not not_1 (not_1_out, \使能 );
  Register #(.width(32)) register_1 (.D(multiplexer_1_out), .en(not_1_out), .Q(out_8), .clk(in_5), .clr(in_7));
  Register #(.width(32)) register_2 (.D(multiplexer_2_out), .en(not_1_out), .Q(out_9), .clk(in_5), .clr(in_7));
  Register #(.width(1)) register_3 (.D(multiplexer_3_out), .en(not_1_out), .Q(out_10), .clk(in_5), .clr(in_7));

  // Notes on the sheet:
  //   IR
  //   PC
endmodule

module ID_EX (
  input  \锁定 ,
  input  in_2,
  input  in_3,
  input  in_4,
  input  [16:0] in_5,
  input  [31:0] in_6,
  input  [31:0] in_7,
  input  [31:0] in_8,
  input  [31:0] in_9,
  input  [15:0] in_10,
  input  in_11,
  input  \同步清零 ,
  input  in_13,
  input  \异步清零 ,
  output out_15,
  output out_16,
  output out_17,
  output [16:0] out_18,
  output [31:0] out_19,
  output [31:0] out_20,
  output [31:0] out_21,
  output [31:0] out_22,
  output [15:0] out_23,
  output out_24
);

  wire multiplexer_1_out, multiplexer_2_out, multiplexer_3_out, multiplexer_10_out, not_1_out;
  wire [15:0] multiplexer_9_out;
  wire [16:0] multiplexer_4_out;
  wire [31:0] multiplexer_5_out, multiplexer_6_out, multiplexer_7_out, multiplexer_8_out;

  Multiplexer #(.enable("false")) multiplexer_1 (.in0(in_2), .in1(1'b0), .out(multiplexer_1_out), .sel(\同步清零 ));
  Multiplexer #(.enable("false")) multiplexer_2 (.in0(in_3), .in1(1'b0), .out(multiplexer_2_out), .sel(\同步清零 ));
  Multiplexer #(.enable("false")) multiplexer_3 (.in0(in_4), .in1(1'b0), .out(multiplexer_3_out), .sel(\同步清零 ));
  Multiplexer #(.width(17), .enable("false")) multiplexer_4 (
    .in0(in_5), .in1({17{1'b0}}), .out(multiplexer_4_out), .sel(\同步清零 ));
  Multiplexer #(.width(32), .enable("false")) multiplexer_5 (
    .in0(in_6), .in1({32{1'b0}}), .out(multiplexer_5_out), .sel(\同步清零 ));
  Multiplexer #(.width(32), .enable("false")) multiplexer_6 (
    .in0(in_7), .in1({32{1'b0}}), .out(multiplexer_6_out), .sel(\同步清零 ));
  Multiplexer #(.width(32), .enable("false")) multiplexer_7 (
    .in0(in_8), .in1({32{1'b0}}), .out(multiplexer_7_out), .sel(\同步清零 ));
  Multiplexer #(.width(32), .enable("false")) multiplexer_8 (
    .in0(in_9), .in1({32{1'b0}}), .out(multiplexer_8_out), .sel(\同步清零 ));
  Multiplexer #(.width(16), .enable("false")) multiplexer_9 (
    .in0(in_10), .in1({16{1'b0}}), .out(multiplexer_9_out), .sel(\同步清零 ));
  Multiplexer #(.enable("false")) multiplexer_10 (.in0(in_11), .in1(1'b0), .out(multiplexer_10_out), .sel(\同步清零 ));
  not not_1 (not_1_out, \锁定 );
  Register #(.width(1)) register_1 (.D(multiplexer_1_out), .en(not_1_out), .Q(out_15), .clk(in_13), .clr(\异步清零 ));
  Register #(.width(1)) register_2 (.D(multiplexer_2_out), .en(not_1_out), .Q(out_16), .clk(in_13), .clr(\异步清零 ));
  Register #(.width(1)) register_3 (.D(multiplexer_3_out), .en(not_1_out), .Q(out_17), .clk(in_13), .clr(\异步清零 ));
  Register #(.width(17)) register_4 (.D(multiplexer_4_out), .en(not_1_out), .Q(out_18), .clk(in_13), .clr(\异步清零 ));
  Register #(.width(32)) register_5 (.D(multiplexer_5_out), .en(not_1_out), .Q(out_19), .clk(in_13), .clr(\异步清零 ));
  Register #(.width(32)) register_6 (.D(multiplexer_6_out), .en(not_1_out), .Q(out_20), .clk(in_13), .clr(\异步清零 ));
  Register #(.width(32)) register_7 (.D(multiplexer_7_out), .en(not_1_out), .Q(out_21), .clk(in_13), .clr(\异步清零 ));
  Register #(.width(32)) register_8 (.D(multiplexer_8_out), .en(not_1_out), .Q(out_22), .clk(in_13), .clr(\异步清零 ));
  Register #(.width(16)) register_9 (.D(multiplexer_9_out), .en(not_1_out), .Q(out_23), .clk(in_13), .clr(\异步清零 ));
  Register #(.width(1)) register_10 (.D(multiplexer_10_out), .en(not_1_out), .Q(out_24), .clk(in_13), .clr(\异步清零 ));

  // Notes on the sheet:
  //   CTRL
  //   IR
  //   PC
  //   R1
  //   R2
  //   Imm
endmodule

module EX_MEM (
  input  \锁定 ,
  input  in_2,
  input  in_3,
  input  [9:0] in_4,
  input  in_5,
  input  [31:0] in_6,
  input  [31:0] in_7,
  input  [31:0] in_8,
  input  [31:0] in_9,
  input  in_10,
  input  in_11,
  input  in_12,
  input  in_13,
  input  \异步清零 ,
  output out_15,
  output out_16,
  output [9:0] out_17,
  output out_18,
  output [31:0] out_19,
  output [31:0] out_20,
  output [31:0] out_21,
  output [31:0] out_22,
  output out_23,
  output out_24
);

  wire multiplexer_1_out, multiplexer_2_out, multiplexer_4_out, multiplexer_9_out, multiplexer_10_out,
       not_1_out;
  wire [9:0] multiplexer_3_out;
  wire [31:0] multiplexer_5_out, multiplexer_6_out, multiplexer_7_out, multiplexer_8_out;

  not not_1 (not_1_out, \锁定 );
  Multiplexer #(.enable("false")) multiplexer_1 (.in0(in_2), .in1(1'b0), .out(multiplexer_1_out), .sel(in_13));
  Multiplexer #(.enable("false")) multiplexer_2 (.in0(in_3), .in1(1'b0), .out(multiplexer_2_out), .sel(in_13));
  Multiplexer #(.width(10), .enable("false")) multiplexer_3 (
    .in0(in_4), .out(multiplexer_3_out), .sel(in_13));  // open: in1
  Multiplexer #(.enable("false")) multiplexer_4 (.in0(in_5), .in1(1'b0), .out(multiplexer_4_out), .sel(in_13));
  Multiplexer #(.width(32), .enable("false")) multiplexer_5 (
    .in0(in_6), .in1({32{1'b0}}), .out(multiplexer_5_out), .sel(in_13));
  Multiplexer #(.width(32), .enable("false")) multiplexer_6 (
    .in0(in_7), .in1({32{1'b0}}), .out(multiplexer_6_out), .sel(in_13));
  Multiplexer #(.width(32), .enable("false")) multiplexer_7 (
    .in0(in_8), .in1({32{1'b0}}), .out(multiplexer_7_out), .sel(in_13));
  Multiplexer #(.width(32), .enable("false")) multiplexer_8 (
    .in0(in_9), .in1({32{1'b0}}), .out(multiplexer_8_out), .sel(in_13));
  Multiplexer #(.enable("false")) multiplexer_9 (.in0(in_10), .in1(1'b0), .out(multiplexer_9_out), .sel(in_13));
  Multiplexer #(.enable("false")) multiplexer_10 (.in0(in_11), .in1(1'b0), .out(multiplexer_10_out), .sel(in_13));
  Register #(.width(1)) register_1 (.D(multiplexer_1_out), .en(not_1_out), .Q(out_15), .clk(in_12), .clr(\异步清零 ));
  Register #(.width(1)) register_2 (.D(multiplexer_2_out), .en(not_1_out), .Q(out_16), .clk(in_12), .clr(\异步清零 ));
  Register #(.width(10)) register_3 (.D(multiplexer_3_out), .en(not_1_out), .Q(out_17), .clk(in_12), .clr(\异步清零 ));
  Register #(.width(1)) register_4 (.D(multiplexer_4_out), .en(not_1_out), .Q(out_18), .clk(in_12), .clr(\异步清零 ));
  Register #(.width(32)) register_5 (.D(multiplexer_5_out), .en(not_1_out), .Q(out_19), .clk(in_12), .clr(\异步清零 ));
  Register #(.width(32)) register_6 (.D(multiplexer_6_out), .en(not_1_out), .Q(out_20), .clk(in_12), .clr(\异步清零 ));
  Register #(.width(32)) register_7 (.D(multiplexer_7_out), .en(not_1_out), .Q(out_21), .clk(in_12), .clr(\异步清零 ));
  Register #(.width(32)) register_8 (.D(multiplexer_8_out), .en(not_1_out), .Q(out_22), .clk(in_12), .clr(\异步清零 ));
  Register #(.width(1)) register_9 (.D(multiplexer_9_out), .en(not_1_out), .Q(out_23), .clk(in_12), .clr(\异步清零 ));
  Register #(.width(1)) register_10 (.D(multiplexer_10_out), .en(not_1_out), .Q(out_24), .clk(in_12), .clr(\异步清零 ));

  // Notes on the sheet:
  //   CTRL
  //   Equal
  //   Result
  //   R2/MDin
endmodule

module MEM_WB (
  input  in_1,
  input  in_2,
  input  in_3,
  input  [6:0] in_4,
  input  [31:0] in_5,
  input  [31:0] in_6,
  input  [31:0] in_7,
  input  [31:0] in_8,
  input  in_9,
  input  in_10,
  input  in_11,
  input  in_12,
  input  in_13,
  input  in_14,
  output out_15,
  output out_16,
  output [6:0] out_17,
  output [31:0] out_18,
  output [31:0] out_19,
  output [31:0] out_20,
  output [31:0] out_21,
  output out_22,
  output out_23
);

  wire multiplexer_1_out, multiplexer_2_out, multiplexer_8_out, multiplexer_9_out, not_1_out, or_1_out;
  wire [6:0] multiplexer_3_out;
  wire [31:0] multiplexer_4_out, multiplexer_5_out, multiplexer_6_out, multiplexer_7_out;

  Multiplexer #(.enable("false")) multiplexer_1 (.in0(in_2), .in1(1'b0), .out(multiplexer_1_out), .sel(in_13));
  Multiplexer #(.enable("false")) multiplexer_2 (.in0(in_3), .in1(1'b0), .out(multiplexer_2_out), .sel(in_13));
  Multiplexer #(.width(7), .enable("false")) multiplexer_3 (
    .in0(in_4), .in1({7{1'b0}}), .out(multiplexer_3_out), .sel(in_13));
  Multiplexer #(.width(32), .enable("false")) multiplexer_4 (
    .in0(in_5), .in1({32{1'b0}}), .out(multiplexer_4_out), .sel(in_13));
  Multiplexer #(.width(32), .enable("false")) multiplexer_5 (
    .in0(in_6), .in1({32{1'b0}}), .out(multiplexer_5_out), .sel(in_13));
  Multiplexer #(.width(32), .enable("false")) multiplexer_6 (
    .in0(in_7), .in1({32{1'b0}}), .out(multiplexer_6_out), .sel(in_13));
  Multiplexer #(.width(32), .enable("false")) multiplexer_7 (
    .in0(in_8), .in1({32{1'b0}}), .out(multiplexer_7_out), .sel(in_13));
  Multiplexer #(.enable("false")) multiplexer_8 (.in0(in_9), .in1(1'b0), .out(multiplexer_8_out), .sel(in_13));
  Multiplexer #(.enable("false")) multiplexer_9 (.in0(in_11), .in1(1'b0), .out(multiplexer_9_out), .sel(in_13));
  not not_1 (not_1_out, in_1);
  Register #(.width(1)) register_1 (.D(multiplexer_1_out), .en(not_1_out), .Q(out_15), .clk(in_12), .clr(in_14));
  Register #(.width(1)) register_2 (.D(multiplexer_2_out), .en(not_1_out), .Q(out_16), .clk(in_12), .clr(in_14));
  Register #(.width(7)) register_3 (.D(multiplexer_3_out), .en(not_1_out), .Q(out_17), .clk(in_12), .clr(in_14));
  Register #(.width(32)) register_4 (.D(multiplexer_4_out), .en(not_1_out), .Q(out_18), .clk(in_12), .clr(in_14));
  Register #(.width(32)) register_5 (.D(multiplexer_5_out), .en(not_1_out), .Q(out_19), .clk(in_12), .clr(in_14));
  Register #(.width(32)) register_6 (.D(multiplexer_6_out), .en(not_1_out), .Q(out_20), .clk(in_12), .clr(in_14));
  Register #(.width(32)) register_7 (.D(multiplexer_7_out), .en(not_1_out), .Q(out_21), .clk(in_12), .clr(in_14));
  Register #(.width(1)) register_8 (.D(multiplexer_8_out), .en(not_1_out), .Q(out_22), .clk(in_12), .clr(or_1_out));
  or or_1 (or_1_out, in_14, in_10);
  Register #(.width(1)) register_9 (.D(multiplexer_9_out), .en(not_1_out), .Q(out_23), .clk(in_12), .clr(in_14));

  // Notes on the sheet:
  //   CTRL
  //   Result
  //   RDout
endmodule

module Temp (
  output JAL,
  output BLEZ,
  output UNSIGN
);

  wire not_1_out, not_2_out, not_3_out, not_4_out, not_5_out, not_6_out, not_7_out, not_8_out, not_9_out,
       not_10_out, not_11_out, not_12_out, undriven, undriven_2, undriven_3, undriven_4, undriven_5,
       undriven_6, undriven_7;

  not not_1 (not_1_out, undriven_5);
  not not_2 (not_2_out, undriven_4);
  not not_3 (not_3_out, undriven_3);
  not not_4 (not_4_out, undriven_2);
  not not_5 (not_5_out, undriven);
  not not_6 (not_6_out, undriven_3);
  not not_7 (not_7_out, undriven_4);
  not not_8 (not_8_out, undriven_5);
  not not_9 (not_9_out, undriven);
  not not_10 (not_10_out, undriven_6);
  not not_11 (not_11_out, undriven_3);
  not not_12 (not_12_out, undriven_4);
  and and_1 (JAL, not_1_out, not_2_out, not_3_out, not_4_out, undriven_6, undriven_7);
  and and_2 (BLEZ, not_5_out, undriven_6, undriven_2, not_6_out, not_7_out, not_8_out);
  and and_3 (UNSIGN, not_9_out, not_10_out, undriven_2, not_11_out, not_12_out, undriven_5);
endmodule
