// Logisim project 梁一飞_CS1706_U201714762（流水线）.circ as structural Verilog: 20 circuits, main circuit ◇单周期MIPS
module \单周期MIPS  (
  input  IR1,
  input  IR2,
  input  IR3,
  output RegWrite,
  output MemWrite,
  output [31:0] PC,
  output [31:0] IR,
  output [31:0] RDin,
  output [31:0] MDin,
  output [31:0] LedData
);

  wire and_1_out, and_2_out, and_3_out, and_4_out, CLK, comparator_1_eq, Go, IR1_t, IR2_t, IR3_t, IRA, IRB,
       IRC, mips_alu_1_equal, not_1_out, not_2_out, not_3_out, or_4_out, or_5_out, SEL1, SignedExt, W1, W2,
       W3, \单周期硬布线控制器_1_alu_src , \单周期硬布线控制器_1_beq , \单周期硬布线控制器_1_blez , \单周期硬布线控制器_1_bne ,
       \单周期硬布线控制器_1_jal , \单周期硬布线控制器_1_jmp , \单周期硬布线控制器_1_jr , \单周期硬布线控制器_1_memtoreg , \单周期硬布线控制器_1_regdst ,
       \单周期硬布线控制器_1_sb , \单周期硬布线控制器_1_srav , \单周期硬布线控制器_1_syscall , \总复位_out ;
  wire [1:0] SEL;
  wire [3:0] \单周期硬布线控制器_1_alu_op ;
  wire [4:0] mips_regifile_1_r1, multiplexer_5_out, multiplexer_6_out, multiplexer_7_out, multiplexer_8_out,
       multiplexer_10_out;
  wire [15:0] \总周期数 ;
  wire [31:0] adder_1_out, adder_2_out, adder_3_out, bit_extender_1_out, bit_extender_2_out, DATA, DATA1,
       multiplexer_1_out, multiplexer_2_out, multiplexer_3_out, multiplexer_4_out, multiplexer_9_out,
       multiplexer_11_out, multiplexer_13_out, multiplexer_14_out, multiplexer_15_out, shifter_1_out;
  wire [31:2] mips_alu_1_result;
  wire [31:5] mips_regifile_1_r1_2;

  Clock #(.highDuration(1), .lowDuration(1)) clock_1 (.out(CLK));
  Button _1 (.out(IRA));
  Button _2 (.out(IRB));
  Button _3 (.out(IRC));
  Button \u_继续运行  (.out(Go));
  LED #(.active("true")) led_1 (.in(W1));
  LED #(.active("true")) led_2 (.in(W2));
  LED #(.active("true")) led_3 (.in(W3));
  Multiplexer #(.select(1), .width(32), .disabled("Z"), .enable("false")) multiplexer_1 (
    .in0(multiplexer_2_out), .in1({mips_regifile_1_r1_2, mips_regifile_1_r1}), .out(multiplexer_1_out),
    .sel(\单周期硬布线控制器_1_jr ));
  Multiplexer #(.select(1), .width(32), .disabled("Z"), .enable("false")) multiplexer_2 (
    .in0(multiplexer_3_out), .in1({IR[31:28], IR[25:0], 2'b00}), .out(multiplexer_2_out),
    .sel(\单周期硬布线控制器_1_jmp ));
  Multiplexer #(.select(1), .width(32), .disabled("Z"), .enable("false")) multiplexer_3 (
    .in0(multiplexer_4_out), .in1(adder_3_out), .out(multiplexer_3_out), .sel(or_4_out));
  Multiplexer #(.select(1), .width(32), .disabled("Z"), .enable("false")) multiplexer_4 (
    .in0(adder_1_out), .in1(adder_3_out), .out(multiplexer_4_out), .sel(SEL1));
  Button \u_总复位  (.out(\总复位_out ));
  Hex_Digit_Display hex_digit_display_1 (.value(LedData[31:28]));  // open: dp
  Register #(.width(32), .trigger("rising"), .Select("low")) u_PC (
    .D(multiplexer_1_out), .en(not_3_out), .Q(PC), .clk(CLK), .clr(\总复位_out ));
  Hex_Digit_Display hex_digit_display_2 (.value(LedData[27:24]));  // open: dp
  Hex_Digit_Display hex_digit_display_3 (.value(LedData[23:20]));  // open: dp
  Counter #(.width(16), .max('hffff), .ongoal("wrap"), .trigger("rising"), .behavior("old")) counter_1 (
    .count(not_3_out), .Q(\总周期数 ), .clk(CLK), .clr(\总复位_out ));  // open: load, D, carry, preset
  Hex_Digit_Display hex_digit_display_4 (.value(LedData[15:12]));  // open: dp
  Hex_Digit_Display hex_digit_display_5 (.value(LedData[19:16]));  // open: dp
  Hex_Digit_Display hex_digit_display_6 (.value(LedData[7:4]));  // open: dp
  Hex_Digit_Display hex_digit_display_7 (.value(LedData[11:8]));  // open: dp
  // Probe on \总周期数 
  ROM #(.addrWidth(10), .dataWidth(32), .Select("high")) rom_1 (.addr(PC[11:2]), .data(IR));
  Adder #(.width(32)) adder_1 (.a(PC), .b(32'h4), .out(adder_1_out));  // open: cin, cout
  Hex_Digit_Display hex_digit_display_8 (.value(LedData[3:0]));  // open: dp
  or or_1 (IR1_t, IR1, IRA);
  or or_2 (IR2_t, IR2, IRB);
  \单周期硬布线控制器  \u_单周期硬布线控制器_1  (
    .Func(IR[5:0]), .OP(IR[31:26]), .ALU_OP(\单周期硬布线控制器_1_alu_op ), .MemToReg(\单周期硬布线控制器_1_memtoreg ),
    .MemWrite(MemWrite), .ALU_SRC(\单周期硬布线控制器_1_alu_src ), .RegWrite(RegWrite),
    .SysCALL(\单周期硬布线控制器_1_syscall ), .SignedExt(SignedExt), .RegDst(\单周期硬布线控制器_1_regdst ),
    .JR(\单周期硬布线控制器_1_jr ), .JMP(\单周期硬布线控制器_1_jmp ), .Beq(\单周期硬布线控制器_1_beq ), .JAL(\单周期硬布线控制器_1_jal ),
    .Bne(\单周期硬布线控制器_1_bne ), .SRAV(\单周期硬布线控制器_1_srav ), .SB(\单周期硬布线控制器_1_sb ), .BLEZ(\单周期硬布线控制器_1_blez ));
  Multiplexer #(.select(1), .width(5), .disabled("Z"), .enable("false")) multiplexer_5 (
    .in0(IR[25:21]), .in1(5'b00010), .out(multiplexer_5_out), .sel(\单周期硬布线控制器_1_syscall ));
  Multiplexer #(.select(1), .width(5), .disabled("Z"), .enable("false")) multiplexer_6 (
    .in0(IR[20:16]), .in1(5'b00100), .out(multiplexer_6_out), .sel(\单周期硬布线控制器_1_syscall ));
  assign bit_extender_1_out = {{16{1'b0}}, IR[15:0]};  // Bit_Extender bit_extender_1
  assign bit_extender_2_out = {{16{IR[15]}}, IR[15:0]};  // Bit_Extender bit_extender_2
  Adder #(.width(32)) adder_2 (.a(adder_1_out), .b({32{1'b0}}), .out(adder_2_out));  // open: cin, cout
  Multiplexer #(.select(1), .width(5), .disabled("Z"), .enable("false")) multiplexer_7 (
    .in0(IR[20:16]), .in1(IR[15:11]), .out(multiplexer_7_out), .sel(\单周期硬布线控制器_1_regdst ));
  Multiplexer #(.select(1), .width(5), .disabled("Z"), .enable("false")) multiplexer_8 (
    .in0(multiplexer_7_out), .in1({5{1'b1}}), .out(multiplexer_8_out), .sel(\单周期硬布线控制器_1_jal ));
  Multiplexer #(.select(1), .width(32), .disabled("Z"), .enable("false")) multiplexer_9 (
    .in0(bit_extender_1_out), .in1(bit_extender_2_out), .out(multiplexer_9_out), .sel(SignedExt));
  Multiplexer #(.select(1), .width(5), .disabled("Z"), .enable("false")) multiplexer_10 (
    .in0(IR[10:6]), .in1(mips_regifile_1_r1), .out(multiplexer_10_out), .sel(\单周期硬布线控制器_1_srav ));
  or or_3 (IR3_t, IR3, IRC);
  Multiplexer #(.select(1), .width(32), .disabled("Z"), .enable("false")) multiplexer_11 (
    .in0(MDin), .in1(multiplexer_9_out), .out(multiplexer_11_out), .sel(\单周期硬布线控制器_1_alu_src ));
  Multiplexer #(.select(1), .width(32), .disabled("Z"), .enable("false")) multiplexer_12 (
    .in0(multiplexer_14_out), .in1(adder_2_out), .out(RDin), .sel(\单周期硬布线控制器_1_jal ));
  MIPS_Regifile mips_regifile_1 (
    .Din(RDin), .Clk(CLK), .R1({mips_regifile_1_r1_2, mips_regifile_1_r1}), .R2(MDin), .WE(RegWrite),
    .W_num(multiplexer_8_out), .R1_num(multiplexer_5_out), .R2_num(multiplexer_6_out));
  Multiplexer #(.select(1), .width(32), .disabled("Z"), .enable("false")) multiplexer_13 (
    .in0(multiplexer_11_out), .in1({32{1'b0}}), .out(multiplexer_13_out), .sel(\单周期硬布线控制器_1_blez ));
  Shifter #(.width(32), .shift("ll")) shifter_1 (.in(bit_extender_2_out), .\dist (5'b00010), .out(shifter_1_out));
  not not_1 (not_1_out, mips_alu_1_equal);
  Adder #(.width(32)) adder_3 (.a(shifter_1_out), .b(adder_1_out), .out(adder_3_out));  // open: cin, cout
  Multiplexer #(.select(1), .width(32), .disabled("Z"), .enable("false")) multiplexer_14 (
    .in0({mips_alu_1_result, SEL}), .in1(DATA), .out(multiplexer_14_out), .sel(\单周期硬布线控制器_1_memtoreg ));
  and and_1 (and_1_out, mips_alu_1_equal, \单周期硬布线控制器_1_beq );
  and and_2 (and_2_out, \单周期硬布线控制器_1_bne , not_1_out);
  Comparator #(.width(32), .mode("twosComplement")) comparator_1 (
    .a(32'h22), .b({mips_regifile_1_r1_2, mips_regifile_1_r1}), .eq(comparator_1_eq));  // open: gt, lt
  MIPS_ALU mips_alu_1 (
    .X({mips_regifile_1_r1_2, mips_regifile_1_r1}), .Y(multiplexer_13_out), .AluOP(\单周期硬布线控制器_1_alu_op ),
    .Equal(mips_alu_1_equal), .Result({mips_alu_1_result, SEL}), .shamt(multiplexer_10_out));  // open: Result_2
  or or_4 (or_4_out, and_1_out, and_2_out);
  not not_2 (not_2_out, comparator_1_eq);
  and and_3 (and_3_out, \单周期硬布线控制器_1_syscall , comparator_1_eq);
  Multiplexer #(.select(1), .width(32), .disabled("Z"), .enable("false")) multiplexer_15 (
    .in0(MDin), .in1(DATA1), .out(multiplexer_15_out), .sel(\单周期硬布线控制器_1_sb ));
  not not_3 (not_3_out, and_4_out);
  and and_4 (and_4_out, not_2_out, \单周期硬布线控制器_1_syscall );
  Register #(.width(32), .trigger("rising"), .Select("low")) register_1 (
    .D(MDin), .en(and_3_out), .Q(LedData), .clk(CLK));  // open: clr
  RAM #(.addrWidth(10), .dataWidth(32), .bus("separate"), .Select("high")) ram_1 (
    .addr(mips_alu_1_result[11:2]), .din(multiplexer_15_out), .data(DATA), .str(MemWrite), .clk(CLK),
    .clr(\总复位_out ));  // open: sel, ld
  or or_5 (or_5_out, mips_alu_1_equal, SEL[0]);
  and and_5 (SEL1, or_5_out, \单周期硬布线控制器_1_blez );
  Multiplexer #(.select(2), .width(32), .disabled("Z"), .enable("false")) multiplexer_16 (
    .in0({DATA[31:8], MDin[7:0]}), .in1({DATA[31:16], MDin[7:0], DATA[7:0]}),
    .in2({DATA[31:24], MDin[7:0], DATA[15:0]}), .in3({MDin[7:0], DATA[23:0]}), .out(DATA1), .sel(SEL));

  // Other names for the same wires on the sheet: R2[31:0] = MDin

  // Notes on the sheet:
  //   中断源
  //   中断等待指示
  //   总复位信号应将除ROM以外所有存储组件全部清零
  //   数码管输出
  //   指令存储器
  //   数码管输出应该用寄存器锁存，否则显示数据只能一闪而过
  //   指令字
  //   contents of rom_1 (hex, n*v repeats v):
  //   20110001 8000c05 20110001 20120002 20130003 8000c09 20110001 20120002 20130003 8000c0d 20110001
  //   20120002 20130003 8000c11 20110001 20120002 20130003 c000cb8 20100001 20110001 118fc0 112020
  //   20020022 c 118882 12200001 8000c15 112020 20020022 c 20110001 118880 112020 20020022 c 12200001
  //   8000c1f 20110001 118fc0 112020 20020022 c 1188c3 112020 20020022 c 118903 112020 20020022 c 118903
  //   112020 20020022 c 118903 112020 20020022 c 118903 112020 20020022 c 118903 112020 20020022 c 118903
  //   112020 20020022 c 118903 112020 20020022 c 20100001 109fc0 139fc3 8021 2012000c 24160003 26100001
  //   3210000f 20080008 20090001 139900 2709825 132020 20020022 c 1094022 1500fff9 22100001 2018000f
  //   2188024 108700 20080008 20090001 139902 2709825 132021 20020022 c 1094022 1500fff9 108702 2c9b022
  //   12c00001 8000c50 4020 1084027 84400 3508ffff 82021 20020022 c 2010ffff 20110000 ae300000 22100001
  //   22310004 ae300000 22100001 22310004 ae300000 22100001 22310004 ae300000 22100001 22310004 ae300000
  //   22100001 22310004 ae300000 22100001 22310004 ae300000 22100001 22310004 ae300000 22100001 22310004
  //   ae300000 22100001 22310004 ae300000 22100001 22310004 ae300000 22100001 22310004 ae300000 22100001
  //   22310004 ae300000 22100001 22310004 ae300000 22100001 22310004 ae300000 22100001 22310004 ae300000
  //   22100001 22310004 22100001 8020 2011003c 8e130000 8e340000 274402a 11000002 ae330000 ae140000
  //   2231fffc 1611fff8 102020 20020022 c 22100004 2011003c 1611fff2 20020032 c 20100000 22100001 102020
  //   20020022 c 22100002 102020 20020022 c 22100003 102020 20020022 c 22100004 102020 20020022 c 22100005
  //   102020 20020022 c 22100006 102020 20020022 c 22100007 102020 20020022 c 22100008 102020 20020022
  //   20020022 c 3e00008
  //   OP
  //   Func
  //   rs
  //   rt
  //   rd
  //   JMP
  //   JR
  //   SRAV
  //   SB
  //   BLEZ
  //   OP
  //   Func
  //   Beq
  //   Bne
  //   MemToReg
  //   MemWrite
  //   AluOP
  //   AluSrcB
  //   RegWrite
  //   JAL
  //   RegDst
  //   Syscall
  //   为方便自动评测，需要输出PC，IR，寄存器堆写如数据RDin
  //   RAM写使能MemWrite、RAM写入数据MDin等信号
endmodule

// 单周期硬布线控制器
module \单周期硬布线控制器  (
  input  [5:0] OP,
  input  [5:0] Func,
  output [3:0] ALU_OP,
  output MemToReg,
  output MemWrite,
  output SB,
  output BLEZ,
  output ALU_SRC,
  output RegWrite,
  output SysCALL,
  output SignedExt,
  output SRAV,
  output RegDst,
  output Beq,
  output Bne,
  output JR,
  output JMP,
  output JAL
);

  \运算控制器自动生成  \u_运算控制器自动生成_1  (
    .OP0(OP[0]), .OP1(OP[1]), .OP2(OP[2]), .OP3(OP[3]), .OP4(OP[4]), .OP5(OP[5]), .F0(Func[0]), .F1(Func[1]),
    .F2(Func[2]), .F3(Func[3]), .F4(Func[4]), .F5(Func[5]), .S0(ALU_OP[0]), .S1(ALU_OP[1]), .S2(ALU_OP[2]),
    .S3(ALU_OP[3]));
  \控制信号自动生成  \u_控制信号自动生成_1  (
    .OP0(OP[0]), .OP1(OP[1]), .OP2(OP[2]), .OP3(OP[3]), .OP4(OP[4]), .OP5(OP[5]), .F0(Func[0]), .F1(Func[1]),
    .F2(Func[2]), .F3(Func[3]), .F4(Func[4]), .F5(Func[5]), .MemToReg(MemToReg), .MemWrite(MemWrite),
    .SB(SB), .BLEZ(BLEZ), .ALU_SRC(ALU_SRC), .RegWrite(RegWrite), .SysCALL(SysCALL), .SignedExt(SignedExt),
    .SRAV(SRAV), .RegDst(RegDst), .BEQ(Beq), .BNE(Bne), .JR(JR), .JUMP(JMP), .JAL(JAL));

  // Other names for the same wires on the sheet: OP_CODE[5:0] = OP

  // Notes on the sheet:
  //   运算器控制器，根据指令生成运算器功能选择信号
  //   控制信号生成，产生数据通路需要的其他控制信号
endmodule

// 运算器控制器
module \运算控制器自动生成  (
  input  OP0,
  input  OP1,
  input  OP2,
  input  OP3,
  input  OP4,
  input  OP5,
  input  F0,
  input  F1,
  input  F2,
  input  F3,
  input  F4,
  input  F5,
  output S0,
  output S1,
  output S2,
  output S3
);

  wire and_1_out, and_2_out, and_3_out, and_4_out, and_5_out, and_6_out, and_7_out, and_8_out, and_9_out,
       and_10_out, and_11_out, and_12_out, and_13_out, and_14_out, and_15_out, and_16_out, and_17_out,
       and_18_out, and_19_out, and_20_out, and_21_out, and_22_out, and_23_out, and_24_out, and_25_out,
       and_26_out, and_27_out, and_28_out, and_29_out, and_30_out, and_31_out, and_32_out, and_33_out,
       and_34_out, and_35_out, and_36_out, and_37_out, and_38_out, and_39_out, and_40_out, and_41_out,
       and_42_out, not_1_out, not_2_out, not_3_out, not_4_out, not_5_out, not_6_out, not_7_out, not_8_out,
       not_9_out, not_10_out, not_11_out, not_12_out, not_13_out, not_14_out, not_15_out, not_16_out,
       not_17_out, not_18_out, not_19_out, not_20_out, not_21_out, not_22_out, not_23_out, not_24_out,
       not_25_out, not_26_out, not_27_out, not_28_out, not_29_out, not_30_out, not_31_out, not_32_out,
       not_33_out, not_34_out, not_35_out, not_36_out, not_37_out, not_38_out, not_39_out, not_40_out,
       not_41_out, not_42_out, not_43_out, not_44_out, not_45_out, not_46_out, not_47_out, not_48_out,
       not_49_out, not_50_out, not_51_out, not_52_out, not_53_out, not_54_out, not_55_out, not_56_out,
       not_57_out, not_58_out, not_59_out, not_60_out, not_61_out, not_62_out, not_63_out, not_64_out,
       not_65_out, not_66_out, not_67_out, not_68_out, not_69_out, not_70_out, not_71_out, not_72_out,
       not_73_out, not_74_out, not_75_out, not_76_out, not_77_out, not_78_out, not_79_out, not_80_out,
       not_81_out, not_82_out, not_83_out, not_84_out, not_85_out, not_86_out, not_87_out, not_88_out,
       not_89_out, not_90_out, not_91_out, not_92_out, not_93_out, not_94_out, not_95_out, not_96_out,
       not_97_out, not_98_out, not_99_out, not_100_out, not_101_out, not_102_out, not_103_out, not_104_out,
       not_105_out, not_106_out, not_107_out, not_108_out, not_109_out, not_110_out, not_111_out,
       not_112_out, not_113_out, not_114_out, not_115_out, not_116_out, not_117_out, not_118_out,
       not_119_out, not_120_out, not_121_out, not_122_out, not_123_out, not_124_out, not_125_out,
       not_126_out, not_127_out, not_128_out, not_129_out, not_130_out, not_131_out, not_132_out,
       not_133_out, not_134_out, not_135_out, not_136_out, not_137_out, not_138_out, not_139_out,
       not_140_out, not_141_out, not_142_out, not_143_out, not_144_out, not_145_out, not_146_out,
       not_147_out, not_148_out, not_149_out, not_150_out, not_151_out, not_152_out, not_153_out,
       not_154_out, not_155_out, not_156_out, not_157_out, not_158_out, not_159_out, not_160_out,
       not_161_out, not_162_out, not_163_out, not_164_out, not_165_out, not_166_out, not_167_out,
       not_168_out, not_169_out, not_170_out, not_171_out, not_172_out, not_173_out, not_174_out,
       not_175_out, not_176_out, not_177_out, not_178_out, not_179_out, not_180_out, not_181_out,
       not_182_out, not_183_out, not_184_out, not_185_out, not_186_out, not_187_out, not_188_out,
       not_189_out, not_190_out, not_191_out, not_192_out, not_193_out, not_194_out, not_195_out,
       not_196_out, not_197_out, not_198_out, not_199_out, not_200_out, not_201_out, not_202_out,
       not_203_out, not_204_out, not_205_out, not_206_out, not_207_out, not_208_out, not_209_out,
       not_210_out, not_211_out, not_212_out, not_213_out, not_214_out, not_215_out, not_216_out,
       not_217_out, not_218_out, not_219_out, not_220_out, not_221_out, not_222_out, not_223_out,
       not_224_out, not_225_out, not_226_out, not_227_out, not_228_out, not_229_out, not_230_out,
       not_231_out, not_232_out, not_233_out, not_234_out, not_235_out, not_236_out, not_237_out,
       not_238_out, not_239_out, not_240_out, not_241_out, not_242_out, not_243_out, not_244_out,
       not_245_out, not_246_out, not_247_out, not_248_out, not_249_out, not_250_out, not_251_out,
       not_252_out, not_253_out, not_254_out, not_255_out, not_256_out, not_257_out, not_258_out,
       not_259_out, not_260_out, not_261_out, not_262_out, not_263_out, not_264_out, not_265_out,
       not_266_out, not_267_out, not_268_out, not_269_out, not_270_out, not_271_out;

  not not_1 (not_1_out, OP5);
  not not_2 (not_2_out, OP4);
  not not_3 (not_3_out, OP3);
  not not_4 (not_4_out, OP2);
  not not_5 (not_5_out, OP1);
  not not_6 (not_6_out, OP0);
  not not_7 (not_7_out, F5);
  not not_8 (not_8_out, F4);
  not not_9 (not_9_out, F3);
  not not_10 (not_10_out, F2);
  not not_11 (not_11_out, OP5);
  not not_12 (not_12_out, OP4);
  not not_13 (not_13_out, OP3);
  not not_14 (not_14_out, OP2);
  not not_15 (not_15_out, OP1);
  not not_16 (not_16_out, OP0);
  not not_17 (not_17_out, F4);
  not not_18 (not_18_out, F3);
  not not_19 (not_19_out, F2);
  not not_20 (not_20_out, F1);
  not not_21 (not_21_out, F0);
  not not_22 (not_22_out, OP5);
  not not_23 (not_23_out, OP4);
  not not_24 (not_24_out, OP3);
  not not_25 (not_25_out, OP2);
  not not_26 (not_26_out, OP1);
  not not_27 (not_27_out, OP0);
  not not_28 (not_28_out, F4);
  not not_29 (not_29_out, F3);
  not not_30 (not_30_out, F2);
  not not_31 (not_31_out, F1);
  not not_32 (not_32_out, OP5);
  not not_33 (not_33_out, OP4);
  not not_34 (not_34_out, OP3);
  not not_35 (not_35_out, OP2);
  not not_36 (not_36_out, OP1);
  not not_37 (not_37_out, OP0);
  not not_38 (not_38_out, F4);
  not not_39 (not_39_out, F3);
  not not_40 (not_40_out, F1);
  not not_41 (not_41_out, F0);
  not not_42 (not_42_out, OP5);
  not not_43 (not_43_out, OP4);
  not not_44 (not_44_out, OP3);
  not not_45 (not_45_out, OP2);
  not not_46 (not_46_out, OP1);
  not not_47 (not_47_out, OP0);
  not not_48 (not_48_out, F4);
  not not_49 (not_49_out, F2);
  not not_50 (not_50_out, F0);
  not not_51 (not_51_out, OP5);
  not not_52 (not_52_out, OP4);
  not not_53 (not_53_out, OP2);
  not not_54 (not_54_out, OP1);
  not not_55 (not_55_out, OP0);
  not not_56 (not_56_out, OP5);
  not not_57 (not_57_out, OP4);
  not not_58 (not_58_out, OP1);
  not not_59 (not_59_out, OP0);
  not not_60 (not_60_out, OP5);
  not not_61 (not_61_out, OP4);
  not not_62 (not_62_out, OP2);
  not not_63 (not_63_out, OP1);
  not not_64 (not_64_out, OP5);
  not not_65 (not_65_out, OP4);
  not not_66 (not_66_out, OP2);
  not not_67 (not_67_out, OP0);
  not not_68 (not_68_out, OP4);
  not not_69 (not_69_out, OP3);
  not not_70 (not_70_out, OP2);
  not not_71 (not_71_out, OP4);
  not not_72 (not_72_out, OP2);
  not not_73 (not_73_out, OP5);
  not not_74 (not_74_out, OP4);
  not not_75 (not_75_out, OP3);
  not not_76 (not_76_out, OP2);
  not not_77 (not_77_out, OP1);
  not not_78 (not_78_out, OP0);
  not not_79 (not_79_out, F5);
  not not_80 (not_80_out, F4);
  not not_81 (not_81_out, F3);
  not not_82 (not_82_out, OP4);
  not not_83 (not_83_out, OP2);
  not not_84 (not_84_out, OP1);
  not not_85 (not_85_out, OP0);
  not not_86 (not_86_out, OP5);
  not not_87 (not_87_out, OP4);
  not not_88 (not_88_out, OP3);
  not not_89 (not_89_out, OP0);
  not not_90 (not_90_out, OP5);
  not not_91 (not_91_out, OP4);
  not not_92 (not_92_out, OP3);
  not not_93 (not_93_out, OP2);
  not not_94 (not_94_out, OP1);
  not not_95 (not_95_out, OP0);
  not not_96 (not_96_out, F5);
  not not_97 (not_97_out, F4);
  not not_98 (not_98_out, F3);
  not not_99 (not_99_out, F2);
  not not_100 (not_100_out, F0);
  not not_101 (not_101_out, OP5);
  not not_102 (not_102_out, OP4);
  not not_103 (not_103_out, OP3);
  not not_104 (not_104_out, OP2);
  not not_105 (not_105_out, OP1);
  not not_106 (not_106_out, OP0);
  not not_107 (not_107_out, F4);
  not not_108 (not_108_out, F3);
  not not_109 (not_109_out, F2);
  not not_110 (not_110_out, F0);
  not not_111 (not_111_out, OP5);
  not not_112 (not_112_out, OP4);
  not not_113 (not_113_out, OP3);
  not not_114 (not_114_out, OP2);
  not not_115 (not_115_out, OP1);
  not not_116 (not_116_out, OP0);
  not not_117 (not_117_out, F4);
  not not_118 (not_118_out, F3);
  not not_119 (not_119_out, F1);
  not not_120 (not_120_out, F0);
  not not_121 (not_121_out, OP5);
  not not_122 (not_122_out, OP4);
  not not_123 (not_123_out, OP3);
  not not_124 (not_124_out, OP2);
  not not_125 (not_125_out, OP1);
  not not_126 (not_126_out, OP0);
  not not_127 (not_127_out, F4);
  not not_128 (not_128_out, F3);
  not not_129 (not_129_out, OP5);
  not not_130 (not_130_out, OP4);
  not not_131 (not_131_out, OP3);
  not not_132 (not_132_out, OP2);
  not not_133 (not_133_out, OP1);
  not not_134 (not_134_out, OP0);
  not not_135 (not_135_out, F4);
  not not_136 (not_136_out, F2);
  not not_137 (not_137_out, F0);
  not not_138 (not_138_out, OP5);
  not not_139 (not_139_out, OP4);
  not not_140 (not_140_out, OP1);
  not not_141 (not_141_out, OP0);
  not not_142 (not_142_out, OP5);
  not not_143 (not_143_out, OP4);
  not not_144 (not_144_out, OP2);
  not not_145 (not_145_out, OP0);
  not not_146 (not_146_out, OP5);
  not not_147 (not_147_out, OP4);
  not not_148 (not_148_out, OP3);
  not not_149 (not_149_out, OP0);
  not not_150 (not_150_out, OP5);
  not not_151 (not_151_out, OP4);
  not not_152 (not_152_out, OP3);
  not not_153 (not_153_out, OP2);
  not not_154 (not_154_out, OP1);
  not not_155 (not_155_out, OP0);
  not not_156 (not_156_out, F4);
  not not_157 (not_157_out, F3);
  not not_158 (not_158_out, F2);
  not not_159 (not_159_out, F1);
  not not_160 (not_160_out, F0);
  not not_161 (not_161_out, OP5);
  not not_162 (not_162_out, OP4);
  not not_163 (not_163_out, OP3);
  not not_164 (not_164_out, OP2);
  not not_165 (not_165_out, OP1);
  not not_166 (not_166_out, OP0);
  not not_167 (not_167_out, F4);
  not not_168 (not_168_out, F3);
  not not_169 (not_169_out, F2);
  not not_170 (not_170_out, F1);
  not not_171 (not_171_out, OP5);
  not not_172 (not_172_out, OP4);
  not not_173 (not_173_out, OP3);
  not not_174 (not_174_out, OP2);
  not not_175 (not_175_out, OP1);
  not not_176 (not_176_out, OP0);
  not not_177 (not_177_out, F4);
  not not_178 (not_178_out, F3);
  not not_179 (not_179_out, F2);
  not not_180 (not_180_out, F0);
  not not_181 (not_181_out, OP5);
  not not_182 (not_182_out, OP4);
  not not_183 (not_183_out, OP3);
  not not_184 (not_184_out, OP2);
  not not_185 (not_185_out, OP1);
  not not_186 (not_186_out, OP0);
  not not_187 (not_187_out, F4);
  not not_188 (not_188_out, F3);
  not not_189 (not_189_out, F1);
  not not_190 (not_190_out, F0);
  not not_191 (not_191_out, OP5);
  not not_192 (not_192_out, OP4);
  not not_193 (not_193_out, OP3);
  not not_194 (not_194_out, OP2);
  not not_195 (not_195_out, OP1);
  not not_196 (not_196_out, OP0);
  not not_197 (not_197_out, F4);
  not not_198 (not_198_out, F2);
  not not_199 (not_199_out, OP5);
  not not_200 (not_200_out, OP4);
  not not_201 (not_201_out, OP2);
  not not_202 (not_202_out, OP1);
  not not_203 (not_203_out, OP0);
  not not_204 (not_204_out, OP5);
  not not_205 (not_205_out, OP4);
  not not_206 (not_206_out, OP1);
  not not_207 (not_207_out, OP0);
  not not_208 (not_208_out, OP5);
  not not_209 (not_209_out, OP4);
  not not_210 (not_210_out, OP2);
  not not_211 (not_211_out, OP1);
  not not_212 (not_212_out, OP4);
  not not_213 (not_213_out, OP3);
  not not_214 (not_214_out, OP2);
  not not_215 (not_215_out, OP4);
  not not_216 (not_216_out, OP2);
  not not_217 (not_217_out, OP5);
  not not_218 (not_218_out, OP4);
  not not_219 (not_219_out, OP2);
  not not_220 (not_220_out, OP4);
  not not_221 (not_221_out, OP2);
  not not_222 (not_222_out, OP1);
  not not_223 (not_223_out, OP0);
  not not_224 (not_224_out, OP5);
  not not_225 (not_225_out, OP4);
  not not_226 (not_226_out, OP3);
  not not_227 (not_227_out, OP2);
  not not_228 (not_228_out, OP1);
  not not_229 (not_229_out, OP0);
  not not_230 (not_230_out, F4);
  not not_231 (not_231_out, F3);
  not not_232 (not_232_out, F1);
  not not_233 (not_233_out, OP5);
  not not_234 (not_234_out, OP4);
  not not_235 (not_235_out, OP3);
  not not_236 (not_236_out, OP2);
  not not_237 (not_237_out, OP1);
  not not_238 (not_238_out, OP0);
  not not_239 (not_239_out, F4);
  not not_240 (not_240_out, F3);
  not not_241 (not_241_out, OP5);
  not not_242 (not_242_out, OP4);
  not not_243 (not_243_out, OP3);
  not not_244 (not_244_out, OP2);
  not not_245 (not_245_out, OP1);
  not not_246 (not_246_out, OP0);
  not not_247 (not_247_out, F4);
  not not_248 (not_248_out, F2);
  not not_249 (not_249_out, F0);
  not not_250 (not_250_out, OP5);
  not not_251 (not_251_out, OP4);
  not not_252 (not_252_out, OP3);
  not not_253 (not_253_out, OP2);
  not not_254 (not_254_out, OP1);
  not not_255 (not_255_out, OP0);
  not not_256 (not_256_out, F4);
  not not_257 (not_257_out, F2);
  not not_258 (not_258_out, OP5);
  not not_259 (not_259_out, OP4);
  not not_260 (not_260_out, OP2);
  not not_261 (not_261_out, OP0);
  not not_262 (not_262_out, OP5);
  not not_263 (not_263_out, OP4);
  not not_264 (not_264_out, OP1);
  not not_265 (not_265_out, OP5);
  not not_266 (not_266_out, OP4);
  not not_267 (not_267_out, OP2);
  not not_268 (not_268_out, OP5);
  not not_269 (not_269_out, OP4);
  not not_270 (not_270_out, OP3);
  not not_271 (not_271_out, OP0);
  and and_1 (and_1_out, not_1_out, not_2_out, not_3_out, not_4_out, not_5_out, not_6_out, not_7_out, not_8_out, not_9_out, not_10_out, F1, F0);
  and and_2 (and_2_out, not_11_out, not_12_out, not_13_out, not_14_out, not_15_out, not_16_out, F5, not_17_out, not_18_out, not_19_out, not_20_out, not_21_out);
  and and_3 (and_3_out, not_22_out, not_23_out, not_24_out, not_25_out, not_26_out, not_27_out, F5, not_28_out, not_29_out, not_30_out, not_31_out, F0);
  and and_4 (and_4_out, not_32_out, not_33_out, not_34_out, not_35_out, not_36_out, not_37_out, F5, not_38_out, not_39_out, F2, not_40_out, not_41_out);
  and and_5 (and_5_out, not_42_out, not_43_out, not_44_out, not_45_out, not_46_out, not_47_out, F5, not_48_out, F3, not_49_out, F1, not_50_out);
  and and_6 (and_6_out, not_51_out, not_52_out, OP3, not_53_out, not_54_out, not_55_out);
  and and_7 (and_7_out, not_56_out, not_57_out, OP3, OP2, not_58_out, not_59_out);
  and and_8 (and_8_out, not_60_out, not_61_out, OP3, not_62_out, not_63_out, OP0);
  and and_9 (and_9_out, not_64_out, not_65_out, OP3, not_66_out, OP1, not_67_out);
  and and_10 (and_10_out, OP5, not_68_out, not_69_out, not_70_out, OP1, OP0);
  and and_11 (and_11_out, OP5, not_71_out, OP3, not_72_out, OP1, OP0);
  and and_12 (and_12_out, not_73_out, not_74_out, not_75_out, not_76_out, not_77_out, not_78_out, not_79_out, not_80_out, not_81_out, F2, F1, F0);
  and and_13 (and_13_out, OP5, not_82_out, OP3, not_83_out, not_84_out, not_85_out);
  and and_14 (and_14_out, not_86_out, not_87_out, not_88_out, OP2, OP1, not_89_out);
  and and_15 (and_15_out, not_90_out, not_91_out, not_92_out, not_93_out, not_94_out, not_95_out, not_96_out, not_97_out, not_98_out, not_99_out, F1, not_100_out);
  and and_16 (and_16_out, not_101_out, not_102_out, not_103_out, not_104_out, not_105_out, not_106_out, F5, not_107_out, not_108_out, not_109_out, F1, not_110_out);
  and and_17 (and_17_out, not_111_out, not_112_out, not_113_out, not_114_out, not_115_out, not_116_out, F5, not_117_out, not_118_out, F2, not_119_out, not_120_out);
  and and_18 (and_18_out, not_121_out, not_122_out, not_123_out, not_124_out, not_125_out, not_126_out, F5, not_127_out, not_128_out, F2, F1, F0);
  and and_19 (and_19_out, not_129_out, not_130_out, not_131_out, not_132_out, not_133_out, not_134_out, F5, not_135_out, F3, not_136_out, F1, not_137_out);
  and and_20 (and_20_out, not_138_out, not_139_out, OP3, OP2, not_140_out, not_141_out);
  and and_21 (and_21_out, not_142_out, not_143_out, OP3, not_144_out, OP1, not_145_out);
  and and_22 (and_22_out, not_146_out, not_147_out, not_148_out, OP2, OP1, not_149_out);
  and and_23 (and_23_out, not_150_out, not_151_out, not_152_out, not_153_out, not_154_out, not_155_out, F5, not_156_out, not_157_out, not_158_out, not_159_out, not_160_out);
  and and_24 (and_24_out, not_161_out, not_162_out, not_163_out, not_164_out, not_165_out, not_166_out, F5, not_167_out, not_168_out, not_169_out, not_170_out, F0);
  and and_25 (and_25_out, not_171_out, not_172_out, not_173_out, not_174_out, not_175_out, not_176_out, F5, not_177_out, not_178_out, not_179_out, F1, not_180_out);
  and and_26 (and_26_out, not_181_out, not_182_out, not_183_out, not_184_out, not_185_out, not_186_out, F5, not_187_out, not_188_out, F2, not_189_out, not_190_out);
  and and_27 (and_27_out, not_191_out, not_192_out, not_193_out, not_194_out, not_195_out, not_196_out, F5, not_197_out, F3, not_198_out, F1, F0);
  and and_28 (and_28_out, not_199_out, not_200_out, OP3, not_201_out, not_202_out, not_203_out);
  and and_29 (and_29_out, not_204_out, not_205_out, OP3, OP2, not_206_out, not_207_out);
  and and_30 (and_30_out, not_208_out, not_209_out, OP3, not_210_out, not_211_out, OP0);
  and and_31 (and_31_out, OP5, not_212_out, not_213_out, not_214_out, OP1, OP0);
  and and_32 (and_32_out, OP5, not_215_out, OP3, not_216_out, OP1, OP0);
  and and_33 (and_33_out, not_217_out, not_218_out, OP3, not_219_out, OP1, OP0);
  and and_34 (and_34_out, OP5, not_220_out, OP3, not_221_out, not_222_out, not_223_out);
  and and_35 (and_35_out, not_224_out, not_225_out, not_226_out, not_227_out, not_228_out, not_229_out, F5, not_230_out, not_231_out, F2, not_232_out, F0);
  and and_36 (and_36_out, not_233_out, not_234_out, not_235_out, not_236_out, not_237_out, not_238_out, F5, not_239_out, not_240_out, F2, F1, F0);
  and and_37 (and_37_out, not_241_out, not_242_out, not_243_out, not_244_out, not_245_out, not_246_out, F5, not_247_out, F3, not_248_out, F1, not_249_out);
  and and_38 (and_38_out, not_250_out, not_251_out, not_252_out, not_253_out, not_254_out, not_255_out, F5, not_256_out, F3, not_257_out, F1, F0);
  and and_39 (and_39_out, not_258_out, not_259_out, OP3, not_260_out, OP1, not_261_out);
  and and_40 (and_40_out, not_262_out, not_263_out, OP3, OP2, not_264_out, OP0);
  and and_41 (and_41_out, not_265_out, not_266_out, OP3, not_267_out, OP1, OP0);
  and and_42 (and_42_out, not_268_out, not_269_out, not_270_out, OP2, OP1, not_271_out);
  or or_1 (S1, and_15_out, and_16_out, and_17_out, and_18_out, and_19_out, and_20_out, and_21_out, and_22_out);
  or or_2 (S3, and_35_out, and_36_out, and_37_out, and_38_out, and_39_out, and_40_out, and_41_out, and_42_out);
  or or_3 (S0, and_1_out, and_2_out, and_3_out, and_4_out, and_5_out, and_6_out, and_7_out, and_8_out, and_9_out, and_10_out, and_11_out, and_12_out, and_13_out, and_14_out);
  or or_4 (S2, and_23_out, and_24_out, and_25_out, and_26_out, and_27_out, and_28_out, and_29_out, and_30_out, and_31_out, and_32_out, and_33_out, and_34_out);
endmodule

// 控制信号生成
module \控制信号自动生成  (
  input  OP0,
  input  OP1,
  input  OP2,
  input  OP3,
  input  OP4,
  input  OP5,
  input  F0,
  input  F1,
  input  F2,
  input  F3,
  input  F4,
  input  F5,
  output MemToReg,
  output MemWrite,
  output SB,
  output BLEZ,
  output ALU_SRC,
  output RegWrite,
  output SysCALL,
  output SignedExt,
  output SRAV,
  output RegDst,
  output BEQ,
  output BNE,
  output JR,
  output JUMP,
  output JAL
);

  wire and_2_out, and_3_out, and_6_out, and_7_out, and_8_out, and_9_out, and_10_out, and_11_out, and_12_out,
       and_13_out, and_14_out, and_15_out, and_16_out, and_17_out, and_18_out, and_19_out, and_20_out,
       and_21_out, and_22_out, and_23_out, and_24_out, and_25_out, and_26_out, and_27_out, and_28_out,
       and_29_out, and_30_out, and_31_out, and_32_out, and_33_out, and_34_out, and_36_out, and_37_out,
       and_38_out, and_39_out, and_40_out, and_41_out, and_42_out, and_44_out, and_45_out, and_46_out,
       and_47_out, and_48_out, and_49_out, and_50_out, and_51_out, and_52_out, and_53_out, and_54_out,
       and_55_out, and_59_out, and_60_out, and_61_out, not_1_out, not_2_out, not_3_out, not_4_out, not_5_out,
       not_6_out, not_7_out, not_8_out, not_9_out, not_10_out, not_11_out, not_12_out, not_13_out,
       not_14_out, not_15_out, not_16_out, not_17_out, not_18_out, not_19_out, not_20_out, not_21_out,
       not_22_out, not_23_out, not_24_out, not_25_out, not_26_out, not_27_out, not_28_out, not_29_out,
       not_30_out, not_31_out, not_32_out, not_33_out, not_34_out, not_35_out, not_36_out, not_37_out,
       not_38_out, not_39_out, not_40_out, not_41_out, not_42_out, not_43_out, not_44_out, not_45_out,
       not_46_out, not_47_out, not_48_out, not_49_out, not_50_out, not_51_out, not_52_out, not_53_out,
       not_54_out, not_55_out, not_56_out, not_57_out, not_58_out, not_59_out, not_60_out, not_61_out,
       not_62_out, not_63_out, not_64_out, not_65_out, not_66_out, not_67_out, not_68_out, not_69_out,
       not_70_out, not_71_out, not_72_out, not_73_out, not_74_out, not_75_out, not_76_out, not_77_out,
       not_78_out, not_79_out, not_80_out, not_81_out, not_82_out, not_83_out, not_84_out, not_85_out,
       not_86_out, not_87_out, not_88_out, not_89_out, not_90_out, not_91_out, not_92_out, not_93_out,
       not_94_out, not_95_out, not_96_out, not_97_out, not_98_out, not_99_out, not_100_out, not_101_out,
       not_102_out, not_103_out, not_104_out, not_105_out, not_106_out, not_107_out, not_108_out,
       not_109_out, not_110_out, not_111_out, not_112_out, not_113_out, not_114_out, not_115_out,
       not_116_out, not_117_out, not_118_out, not_119_out, not_120_out, not_121_out, not_122_out,
       not_123_out, not_124_out, not_125_out, not_126_out, not_127_out, not_128_out, not_129_out,
       not_130_out, not_131_out, not_132_out, not_133_out, not_134_out, not_135_out, not_136_out,
       not_137_out, not_138_out, not_139_out, not_140_out, not_141_out, not_142_out, not_143_out,
       not_144_out, not_145_out, not_146_out, not_147_out, not_148_out, not_149_out, not_150_out,
       not_151_out, not_152_out, not_153_out, not_154_out, not_155_out, not_156_out, not_157_out,
       not_158_out, not_159_out, not_160_out, not_161_out, not_162_out, not_163_out, not_164_out,
       not_165_out, not_166_out, not_167_out, not_168_out, not_169_out, not_170_out, not_171_out,
       not_172_out, not_173_out, not_174_out, not_175_out, not_176_out, not_177_out, not_178_out,
       not_179_out, not_180_out, not_181_out, not_182_out, not_183_out, not_184_out, not_185_out,
       not_186_out, not_187_out, not_188_out, not_189_out, not_190_out, not_191_out, not_192_out,
       not_193_out, not_194_out, not_195_out, not_196_out, not_197_out, not_198_out, not_199_out,
       not_200_out, not_201_out, not_202_out, not_203_out, not_204_out, not_205_out, not_206_out,
       not_207_out, not_208_out, not_209_out, not_210_out, not_211_out, not_212_out, not_213_out,
       not_214_out, not_215_out, not_216_out, not_217_out, not_218_out, not_219_out, not_220_out,
       not_221_out, not_222_out, not_223_out, not_224_out, not_225_out, not_226_out, not_227_out,
       not_228_out, not_229_out, not_230_out, not_231_out, not_232_out, not_233_out, not_234_out,
       not_235_out, not_236_out, not_237_out, not_238_out, not_239_out, not_240_out, not_241_out,
       not_242_out, not_243_out, not_244_out, not_245_out, not_246_out, not_247_out, not_248_out,
       not_249_out, not_250_out, not_251_out, not_252_out, not_253_out, not_254_out, not_255_out,
       not_256_out, not_257_out, not_258_out, not_259_out, not_260_out, not_261_out, not_262_out,
       not_263_out, not_264_out, not_265_out, not_266_out, not_267_out, not_268_out, not_269_out,
       not_270_out, not_271_out, not_272_out, not_273_out, not_274_out, not_275_out, not_276_out,
       not_277_out, not_278_out, not_279_out, not_280_out, not_281_out, not_282_out, not_283_out,
       not_284_out, not_285_out, not_286_out, not_287_out, not_288_out, not_289_out, not_290_out,
       not_291_out, not_292_out, not_293_out, not_294_out, not_295_out, not_296_out, not_297_out,
       not_298_out, not_299_out, not_300_out, not_301_out, not_302_out, not_303_out, not_304_out,
       not_305_out, not_306_out, not_307_out, not_308_out, not_309_out, not_310_out, not_311_out,
       not_312_out, not_313_out, not_314_out, not_315_out, not_316_out, not_317_out, not_318_out,
       not_319_out, not_320_out, not_321_out, not_322_out, not_323_out, not_324_out, not_325_out,
       not_326_out, not_327_out, not_328_out, not_329_out, not_330_out, not_331_out, not_332_out,
       not_333_out, not_334_out, not_335_out, not_336_out, not_337_out, not_338_out, not_339_out,
       not_340_out, not_341_out, not_342_out, not_343_out, not_344_out, not_345_out, not_346_out,
       not_347_out, not_348_out, not_349_out, not_350_out, not_351_out, not_352_out, not_353_out,
       not_354_out, not_355_out, not_356_out, not_357_out, not_358_out, not_359_out, not_360_out,
       not_361_out, not_362_out, not_363_out, not_364_out, not_365_out, not_366_out, not_367_out,
       not_368_out, not_369_out, not_370_out, not_371_out, not_372_out, not_373_out, not_374_out,
       not_375_out, not_376_out, not_377_out, not_378_out, not_379_out, not_380_out, not_381_out,
       not_382_out, not_383_out, not_384_out, not_385_out, not_386_out, not_387_out, not_388_out,
       not_389_out, not_390_out, not_391_out, not_392_out, not_393_out, not_394_out, not_395_out,
       not_396_out, not_397_out, not_398_out, not_399_out, not_400_out, not_401_out;

  not not_1 (not_1_out, OP4);
  not not_2 (not_2_out, OP3);
  not not_3 (not_3_out, OP2);
  not not_4 (not_4_out, OP4);
  not not_5 (not_5_out, OP2);
  not not_6 (not_6_out, OP4);
  not not_7 (not_7_out, OP2);
  not not_8 (not_8_out, OP1);
  not not_9 (not_9_out, OP0);
  not not_10 (not_10_out, OP4);
  not not_11 (not_11_out, OP2);
  not not_12 (not_12_out, OP1);
  not not_13 (not_13_out, OP0);
  not not_14 (not_14_out, OP5);
  not not_15 (not_15_out, OP4);
  not not_16 (not_16_out, OP3);
  not not_17 (not_17_out, OP0);
  not not_18 (not_18_out, OP5);
  not not_19 (not_19_out, OP4);
  not not_20 (not_20_out, OP2);
  not not_21 (not_21_out, OP1);
  not not_22 (not_22_out, OP0);
  not not_23 (not_23_out, OP5);
  not not_24 (not_24_out, OP4);
  not not_25 (not_25_out, OP1);
  not not_26 (not_26_out, OP0);
  not not_27 (not_27_out, OP5);
  not not_28 (not_28_out, OP4);
  not not_29 (not_29_out, OP2);
  not not_30 (not_30_out, OP1);
  not not_31 (not_31_out, OP5);
  not not_32 (not_32_out, OP4);
  not not_33 (not_33_out, OP2);
  not not_34 (not_34_out, OP0);
  not not_35 (not_35_out, OP5);
  not not_36 (not_36_out, OP4);
  not not_37 (not_37_out, OP1);
  not not_38 (not_38_out, OP4);
  not not_39 (not_39_out, OP3);
  not not_40 (not_40_out, OP2);
  not not_41 (not_41_out, OP4);
  not not_42 (not_42_out, OP2);
  not not_43 (not_43_out, OP5);
  not not_44 (not_44_out, OP4);
  not not_45 (not_45_out, OP2);
  not not_46 (not_46_out, OP4);
  not not_47 (not_47_out, OP2);
  not not_48 (not_48_out, OP1);
  not not_49 (not_49_out, OP0);
  not not_50 (not_50_out, OP5);
  not not_51 (not_51_out, OP4);
  not not_52 (not_52_out, OP3);
  not not_53 (not_53_out, OP2);
  not not_54 (not_54_out, OP1);
  not not_55 (not_55_out, OP0);
  not not_56 (not_56_out, F5);
  not not_57 (not_57_out, F4);
  not not_58 (not_58_out, F3);
  not not_59 (not_59_out, F2);
  not not_60 (not_60_out, F1);
  not not_61 (not_61_out, F0);
  not not_62 (not_62_out, OP5);
  not not_63 (not_63_out, OP4);
  not not_64 (not_64_out, OP3);
  not not_65 (not_65_out, OP2);
  not not_66 (not_66_out, OP1);
  not not_67 (not_67_out, OP0);
  not not_68 (not_68_out, F5);
  not not_69 (not_69_out, F4);
  not not_70 (not_70_out, F3);
  not not_71 (not_71_out, F2);
  not not_72 (not_72_out, OP5);
  not not_73 (not_73_out, OP4);
  not not_74 (not_74_out, OP3);
  not not_75 (not_75_out, OP2);
  not not_76 (not_76_out, OP1);
  not not_77 (not_77_out, OP0);
  not not_78 (not_78_out, F5);
  not not_79 (not_79_out, F4);
  not not_80 (not_80_out, F3);
  not not_81 (not_81_out, F2);
  not not_82 (not_82_out, F0);
  not not_83 (not_83_out, OP5);
  not not_84 (not_84_out, OP4);
  not not_85 (not_85_out, OP3);
  not not_86 (not_86_out, OP2);
  not not_87 (not_87_out, OP1);
  not not_88 (not_88_out, OP0);
  not not_89 (not_89_out, F4);
  not not_90 (not_90_out, F3);
  not not_91 (not_91_out, F2);
  not not_92 (not_92_out, F1);
  not not_93 (not_93_out, F0);
  not not_94 (not_94_out, OP5);
  not not_95 (not_95_out, OP4);
  not not_96 (not_96_out, OP3);
  not not_97 (not_97_out, OP2);
  not not_98 (not_98_out, OP1);
  not not_99 (not_99_out, OP0);
  not not_100 (not_100_out, F4);
  not not_101 (not_101_out, F3);
  not not_102 (not_102_out, F2);
  not not_103 (not_103_out, F1);
  not not_104 (not_104_out, OP5);
  not not_105 (not_105_out, OP4);
  not not_106 (not_106_out, OP3);
  not not_107 (not_107_out, OP2);
  not not_108 (not_108_out, OP1);
  not not_109 (not_109_out, OP0);
  not not_110 (not_110_out, F4);
  not not_111 (not_111_out, F3);
  not not_112 (not_112_out, F2);
  not not_113 (not_113_out, F0);
  not not_114 (not_114_out, OP5);
  not not_115 (not_115_out, OP4);
  not not_116 (not_116_out, OP3);
  not not_117 (not_117_out, OP2);
  not not_118 (not_118_out, OP1);
  not not_119 (not_119_out, OP0);
  not not_120 (not_120_out, F4);
  not not_121 (not_121_out, F3);
  not not_122 (not_122_out, F1);
  not not_123 (not_123_out, F0);
  not not_124 (not_124_out, OP5);
  not not_125 (not_125_out, OP4);
  not not_126 (not_126_out, OP3);
  not not_127 (not_127_out, OP2);
  not not_128 (not_128_out, OP1);
  not not_129 (not_129_out, OP0);
  not not_130 (not_130_out, F4);
  not not_131 (not_131_out, F3);
  not not_132 (not_132_out, F1);
  not not_133 (not_133_out, OP5);
  not not_134 (not_134_out, OP4);
  not not_135 (not_135_out, OP3);
  not not_136 (not_136_out, OP2);
  not not_137 (not_137_out, OP1);
  not not_138 (not_138_out, OP0);
  not not_139 (not_139_out, F4);
  not not_140 (not_140_out, F3);
  not not_141 (not_141_out, OP5);
  not not_142 (not_142_out, OP4);
  not not_143 (not_143_out, OP3);
  not not_144 (not_144_out, OP2);
  not not_145 (not_145_out, OP1);
  not not_146 (not_146_out, OP0);
  not not_147 (not_147_out, F4);
  not not_148 (not_148_out, F2);
  not not_149 (not_149_out, F0);
  not not_150 (not_150_out, OP5);
  not not_151 (not_151_out, OP4);
  not not_152 (not_152_out, OP3);
  not not_153 (not_153_out, OP2);
  not not_154 (not_154_out, OP1);
  not not_155 (not_155_out, OP0);
  not not_156 (not_156_out, F4);
  not not_157 (not_157_out, F2);
  not not_158 (not_158_out, OP5);
  not not_159 (not_159_out, OP4);
  not not_160 (not_160_out, OP3);
  not not_161 (not_161_out, OP2);
  not not_162 (not_162_out, OP5);
  not not_163 (not_163_out, OP4);
  not not_164 (not_164_out, OP2);
  not not_165 (not_165_out, OP1);
  not not_166 (not_166_out, OP0);
  not not_167 (not_167_out, OP5);
  not not_168 (not_168_out, OP4);
  not not_169 (not_169_out, OP1);
  not not_170 (not_170_out, OP0);
  not not_171 (not_171_out, OP5);
  not not_172 (not_172_out, OP4);
  not not_173 (not_173_out, OP2);
  not not_174 (not_174_out, OP1);
  not not_175 (not_175_out, OP5);
  not not_176 (not_176_out, OP4);
  not not_177 (not_177_out, OP2);
  not not_178 (not_178_out, OP0);
  not not_179 (not_179_out, OP5);
  not not_180 (not_180_out, OP4);
  not not_181 (not_181_out, OP1);
  not not_182 (not_182_out, OP4);
  not not_183 (not_183_out, OP3);
  not not_184 (not_184_out, OP2);
  not not_185 (not_185_out, OP5);
  not not_186 (not_186_out, OP4);
  not not_187 (not_187_out, OP3);
  not not_188 (not_188_out, OP2);
  not not_189 (not_189_out, OP1);
  not not_190 (not_190_out, OP0);
  not not_191 (not_191_out, F5);
  not not_192 (not_192_out, F4);
  not not_193 (not_193_out, F3);
  not not_194 (not_194_out, OP5);
  not not_195 (not_195_out, OP4);
  not not_196 (not_196_out, OP2);
  not not_197 (not_197_out, OP5);
  not not_198 (not_198_out, OP4);
  not not_199 (not_199_out, OP3);
  not not_200 (not_200_out, OP2);
  not not_201 (not_201_out, OP1);
  not not_202 (not_202_out, OP0);
  not not_203 (not_203_out, F5);
  not not_204 (not_204_out, F4);
  not not_205 (not_205_out, F1);
  not not_206 (not_206_out, F0);
  not not_207 (not_207_out, OP5);
  not not_208 (not_208_out, OP4);
  not not_209 (not_209_out, OP2);
  not not_210 (not_210_out, OP1);
  not not_211 (not_211_out, OP0);
  not not_212 (not_212_out, OP5);
  not not_213 (not_213_out, OP4);
  not not_214 (not_214_out, OP2);
  not not_215 (not_215_out, OP1);
  not not_216 (not_216_out, OP5);
  not not_217 (not_217_out, OP4);
  not not_218 (not_218_out, OP2);
  not not_219 (not_219_out, OP0);
  not not_220 (not_220_out, OP4);
  not not_221 (not_221_out, OP3);
  not not_222 (not_222_out, OP2);
  not not_223 (not_223_out, OP4);
  not not_224 (not_224_out, OP2);
  not not_225 (not_225_out, OP5);
  not not_226 (not_226_out, OP4);
  not not_227 (not_227_out, OP2);
  not not_228 (not_228_out, OP4);
  not not_229 (not_229_out, OP2);
  not not_230 (not_230_out, OP1);
  not not_231 (not_231_out, OP0);
  not not_232 (not_232_out, OP5);
  not not_233 (not_233_out, OP4);
  not not_234 (not_234_out, OP3);
  not not_235 (not_235_out, OP2);
  not not_236 (not_236_out, OP1);
  not not_237 (not_237_out, OP0);
  not not_238 (not_238_out, F5);
  not not_239 (not_239_out, F4);
  not not_240 (not_240_out, F3);
  not not_241 (not_241_out, OP5);
  not not_242 (not_242_out, OP4);
  not not_243 (not_243_out, OP3);
  not not_244 (not_244_out, OP2);
  not not_245 (not_245_out, OP1);
  not not_246 (not_246_out, OP0);
  not not_247 (not_247_out, F5);
  not not_248 (not_248_out, F4);
  not not_249 (not_249_out, F3);
  not not_250 (not_250_out, F2);
  not not_251 (not_251_out, F1);
  not not_252 (not_252_out, F0);
  not not_253 (not_253_out, OP5);
  not not_254 (not_254_out, OP4);
  not not_255 (not_255_out, OP3);
  not not_256 (not_256_out, OP2);
  not not_257 (not_257_out, OP1);
  not not_258 (not_258_out, OP0);
  not not_259 (not_259_out, F5);
  not not_260 (not_260_out, F4);
  not not_261 (not_261_out, F3);
  not not_262 (not_262_out, F2);
  not not_263 (not_263_out, OP5);
  not not_264 (not_264_out, OP4);
  not not_265 (not_265_out, OP3);
  not not_266 (not_266_out, OP2);
  not not_267 (not_267_out, OP1);
  not not_268 (not_268_out, OP0);
  not not_269 (not_269_out, F5);
  not not_270 (not_270_out, F4);
  not not_271 (not_271_out, F3);
  not not_272 (not_272_out, F2);
  not not_273 (not_273_out, F0);
  not not_274 (not_274_out, OP5);
  not not_275 (not_275_out, OP4);
  not not_276 (not_276_out, OP3);
  not not_277 (not_277_out, OP2);
  not not_278 (not_278_out, OP1);
  not not_279 (not_279_out, OP0);
  not not_280 (not_280_out, F4);
  not not_281 (not_281_out, F3);
  not not_282 (not_282_out, F2);
  not not_283 (not_283_out, F1);
  not not_284 (not_284_out, F0);
  not not_285 (not_285_out, OP5);
  not not_286 (not_286_out, OP4);
  not not_287 (not_287_out, OP3);
  not not_288 (not_288_out, OP2);
  not not_289 (not_289_out, OP1);
  not not_290 (not_290_out, OP0);
  not not_291 (not_291_out, F4);
  not not_292 (not_292_out, F3);
  not not_293 (not_293_out, F2);
  not not_294 (not_294_out, F1);
  not not_295 (not_295_out, OP5);
  not not_296 (not_296_out, OP4);
  not not_297 (not_297_out, OP3);
  not not_298 (not_298_out, OP2);
  not not_299 (not_299_out, OP1);
  not not_300 (not_300_out, OP0);
  not not_301 (not_301_out, F4);
  not not_302 (not_302_out, F3);
  not not_303 (not_303_out, F2);
  not not_304 (not_304_out, F0);
  not not_305 (not_305_out, OP5);
  not not_306 (not_306_out, OP4);
  not not_307 (not_307_out, OP3);
  not not_308 (not_308_out, OP2);
  not not_309 (not_309_out, OP1);
  not not_310 (not_310_out, OP0);
  not not_311 (not_311_out, F4);
  not not_312 (not_312_out, F3);
  not not_313 (not_313_out, F1);
  not not_314 (not_314_out, F0);
  not not_315 (not_315_out, OP5);
  not not_316 (not_316_out, OP4);
  not not_317 (not_317_out, OP3);
  not not_318 (not_318_out, OP2);
  not not_319 (not_319_out, OP1);
  not not_320 (not_320_out, OP0);
  not not_321 (not_321_out, F4);
  not not_322 (not_322_out, F3);
  not not_323 (not_323_out, F1);
  not not_324 (not_324_out, OP5);
  not not_325 (not_325_out, OP4);
  not not_326 (not_326_out, OP3);
  not not_327 (not_327_out, OP2);
  not not_328 (not_328_out, OP1);
  not not_329 (not_329_out, OP0);
  not not_330 (not_330_out, F4);
  not not_331 (not_331_out, F3);
  not not_332 (not_332_out, OP5);
  not not_333 (not_333_out, OP4);
  not not_334 (not_334_out, OP3);
  not not_335 (not_335_out, OP2);
  not not_336 (not_336_out, OP1);
  not not_337 (not_337_out, OP0);
  not not_338 (not_338_out, F4);
  not not_339 (not_339_out, F2);
  not not_340 (not_340_out, F0);
  not not_341 (not_341_out, OP5);
  not not_342 (not_342_out, OP4);
  not not_343 (not_343_out, OP3);
  not not_344 (not_344_out, OP2);
  not not_345 (not_345_out, OP1);
  not not_346 (not_346_out, OP0);
  not not_347 (not_347_out, F4);
  not not_348 (not_348_out, F2);
  not not_349 (not_349_out, OP5);
  not not_350 (not_350_out, OP4);
  not not_351 (not_351_out, OP3);
  not not_352 (not_352_out, OP2);
  not not_353 (not_353_out, OP1);
  not not_354 (not_354_out, OP0);
  not not_355 (not_355_out, F5);
  not not_356 (not_356_out, F4);
  not not_357 (not_357_out, F3);
  not not_358 (not_358_out, OP5);
  not not_359 (not_359_out, OP4);
  not not_360 (not_360_out, OP3);
  not not_361 (not_361_out, OP1);
  not not_362 (not_362_out, OP0);
  not not_363 (not_363_out, OP5);
  not not_364 (not_364_out, OP4);
  not not_365 (not_365_out, OP3);
  not not_366 (not_366_out, OP1);
  not not_367 (not_367_out, OP5);
  not not_368 (not_368_out, OP4);
  not not_369 (not_369_out, OP3);
  not not_370 (not_370_out, OP2);
  not not_371 (not_371_out, OP1);
  not not_372 (not_372_out, OP0);
  not not_373 (not_373_out, F5);
  not not_374 (not_374_out, F4);
  not not_375 (not_375_out, F2);
  not not_376 (not_376_out, F1);
  not not_377 (not_377_out, F0);
  not not_378 (not_378_out, OP5);
  not not_379 (not_379_out, OP4);
  not not_380 (not_380_out, OP3);
  not not_381 (not_381_out, OP2);
  not not_382 (not_382_out, OP1);
  not not_383 (not_383_out, OP0);
  not not_384 (not_384_out, F5);
  not not_385 (not_385_out, F4);
  not not_386 (not_386_out, F2);
  not not_387 (not_387_out, F1);
  not not_388 (not_388_out, F0);
  not not_389 (not_389_out, OP5);
  not not_390 (not_390_out, OP4);
  not not_391 (not_391_out, OP3);
  not not_392 (not_392_out, OP2);
  not not_393 (not_393_out, OP0);
  not not_394 (not_394_out, OP5);
  not not_395 (not_395_out, OP4);
  not not_396 (not_396_out, OP3);
  not not_397 (not_397_out, OP2);
  not not_398 (not_398_out, OP5);
  not not_399 (not_399_out, OP4);
  not not_400 (not_400_out, OP3);
  not not_401 (not_401_out, OP2);
  and and_1 (MemToReg, OP5, not_1_out, not_2_out, not_3_out, OP1, OP0);
  and and_2 (and_2_out, OP5, not_4_out, OP3, not_5_out, OP1, OP0);
  and and_3 (and_3_out, OP5, not_6_out, OP3, not_7_out, not_8_out, not_9_out);
  and and_4 (SB, OP5, not_10_out, OP3, not_11_out, not_12_out, not_13_out);
  and and_5 (BLEZ, not_14_out, not_15_out, not_16_out, OP2, OP1, not_17_out);
  and and_6 (and_6_out, not_18_out, not_19_out, OP3, not_20_out, not_21_out, not_22_out);
  and and_7 (and_7_out, not_23_out, not_24_out, OP3, OP2, not_25_out, not_26_out);
  and and_8 (and_8_out, not_27_out, not_28_out, OP3, not_29_out, not_30_out, OP0);
  and and_9 (and_9_out, not_31_out, not_32_out, OP3, not_33_out, OP1, not_34_out);
  and and_10 (and_10_out, not_35_out, not_36_out, OP3, OP2, not_37_out, OP0);
  and and_11 (and_11_out, OP5, not_38_out, not_39_out, not_40_out, OP1, OP0);
  and and_12 (and_12_out, OP5, not_41_out, OP3, not_42_out, OP1, OP0);
  and and_13 (and_13_out, not_43_out, not_44_out, OP3, not_45_out, OP1, OP0);
  and and_14 (and_14_out, OP5, not_46_out, OP3, not_47_out, not_48_out, not_49_out);
  and and_15 (and_15_out, not_50_out, not_51_out, not_52_out, not_53_out, not_54_out, not_55_out, not_56_out, not_57_out, not_58_out, not_59_out, not_60_out, not_61_out);
  and and_16 (and_16_out, not_62_out, not_63_out, not_64_out, not_65_out, not_66_out, not_67_out, not_68_out, not_69_out, not_70_out, not_71_out, F1, F0);
  and and_17 (and_17_out, not_72_out, not_73_out, not_74_out, not_75_out, not_76_out, not_77_out, not_78_out, not_79_out, not_80_out, not_81_out, F1, not_82_out);
  and and_18 (and_18_out, not_83_out, not_84_out, not_85_out, not_86_out, not_87_out, not_88_out, F5, not_89_out, not_90_out, not_91_out, not_92_out, not_93_out);
  and and_19 (and_19_out, not_94_out, not_95_out, not_96_out, not_97_out, not_98_out, not_99_out, F5, not_100_out, not_101_out, not_102_out, not_103_out, F0);
  and and_20 (and_20_out, not_104_out, not_105_out, not_106_out, not_107_out, not_108_out, not_109_out, F5, not_110_out, not_111_out, not_112_out, F1, not_113_out);
  and and_21 (and_21_out, not_114_out, not_115_out, not_116_out, not_117_out, not_118_out, not_119_out, F5, not_120_out, not_121_out, F2, not_122_out, not_123_out);
  and and_22 (and_22_out, not_124_out, not_125_out, not_126_out, not_127_out, not_128_out, not_129_out, F5, not_130_out, not_131_out, F2, not_132_out, F0);
  and and_23 (and_23_out, not_133_out, not_134_out, not_135_out, not_136_out, not_137_out, not_138_out, F5, not_139_out, not_140_out, F2, F1, F0);
  and and_24 (and_24_out, not_141_out, not_142_out, not_143_out, not_144_out, not_145_out, not_146_out, F5, not_147_out, F3, not_148_out, F1, not_149_out);
  and and_25 (and_25_out, not_150_out, not_151_out, not_152_out, not_153_out, not_154_out, not_155_out, F5, not_156_out, F3, not_157_out, F1, F0);
  and and_26 (and_26_out, not_158_out, not_159_out, not_160_out, not_161_out, OP1, OP0);
  and and_27 (and_27_out, not_162_out, not_163_out, OP3, not_164_out, not_165_out, not_166_out);
  and and_28 (and_28_out, not_167_out, not_168_out, OP3, OP2, not_169_out, not_170_out);
  and and_29 (and_29_out, not_171_out, not_172_out, OP3, not_173_out, not_174_out, OP0);
  and and_30 (and_30_out, not_175_out, not_176_out, OP3, not_177_out, OP1, not_178_out);
  and and_31 (and_31_out, not_179_out, not_180_out, OP3, OP2, not_181_out, OP0);
  and and_32 (and_32_out, OP5, not_182_out, not_183_out, not_184_out, OP1, OP0);
  and and_33 (and_33_out, not_185_out, not_186_out, not_187_out, not_188_out, not_189_out, not_190_out, not_191_out, not_192_out, not_193_out, F2, F1, F0);
  and and_34 (and_34_out, not_194_out, not_195_out, OP3, not_196_out, OP1, OP0);
  and and_35 (SysCALL, not_197_out, not_198_out, not_199_out, not_200_out, not_201_out, not_202_out, not_203_out, not_204_out, F3, F2, not_205_out, not_206_out);
  and and_36 (and_36_out, not_207_out, not_208_out, OP3, not_209_out, not_210_out, not_211_out);
  and and_37 (and_37_out, not_212_out, not_213_out, OP3, not_214_out, not_215_out, OP0);
  and and_38 (and_38_out, not_216_out, not_217_out, OP3, not_218_out, OP1, not_219_out);
  and and_39 (and_39_out, OP5, not_220_out, not_221_out, not_222_out, OP1, OP0);
  and and_40 (and_40_out, OP5, not_223_out, OP3, not_224_out, OP1, OP0);
  and and_41 (and_41_out, not_225_out, not_226_out, OP3, not_227_out, OP1, OP0);
  and and_42 (and_42_out, OP5, not_228_out, OP3, not_229_out, not_230_out, not_231_out);
  and and_43 (SRAV, not_232_out, not_233_out, not_234_out, not_235_out, not_236_out, not_237_out, not_238_out, not_239_out, not_240_out, F2, F1, F0);
  and and_44 (and_44_out, not_241_out, not_242_out, not_243_out, not_244_out, not_245_out, not_246_out, not_247_out, not_248_out, not_249_out, not_250_out, not_251_out, not_252_out);
  and and_45 (and_45_out, not_253_out, not_254_out, not_255_out, not_256_out, not_257_out, not_258_out, not_259_out, not_260_out, not_261_out, not_262_out, F1, F0);
  and and_46 (and_46_out, not_263_out, not_264_out, not_265_out, not_266_out, not_267_out, not_268_out, not_269_out, not_270_out, not_271_out, not_272_out, F1, not_273_out);
  and and_47 (and_47_out, not_274_out, not_275_out, not_276_out, not_277_out, not_278_out, not_279_out, F5, not_280_out, not_281_out, not_282_out, not_283_out, not_284_out);
  and and_48 (and_48_out, not_285_out, not_286_out, not_287_out, not_288_out, not_289_out, not_290_out, F5, not_291_out, not_292_out, not_293_out, not_294_out, F0);
  and and_49 (and_49_out, not_295_out, not_296_out, not_297_out, not_298_out, not_299_out, not_300_out, F5, not_301_out, not_302_out, not_303_out, F1, not_304_out);
  and and_50 (and_50_out, not_305_out, not_306_out, not_307_out, not_308_out, not_309_out, not_310_out, F5, not_311_out, not_312_out, F2, not_313_out, not_314_out);
  and and_51 (and_51_out, not_315_out, not_316_out, not_317_out, not_318_out, not_319_out, not_320_out, F5, not_321_out, not_322_out, F2, not_323_out, F0);
  and and_52 (and_52_out, not_324_out, not_325_out, not_326_out, not_327_out, not_328_out, not_329_out, F5, not_330_out, not_331_out, F2, F1, F0);
  and and_53 (and_53_out, not_332_out, not_333_out, not_334_out, not_335_out, not_336_out, not_337_out, F5, not_338_out, F3, not_339_out, F1, not_340_out);
  and and_54 (and_54_out, not_341_out, not_342_out, not_343_out, not_344_out, not_345_out, not_346_out, F5, not_347_out, F3, not_348_out, F1, F0);
  and and_55 (and_55_out, not_349_out, not_350_out, not_351_out, not_352_out, not_353_out, not_354_out, not_355_out, not_356_out, not_357_out, F2, F1, F0);
  and and_56 (BEQ, not_358_out, not_359_out, not_360_out, OP2, not_361_out, not_362_out);
  and and_57 (BNE, not_363_out, not_364_out, not_365_out, OP2, not_366_out, OP0);
  and and_58 (JR, not_367_out, not_368_out, not_369_out, not_370_out, not_371_out, not_372_out, not_373_out, not_374_out, F3, not_375_out, not_376_out, not_377_out);
  and and_59 (and_59_out, not_378_out, not_379_out, not_380_out, not_381_out, not_382_out, not_383_out, not_384_out, not_385_out, F3, not_386_out, not_387_out, not_388_out);
  and and_60 (and_60_out, not_389_out, not_390_out, not_391_out, not_392_out, OP1, not_393_out);
  and and_61 (and_61_out, not_394_out, not_395_out, not_396_out, not_397_out, OP1, OP0);
  and and_62 (JAL, not_398_out, not_399_out, not_400_out, not_401_out, OP1, OP0);
  or or_1 (MemWrite, and_2_out, and_3_out);
  or or_2 (ALU_SRC, and_6_out, and_7_out, and_8_out, and_9_out, and_10_out, and_11_out, and_12_out, and_13_out, and_14_out);
  or or_3 (SignedExt, and_36_out, and_37_out, and_38_out, and_39_out, and_40_out, and_41_out, and_42_out);
  or or_4 (JUMP, and_59_out, and_60_out, and_61_out);
  or or_5 (RegWrite, and_15_out, and_16_out, and_17_out, and_18_out, and_19_out, and_20_out, and_21_out, and_22_out, and_23_out, and_24_out, and_25_out, and_26_out, and_27_out, and_28_out, and_29_out, and_30_out, and_31_out, and_32_out, and_33_out, and_34_out);
  or or_6 (RegDst, and_44_out, and_45_out, and_46_out, and_47_out, and_48_out, and_49_out, and_50_out, and_51_out, and_52_out, and_53_out, and_54_out, and_55_out);
endmodule

// ALU
module MIPS_ALU (
  input  [4:0] shamt,
  input  [31:0] X,
  input  [31:0] Y,
  input  [3:0] AluOP,
  output Equal,
  output [31:0] Result,
  output [31:0] Result_2
);

  wire [0:0] comparator_1_lt, comparator_2_lt;
  wire [31:0] adder_1_out, AND_out, divider_1_out, divider_1_rem, multiplier_1_cout, multiplier_1_out,
       NOR_out, OR_out, shifter_1_out, shifter_2_out, shifter_3_out, subtractor_1_out, XOR_out;

  assign AND_out = X & Y;  // AND_Gate AND, 32 bits wide
  assign OR_out = X | Y;  // OR_Gate OR, 32 bits wide
  Shifter #(.width(32), .shift("ll")) shifter_1 (.in(Y), .\dist (shamt), .out(shifter_1_out));
  Shifter #(.width(32), .shift("ar")) shifter_2 (.in(Y), .\dist (shamt), .out(shifter_2_out));
  Shifter #(.width(32), .shift("lr")) shifter_3 (.in(Y), .\dist (shamt), .out(shifter_3_out));
  Multiplier #(.width(32)) multiplier_1 (.a(X), .b(Y), .out(multiplier_1_out), .cout(multiplier_1_cout));  // open: cin
  Divider #(.width(32)) divider_1 (.a(X), .b(Y), .out(divider_1_out), .rem(divider_1_rem));  // open: upper
  Adder #(.width(32)) adder_1 (.a(X), .b(Y), .out(adder_1_out));  // open: cin, cout
  Subtractor #(.width(32)) subtractor_1 (.a(X), .b(Y), .out(subtractor_1_out));  // open: bin, bout
  assign XOR_out = X ^ Y;  // XOR_Gate XOR, 32 bits wide
  assign NOR_out = ~(X | Y);  // NOR_Gate NOR, 32 bits wide
  Comparator #(.width(32), .mode("twosComplement")) comparator_1 (
    .a(X), .b(Y), .eq(Equal), .lt(comparator_1_lt[0]));  // open: gt
  Comparator #(.width(32), .mode("unsigned")) comparator_2 (.a(X), .b(Y), .lt(comparator_2_lt[0]));  // open: gt, eq
  Multiplexer #(.select(4), .width(32), .disabled("Z"), .enable("false")) multiplexer_1 (
    .in0(shifter_1_out), .in1(shifter_2_out), .in2(shifter_3_out), .in3(multiplier_1_out),
    .in4(divider_1_out), .in5(adder_1_out), .in6(subtractor_1_out), .in7(AND_out), .in8(OR_out),
    .in9(XOR_out), .in10(NOR_out), .in11({{31{1'b0}}, comparator_1_lt[0]}),
    .in12({{31{1'b0}}, comparator_2_lt[0]}), .in13({32{1'b0}}), .in14({32{1'b0}}), .in15({32{1'b0}}),
    .out(Result), .sel(AluOP));
  Multiplexer #(.select(4), .width(32), .disabled("Z"), .enable("false")) multiplexer_2 (
    .in0({32{1'b0}}), .in1({32{1'b0}}), .in2({32{1'b0}}), .in3(multiplier_1_cout), .in4(divider_1_rem),
    .in5({32{1'b0}}), .in6({32{1'b0}}), .in7({32{1'b0}}), .in8({32{1'b0}}), .in9({32{1'b0}}),
    .in10({32{1'b0}}), .in11({32{1'b0}}), .in12({32{1'b0}}), .in13({32{1'b0}}), .in14({32{1'b0}}),
    .in15({32{1'b0}}), .out(Result_2), .sel(AluOP));

  // Other names for the same wires on the sheet: Result2[31:0] = Result_2; S[3:0] = AluOP

  // Notes on the sheet:
  //   不要改变此引脚区域内容，也不要改变ALU封装形式
  //   输入引脚
  //   输出引脚
endmodule

module MIPS_Regifile (
  input  [31:0] Din,
  input  Clk,
  input  WE,
  input  [4:0] R1_num,
  input  [4:0] W_num,
  input  [4:0] R2_num,
  output [31:0] R1,
  output [31:0] R2
);

  // RegisterFile registerfile_1: pin names not known; wires that end beside it: Din, Clk, WE, W_num, R1_num, R2_num, R1, R2
endmodule

module \理想流水线  (
  output RegWrite,
  output MemWrite,
  output [31:0] IF_PC,
  output [31:0] ID_PC,
  output [31:0] EX_PC,
  output [31:0] M_PC,
  output [31:0] WB_PC,
  output [31:0] RDin,
  output [31:0] MDin,
  output [31:0] LedData
);

  wire and_1_out, and_2_out, and_3_out, and_4_out, and_5_out, CLK, clock_1_out, clock_2_out, comparator_1_eq,
       comparator_1_lt, comparator_2_eq, comparator_3_eq, d_ff_1_q, ex_mem_1_out_19, ex_mem_1_out_23,
       ex_mem_1_out_24, ex_mem_1_out_25, Go, Halt, id_ex_1_out_31, id_ex_1_out_32, id_ex_1_out_33,
       id_ex_1_out_34, id_ex_1_out_36, id_ex_1_out_37, id_ex_1_out_39, id_ex_1_out_41, id_ex_1_out_42,
       id_ex_1_out_43, id_ex_1_out_44, id_ex_1_out_45, id_ex_1_out_46, IR1, IR2, IR3, mem_wb_1_out_16,
       mem_wb_1_out_17, mem_wb_1_out_21, mips_alu_1_equal, nand_1_out, not_1_out, not_2_out, not_3_out,
       or_1_out, or_2_out, or_3_out, regw_EX, regw_MEM, RST, W1, W2, W3, \单周期硬布线控制器_1_alu_src ,
       \单周期硬布线控制器_1_beq , \单周期硬布线控制器_1_blez , \单周期硬布线控制器_1_bne , \单周期硬布线控制器_1_jal , \单周期硬布线控制器_1_jmp ,
       \单周期硬布线控制器_1_jr , \单周期硬布线控制器_1_memtoreg , \单周期硬布线控制器_1_memwrite , \单周期硬布线控制器_1_regdst ,
       \单周期硬布线控制器_1_regwrite , \单周期硬布线控制器_1_sb , \单周期硬布线控制器_1_signedext , \单周期硬布线控制器_1_srav ,
       \单周期硬布线控制器_1_syscall , \总复位_2_out ;
  wire [3:0] id_ex_1_out_35, \单周期硬布线控制器_1_alu_op ;
  wire [4:0] id_ex_1_out_27, id_ex_1_out_47, mem_wb_1_out_13, multiplexer_7_out, multiplexer_8_out,
       multiplexer_11_out, R1_num, R2_num, W__EX, W__MEM;
  wire [12:0] CNT_num;
  wire [15:0] id_ex_1_out_49, \LoadUse次数 , \总周期数 , \插入气泡数 , \无条件分支数 , \条件分支成功数 ;
  wire [31:0] adder_1_out, adder_2_out, adder_3_out, adder_4_out, bit_extender_1_out, bit_extender_2_out,
       EX_IR, ex_mem_1_out_20, ex_mem_1_out_21, id_ex_1_out_48, ID_IR, IF_IR, MEM_IR, mem_wb_1_out_18,
       mem_wb_1_out_19, mips_alu_1_result, mips_regifile_1_r1, mips_regifile_1_r2, multiplexer_1_out,
       multiplexer_2_out, multiplexer_3_out, multiplexer_4_out, multiplexer_10_out, multiplexer_12_out,
       multiplexer_13_out, multiplexer_14_out, multiplexer_16_out, ram_1_data, shifter_1_out, WB_IR;
  wire [31:5] id_ex_1_out_47_2;

  Button \u_总复位  (.out(RST));
  Button _1 (.out(IR1));
  Button button_1 (.out(IR2));
  Button button_2 (.out(IR3));
  // Probe on \总周期数 
  // Probe on \总周期数 
  Button \u_继续运行  (.out(Go));
  LED #(.active("true")) led_1 (.in(W1));
  LED #(.active("true")) led_2 (.in(W2));
  LED #(.active("true")) led_3 (.in(W3));
  not not_1 (not_1_out, Halt);
  Button \u_总复位_2  (.out(\总复位_2_out ));
  Hex_Digit_Display hex_digit_display_1 (.value(LedData[31:28]));  // open: dp
  // Probe on IF_PC[19:0]
  // Mips_Probe mips_probe_1: pin names not known; wires that end beside it: IF_IR
  Multiplexer #(.select(1), .width(32), .disabled("Z"), .enable("false")) multiplexer_1 (
    .in0(adder_1_out), .in1(adder_3_out), .out(multiplexer_1_out), .sel(and_3_out));
  Multiplexer #(.select(1), .width(32), .disabled("Z"), .enable("false")) multiplexer_2 (
    .in0(multiplexer_1_out), .in1(adder_3_out), .out(multiplexer_2_out), .sel(or_3_out));
  Multiplexer #(.select(1), .width(32), .disabled("Z"), .enable("false")) multiplexer_3 (
    .in0(multiplexer_2_out), .in1({IF_PC[31:28], EX_IR[25:0], 2'b00}), .out(multiplexer_3_out),
    .sel(id_ex_1_out_45));
  Multiplexer #(.select(1), .width(32), .disabled("Z"), .enable("false")) multiplexer_4 (
    .in0(multiplexer_3_out), .in1({id_ex_1_out_47_2, id_ex_1_out_47}), .out(multiplexer_4_out),
    .sel(id_ex_1_out_46));
  Register #(.width(32), .trigger("rising"), .Select("low")) PC (
    .D(multiplexer_4_out), .en(Halt), .Q(IF_PC), .clk(CLK), .clr(\总复位_2_out ));
  Hex_Digit_Display hex_digit_display_2 (.value(LedData[27:24]));  // open: dp
  Hex_Digit_Display hex_digit_display_3 (.value(LedData[23:20]));  // open: dp
  // Probe on ID_PC[19:0]
  // Mips_Probe mips_probe_2: pin names not known; wires that end beside it: ID_IR
  Counter #(.width(16), .max('hffff), .ongoal("wrap"), .trigger("rising"), .behavior("old")) counter_1 (
    .count(Halt), .Q(\总周期数 ), .clk(CLK), .clr(\总复位_2_out ));  // open: load, D, carry, preset
  Hex_Digit_Display hex_digit_display_4 (.value(LedData[19:16]));  // open: dp
  Hex_Digit_Display hex_digit_display_5 (.value(LedData[15:12]));  // open: dp
  Hex_Digit_Display hex_digit_display_6 (.value(LedData[7:4]));  // open: dp
  Hex_Digit_Display hex_digit_display_7 (.value(LedData[11:8]));  // open: dp
  Clock #(.highDuration(1), .lowDuration(1)) clock_1 (.out(clock_1_out));
  // Probe on EX_PC[19:0]
  // Mips_Probe mips_probe_3: pin names not known; wires that end beside it: clock_1_out, EX_IR, CLK
  ROM #(.addrWidth(10), .dataWidth(32), .Select("high")) rom_1 (.addr(IF_PC[11:2]), .data(IF_IR));
  Adder #(.width(32)) adder_1 (.a(IF_PC), .b(32'h4), .out(adder_1_out));  // open: cin, cout
  Hex_Digit_Display hex_digit_display_8 (.value(LedData[3:0]));  // open: dp
  IF_ID if_id_1 (
    .in_1(CLK), .in_2(not_1_out), .in_3(\总复位_2_out ), .in_4(IF_IR), .in_5(IF_PC), .out_6(ID_IR), .out_7(ID_PC));
  // Probe on \总周期数 
  // Probe on M_PC[19:0]
  // Mips_Probe mips_probe_4: pin names not known; wires that end beside it: MEM_IR
  // Probe on \总周期数 
  // Probe on \无条件分支数 
  // Probe on \条件分支成功数 
  // Probe on \插入气泡数 
  // Probe on \LoadUse次数 
  // Probe on IF_PC[11:0]
  // Probe on WB_PC[19:0]
  // Mips_Probe mips_probe_5: pin names not known; wires that end beside it: WB_IR
  // Probe on ID_PC[11:0]
  // Probe on EX_PC[11:0]
  // Probe on M_PC[11:0]
  \单周期硬布线控制器  \u_单周期硬布线控制器_1  (
    .Func(ID_IR[5:0]), .OP(ID_IR[31:26]), .ALU_OP(\单周期硬布线控制器_1_alu_op ), .MemToReg(\单周期硬布线控制器_1_memtoreg ),
    .MemWrite(\单周期硬布线控制器_1_memwrite ), .ALU_SRC(\单周期硬布线控制器_1_alu_src ), .RegWrite(\单周期硬布线控制器_1_regwrite ),
    .SysCALL(\单周期硬布线控制器_1_syscall ), .SignedExt(\单周期硬布线控制器_1_signedext ), .RegDst(\单周期硬布线控制器_1_regdst ),
    .JR(\单周期硬布线控制器_1_jr ), .JMP(\单周期硬布线控制器_1_jmp ), .Beq(\单周期硬布线控制器_1_beq ), .JAL(\单周期硬布线控制器_1_jal ),
    .Bne(\单周期硬布线控制器_1_bne ), .SRAV(\单周期硬布线控制器_1_srav ), .SB(\单周期硬布线控制器_1_sb ), .BLEZ(\单周期硬布线控制器_1_blez ));
  Multiplexer #(.select(1), .width(5), .disabled("Z"), .enable("false")) multiplexer_5 (
    .in0(ID_IR[25:21]), .in1(5'b00100), .out(R1_num), .sel(\单周期硬布线控制器_1_syscall ));
  Multiplexer #(.select(1), .width(5), .disabled("Z"), .enable("false")) multiplexer_6 (
    .in0(ID_IR[20:16]), .in1(5'b00010), .out(R2_num), .sel(\单周期硬布线控制器_1_syscall ));
  Multiplexer #(.select(1), .width(5), .disabled("Z"), .enable("false")) multiplexer_7 (
    .in0(ID_IR[20:16]), .in1(ID_IR[15:11]), .out(multiplexer_7_out), .sel(\单周期硬布线控制器_1_regdst ));
  Adder #(.width(32)) adder_2 (.a(EX_PC), .b(32'h4), .out(adder_2_out));  // open: cin, cout
  // Probe on WB_PC[11:0]
  D_Flip_Flop #(.trigger("high"), .Pre_Clr_Positions("LEGACY"), .NegatePresetClear("false"), .enable("true"), .NewFFLayout("false")) d_ff_1 (
    .Q(d_ff_1_q), .reset(1'b1));  // open: clk, D, Qn, preset, en
  Multiplexer #(.select(1), .width(5), .disabled("Z"), .enable("false")) multiplexer_8 (
    .in0(multiplexer_7_out), .in1({5{1'b1}}), .out(multiplexer_8_out), .sel(\单周期硬布线控制器_1_jal ));
  // Probe on 13'hf
  Clock #(.highDuration(1), .lowDuration(1)) clock_2 (.out(clock_2_out));
  Multiplexer #(.select(1), .width(32), .disabled("Z"), .enable("false")) multiplexer_9 (
    .in0(multiplexer_13_out), .in1(adder_4_out), .out(RDin), .sel(mem_wb_1_out_17));
  Shifter #(.width(32), .shift("ll")) shifter_1 (.in(bit_extender_2_out), .\dist (5'b00010), .out(shifter_1_out));
  Comparator #(.width(13), .mode("twosComplement")) comparator_1 (
    .a(CNT_num), .b(13'hf), .eq(comparator_1_eq), .lt(comparator_1_lt));  // open: gt
  MIPS_Regifile mips_regifile_1 (
    .Din(RDin), .Clk(CLK), .R1(mips_regifile_1_r1), .R2(mips_regifile_1_r2), .WE(RegWrite),
    .W_num(mem_wb_1_out_13), .R1_num(R1_num), .R2_num(R2_num));
  Adder #(.width(32)) adder_3 (.a(shifter_1_out), .b(adder_2_out), .out(adder_3_out));  // open: cin, cout
  nand nand_1 (nand_1_out, d_ff_1_q, comparator_1_eq);
  Counter #(.width(13), .max('h1fff), .ongoal("stay"), .trigger("rising"), .behavior("old")) counter_2 (
    .count(comparator_1_lt), .Q(CNT_num), .clk(clock_2_out));  // open: load, D, carry, clr, preset
  ID_EX id_ex_1 (
    .in_1(CLK), .in_2(not_1_out), .in_3(\总复位_2_out ), .in_4(ID_IR), .out_29(EX_IR), .in_5(ID_PC),
    .out_30(EX_PC), .in_6(\单周期硬布线控制器_1_beq ), .out_31(id_ex_1_out_31), .in_7(\单周期硬布线控制器_1_bne ),
    .out_32(id_ex_1_out_32), .in_8(\单周期硬布线控制器_1_memwrite ), .out_33(id_ex_1_out_33),
    .in_9(\单周期硬布线控制器_1_memtoreg ), .out_34(id_ex_1_out_34), .in_10(\单周期硬布线控制器_1_alu_op ),
    .out_35(id_ex_1_out_35), .in_11(\单周期硬布线控制器_1_alu_src ), .out_36(id_ex_1_out_36),
    .in_12(\单周期硬布线控制器_1_signedext ), .out_37(id_ex_1_out_37), .in_13(\单周期硬布线控制器_1_regwrite ),
    .out_38(regw_EX), .in_14(\单周期硬布线控制器_1_jal ), .out_39(id_ex_1_out_39), .in_16(\单周期硬布线控制器_1_syscall ),
    .out_41(id_ex_1_out_41), .in_17(\单周期硬布线控制器_1_blez ), .out_42(id_ex_1_out_42), .in_18(\单周期硬布线控制器_1_srav ),
    .out_43(id_ex_1_out_43), .in_19(\单周期硬布线控制器_1_sb ), .out_44(id_ex_1_out_44), .in_20(\单周期硬布线控制器_1_jmp ),
    .out_45(id_ex_1_out_45), .in_21(\单周期硬布线控制器_1_jr ), .out_46(id_ex_1_out_46), .in_24(mips_regifile_1_r1),
    .out_47({id_ex_1_out_47_2, id_ex_1_out_47}), .in_25(mips_regifile_1_r2), .out_48(id_ex_1_out_48),
    .in_26(ID_IR[15:0]), .out_49(id_ex_1_out_49), .in_22(ID_IR[10:6]), .in_23(multiplexer_8_out),
    .out_27(id_ex_1_out_27), .out_28(W__EX));  // open: in_15, out_40
  assign CLK = nand_1_out ? clock_2_out : 1'bz;  // Controlled_Buffer controlled_buffer_1
  Pull_Resistor #(.pull(1)) pull_resistor_1 (.node(CLK));
  Multiplexer #(.select(1), .width(32), .disabled("Z"), .enable("false")) multiplexer_10 (
    .in0(id_ex_1_out_48), .in1(multiplexer_14_out), .out(multiplexer_10_out), .sel(id_ex_1_out_36));
  Multiplexer #(.select(1), .width(5), .disabled("Z"), .enable("false")) multiplexer_11 (
    .in0(id_ex_1_out_27), .in1(id_ex_1_out_47), .out(multiplexer_11_out), .sel(id_ex_1_out_43));
  Comparator #(.width(32), .mode("twosComplement")) comparator_2 (
    .a(32'h1), .b(id_ex_1_out_48), .eq(comparator_2_eq));  // open: gt, lt
  Comparator #(.width(32), .mode("twosComplement")) comparator_3 (
    .a(32'h22), .b(id_ex_1_out_48), .eq(comparator_3_eq));  // open: gt, lt
  Multiplexer #(.select(1), .width(32), .disabled("Z"), .enable("false")) multiplexer_12 (
    .in0(multiplexer_10_out), .in1({32{1'b0}}), .out(multiplexer_12_out), .sel(id_ex_1_out_42));
  assign bit_extender_1_out = {{16{1'b0}}, id_ex_1_out_49};  // Bit_Extender bit_extender_1
  assign bit_extender_2_out = {{16{id_ex_1_out_49[15]}}, id_ex_1_out_49};  // Bit_Extender bit_extender_2
  or or_1 (or_1_out, comparator_2_eq, comparator_3_eq);
  MIPS_ALU mips_alu_1 (
    .X({id_ex_1_out_47_2, id_ex_1_out_47}), .Y(multiplexer_12_out), .AluOP(id_ex_1_out_35),
    .Equal(mips_alu_1_equal), .Result(mips_alu_1_result), .shamt(multiplexer_11_out));  // open: Result_2
  Multiplexer #(.select(1), .width(32), .disabled("Z"), .enable("false")) multiplexer_13 (
    .in0(mem_wb_1_out_19), .in1(mem_wb_1_out_18), .out(multiplexer_13_out), .sel(mem_wb_1_out_16));
  Multiplexer #(.select(1), .width(32), .disabled("Z"), .enable("false")) multiplexer_14 (
    .in0(bit_extender_1_out), .in1(bit_extender_2_out), .out(multiplexer_14_out), .sel(id_ex_1_out_37));
  not not_2 (not_2_out, mips_alu_1_equal);
  EX_MEM ex_mem_1 (
    .in_1(CLK), .in_2(not_1_out), .in_3(\总复位_2_out ), .in_4(EX_IR), .out_16(MEM_IR), .in_5(EX_PC),
    .out_17(M_PC), .in_6(id_ex_1_out_33), .out_18(MemWrite), .in_7(id_ex_1_out_34), .out_19(ex_mem_1_out_19),
    .in_8(id_ex_1_out_48), .out_20(ex_mem_1_out_20), .in_10(regw_EX), .out_22(regw_MEM), .in_12(and_5_out),
    .out_24(ex_mem_1_out_24), .in_13(id_ex_1_out_44), .out_25(ex_mem_1_out_25), .in_9(mips_alu_1_result),
    .out_21(ex_mem_1_out_21), .in_14(W__EX), .out_15(W__MEM), .in_11(id_ex_1_out_39), .out_23(ex_mem_1_out_23));
  and and_1 (and_1_out, mips_alu_1_equal, id_ex_1_out_31);
  and and_2 (and_2_out, id_ex_1_out_32, not_2_out);
  or or_2 (or_2_out, mips_alu_1_equal, mips_alu_1_result[0]);
  and and_3 (and_3_out, or_2_out, id_ex_1_out_42);
  or or_3 (or_3_out, and_1_out, and_2_out);
  not not_3 (not_3_out, or_1_out);
  and and_4 (and_4_out, or_1_out, id_ex_1_out_41);
  and and_5 (and_5_out, not_3_out, id_ex_1_out_41);
  Register #(.width(32), .trigger("rising"), .Select("low")) register_1 (
    .D({id_ex_1_out_47_2, id_ex_1_out_47}), .en(and_4_out), .Q(LedData), .clk(CLK));  // open: clr
  not not_4 (Halt, mem_wb_1_out_21);
  Multiplexer #(.select(1), .width(32), .disabled("Z"), .enable("false")) multiplexer_15 (
    .in0(ex_mem_1_out_20), .in1(multiplexer_16_out), .out(MDin), .sel(ex_mem_1_out_25));
  RAM #(.addrWidth(10), .dataWidth(32), .bus("separate"), .Select("high")) ram_1 (
    .addr(ex_mem_1_out_21[11:2]), .din(MDin), .data(ram_1_data), .str(MemWrite), .clk(CLK), .clr(\总复位_2_out ));  // open: sel, ld
  MEM_WB mem_wb_1 (
    .in_1(CLK), .in_2(not_1_out), .in_3(\总复位_2_out ), .in_4(MEM_IR), .out_14(WB_IR), .in_5(M_PC),
    .out_15(WB_PC), .in_6(ex_mem_1_out_19), .out_16(mem_wb_1_out_16), .in_8(ram_1_data),
    .out_18(mem_wb_1_out_18), .in_9(ex_mem_1_out_21), .out_19(mem_wb_1_out_19), .in_10(regw_MEM),
    .out_20(RegWrite), .in_11(ex_mem_1_out_24), .out_21(mem_wb_1_out_21), .in_12(W__MEM),
    .out_13(mem_wb_1_out_13), .in_7(ex_mem_1_out_23), .out_17(mem_wb_1_out_17));
  Multiplexer #(.select(2), .width(32), .disabled("Z"), .enable("false")) multiplexer_16 (
    .in0({ram_1_data[31:8], ex_mem_1_out_20[7:0]}),
    .in1({ram_1_data[31:16], ex_mem_1_out_20[7:0], ram_1_data[7:0]}),
    .in2({ram_1_data[31:24], ex_mem_1_out_20[7:0], ram_1_data[15:0]}),
    .in3({ex_mem_1_out_20[7:0], ram_1_data[23:0]}), .out(multiplexer_16_out), .sel(mips_alu_1_result[1:0]));
  Adder #(.width(32)) adder_4 (.a(WB_PC), .b(32'h4), .out(adder_4_out));  // open: cin, cout

  // Other names for the same wires on the sheet: MEM_PC[31:0] = M_PC

  // Notes on the sheet:
  //   中断源
  //   中断等待指示
  //   数码管输出
  //   指令存储器
  //   指令字
  //   contents of rom_1 (hex, n*v repeats v):
  //   20100000 20110000 20120000 20130000 36100000 36310001 36520002 36730003 ae100000 ae110004 ae120008
  //   ae13000c 2002000a 20110000 20120000 20130000 c
  //   OP
  //   Func
  //   rs
  //   rt
  //   rd
  //   JMP
  //   JR
  //   SignedExt
  //   SRAV
  //   SB
  //   BLEZ
  //   OP
  //   Func
  //   流水调试日志用
  //   Bne
  //   MemToReg
  //   MemWrite
  //   AluOP
  //   AluSrcB
  //   RegWrite
  //   JAL
  //   RegDst
  //   Syscall
  //   控制位
  //   暂停节拍，不能为0
  //   可计数暂停的时钟源
  //   为方便自动评测，需要输出流水线各段保存的PC值，注意是PC不是PC+4，另外ID段寄存器写入信息，Mem段内存写入信息也要输出
endmodule

module \气泡流水线  (
  output RegWrite,
  output MemWrite,
  output [31:0] IF_PC,
  output [31:0] ID_PC,
  output [31:0] EX_PC,
  output [31:0] M_PC,
  output [31:0] WB_PC,
  output [31:0] RDin,
  output [31:0] MDin,
  output [31:0] LedData
);

  wire and_1_out, and_2_out, and_3_out, and_4_out, and_5_out, and_6_out, and_7_out, and_8_out, and_9_out,
       CLK, clock_1_out, comparator_1_eq, comparator_1_lt, comparator_2_eq, comparator_3_eq, d_ff_1_q,
       ex_mem_1_out_19, ex_mem_1_out_23, ex_mem_1_out_24, ex_mem_1_out_25, Go, Halt, id_ex_1_out_31,
       id_ex_1_out_32, id_ex_1_out_33, id_ex_1_out_34, id_ex_1_out_36, id_ex_1_out_37, id_ex_1_out_39,
       id_ex_1_out_41, id_ex_1_out_42, id_ex_1_out_43, id_ex_1_out_44, id_ex_1_out_45, id_ex_1_out_46, IR1,
       IR2, IR3, mem_wb_1_out_16, mem_wb_1_out_17, mem_wb_1_out_21, mips_alu_1_equal, nand_1_out, not_1_out,
       not_2_out, not_3_out, not_4_out, or_3_out, or_4_out, or_5_out, or_6_out, or_7_out, or_8_out, regw_EX,
       regw_MEM, RST, W1, W2, W3, \单周期硬布线控制器_1_alu_src , \单周期硬布线控制器_1_beq , \单周期硬布线控制器_1_blez ,
       \单周期硬布线控制器_1_bne , \单周期硬布线控制器_1_jal , \单周期硬布线控制器_1_jmp , \单周期硬布线控制器_1_jr , \单周期硬布线控制器_1_memtoreg ,
       \单周期硬布线控制器_1_memwrite , \单周期硬布线控制器_1_regdst , \单周期硬布线控制器_1_regwrite , \单周期硬布线控制器_1_sb ,
       \单周期硬布线控制器_1_signedext , \单周期硬布线控制器_1_srav , \单周期硬布线控制器_1_syscall , \总复位_2_out , \数据相关 , \无条件分支 ,
       \条件分支 ;
  wire [3:0] id_ex_1_out_35, \单周期硬布线控制器_1_alu_op ;
  wire [4:0] id_ex_1_out_27, id_ex_1_out_47, mem_wb_1_out_13, multiplexer_7_out, multiplexer_8_out,
       multiplexer_11_out, R1_num, R2_num, W__EX, W__MEM;
  wire [12:0] CNT_num;
  wire [15:0] id_ex_1_out_49, \LoadUse次数 , \总周期数 , \插入气泡数 , \无条件分支数 , \条件分支成功数 ;
  wire [31:0] adder_1_out, adder_2_out, adder_3_out, adder_4_out, bit_extender_1_out, bit_extender_2_out,
       EX_IR, ex_mem_1_out_20, ex_mem_1_out_21, id_ex_1_out_48, ID_IR, IF_IR, MEM_IR, mem_wb_1_out_18,
       mem_wb_1_out_19, mips_alu_1_result, mips_regifile_1_r1, mips_regifile_1_r2, multiplexer_1_out,
       multiplexer_2_out, multiplexer_3_out, multiplexer_4_out, multiplexer_10_out, multiplexer_12_out,
       multiplexer_13_out, multiplexer_14_out, multiplexer_16_out, ram_1_data, shifter_1_out, WB_IR;
  wire [31:5] id_ex_1_out_47_2;

  Button \u_总复位  (.out(RST));
  Button _1 (.out(IR1));
  Button _2 (.out(IR2));
  Button _3 (.out(IR3));
  // Probe on \总周期数 
  // Probe on \总周期数 
  or or_1 (\条件分支 , or_8_out, and_6_out);
  or or_2 (\无条件分支 , id_ex_1_out_46, id_ex_1_out_45);
  Button \u_继续运行  (.out(Go));
  LED #(.active("true")) led_1 (.in(W1));
  LED #(.active("true")) led_2 (.in(W2));
  LED #(.active("true")) led_3 (.in(W3));
  not not_1 (not_1_out, Halt);
  not not_2 (not_2_out, \数据相关 );
  Button \u_总复位_2  (.out(\总复位_2_out ));
  Hex_Digit_Display hex_digit_display_1 (.value(LedData[31:28]));  // open: dp
  // Probe on IF_PC[19:0]
  // Mips_Probe mips_probe_1: pin names not known; wires that end beside it: IF_IR
  Multiplexer #(.select(1), .width(32), .disabled("Z"), .enable("false")) multiplexer_1 (
    .in0(adder_1_out), .in1(adder_3_out), .out(multiplexer_1_out), .sel(and_6_out));
  Multiplexer #(.select(1), .width(32), .disabled("Z"), .enable("false")) multiplexer_2 (
    .in0(multiplexer_1_out), .in1(adder_3_out), .out(multiplexer_2_out), .sel(or_8_out));
  Multiplexer #(.select(1), .width(32), .disabled("Z"), .enable("false")) multiplexer_3 (
    .in0(multiplexer_2_out), .in1({IF_PC[31:28], EX_IR[25:0], 2'b00}), .out(multiplexer_3_out),
    .sel(id_ex_1_out_45));
  Multiplexer #(.select(1), .width(32), .disabled("Z"), .enable("false")) multiplexer_4 (
    .in0(multiplexer_3_out), .in1({id_ex_1_out_47_2, id_ex_1_out_47}), .out(multiplexer_4_out),
    .sel(id_ex_1_out_46));
  Register #(.width(32), .trigger("rising"), .Select("low")) PC (
    .D(multiplexer_4_out), .en(and_1_out), .Q(IF_PC), .clk(CLK), .clr(\总复位_2_out ));
  and and_1 (and_1_out, Halt, not_2_out);
  Hex_Digit_Display hex_digit_display_2 (.value(LedData[23:20]));  // open: dp
  Hex_Digit_Display hex_digit_display_3 (.value(LedData[27:24]));  // open: dp
  // Probe on ID_PC[19:0]
  // Mips_Probe mips_probe_2: pin names not known; wires that end beside it: ID_IR
  Counter #(.width(16), .max('hffff), .ongoal("wrap"), .trigger("rising"), .behavior("old")) counter_1 (
    .count(Halt), .Q(\总周期数 ), .clk(CLK), .clr(\总复位_2_out ));  // open: load, D, carry, preset
  Hex_Digit_Display hex_digit_display_4 (.value(LedData[19:16]));  // open: dp
  Hex_Digit_Display hex_digit_display_5 (.value(LedData[15:12]));  // open: dp
  Hex_Digit_Display hex_digit_display_6 (.value(LedData[11:8]));  // open: dp
  Hex_Digit_Display hex_digit_display_7 (.value(LedData[7:4]));  // open: dp
  // Probe on EX_PC[19:0]
  // Mips_Probe mips_probe_3: pin names not known; wires that end beside it: EX_IR
  ROM #(.addrWidth(10), .dataWidth(32), .Select("high")) rom_1 (.addr(IF_PC[11:2]), .data(IF_IR));
  Adder #(.width(32)) adder_1 (.a(IF_PC), .b(32'h4), .out(adder_1_out));  // open: cin, cout
  or or_3 (or_3_out, \数据相关 , not_1_out);
  Hex_Digit_Display hex_digit_display_8 (.value(LedData[3:0]));  // open: dp
  IF_ID if_id_1 (
    .in_1(CLK), .in_2(or_3_out), .in_3(or_4_out), .in_4(IF_IR), .in_5(IF_PC), .out_6(ID_IR), .out_7(ID_PC));
  or or_4 (or_4_out, \条件分支 , \总复位_2_out , \无条件分支 );
  // Probe on \总周期数 
  // Probe on M_PC[19:0]
  // Mips_Probe mips_probe_4: pin names not known; wires that end beside it: MEM_IR
  // Probe on \总周期数 
  // Probe on \无条件分支数 
  // Probe on \条件分支成功数 
  // Probe on \插入气泡数 
  // Probe on \LoadUse次数 
  // Probe on IF_PC[11:0]
  // Probe on WB_PC[19:0]
  // Mips_Probe mips_probe_5: pin names not known; wires that end beside it: WB_IR
  // Probe on ID_PC[11:0]
  // Probe on EX_PC[11:0]
  \数据相关检测  \u_数据相关检测_1  (
    .OP(ID_IR[31:26]), .EX_W_num(W__EX), .MEM_W_num(W__MEM), .MEM_regw(regw_MEM), .\数据相关 (\数据相关 ),
    .Func(ID_IR[5:0]), .ID_R1_num(R1_num), .R2used(R2_num), .EX_regw(regw_EX));
  // Probe on M_PC[11:0]
  \单周期硬布线控制器  \u_单周期硬布线控制器_1  (
    .Func(ID_IR[5:0]), .OP(ID_IR[31:26]), .ALU_OP(\单周期硬布线控制器_1_alu_op ), .MemToReg(\单周期硬布线控制器_1_memtoreg ),
    .MemWrite(\单周期硬布线控制器_1_memwrite ), .ALU_SRC(\单周期硬布线控制器_1_alu_src ), .RegWrite(\单周期硬布线控制器_1_regwrite ),
    .SysCALL(\单周期硬布线控制器_1_syscall ), .SignedExt(\单周期硬布线控制器_1_signedext ), .RegDst(\单周期硬布线控制器_1_regdst ),
    .JR(\单周期硬布线控制器_1_jr ), .JMP(\单周期硬布线控制器_1_jmp ), .Beq(\单周期硬布线控制器_1_beq ), .JAL(\单周期硬布线控制器_1_jal ),
    .Bne(\单周期硬布线控制器_1_bne ), .SRAV(\单周期硬布线控制器_1_srav ), .SB(\单周期硬布线控制器_1_sb ), .BLEZ(\单周期硬布线控制器_1_blez ));
  Multiplexer #(.select(1), .width(5), .disabled("Z"), .enable("false")) multiplexer_5 (
    .in0(ID_IR[25:21]), .in1(5'b00100), .out(R1_num), .sel(\单周期硬布线控制器_1_syscall ));
  Multiplexer #(.select(1), .width(5), .disabled("Z"), .enable("false")) multiplexer_6 (
    .in0(ID_IR[20:16]), .in1(5'b00010), .out(R2_num), .sel(\单周期硬布线控制器_1_syscall ));
  Multiplexer #(.select(1), .width(5), .disabled("Z"), .enable("false")) multiplexer_7 (
    .in0(ID_IR[20:16]), .in1(ID_IR[15:11]), .out(multiplexer_7_out), .sel(\单周期硬布线控制器_1_regdst ));
  Adder #(.width(32)) adder_2 (.a(EX_PC), .b(32'h4), .out(adder_2_out));  // open: cin, cout
  // Probe on WB_PC[11:0]
  D_Flip_Flop #(.trigger("high"), .Pre_Clr_Positions("LEGACY"), .NegatePresetClear("false"), .enable("true"), .NewFFLayout("false")) d_ff_1 (
    .Q(d_ff_1_q), .reset(1'b1));  // open: clk, D, Qn, preset, en
  Multiplexer #(.select(1), .width(5), .disabled("Z"), .enable("false")) multiplexer_8 (
    .in0(multiplexer_7_out), .in1({5{1'b1}}), .out(multiplexer_8_out), .sel(\单周期硬布线控制器_1_jal ));
  // Probe on 13'hf
  Clock #(.highDuration(1), .lowDuration(1)) clock_1 (.out(clock_1_out));
  Multiplexer #(.select(1), .width(32), .disabled("Z"), .enable("false")) multiplexer_9 (
    .in0(multiplexer_13_out), .in1(adder_4_out), .out(RDin), .sel(mem_wb_1_out_17));
  Shifter #(.width(32), .shift("ll")) shifter_1 (.in(bit_extender_2_out), .\dist (5'b00010), .out(shifter_1_out));
  Comparator #(.width(13), .mode("twosComplement")) comparator_1 (
    .a(CNT_num), .b(13'hf), .eq(comparator_1_eq), .lt(comparator_1_lt));  // open: gt
  MIPS_Regifile mips_regifile_1 (
    .Din(RDin), .Clk(CLK), .R1(mips_regifile_1_r1), .R2(mips_regifile_1_r2), .WE(RegWrite),
    .W_num(mem_wb_1_out_13), .R1_num(R1_num), .R2_num(R2_num));
  Adder #(.width(32)) adder_3 (.a(shifter_1_out), .b(adder_2_out), .out(adder_3_out));  // open: cin, cout
  nand nand_1 (nand_1_out, d_ff_1_q, comparator_1_eq);
  Counter #(.width(13), .max('h1fff), .ongoal("stay"), .trigger("rising"), .behavior("old")) counter_2 (
    .count(comparator_1_lt), .Q(CNT_num), .clk(clock_1_out));  // open: load, D, carry, clr, preset
  ID_EX id_ex_1 (
    .in_1(CLK), .in_2(not_1_out), .in_3(or_5_out), .in_4(ID_IR), .out_29(EX_IR), .in_5(ID_PC),
    .out_30(EX_PC), .in_6(\单周期硬布线控制器_1_beq ), .out_31(id_ex_1_out_31), .in_7(\单周期硬布线控制器_1_bne ),
    .out_32(id_ex_1_out_32), .in_8(\单周期硬布线控制器_1_memwrite ), .out_33(id_ex_1_out_33),
    .in_9(\单周期硬布线控制器_1_memtoreg ), .out_34(id_ex_1_out_34), .in_10(\单周期硬布线控制器_1_alu_op ),
    .out_35(id_ex_1_out_35), .in_11(\单周期硬布线控制器_1_alu_src ), .out_36(id_ex_1_out_36),
    .in_12(\单周期硬布线控制器_1_signedext ), .out_37(id_ex_1_out_37), .in_13(\单周期硬布线控制器_1_regwrite ),
    .out_38(regw_EX), .in_14(\单周期硬布线控制器_1_jal ), .out_39(id_ex_1_out_39), .in_16(\单周期硬布线控制器_1_syscall ),
    .out_41(id_ex_1_out_41), .in_17(\单周期硬布线控制器_1_blez ), .out_42(id_ex_1_out_42), .in_18(\单周期硬布线控制器_1_srav ),
    .out_43(id_ex_1_out_43), .in_19(\单周期硬布线控制器_1_sb ), .out_44(id_ex_1_out_44), .in_20(\单周期硬布线控制器_1_jmp ),
    .out_45(id_ex_1_out_45), .in_21(\单周期硬布线控制器_1_jr ), .out_46(id_ex_1_out_46), .in_24(mips_regifile_1_r1),
    .out_47({id_ex_1_out_47_2, id_ex_1_out_47}), .in_25(mips_regifile_1_r2), .out_48(id_ex_1_out_48),
    .in_26(ID_IR[15:0]), .out_49(id_ex_1_out_49), .in_22(ID_IR[10:6]), .in_23(multiplexer_8_out),
    .out_27(id_ex_1_out_27), .out_28(W__EX));  // open: in_15, out_40
  or or_5 (or_5_out, \数据相关 , \条件分支 , \无条件分支 , \总复位_2_out );
  assign CLK = nand_1_out ? clock_1_out : 1'bz;  // Controlled_Buffer controlled_buffer_1
  Pull_Resistor #(.pull(1)) pull_resistor_1 (.node(CLK));
  Multiplexer #(.select(1), .width(32), .disabled("Z"), .enable("false")) multiplexer_10 (
    .in0(id_ex_1_out_48), .in1(multiplexer_14_out), .out(multiplexer_10_out), .sel(id_ex_1_out_36));
  Multiplexer #(.select(1), .width(5), .disabled("Z"), .enable("false")) multiplexer_11 (
    .in0(id_ex_1_out_27), .in1(id_ex_1_out_47), .out(multiplexer_11_out), .sel(id_ex_1_out_43));
  Comparator #(.width(32), .mode("twosComplement")) comparator_2 (
    .a(32'h1), .b(id_ex_1_out_48), .eq(comparator_2_eq));  // open: gt, lt
  Comparator #(.width(32), .mode("twosComplement")) comparator_3 (
    .a(32'h22), .b(id_ex_1_out_48), .eq(comparator_3_eq));  // open: gt, lt
  Multiplexer #(.select(1), .width(32), .disabled("Z"), .enable("false")) multiplexer_12 (
    .in0(multiplexer_10_out), .in1({32{1'b0}}), .out(multiplexer_12_out), .sel(id_ex_1_out_42));
  assign bit_extender_1_out = {{16{1'b0}}, id_ex_1_out_49};  // Bit_Extender bit_extender_1
  assign bit_extender_2_out = {{16{id_ex_1_out_49[15]}}, id_ex_1_out_49};  // Bit_Extender bit_extender_2
  or or_6 (or_6_out, comparator_2_eq, comparator_3_eq);
  MIPS_ALU mips_alu_1 (
    .X({id_ex_1_out_47_2, id_ex_1_out_47}), .Y(multiplexer_12_out), .AluOP(id_ex_1_out_35),
    .Equal(mips_alu_1_equal), .Result(mips_alu_1_result), .shamt(multiplexer_11_out));  // open: Result_2
  Multiplexer #(.select(1), .width(32), .disabled("Z"), .enable("false")) multiplexer_13 (
    .in0(mem_wb_1_out_19), .in1(mem_wb_1_out_18), .out(multiplexer_13_out), .sel(mem_wb_1_out_16));
  Multiplexer #(.select(1), .width(32), .disabled("Z"), .enable("false")) multiplexer_14 (
    .in0(bit_extender_1_out), .in1(bit_extender_2_out), .out(multiplexer_14_out), .sel(id_ex_1_out_37));
  Counter #(.width(16), .max('hffff), .ongoal("wrap"), .trigger("rising"), .behavior("old")) counter_3 (
    .count(and_2_out), .Q(\条件分支成功数 ), .clk(CLK), .clr(RST));  // open: load, D, carry, preset
  and and_2 (and_2_out, Halt, \条件分支 );
  Counter #(.width(16), .max('hffff), .ongoal("wrap"), .trigger("rising"), .behavior("old")) counter_4 (
    .count(and_3_out), .Q(\无条件分支数 ), .clk(CLK), .clr(RST));  // open: load, D, carry, preset
  and and_3 (and_3_out, Halt, \无条件分支 );
  not not_3 (not_3_out, mips_alu_1_equal);
  EX_MEM ex_mem_1 (
    .in_1(CLK), .in_2(not_1_out), .in_3(\总复位_2_out ), .in_4(EX_IR), .out_16(MEM_IR), .in_5(EX_PC),
    .out_17(M_PC), .in_6(id_ex_1_out_33), .out_18(MemWrite), .in_7(id_ex_1_out_34), .out_19(ex_mem_1_out_19),
    .in_8(id_ex_1_out_48), .out_20(ex_mem_1_out_20), .in_10(regw_EX), .out_22(regw_MEM), .in_12(and_9_out),
    .out_24(ex_mem_1_out_24), .in_13(id_ex_1_out_44), .out_25(ex_mem_1_out_25), .in_9(mips_alu_1_result),
    .out_21(ex_mem_1_out_21), .in_14(W__EX), .out_15(W__MEM), .in_11(id_ex_1_out_39), .out_23(ex_mem_1_out_23));
  and and_4 (and_4_out, mips_alu_1_equal, id_ex_1_out_31);
  and and_5 (and_5_out, id_ex_1_out_32, not_3_out);
  or or_7 (or_7_out, mips_alu_1_equal, mips_alu_1_result[0]);
  and and_6 (and_6_out, or_7_out, id_ex_1_out_42);
  or or_8 (or_8_out, and_4_out, and_5_out);
  not not_4 (not_4_out, or_6_out);
  and and_7 (and_7_out, or_6_out, id_ex_1_out_41);
  and and_8 (and_8_out, Halt, \数据相关 );
  and and_9 (and_9_out, not_4_out, id_ex_1_out_41);
  Register #(.width(32), .trigger("rising"), .Select("low")) register_1 (
    .D({id_ex_1_out_47_2, id_ex_1_out_47}), .en(and_7_out), .Q(LedData), .clk(CLK));  // open: clr
  Counter #(.width(16), .max('hffff), .ongoal("wrap"), .trigger("rising"), .behavior("old")) counter_5 (
    .count(and_8_out), .Q(\插入气泡数 ), .clk(CLK), .clr(RST));  // open: load, D, carry, preset
  not not_5 (Halt, mem_wb_1_out_21);
  Multiplexer #(.select(1), .width(32), .disabled("Z"), .enable("false")) multiplexer_15 (
    .in0(ex_mem_1_out_20), .in1(multiplexer_16_out), .out(MDin), .sel(ex_mem_1_out_25));
  RAM #(.addrWidth(10), .dataWidth(32), .bus("separate"), .Select("high")) ram_1 (
    .addr(ex_mem_1_out_21[11:2]), .din(MDin), .data(ram_1_data), .str(MemWrite), .clk(CLK), .clr(\总复位_2_out ));  // open: sel, ld
  MEM_WB mem_wb_1 (
    .in_1(CLK), .in_2(not_1_out), .in_3(\总复位_2_out ), .in_4(MEM_IR), .out_14(WB_IR), .in_5(M_PC),
    .out_15(WB_PC), .in_6(ex_mem_1_out_19), .out_16(mem_wb_1_out_16), .in_8(ram_1_data),
    .out_18(mem_wb_1_out_18), .in_9(ex_mem_1_out_21), .out_19(mem_wb_1_out_19), .in_10(regw_MEM),
    .out_20(RegWrite), .in_11(ex_mem_1_out_24), .out_21(mem_wb_1_out_21), .in_12(W__MEM),
    .out_13(mem_wb_1_out_13), .in_7(ex_mem_1_out_23), .out_17(mem_wb_1_out_17));
  Multiplexer #(.select(2), .width(32), .disabled("Z"), .enable("false")) multiplexer_16 (
    .in0({ram_1_data[31:8], ex_mem_1_out_20[7:0]}),
    .in1({ram_1_data[31:16], ex_mem_1_out_20[7:0], ram_1_data[7:0]}),
    .in2({ram_1_data[31:24], ex_mem_1_out_20[7:0], ram_1_data[15:0]}),
    .in3({ex_mem_1_out_20[7:0], ram_1_data[23:0]}), .out(multiplexer_16_out), .sel(mips_alu_1_result[1:0]));
  Adder #(.width(32)) adder_4 (.a(WB_PC), .b(32'h4), .out(adder_4_out));  // open: cin, cout

  // Other names for the same wires on the sheet: MEM_PC[31:0] = M_PC

  // Notes on the sheet:
  //   中断源
  //   时空图监测，可删除
  //   中断等待指示
  //   数码管输出
  //   指令存储器
  //   指令字
  //   contents of rom_1 (hex, n*v repeats v):
  //   20090000 200b0020 20110000 20120001 a1310000 112020 20020022 c 2328820 21290001 216bffff 1560fff8
  //   200b0008 20090000 8d310000 112020 20020022 c 21290004 216bffff 1560fff9 2002000a c
  //   OP
  //   Func
  //   rs
  //   rt
  //   rd
  //   JMP
  //   JR
  //   SignedExt
  //   SRAV
  //   SB
  //   BLEZ
  //   OP
  //   Func
  //   流水调试日志用
  //   Bne
  //   MemToReg
  //   MemWrite
  //   AluOP
  //   AluSrcB
  //   RegWrite
  //   JAL
  //   RegDst
  //   Syscall
  //   控制位
  //   暂停节拍，不能为0
  //   可计数暂停的时钟源
  //   为方便自动评测，需要输出流水线各段保存的PC值，注意是PC不是PC+4，另外ID段寄存器写入信息，Mem段内存写入信息也要输出
endmodule
module \重定向流水线  (
  output RegWrite,
  output MemWrite,
  output [31:0] IF_PC,
  output [31:0] ID_PC,
  output [31:0] EX_PC,
  output [31:0] M_PC,
  output [31:0] WB_PC,
  output [31:0] RDin,
  output [31:0] MDin,
  output [31:0] LedData
);

  wire and_1_out, and_2_out, and_3_out, and_4_out, and_5_out, and_6_out, and_7_out, and_8_out, and_9_out,
       CLK, clock_1_out, comparator_1_eq, comparator_1_lt, comparator_2_eq, comparator_3_eq, d_ff_1_q,
       ex_mem_1_out_23, ex_mem_1_out_24, ex_mem_1_out_25, Go, Halt, id_ex_1_out_31, id_ex_1_out_32,
       id_ex_1_out_33, id_ex_1_out_36, id_ex_1_out_37, id_ex_1_out_39, id_ex_1_out_41, id_ex_1_out_42,
       id_ex_1_out_43, id_ex_1_out_44, id_ex_1_out_45, id_ex_1_out_46, IR1, IR2, IR3, \LoadUse相关 ,
       mem_wb_1_out_16, mem_wb_1_out_17, mem_wb_1_out_21, MemToReg_EX, MemToReg_MEM, mips_alu_1_equal,
       nand_1_out, not_1_out, not_2_out, not_3_out, not_4_out, or_3_out, or_4_out, or_5_out, or_6_out,
       or_7_out, regw_EX, regw_MEM, RST, W1, W2, W3, \单周期硬布线控制器_1_alu_src , \单周期硬布线控制器_1_beq ,
       \单周期硬布线控制器_1_blez , \单周期硬布线控制器_1_bne , \单周期硬布线控制器_1_jal , \单周期硬布线控制器_1_jmp , \单周期硬布线控制器_1_jr ,
       \单周期硬布线控制器_1_memtoreg , \单周期硬布线控制器_1_memwrite , \单周期硬布线控制器_1_regdst , \单周期硬布线控制器_1_regwrite ,
       \单周期硬布线控制器_1_sb , \单周期硬布线控制器_1_signedext , \单周期硬布线控制器_1_srav , \单周期硬布线控制器_1_syscall , \总复位_2_out ,
       \无条件分支 , \条件分支 ;
  wire [1:0] forwardR1, forwardR2;
  wire [3:0] forward, id_ex_1_out_35, \单周期硬布线控制器_1_alu_op ;
  wire [4:0] id_ex_1_out_27, mem_wb_1_out_13, multiplexer_7_out, multiplexer_8_out, multiplexer_13_out,
       R1_num, R2_num, W__EX, W__MEM;
  wire [12:0] CNT_num;
  wire [15:0] id_ex_1_out_49, \LoadUse次数 , \总周期数 , \插入气泡数 , \无条件分支数 , \条件分支成功数 ;
  wire [31:0] A, adder_1_out, adder_2_out, adder_3_out, adder_4_out, ALU_MEM, ALU_WB, B, bit_extender_1_out,
       bit_extender_2_out, EX_IR, ex_mem_1_out_20, ID_IR, IF_IR, MDin_WB, MEM_IR, mips_alu_1_result,
       mips_regifile_1_r1, mips_regifile_1_r2, multiplexer_1_out, multiplexer_2_out, multiplexer_3_out,
       multiplexer_4_out, multiplexer_12_out, multiplexer_14_out, multiplexer_15_out, multiplexer_16_out,
       multiplexer_18_out, R1_EX, R2_EX, ram_1_data, shifter_1_out, WB_IR;

  Button \u_总复位  (.out(RST));
  Button _1 (.out(IR1));
  Button _2 (.out(IR2));
  Button _3 (.out(IR3));
  // Probe on \总周期数 
  // Probe on \总周期数 
  or or_1 (\条件分支 , or_7_out, and_6_out);
  or or_2 (\无条件分支 , id_ex_1_out_46, id_ex_1_out_45);
  Button \u_继续运行  (.out(Go));
  LED #(.active("true")) led_1 (.in(W1));
  LED #(.active("true")) led_2 (.in(W2));
  LED #(.active("true")) led_3 (.in(W3));
  not not_1 (not_1_out, Halt);
  not not_2 (not_2_out, \LoadUse相关 );
  Button \u_总复位_2  (.out(\总复位_2_out ));
  Hex_Digit_Display hex_digit_display_1 (.value(LedData[31:28]));  // open: dp
  // Probe on IF_PC[19:0]
  // Mips_Probe mips_probe_1: pin names not known; wires that end beside it: IF_IR
  Multiplexer #(.select(1), .width(32), .disabled("Z"), .enable("false")) multiplexer_1 (
    .in0(adder_1_out), .in1(adder_3_out), .out(multiplexer_1_out), .sel(and_6_out));
  Multiplexer #(.select(1), .width(32), .disabled("Z"), .enable("false")) multiplexer_2 (
    .in0(multiplexer_1_out), .in1(adder_3_out), .out(multiplexer_2_out), .sel(or_7_out));
  Multiplexer #(.select(1), .width(32), .disabled("Z"), .enable("false")) multiplexer_3 (
    .in0(multiplexer_2_out), .in1({IF_PC[31:28], EX_IR[25:0], 2'b00}), .out(multiplexer_3_out),
    .sel(id_ex_1_out_45));
  Multiplexer #(.select(1), .width(32), .disabled("Z"), .enable("false")) multiplexer_4 (
    .in0(multiplexer_3_out), .in1(A), .out(multiplexer_4_out), .sel(id_ex_1_out_46));
  Register #(.width(32), .trigger("rising"), .Select("low")) PC (
    .D(multiplexer_4_out), .en(and_1_out), .Q(IF_PC), .clk(CLK), .clr(\总复位_2_out ));
  and and_1 (and_1_out, Halt, not_2_out);
  Hex_Digit_Display hex_digit_display_2 (.value(LedData[23:20]));  // open: dp
  Hex_Digit_Display hex_digit_display_3 (.value(LedData[27:24]));  // open: dp
  // Probe on ID_PC[19:0]
  // Mips_Probe mips_probe_2: pin names not known; wires that end beside it: ID_IR
  Counter #(.width(16), .max('hffff), .ongoal("wrap"), .trigger("rising"), .behavior("old")) counter_1 (
    .count(Halt), .Q(\总周期数 ), .clk(CLK), .clr(\总复位_2_out ));  // open: load, D, carry, preset
  Hex_Digit_Display hex_digit_display_4 (.value(LedData[19:16]));  // open: dp
  Hex_Digit_Display hex_digit_display_5 (.value(LedData[15:12]));  // open: dp
  Hex_Digit_Display hex_digit_display_6 (.value(LedData[7:4]));  // open: dp
  Hex_Digit_Display hex_digit_display_7 (.value(LedData[11:8]));  // open: dp
  // Probe on EX_PC[19:0]
  // Mips_Probe mips_probe_3: pin names not known; wires that end beside it: EX_IR
  ROM #(.addrWidth(10), .dataWidth(32), .Select("high")) rom_1 (.addr(IF_PC[11:2]), .data(IF_IR));
  Adder #(.width(32)) adder_1 (.a(IF_PC), .b(32'h4), .out(adder_1_out));  // open: cin, cout
  Hex_Digit_Display hex_digit_display_8 (.value(LedData[3:0]));  // open: dp
  IF_ID if_id_1 (
    .in_1(CLK), .in_2(\LoadUse相关 ), .in_3(or_3_out), .in_4(IF_IR), .in_5(IF_PC), .out_6(ID_IR), .out_7(ID_PC));
  or or_3 (or_3_out, \条件分支 , \总复位_2_out , \无条件分支 );
  // Probe on \总周期数 
  // Probe on M_PC[19:0]
  // Mips_Probe mips_probe_4: pin names not known; wires that end beside it: MEM_IR
  // Probe on \总周期数 
  // Probe on \无条件分支数 
  // Probe on \条件分支成功数 
  // Probe on \插入气泡数 
  // Probe on \LoadUse次数 
  // Probe on IF_PC[11:0]
  // Probe on WB_PC[19:0]
  // Mips_Probe mips_probe_5: pin names not known; wires that end beside it: WB_IR
  // Probe on EX_PC[11:0]
  // Probe on ID_PC[11:0]
  \重定向检测  \u_重定向检测_1  (
    .EX_RegWrite(regw_EX), .EX_MemToReg(MemToReg_EX), .EX_WriteReg_num(W__EX), .OP(ID_IR[31:26]),
    .Func(ID_IR[5:0]), .MEM_RegWrite(regw_MEM), .MEM_MemToReg(MemToReg_MEM), .MEM_W_num(W__MEM),
    .R1_num(R1_num), .Load_use(\LoadUse相关 ), .forwardR1(forward[1:0]), .R2_num(R2_num),
    .forwardR2(forward[3:2]));
  // Probe on M_PC[11:0]
  \单周期硬布线控制器  \u_单周期硬布线控制器_1  (
    .Func(ID_IR[5:0]), .OP(ID_IR[31:26]), .ALU_OP(\单周期硬布线控制器_1_alu_op ), .MemToReg(\单周期硬布线控制器_1_memtoreg ),
    .MemWrite(\单周期硬布线控制器_1_memwrite ), .ALU_SRC(\单周期硬布线控制器_1_alu_src ), .RegWrite(\单周期硬布线控制器_1_regwrite ),
    .SysCALL(\单周期硬布线控制器_1_syscall ), .SignedExt(\单周期硬布线控制器_1_signedext ), .RegDst(\单周期硬布线控制器_1_regdst ),
    .JR(\单周期硬布线控制器_1_jr ), .JMP(\单周期硬布线控制器_1_jmp ), .Beq(\单周期硬布线控制器_1_beq ), .JAL(\单周期硬布线控制器_1_jal ),
    .Bne(\单周期硬布线控制器_1_bne ), .SRAV(\单周期硬布线控制器_1_srav ), .SB(\单周期硬布线控制器_1_sb ), .BLEZ(\单周期硬布线控制器_1_blez ));
  Multiplexer #(.select(1), .width(5), .disabled("Z"), .enable("false")) multiplexer_5 (
    .in0(ID_IR[25:21]), .in1(5'b00100), .out(R1_num), .sel(\单周期硬布线控制器_1_syscall ));
  Multiplexer #(.select(1), .width(5), .disabled("Z"), .enable("false")) multiplexer_6 (
    .in0(ID_IR[20:16]), .in1(5'b00010), .out(R2_num), .sel(\单周期硬布线控制器_1_syscall ));
  Multiplexer #(.select(1), .width(5), .disabled("Z"), .enable("false")) multiplexer_7 (
    .in0(ID_IR[20:16]), .in1(ID_IR[15:11]), .out(multiplexer_7_out), .sel(\单周期硬布线控制器_1_regdst ));
  Adder #(.width(32)) adder_2 (.a(EX_PC), .b(32'h4), .out(adder_2_out));  // open: cin, cout
  // Probe on WB_PC[11:0]
  D_Flip_Flop #(.trigger("high"), .Pre_Clr_Positions("LEGACY"), .NegatePresetClear("false"), .enable("true"), .NewFFLayout("false")) d_ff_1 (
    .Q(d_ff_1_q), .reset(1'b1));  // open: clk, D, Qn, preset, en
  Multiplexer #(.select(1), .width(5), .disabled("Z"), .enable("false")) multiplexer_8 (
    .in0(multiplexer_7_out), .in1({5{1'b1}}), .out(multiplexer_8_out), .sel(\单周期硬布线控制器_1_jal ));
  // Probe on 13'hf
  Clock #(.highDuration(1), .lowDuration(1)) clock_1 (.out(clock_1_out));
  Multiplexer #(.select(1), .width(32), .disabled("Z"), .enable("false")) multiplexer_9 (
    .in0(multiplexer_15_out), .in1(adder_4_out), .out(RDin), .sel(mem_wb_1_out_17));
  Shifter #(.width(32), .shift("ll")) shifter_1 (.in(bit_extender_2_out), .\dist (5'b00010), .out(shifter_1_out));
  Comparator #(.width(13), .mode("twosComplement")) comparator_1 (
    .a(CNT_num), .b(13'hf), .eq(comparator_1_eq), .lt(comparator_1_lt));  // open: gt
  MIPS_Regifile mips_regifile_1 (
    .Din(RDin), .Clk(CLK), .R1(mips_regifile_1_r1), .R2(mips_regifile_1_r2), .WE(RegWrite),
    .W_num(mem_wb_1_out_13), .R1_num(R1_num), .R2_num(R2_num));
  Adder #(.width(32)) adder_3 (.a(shifter_1_out), .b(adder_2_out), .out(adder_3_out));  // open: cin, cout
  nand nand_1 (nand_1_out, d_ff_1_q, comparator_1_eq);
  Counter #(.width(13), .max('h1fff), .ongoal("stay"), .trigger("rising"), .behavior("old")) counter_2 (
    .count(comparator_1_lt), .Q(CNT_num), .clk(clock_1_out));  // open: load, D, carry, clr, preset
  ID_EX id_ex_1 (
    .in_1(CLK), .in_2(not_1_out), .in_3(or_4_out), .in_4(ID_IR), .out_29(EX_IR), .in_5(ID_PC),
    .out_30(EX_PC), .in_6(\单周期硬布线控制器_1_beq ), .out_31(id_ex_1_out_31), .in_7(\单周期硬布线控制器_1_bne ),
    .out_32(id_ex_1_out_32), .in_8(\单周期硬布线控制器_1_memwrite ), .out_33(id_ex_1_out_33),
    .in_9(\单周期硬布线控制器_1_memtoreg ), .out_34(MemToReg_EX), .in_10(\单周期硬布线控制器_1_alu_op ),
    .out_35(id_ex_1_out_35), .in_11(\单周期硬布线控制器_1_alu_src ), .out_36(id_ex_1_out_36),
    .in_12(\单周期硬布线控制器_1_signedext ), .out_37(id_ex_1_out_37), .in_13(\单周期硬布线控制器_1_regwrite ),
    .out_38(regw_EX), .in_14(\单周期硬布线控制器_1_jal ), .out_39(id_ex_1_out_39), .in_16(\单周期硬布线控制器_1_syscall ),
    .out_41(id_ex_1_out_41), .in_17(\单周期硬布线控制器_1_blez ), .out_42(id_ex_1_out_42), .in_18(\单周期硬布线控制器_1_srav ),
    .out_43(id_ex_1_out_43), .in_19(\单周期硬布线控制器_1_sb ), .out_44(id_ex_1_out_44), .in_20(\单周期硬布线控制器_1_jmp ),
    .out_45(id_ex_1_out_45), .in_21(\单周期硬布线控制器_1_jr ), .out_46(id_ex_1_out_46), .in_24(mips_regifile_1_r1),
    .out_47(R1_EX), .in_25(mips_regifile_1_r2), .out_48(R2_EX), .in_26(ID_IR[15:0]), .out_49(id_ex_1_out_49),
    .in_22(ID_IR[10:6]), .in_23(multiplexer_8_out), .out_27(id_ex_1_out_27), .out_28(W__EX), .in_15(forward),
    .out_40({forwardR2, forwardR1}));
  or or_4 (or_4_out, \LoadUse相关 , \条件分支 , \无条件分支 , \总复位_2_out );
  assign CLK = nand_1_out ? clock_1_out : 1'bz;  // Controlled_Buffer controlled_buffer_1
  Pull_Resistor #(.pull(1)) pull_resistor_1 (.node(CLK));
  Multiplexer #(.select(2), .width(32), .disabled("Z"), .enable("false")) multiplexer_10 (
    .in0(R1_EX), .in1(MDin_WB), .in2(ALU_WB), .in3(ALU_MEM), .out(A), .sel(forwardR1));
  Multiplexer #(.select(2), .width(32), .disabled("Z"), .enable("false")) multiplexer_11 (
    .in0(R2_EX), .in1(MDin_WB), .in2(ALU_WB), .in3(ALU_MEM), .out(B), .sel(forwardR2));
  Multiplexer #(.select(1), .width(32), .disabled("Z"), .enable("false")) multiplexer_12 (
    .in0(B), .in1(multiplexer_16_out), .out(multiplexer_12_out), .sel(id_ex_1_out_36));
  Multiplexer #(.select(1), .width(5), .disabled("Z"), .enable("false")) multiplexer_13 (
    .in0(id_ex_1_out_27), .in1(A[4:0]), .out(multiplexer_13_out), .sel(id_ex_1_out_43));
  Comparator #(.width(32), .mode("twosComplement")) comparator_2 (
    .a(32'h1), .b(B), .eq(comparator_2_eq));  // open: gt, lt
  Comparator #(.width(32), .mode("twosComplement")) comparator_3 (
    .a(32'h22), .b(B), .eq(comparator_3_eq));  // open: gt, lt
  Multiplexer #(.select(1), .width(32), .disabled("Z"), .enable("false")) multiplexer_14 (
    .in0(multiplexer_12_out), .in1({32{1'b0}}), .out(multiplexer_14_out), .sel(id_ex_1_out_42));
  assign bit_extender_1_out = {{16{1'b0}}, id_ex_1_out_49};  // Bit_Extender bit_extender_1
  assign bit_extender_2_out = {{16{id_ex_1_out_49[15]}}, id_ex_1_out_49};  // Bit_Extender bit_extender_2
  or or_5 (or_5_out, comparator_2_eq, comparator_3_eq);
  MIPS_ALU mips_alu_1 (
    .X(A), .Y(multiplexer_14_out), .AluOP(id_ex_1_out_35), .Equal(mips_alu_1_equal),
    .Result(mips_alu_1_result), .shamt(multiplexer_13_out));  // open: Result_2
  Multiplexer #(.select(1), .width(32), .disabled("Z"), .enable("false")) multiplexer_15 (
    .in0(ALU_WB), .in1(MDin_WB), .out(multiplexer_15_out), .sel(mem_wb_1_out_16));
  Multiplexer #(.select(1), .width(32), .disabled("Z"), .enable("false")) multiplexer_16 (
    .in0(bit_extender_1_out), .in1(bit_extender_2_out), .out(multiplexer_16_out), .sel(id_ex_1_out_37));
  Counter #(.width(16), .max('hffff), .ongoal("wrap"), .trigger("rising"), .behavior("old")) counter_3 (
    .count(and_2_out), .Q(\条件分支成功数 ), .clk(CLK), .clr(RST));  // open: load, D, carry, preset
  and and_2 (and_2_out, Halt, \条件分支 );
  Counter #(.width(16), .max('hffff), .ongoal("wrap"), .trigger("rising"), .behavior("old")) counter_4 (
    .count(and_3_out), .Q(\无条件分支数 ), .clk(CLK), .clr(RST));  // open: load, D, carry, preset
  and and_3 (and_3_out, Halt, \无条件分支 );
  not not_3 (not_3_out, mips_alu_1_equal);
  EX_MEM ex_mem_1 (
    .in_1(CLK), .in_2(not_1_out), .in_3(\总复位_2_out ), .in_4(EX_IR), .out_16(MEM_IR), .in_5(EX_PC),
    .out_17(M_PC), .in_6(id_ex_1_out_33), .out_18(MemWrite), .in_7(MemToReg_EX), .out_19(MemToReg_MEM),
    .in_8(B), .out_20(ex_mem_1_out_20), .in_10(regw_EX), .out_22(regw_MEM), .in_12(and_9_out),
    .out_24(ex_mem_1_out_24), .in_13(id_ex_1_out_44), .out_25(ex_mem_1_out_25), .in_9(mips_alu_1_result),
    .out_21(ALU_MEM), .in_14(W__EX), .out_15(W__MEM), .in_11(id_ex_1_out_39), .out_23(ex_mem_1_out_23));
  and and_4 (and_4_out, mips_alu_1_equal, id_ex_1_out_31);
  and and_5 (and_5_out, id_ex_1_out_32, not_3_out);
  or or_6 (or_6_out, mips_alu_1_equal, mips_alu_1_result[0]);
  and and_6 (and_6_out, or_6_out, id_ex_1_out_42);
  or or_7 (or_7_out, and_4_out, and_5_out);
  not not_4 (not_4_out, or_5_out);
  and and_7 (and_7_out, or_5_out, id_ex_1_out_41);
  and and_8 (and_8_out, Halt, \LoadUse相关 );
  and and_9 (and_9_out, not_4_out, id_ex_1_out_41);
  Register #(.width(32), .trigger("rising"), .Select("low")) register_1 (
    .D(A), .en(and_7_out), .Q(LedData), .clk(CLK));  // open: clr
  Counter #(.width(16), .max('hffff), .ongoal("wrap"), .trigger("rising"), .behavior("old")) counter_5 (
    .count(and_8_out), .Q(\LoadUse次数 ), .clk(CLK), .clr(RST));  // open: load, D, carry, preset
  not not_5 (Halt, mem_wb_1_out_21);
  Multiplexer #(.select(1), .width(32), .disabled("Z"), .enable("false")) multiplexer_17 (
    .in0(ex_mem_1_out_20), .in1(multiplexer_18_out), .out(MDin), .sel(ex_mem_1_out_25));
  RAM #(.addrWidth(10), .dataWidth(32), .bus("separate"), .Select("high")) ram_1 (
    .addr(ALU_MEM[11:2]), .din(MDin), .data(ram_1_data), .str(MemWrite), .clk(CLK), .clr(\总复位_2_out ));  // open: sel, ld
  MEM_WB mem_wb_1 (
    .in_1(CLK), .in_2(not_1_out), .in_3(\总复位_2_out ), .in_4(MEM_IR), .out_14(WB_IR), .in_5(M_PC),
    .out_15(WB_PC), .in_6(MemToReg_MEM), .out_16(mem_wb_1_out_16), .in_8(ram_1_data), .out_18(MDin_WB),
    .in_9(ALU_MEM), .out_19(ALU_WB), .in_10(regw_MEM), .out_20(RegWrite), .in_11(ex_mem_1_out_24),
    .out_21(mem_wb_1_out_21), .in_12(W__MEM), .out_13(mem_wb_1_out_13), .in_7(ex_mem_1_out_23),
    .out_17(mem_wb_1_out_17));
  Multiplexer #(.select(2), .width(32), .disabled("Z"), .enable("false")) multiplexer_18 (
    .in0({ram_1_data[31:8], ex_mem_1_out_20[7:0]}),
    .in1({ram_1_data[31:16], ex_mem_1_out_20[7:0], ram_1_data[7:0]}),
    .in2({ram_1_data[31:24], ex_mem_1_out_20[7:0], ram_1_data[15:0]}),
    .in3({ex_mem_1_out_20[7:0], ram_1_data[23:0]}), .out(multiplexer_18_out), .sel(mips_alu_1_result[1:0]));
  Adder #(.width(32)) adder_4 (.a(WB_PC), .b(32'h4), .out(adder_4_out));  // open: cin, cout

  // Other names for the same wires on the sheet: MEM_PC[31:0] = M_PC

  // Notes on the sheet:
  //   中断源
  //   时空图监测，可删除
  //   中断等待指示
  //   数码管输出
  //   指令存储器
  //   指令字
  //   contents of rom_1 (hex, n*v repeats v):
  //   2008ffff 20090000 20111997 112020 20020022 c 2288820 2e291949 1120fffa 2002000a c
  //   OP
  //   Func
  //   rs
  //   rt
  //   rd
  //   JMP
  //   JR
  //   SignedExt
  //   SRAV
  //   SB
  //   BLEZ
  //   OP
  //   Func
  //   流水调试日志用
  //   Bne
  //   MemToReg
  //   MemWrite
  //   AluOP
  //   AluSrcB
  //   RegWrite
  //   JAL
  //   RegDst
  //   Syscall
  //   控制位
  //   暂停节拍，不能为0
  //   可计数暂停的时钟源
  //   为方便自动评测，需要输出流水线各段保存的PC值，注意是PC不是PC+4，另外ID段寄存器写入信息，Mem段内存写入信息也要输出
endmodule

module \中断按键参考电路  (
  input  \同步清零信号 ,
  output \与中断屏蔽位与 
);

  wire \_1号中断_out , and_1_out, clock_1_out, d_ff_1_q, or_1_out, or_2_out;

  Clock #(.highDuration(1), .lowDuration(1)) clock_1 (.out(clock_1_out));
  Button \_1号中断  (.out(\_1号中断_out ));
  or or_1 (or_1_out, \与中断屏蔽位与 , d_ff_1_q);
  LED #(.active("true")) \_1号中断等待指示灯  (.in(or_1_out));
  D_Flip_Flop #(.trigger("rising"), .Pre_Clr_Positions("LEGACY"), .NegatePresetClear("false"), .enable("true"), .NewFFLayout("false")) d_ff_1 (
    .clk(\_1号中断_out ), .D(1'b1), .Q(d_ff_1_q), .reset(\与中断屏蔽位与 ));  // open: Qn, preset, en
  or or_2 (or_2_out, d_ff_1_q, \与中断屏蔽位与 );
  and and_1 (and_1_out, or_2_out, ~\同步清零信号 );  // AND_Gate
  D_Flip_Flop #(.trigger("rising"), .Pre_Clr_Positions("LEGACY"), .NegatePresetClear("false"), .enable("true"), .NewFFLayout("false")) IR1 (
    .clk(clock_1_out), .D(and_1_out), .Q(\与中断屏蔽位与 ));  // open: Qn, preset, en, reset
  \单周期硬布线控制器  \u_单周期硬布线控制器_1  ();  // open: Func, OP, ALU_OP, MemToReg, MemWrite, ALU_SRC, RegWrite, SysCALL, SignedExt, RegDst, JR, JMP, Beq, JAL, Bne, SRAV, SB, BLEZ

  // Notes on the sheet:
  //   中断信号采样参考电路
  //   Reset 
endmodule

module \单周期MIPS_单级中断  (
  input  IR1,
  input  IR2,
  input  IR3,
  output RegWrite,
  output MemWrite,
  output [31:0] PC,
  output [31:0] IR,
  output [31:0] RDin,
  output [31:0] MDin,
  output [31:0] LedData
);

  wire CLK, Go, IR1_t, IR2_t, IR3_t, IRA, IRB, IRC, SignedExt, W1, W2, W3, \单周期硬布线控制器_1_alu_src ,
       \单周期硬布线控制器_1_beq , \单周期硬布线控制器_1_bne , \单周期硬布线控制器_1_jal , \单周期硬布线控制器_1_jmp , \单周期硬布线控制器_1_jr ,
       \单周期硬布线控制器_1_memtoreg , \单周期硬布线控制器_1_memwrite , \单周期硬布线控制器_1_regdst , \单周期硬布线控制器_1_regwrite ,
       \单周期硬布线控制器_1_syscall ;
  wire [3:0] \单周期硬布线控制器_1_alu_op ;
  wire [5:0] undriven, undriven_2;
  wire [15:0] \总周期数 ;
  wire [31:0] rom_1_data;

  Clock #(.highDuration(1), .lowDuration(1)) clock_1 (.out(CLK));
  Button _1 (.out(IRA));
  Button _2 (.out(IRB));
  Button _3 (.out(IRC));
  Register #(.width(32), .trigger("rising"), .Select("low")) u_PC ();  // open: D, en, Q, clk, clr
  Button \u_继续运行  (.out(Go));
  LED #(.active("true")) led_1 (.in(W1));
  LED #(.active("true")) led_2 (.in(W2));
  LED #(.active("true")) led_3 (.in(W3));
  Hex_Digit_Display hex_digit_display_1 (.value(LedData[31:28]));  // open: dp
  ROM #(.addrWidth(10), .dataWidth(32), .Select("high")) rom_1 (.data(rom_1_data));  // open: addr
  Hex_Digit_Display hex_digit_display_2 (.value(LedData[27:24]));  // open: dp
  Hex_Digit_Display hex_digit_display_3 (.value(LedData[23:20]));  // open: dp
  // Mips_Probe mips_probe_1: pin names not known; wires that end beside it: rom_1_data
  Hex_Digit_Display hex_digit_display_4 (.value(LedData[19:16]));  // open: dp
  Hex_Digit_Display hex_digit_display_5 (.value(LedData[15:12]));  // open: dp
  Hex_Digit_Display hex_digit_display_6 (.value(LedData[7:4]));  // open: dp
  Hex_Digit_Display hex_digit_display_7 (.value(LedData[11:8]));  // open: dp
  // Probe on \总周期数 
  MIPS_Regifile mips_regifile_1 ();  // open: Din, Clk, R1, R2, WE, W_num, R1_num, R2_num
  Hex_Digit_Display hex_digit_display_8 (.value(LedData[3:0]));  // open: dp
  MIPS_ALU mips_alu_1 ();  // open: X, Y, AluOP, Equal, Result, Result_2, shamt
  or or_1 (IR1_t, IR1, IRA);
  or or_2 (IR2_t, IR2, IRB);
  RAM #(.addrWidth(10), .dataWidth(32), .bus("separate"), .Select("high")) ram_1 ();  // open: addr, din, data, str, sel, clk, ld, clr
  \单周期硬布线控制器  \u_单周期硬布线控制器_1  (
    .Func(undriven_2), .OP(undriven), .ALU_OP(\单周期硬布线控制器_1_alu_op ), .MemToReg(\单周期硬布线控制器_1_memtoreg ),
    .MemWrite(\单周期硬布线控制器_1_memwrite ), .ALU_SRC(\单周期硬布线控制器_1_alu_src ), .RegWrite(\单周期硬布线控制器_1_regwrite ),
    .SysCALL(\单周期硬布线控制器_1_syscall ), .SignedExt(SignedExt), .RegDst(\单周期硬布线控制器_1_regdst ),
    .JR(\单周期硬布线控制器_1_jr ), .JMP(\单周期硬布线控制器_1_jmp ), .Beq(\单周期硬布线控制器_1_beq ), .JAL(\单周期硬布线控制器_1_jal ),
    .Bne(\单周期硬布线控制器_1_bne ));  // open: SRAV, SB, BLEZ
  or or_3 (IR3_t, IR3, IRC);

  // Notes on the sheet:
  //   中断源
  //   中断等待指示
  //   总复位信号应将除ROM以外所有存储组件全部清零
  //   指令存储器
  //   contents of rom_1 (hex, n*v repeats v):
  //   20110001 8000c05 20110001 20120002 20130003 8000c09 20110001 20120002 20130003 8000c0d 20110001
  //   20120002 20130003 8000c11 20110001 20120002 20130003 c000cb8 20100001 20110001 118fc0 112020
  //   20020022 c 118882 12200001 8000c15 112020 20020022 c 20110001 118880 112020 20020022 c 12200001
  //   8000c1f 20110001 118fc0 112020 20020022 c 1188c3 112020 20020022 c 118903 112020 20020022 c 118903
  //   112020 20020022 c 118903 112020 20020022 c 118903 112020 20020022 c 118903 112020 20020022 c 118903
  //   112020 20020022 c 118903 112020 20020022 c 20100001 109fc0 139fc3 8021 2012000c 24160003 26100001
  //   3210000f 20080008 20090001 139900 2709825 132020 20020022 c 1094022 1500fff9 22100001 2018000f
  //   2188024 108700 20080008 20090001 139902 2709825 132021 20020022 c 1094022 1500fff9 108702 2c9b022
  //   12c00001 8000c50 4020 1084027 84400 3508ffff 82021 20020022 c 2010ffff 20110000 ae300000 22100001
  //   22310004 ae300000 22100001 22310004 ae300000 22100001 22310004 ae300000 22100001 22310004 ae300000
  //   22100001 22310004 ae300000 22100001 22310004 ae300000 22100001 22310004 ae300000 22100001 22310004
  //   ae300000 22100001 22310004 ae300000 22100001 22310004 ae300000 22100001 22310004 ae300000 22100001
  //   22310004 ae300000 22100001 22310004 ae300000 22100001 22310004 ae300000 22100001 22310004 ae300000
  //   22100001 22310004 22100001 8020 2011003c 8e130000 8e340000 274402a 11000002 ae330000 ae140000
  //   2231fffc 1611fff8 102020 20020022 c 22100004 2011003c 1611fff2 2002000a c 20100000 22100001 102020
  //   20020022 c 22100002 102020 20020022 c 22100003 102020 20020022 c 22100004 102020 20020022 c 22100005
  //   102020 20020022 c 22100006 102020 20020022 c 22100007 102020 20020022 c 22100008 102020 20020022
  //   20020022 c 3e00008
  //   OP
  //   Func
  //   rs
  //   指令字
  //   rt
  //   rd
  //   数码管输出
  //   数码管输出应该用寄存器锁存，否则显示数据只能一闪而过
  //   JMP
  //   JR
  //   OP
  //   Func
  //   Syscall
  //   Beq
  //   Bne
  //   MemToReg
  //   MemWrite
  //   AluOP
  //   AluSrcB
  //   RegWrite
  //   JAL
  //   RegDst
  //   为方便自动评测，需要输出PC，IR，寄存器堆写如数据RDin
  //   RAM写使能MemWrite、RAM写入数据MDin等信号
endmodule

module \单周期MIPS_多级中断  (
  input  IR1,
  input  IR2,
  input  IR3,
  output RegWrite,
  output MemWrite,
  output [31:0] PC,
  output [31:0] IR,
  output [31:0] RDin,
  output [31:0] MDin,
  output [31:0] LedData
);

  wire CLK, Go, IR1_t, IR2_t, IR3_t, IRA, IRB, IRC, SignedExt, W1, W2, W3, \单周期硬布线控制器_1_alu_src ,
       \单周期硬布线控制器_1_beq , \单周期硬布线控制器_1_bne , \单周期硬布线控制器_1_jal , \单周期硬布线控制器_1_jmp , \单周期硬布线控制器_1_jr ,
       \单周期硬布线控制器_1_memtoreg , \单周期硬布线控制器_1_memwrite , \单周期硬布线控制器_1_regdst , \单周期硬布线控制器_1_regwrite ,
       \单周期硬布线控制器_1_syscall ;
  wire [3:0] \单周期硬布线控制器_1_alu_op ;
  wire [5:0] undriven, undriven_2;
  wire [15:0] \总周期数 ;
  wire [31:0] rom_1_data;

  Clock #(.highDuration(1), .lowDuration(1)) clock_1 (.out(CLK));
  Button _1 (.out(IRA));
  Button _2 (.out(IRB));
  Button _3 (.out(IRC));
  Register #(.width(32), .trigger("rising"), .Select("low")) u_PC ();  // open: D, en, Q, clk, clr
  Button \u_继续运行  (.out(Go));
  LED #(.active("true")) led_1 (.in(W1));
  LED #(.active("true")) led_2 (.in(W2));
  LED #(.active("true")) led_3 (.in(W3));
  Hex_Digit_Display hex_digit_display_1 (.value(LedData[31:28]));  // open: dp
  ROM #(.addrWidth(10), .dataWidth(32), .Select("high")) rom_1 (.data(rom_1_data));  // open: addr
  Hex_Digit_Display hex_digit_display_2 (.value(LedData[27:24]));  // open: dp
  Hex_Digit_Display hex_digit_display_3 (.value(LedData[23:20]));  // open: dp
  // Mips_Probe mips_probe_1: pin names not known; wires that end beside it: rom_1_data
  Hex_Digit_Display hex_digit_display_4 (.value(LedData[19:16]));  // open: dp
  Hex_Digit_Display hex_digit_display_5 (.value(LedData[15:12]));  // open: dp
  Hex_Digit_Display hex_digit_display_6 (.value(LedData[11:8]));  // open: dp
  Hex_Digit_Display hex_digit_display_7 (.value(LedData[7:4]));  // open: dp
  // Probe on \总周期数 
  MIPS_Regifile mips_regifile_1 ();  // open: Din, Clk, R1, R2, WE, W_num, R1_num, R2_num
  Hex_Digit_Display hex_digit_display_8 (.value(LedData[3:0]));  // open: dp
  MIPS_ALU mips_alu_1 ();  // open: X, Y, AluOP, Equal, Result, Result_2, shamt
  or or_1 (IR1_t, IR1, IRA);
  or or_2 (IR2_t, IR2, IRB);
  RAM #(.addrWidth(10), .dataWidth(32), .bus("separate"), .Select("high")) ram_1 ();  // open: addr, din, data, str, sel, clk, ld, clr
  \单周期硬布线控制器  \u_单周期硬布线控制器_1  (
    .Func(undriven_2), .OP(undriven), .ALU_OP(\单周期硬布线控制器_1_alu_op ), .MemToReg(\单周期硬布线控制器_1_memtoreg ),
    .MemWrite(\单周期硬布线控制器_1_memwrite ), .ALU_SRC(\单周期硬布线控制器_1_alu_src ), .RegWrite(\单周期硬布线控制器_1_regwrite ),
    .SysCALL(\单周期硬布线控制器_1_syscall ), .SignedExt(SignedExt), .RegDst(\单周期硬布线控制器_1_regdst ),
    .JR(\单周期硬布线控制器_1_jr ), .JMP(\单周期硬布线控制器_1_jmp ), .Beq(\单周期硬布线控制器_1_beq ), .JAL(\单周期硬布线控制器_1_jal ),
    .Bne(\单周期硬布线控制器_1_bne ));  // open: SRAV, SB, BLEZ
  or or_3 (IR3_t, IR3, IRC);

  // Notes on the sheet:
  //   中断源
  //   中断等待指示
  //   总复位信号应将除ROM以外所有存储组件全部清零
  //   指令存储器
  //   contents of rom_1 (hex, n*v repeats v):
  //   20110001 8000c05 20110001 20120002 20130003 8000c09 20110001 20120002 20130003 8000c0d 20110001
  //   20120002 20130003 8000c11 20110001 20120002 20130003 c000cb8 20100001 20110001 118fc0 112020
  //   20020022 c 118882 12200001 8000c15 112020 20020022 c 20110001 118880 112020 20020022 c 12200001
  //   8000c1f 20110001 118fc0 112020 20020022 c 1188c3 112020 20020022 c 118903 112020 20020022 c 118903
  //   112020 20020022 c 118903 112020 20020022 c 118903 112020 20020022 c 118903 112020 20020022 c 118903
  //   112020 20020022 c 118903 112020 20020022 c 20100001 109fc0 139fc3 8021 2012000c 24160003 26100001
  //   3210000f 20080008 20090001 139900 2709825 132020 20020022 c 1094022 1500fff9 22100001 2018000f
  //   2188024 108700 20080008 20090001 139902 2709825 132021 20020022 c 1094022 1500fff9 108702 2c9b022
  //   12c00001 8000c50 4020 1084027 84400 3508ffff 82021 20020022 c 2010ffff 20110000 ae300000 22100001
  //   22310004 ae300000 22100001 22310004 ae300000 22100001 22310004 ae300000 22100001 22310004 ae300000
  //   22100001 22310004 ae300000 22100001 22310004 ae300000 22100001 22310004 ae300000 22100001 22310004
  //   ae300000 22100001 22310004 ae300000 22100001 22310004 ae300000 22100001 22310004 ae300000 22100001
  //   22310004 ae300000 22100001 22310004 ae300000 22100001 22310004 ae300000 22100001 22310004 ae300000
  //   22100001 22310004 22100001 8020 2011003c 8e130000 8e340000 274402a 11000002 ae330000 ae140000
  //   2231fffc 1611fff8 102020 20020022 c 22100004 2011003c 1611fff2 2002000a c 20100000 22100001 102020
  //   20020022 c 22100002 102020 20020022 c 22100003 102020 20020022 c 22100004 102020 20020022 c 22100005
  //   102020 20020022 c 22100006 102020 20020022 c 22100007 102020 20020022 c 22100008 102020 20020022
  //   20020022 c 3e00008
  //   OP
  //   Func
  //   rs
  //   指令字
  //   rt
  //   rd
  //   数码管输出
  //   数码管输出应该用寄存器锁存，否则显示数据只能一闪而过
  //   JMP
  //   JR
  //   OP
  //   Func
  //   Syscall
  //   Beq
  //   Bne
  //   MemToReg
  //   MemWrite
  //   AluOP
  //   AluSrcB
  //   RegWrite
  //   JAL
  //   RegDst
  //   为方便自动评测，需要输出PC，IR，寄存器堆写如数据RDin
  //   RAM写使能MemWrite、RAM写入数据MDin等信号
endmodule

module \封装正确性测试  (
);

  wire IR1, IR2, IR3, MemW, RegW;
  wire [31:0] EX_PC, ID_PC, IF_PC, IR, LED, MDin, MDinr, MEM_PC, PC, RDin, RDinr, WB_PC;

  \单周期MIPS  \u_单周期mips_1  (
    .RegWrite(RegW), .MemWrite(MemW), .PC(PC), .IR(IR), .RDin(RDin), .MDin(MDin), .LedData(LED));  // open: IR1, IR2, IR3
  \气泡流水线  \u_气泡流水线_1  (
    .RegWrite(RegW), .MemWrite(MemW), .IF_PC(IF_PC), .ID_PC(ID_PC), .EX_PC(EX_PC), .M_PC(MEM_PC),
    .WB_PC(WB_PC), .RDin(RDinr), .MDin(MDinr), .LedData(LED));
  \单周期MIPS_单级中断  \u_单周期mips_单级中断_1  (
    .IR1(IR1), .IR2(IR2), .IR3(IR3), .RegWrite(RegW), .MemWrite(MemW), .PC(PC), .IR(IR), .RDin(RDin),
    .MDin(MDin), .LedData(LED));
  \理想流水线  \u_理想流水线_1  (
    .RegWrite(RegW), .MemWrite(MemW), .IF_PC(IF_PC), .ID_PC(ID_PC), .EX_PC(EX_PC), .M_PC(MEM_PC),
    .WB_PC(WB_PC), .RDin(RDinr), .MDin(MDinr), .LedData(LED));
  \气泡流水线  \u_气泡流水线_2  (
    .RegWrite(RegW), .MemWrite(MemW), .IF_PC(IF_PC), .ID_PC(ID_PC), .EX_PC(EX_PC), .M_PC(MEM_PC),
    .WB_PC(WB_PC), .RDin(RDinr), .MDin(MDinr), .LedData(LED));
  \单周期MIPS_多级中断  \u_单周期mips_多级中断_1  (
    .IR1(IR1), .IR2(IR2), .IR3(IR3), .RegWrite(RegW), .MemWrite(MemW), .PC(PC), .IR(IR), .RDin(RDin),
    .MDin(MDin), .LedData(LED));

  // Notes on the sheet:
  //   单周期封装测试
  //   气泡流水封装测试
  //   单周期+单级中断封装测试
  //   请检查上面封装有无位宽不匹配，引脚标签是否和连接的标签相对应，否则无法在educoder平台上正确测试
  //   理想流水封装测试
  //   重定向流水封装测试
  //   单周期+多级中断封装测试
endmodule

module IF_ID (
  input  in_1,
  input  in_2,
  input  in_3,
  input  [31:0] in_4,
  input  [31:0] in_5,
  output [31:0] out_6,
  output [31:0] out_7
);

  wire not_1_out;
  wire [31:0] multiplexer_1_out, multiplexer_2_out;

  Multiplexer #(.select(1), .width(32), .disabled("Z"), .enable("false")) multiplexer_1 (
    .in0(in_4), .in1({32{1'b0}}), .out(multiplexer_1_out), .sel(in_3));
  Multiplexer #(.select(1), .width(32), .disabled("Z"), .enable("false")) multiplexer_2 (
    .in0(in_5), .in1({32{1'b0}}), .out(multiplexer_2_out), .sel(in_3));
  not not_1 (not_1_out, in_2);
  Register #(.width(32), .trigger("rising"), .Select("low")) register_1 (
    .D(multiplexer_1_out), .en(not_1_out), .Q(out_6), .clk(in_1));  // open: clr
  Register #(.width(32), .trigger("rising"), .Select("low")) register_2 (
    .D(multiplexer_2_out), .en(not_1_out), .Q(out_7), .clk(in_1));  // open: clr

  // Other names for the same wires on the sheet: Clear = in_3; Clk = in_1; Enable = in_2; IRIn[31:0] = in_4;
  //   IROut[31:0] = out_6; PCIn[31:0] = in_5; PCOut[31:0] = out_7
endmodule

module ID_EX (
  input  in_1,
  input  in_2,
  input  in_3,
  input  [31:0] in_4,
  input  [31:0] in_5,
  input  in_6,
  input  in_7,
  input  in_8,
  input  in_9,
  input  [3:0] in_10,
  input  in_11,
  input  in_12,
  input  in_13,
  input  in_14,
  input  [3:0] in_15,
  input  in_16,
  input  in_17,
  input  in_18,
  input  in_19,
  input  in_20,
  input  in_21,
  input  [4:0] in_22,
  input  [4:0] in_23,
  input  [31:0] in_24,
  input  [31:0] in_25,
  input  [15:0] in_26,
  output [4:0] out_27,
  output [4:0] out_28,
  output [31:0] out_29,
  output [31:0] out_30,
  output out_31,
  output out_32,
  output out_33,
  output out_34,
  output [3:0] out_35,
  output out_36,
  output out_37,
  output out_38,
  output out_39,
  output [3:0] out_40,
  output out_41,
  output out_42,
  output out_43,
  output out_44,
  output out_45,
  output out_46,
  output [31:0] out_47,
  output [31:0] out_48,
  output [15:0] out_49
);

  wire multiplexer_1_out, multiplexer_2_out, multiplexer_3_out, multiplexer_4_out, multiplexer_6_out,
       multiplexer_7_out, multiplexer_8_out, multiplexer_9_out, multiplexer_11_out, multiplexer_12_out,
       multiplexer_13_out, multiplexer_14_out, multiplexer_15_out, multiplexer_16_out, not_1_out;
  wire [3:0] multiplexer_5_out, multiplexer_23_out;
  wire [4:0] multiplexer_10_out, multiplexer_22_out;
  wire [15:0] multiplexer_21_out;
  wire [31:0] multiplexer_17_out, multiplexer_18_out, multiplexer_19_out, multiplexer_20_out;

  Multiplexer #(.select(1), .width(1), .disabled("Z"), .enable("false")) multiplexer_1 (
    .in0(in_6), .in1(1'b0), .out(multiplexer_1_out), .sel(in_3));
  Multiplexer #(.select(1), .width(1), .disabled("Z"), .enable("false")) multiplexer_2 (
    .in0(in_7), .in1(1'b0), .out(multiplexer_2_out), .sel(in_3));
  Multiplexer #(.select(1), .width(1), .disabled("Z"), .enable("false")) multiplexer_3 (
    .in0(in_8), .in1(1'b0), .out(multiplexer_3_out), .sel(in_3));
  Multiplexer #(.select(1), .width(1), .disabled("Z"), .enable("false")) multiplexer_4 (
    .in0(in_9), .in1(1'b0), .out(multiplexer_4_out), .sel(in_3));
  Multiplexer #(.select(1), .width(4), .disabled("Z"), .enable("false")) multiplexer_5 (
    .in0(in_10), .in1(4'b0000), .out(multiplexer_5_out), .sel(in_3));
  Multiplexer #(.select(1), .width(1), .disabled("Z"), .enable("false")) multiplexer_6 (
    .in0(in_11), .in1(1'b0), .out(multiplexer_6_out), .sel(in_3));
  Multiplexer #(.select(1), .width(1), .disabled("Z"), .enable("false")) multiplexer_7 (
    .in0(in_12), .in1(1'b0), .out(multiplexer_7_out), .sel(in_3));
  Multiplexer #(.select(1), .width(1), .disabled("Z"), .enable("false")) multiplexer_8 (
    .in0(in_13), .in1(1'b0), .out(multiplexer_8_out), .sel(in_3));
  Multiplexer #(.select(1), .width(1), .disabled("Z"), .enable("false")) multiplexer_9 (
    .in0(in_14), .in1(1'b0), .out(multiplexer_9_out), .sel(in_3));
  Multiplexer #(.select(1), .width(5), .disabled("Z"), .enable("false")) multiplexer_10 (
    .in0(in_22), .in1({5{1'b0}}), .out(multiplexer_10_out), .sel(in_3));
  Multiplexer #(.select(1), .width(1), .disabled("Z"), .enable("false")) multiplexer_11 (
    .in0(in_16), .in1(1'b0), .out(multiplexer_11_out), .sel(in_3));
  Multiplexer #(.select(1), .width(1), .disabled("Z"), .enable("false")) multiplexer_12 (
    .in0(in_17), .in1(1'b0), .out(multiplexer_12_out), .sel(in_3));
  Multiplexer #(.select(1), .width(1), .disabled("Z"), .enable("false")) multiplexer_13 (
    .in0(in_18), .in1(1'b0), .out(multiplexer_13_out), .sel(in_3));
  Multiplexer #(.select(1), .width(1), .disabled("Z"), .enable("false")) multiplexer_14 (
    .in0(in_20), .in1(1'b0), .out(multiplexer_14_out), .sel(in_3));
  Multiplexer #(.select(1), .width(1), .disabled("Z"), .enable("false")) multiplexer_15 (
    .in0(in_21), .in1(1'b0), .out(multiplexer_15_out), .sel(in_3));
  Multiplexer #(.select(1), .width(1), .disabled("Z"), .enable("false")) multiplexer_16 (
    .in0(in_19), .in1(1'b0), .out(multiplexer_16_out), .sel(in_3));
  Multiplexer #(.select(1), .width(32), .disabled("Z"), .enable("false")) multiplexer_17 (
    .in0(in_4), .in1({32{1'b0}}), .out(multiplexer_17_out), .sel(in_3));
  Multiplexer #(.select(1), .width(32), .disabled("Z"), .enable("false")) multiplexer_18 (
    .in0(in_5), .in1({32{1'b0}}), .out(multiplexer_18_out), .sel(in_3));
  Multiplexer #(.select(1), .width(32), .disabled("Z"), .enable("false")) multiplexer_19 (
    .in0(in_24), .in1({32{1'b0}}), .out(multiplexer_19_out), .sel(in_3));
  Multiplexer #(.select(1), .width(32), .disabled("Z"), .enable("false")) multiplexer_20 (
    .in0(in_25), .in1({32{1'b0}}), .out(multiplexer_20_out), .sel(in_3));
  Multiplexer #(.select(1), .width(16), .disabled("Z"), .enable("false")) multiplexer_21 (
    .in0(in_26), .in1({16{1'b0}}), .out(multiplexer_21_out), .sel(in_3));
  Multiplexer #(.select(1), .width(5), .disabled("Z"), .enable("false")) multiplexer_22 (
    .in0(in_23), .in1({5{1'b0}}), .out(multiplexer_22_out), .sel(in_3));
  Multiplexer #(.select(1), .width(4), .disabled("Z"), .enable("false")) multiplexer_23 (
    .in0(in_15), .in1(4'b0000), .out(multiplexer_23_out), .sel(in_3));
  not not_1 (not_1_out, in_2);
  Register #(.width(1), .trigger("rising"), .Select("low")) register_1 (
    .D(multiplexer_1_out), .en(not_1_out), .Q(out_31), .clk(in_1));  // open: clr
  Register #(.width(1), .trigger("rising"), .Select("low")) register_2 (
    .D(multiplexer_2_out), .en(not_1_out), .Q(out_32), .clk(in_1));  // open: clr
  Register #(.width(1), .trigger("rising"), .Select("low")) register_3 (
    .D(multiplexer_3_out), .en(not_1_out), .Q(out_33), .clk(in_1));  // open: clr
  Register #(.width(1), .trigger("rising"), .Select("low")) register_4 (
    .D(multiplexer_4_out), .en(not_1_out), .Q(out_34), .clk(in_1));  // open: clr
  Register #(.width(4), .trigger("rising"), .Select("low")) register_5 (
    .D(multiplexer_5_out), .en(not_1_out), .Q(out_35), .clk(in_1));  // open: clr
  Register #(.width(1), .trigger("rising"), .Select("low")) register_6 (
    .D(multiplexer_6_out), .en(not_1_out), .Q(out_36), .clk(in_1));  // open: clr
  Register #(.width(1), .trigger("rising"), .Select("low")) register_7 (
    .D(multiplexer_7_out), .en(not_1_out), .Q(out_37), .clk(in_1));  // open: clr
  Register #(.width(1), .trigger("rising"), .Select("low")) register_8 (
    .D(multiplexer_8_out), .en(not_1_out), .Q(out_38), .clk(in_1));  // open: clr
  Register #(.width(1), .trigger("rising"), .Select("low")) register_9 (
    .D(multiplexer_9_out), .en(not_1_out), .Q(out_39), .clk(in_1));  // open: clr
  Register #(.width(5), .trigger("rising"), .Select("low")) register_10 (
    .D(multiplexer_10_out), .en(not_1_out), .Q(out_27), .clk(in_1));  // open: clr
  Register #(.width(1), .trigger("rising"), .Select("low")) register_11 (
    .D(multiplexer_11_out), .en(not_1_out), .Q(out_41), .clk(in_1));  // open: clr
  Register #(.width(1), .trigger("rising"), .Select("low")) register_12 (
    .D(multiplexer_12_out), .en(not_1_out), .Q(out_42), .clk(in_1));  // open: clr
  Register #(.width(1), .trigger("rising"), .Select("low")) register_13 (
    .D(multiplexer_13_out), .en(not_1_out), .Q(out_43), .clk(in_1));  // open: clr
  Register #(.width(1), .trigger("rising"), .Select("low")) register_14 (
    .D(multiplexer_14_out), .en(not_1_out), .Q(out_45), .clk(in_1));  // open: clr
  Register #(.width(1), .trigger("rising"), .Select("low")) register_15 (
    .D(multiplexer_15_out), .en(not_1_out), .Q(out_46), .clk(in_1));  // open: clr
  Register #(.width(1), .trigger("rising"), .Select("low")) register_16 (
    .D(multiplexer_16_out), .en(not_1_out), .Q(out_44), .clk(in_1));  // open: clr
  Register #(.width(32), .trigger("rising"), .Select("low")) register_17 (
    .D(multiplexer_17_out), .en(not_1_out), .Q(out_29), .clk(in_1));  // open: clr
  Register #(.width(32), .trigger("rising"), .Select("low")) register_18 (
    .D(multiplexer_18_out), .en(not_1_out), .Q(out_30), .clk(in_1));  // open: clr
  Register #(.width(32), .trigger("rising"), .Select("low")) register_19 (
    .D(multiplexer_19_out), .en(not_1_out), .Q(out_47), .clk(in_1));  // open: clr
  Register #(.width(32), .trigger("rising"), .Select("low")) register_20 (
    .D(multiplexer_20_out), .en(not_1_out), .Q(out_48), .clk(in_1));  // open: clr
  Register #(.width(16), .trigger("rising"), .Select("low")) register_21 (
    .D(multiplexer_21_out), .en(not_1_out), .Q(out_49), .clk(in_1));  // open: clr
  Register #(.width(5), .trigger("rising"), .Select("low")) register_22 (
    .D(multiplexer_22_out), .en(not_1_out), .Q(out_28), .clk(in_1));  // open: clr
  Register #(.width(4), .trigger("rising"), .Select("low")) register_23 (
    .D(multiplexer_23_out), .en(not_1_out), .Q(out_40), .clk(in_1));  // open: clr

  // Other names for the same wires on the sheet: AIn[31:0] = in_24; AluOP[3:0] = in_10; AluOPOut[3:0] = out_35;
  //   AluSrcB = in_11; AluSrcBOut = out_36; AOut[31:0] = out_47; Beq = in_6; BeqOut = out_31; BIn[31:0] = in_25;
  //   BLEZ = in_17; BLEZOut = out_42; Bne = in_7; BneOut = out_32; BOut[31:0] = out_48; Clear = in_3; Clk = in_1;
  //   Enable = in_2; forward[3:0] = in_15; forwardout[3:0] = out_40; ImmIn[15:0] = in_26; ImmOut[15:0] = out_49;
  //   IRIn[31:0] = in_4; IROut[31:0] = out_29; JAL = in_14; JALOut = out_39; JMP = in_20; JMPOut = out_45; JR = in_21;
  //   JROut = out_46; MemToReg = in_9; MemToRegOut = out_34; MemWrite = in_8; MemWriteOut = out_33; PCIn[31:0] = in_5;
  //   PCOut[31:0] = out_30; RegWrite = in_13; RegWriteOut = out_38; SB = in_19; SBOut = out_44; Shamt[4:0] = in_22;
  //   ShamtOut[4:0] = out_27; SignedExt = in_12; SignedExtOut = out_37; SRAV = in_18; SRAVOut = out_43;
  //   Syscall = in_16; SyscallOut = out_41; W_num[4:0] = in_23; W_Out[4:0] = out_28
endmodule

module EX_MEM (
  input  in_1,
  input  in_2,
  input  in_3,
  input  [31:0] in_4,
  input  [31:0] in_5,
  input  in_6,
  input  in_7,
  input  [31:0] in_8,
  input  [31:0] in_9,
  input  in_10,
  input  in_11,
  input  in_12,
  input  in_13,
  input  [4:0] in_14,
  output [4:0] out_15,
  output [31:0] out_16,
  output [31:0] out_17,
  output out_18,
  output out_19,
  output [31:0] out_20,
  output [31:0] out_21,
  output out_22,
  output out_23,
  output out_24,
  output out_25
);

  wire multiplexer_1_out, multiplexer_2_out, multiplexer_3_out, multiplexer_4_out, multiplexer_6_out,
       multiplexer_7_out, not_1_out;
  wire [4:0] multiplexer_5_out;
  wire [31:0] multiplexer_8_out, multiplexer_9_out, multiplexer_10_out, multiplexer_11_out;

  Multiplexer #(.select(1), .width(1), .disabled("Z"), .enable("false")) multiplexer_1 (
    .in0(in_6), .in1(1'b0), .out(multiplexer_1_out), .sel(in_3));
  Multiplexer #(.select(1), .width(1), .disabled("Z"), .enable("false")) multiplexer_2 (
    .in0(in_7), .in1(1'b0), .out(multiplexer_2_out), .sel(in_3));
  Multiplexer #(.select(1), .width(1), .disabled("Z"), .enable("false")) multiplexer_3 (
    .in0(in_10), .in1(1'b0), .out(multiplexer_3_out), .sel(in_3));
  Multiplexer #(.select(1), .width(1), .disabled("Z"), .enable("false")) multiplexer_4 (
    .in0(in_11), .in1(1'b0), .out(multiplexer_4_out), .sel(in_3));
  Multiplexer #(.select(1), .width(5), .disabled("Z"), .enable("false")) multiplexer_5 (
    .in0(in_14), .in1({5{1'b0}}), .out(multiplexer_5_out), .sel(in_3));
  Multiplexer #(.select(1), .width(1), .disabled("Z"), .enable("false")) multiplexer_6 (
    .in0(in_12), .in1(1'b0), .out(multiplexer_6_out), .sel(in_3));
  Multiplexer #(.select(1), .width(1), .disabled("Z"), .enable("false")) multiplexer_7 (
    .in0(in_13), .in1(1'b0), .out(multiplexer_7_out), .sel(in_3));
  Multiplexer #(.select(1), .width(32), .disabled("Z"), .enable("false")) multiplexer_8 (
    .in0(in_4), .in1({32{1'b0}}), .out(multiplexer_8_out), .sel(in_3));
  Multiplexer #(.select(1), .width(32), .disabled("Z"), .enable("false")) multiplexer_9 (
    .in0(in_5), .in1({32{1'b0}}), .out(multiplexer_9_out), .sel(in_3));
  Multiplexer #(.select(1), .width(32), .disabled("Z"), .enable("false")) multiplexer_10 (
    .in0(in_8), .in1({32{1'b0}}), .out(multiplexer_10_out), .sel(in_3));
  Multiplexer #(.select(1), .width(32), .disabled("Z"), .enable("false")) multiplexer_11 (
    .in0(in_9), .in1({32{1'b0}}), .out(multiplexer_11_out), .sel(in_3));
  not not_1 (not_1_out, in_2);
  Register #(.width(1), .trigger("rising"), .Select("low")) register_1 (
    .D(multiplexer_1_out), .en(not_1_out), .Q(out_18), .clk(in_1));  // open: clr
  Register #(.width(1), .trigger("rising"), .Select("low")) register_2 (
    .D(multiplexer_2_out), .en(not_1_out), .Q(out_19), .clk(in_1));  // open: clr
  Register #(.width(1), .trigger("rising"), .Select("low")) register_3 (
    .D(multiplexer_3_out), .en(not_1_out), .Q(out_22), .clk(in_1));  // open: clr
  Register #(.width(1), .trigger("rising"), .Select("low")) register_4 (
    .D(multiplexer_4_out), .en(not_1_out), .Q(out_23), .clk(in_1));  // open: clr
  Register #(.width(5), .trigger("rising"), .Select("low")) register_5 (
    .D(multiplexer_5_out), .en(not_1_out), .Q(out_15), .clk(in_1));  // open: clr
  Register #(.width(1), .trigger("rising"), .Select("low")) register_6 (
    .D(multiplexer_6_out), .en(not_1_out), .Q(out_24), .clk(in_1));  // open: clr
  Register #(.width(1), .trigger("rising"), .Select("low")) register_7 (
    .D(multiplexer_7_out), .en(not_1_out), .Q(out_25), .clk(in_1));  // open: clr
  Register #(.width(32), .trigger("rising"), .Select("low")) register_8 (
    .D(multiplexer_8_out), .en(not_1_out), .Q(out_16), .clk(in_1));  // open: clr
  Register #(.width(32), .trigger("rising"), .Select("low")) register_9 (
    .D(multiplexer_9_out), .en(not_1_out), .Q(out_17), .clk(in_1));  // open: clr
  Register #(.width(32), .trigger("rising"), .Select("low")) register_10 (
    .D(multiplexer_10_out), .en(not_1_out), .Q(out_20), .clk(in_1));  // open: clr
  Register #(.width(32), .trigger("rising"), .Select("low")) register_11 (
    .D(multiplexer_11_out), .en(not_1_out), .Q(out_21), .clk(in_1));  // open: clr

  // Other names for the same wires on the sheet: ALUIn[31:0] = in_9; ALUOut[31:0] = out_21; BIn[31:0] = in_8;
  //   BOut[31:0] = out_20; Clear = in_3; Clk = in_1; Enable = in_2; IRIn[31:0] = in_4; IROut[31:0] = out_16;
  //   JAL = in_11; JALOut = out_23; MemToReg = in_7; MemToRegOut = out_19; MemWrite = in_6; MemWriteOut = out_18;
  //   PCIn[31:0] = in_5; PCOut[31:0] = out_17; RegWrite = in_10; RegWriteOut = out_22; SB = in_13; SBOut = out_25;
  //   Syscall = in_12; SyscallOut = out_24; W_num[4:0] = in_14; W_Out[4:0] = out_15
endmodule

module MEM_WB (
  input  in_1,
  input  in_2,
  input  in_3,
  input  [31:0] in_4,
  input  [31:0] in_5,
  input  in_6,
  input  in_7,
  input  [31:0] in_8,
  input  [31:0] in_9,
  input  in_10,
  input  in_11,
  input  [4:0] in_12,
  output [4:0] out_13,
  output [31:0] out_14,
  output [31:0] out_15,
  output out_16,
  output out_17,
  output [31:0] out_18,
  output [31:0] out_19,
  output out_20,
  output out_21
);

  wire multiplexer_4_out, multiplexer_5_out, multiplexer_6_out, multiplexer_7_out, pull_resistor_2_node;
  wire [4:0] multiplexer_2_out;
  wire [31:0] multiplexer_1_out, multiplexer_3_out, multiplexer_8_out, multiplexer_9_out;

  Pull_Resistor #(.pull(0)) pull_resistor_1 (.node(in_3));
  Multiplexer #(.select(1), .width(32), .disabled("Z"), .enable("false")) multiplexer_1 (
    .in0(in_4), .in1({32{1'b0}}), .out(multiplexer_1_out), .sel(in_3));
  Multiplexer #(.select(1), .width(5), .disabled("Z"), .enable("false")) multiplexer_2 (
    .in0(in_12), .in1({5{1'b0}}), .out(multiplexer_2_out), .sel(in_3));
  Multiplexer #(.select(1), .width(32), .disabled("Z"), .enable("false")) multiplexer_3 (
    .in0(in_5), .in1({32{1'b0}}), .out(multiplexer_3_out), .sel(in_3));
  Multiplexer #(.select(1), .width(1), .disabled("Z"), .enable("false")) multiplexer_4 (
    .in0(in_6), .in1(1'b0), .out(multiplexer_4_out), .sel(in_3));
  Multiplexer #(.select(1), .width(1), .disabled("Z"), .enable("false")) multiplexer_5 (
    .in0(in_10), .in1(1'b0), .out(multiplexer_5_out), .sel(in_3));
  Multiplexer #(.select(1), .width(1), .disabled("Z"), .enable("false")) multiplexer_6 (
    .in0(in_7), .in1(1'b0), .out(multiplexer_6_out), .sel(in_3));
  Multiplexer #(.select(1), .width(1), .disabled("Z"), .enable("false")) multiplexer_7 (
    .in0(in_11), .in1(1'b0), .out(multiplexer_7_out), .sel(in_3));
  Multiplexer #(.select(1), .width(32), .disabled("Z"), .enable("false")) multiplexer_8 (
    .in0(in_9), .in1({32{1'b0}}), .out(multiplexer_8_out), .sel(in_3));
  Multiplexer #(.select(1), .width(32), .disabled("Z"), .enable("false")) multiplexer_9 (
    .in0(in_8), .in1({32{1'b0}}), .out(multiplexer_9_out), .sel(in_3));
  Pull_Resistor #(.pull(0)) pull_resistor_2 (.node(pull_resistor_2_node));
  not not_1 (pull_resistor_2_node, in_2);
  Register #(.width(32), .trigger("rising"), .Select("low")) register_1 (
    .D(multiplexer_1_out), .en(pull_resistor_2_node), .Q(out_14), .clk(in_1));  // open: clr
  Register #(.width(5), .trigger("rising"), .Select("low")) register_2 (
    .D(multiplexer_2_out), .en(pull_resistor_2_node), .Q(out_13), .clk(in_1));  // open: clr
  Register #(.width(32), .trigger("rising"), .Select("low")) register_3 (
    .D(multiplexer_3_out), .en(pull_resistor_2_node), .Q(out_15), .clk(in_1));  // open: clr
  Register #(.width(1), .trigger("rising"), .Select("low")) register_4 (
    .D(multiplexer_4_out), .en(pull_resistor_2_node), .Q(out_16), .clk(in_1));  // open: clr
  Register #(.width(1), .trigger("rising"), .Select("low")) register_5 (
    .D(multiplexer_5_out), .en(pull_resistor_2_node), .Q(out_20), .clk(in_1));  // open: clr
  Register #(.width(1), .trigger("rising"), .Select("low")) register_6 (
    .D(multiplexer_6_out), .en(pull_resistor_2_node), .Q(out_17), .clk(in_1));  // open: clr
  Register #(.width(1), .trigger("rising"), .Select("low")) register_7 (
    .D(multiplexer_7_out), .en(pull_resistor_2_node), .Q(out_21), .clk(in_1));  // open: clr
  Register #(.width(32), .trigger("rising"), .Select("low")) register_8 (
    .D(multiplexer_8_out), .en(pull_resistor_2_node), .Q(out_19), .clk(in_1));  // open: clr
  Register #(.width(32), .trigger("rising"), .Select("low")) register_9 (
    .D(multiplexer_9_out), .en(pull_resistor_2_node), .Q(out_18), .clk(in_1));  // open: clr

  // Other names for the same wires on the sheet: ALUIn[31:0] = in_9; ALUOut[31:0] = out_19; Clear = in_3; Clk = in_1;
  //   Enable = in_2; IRIn[31:0] = in_4; IROut[31:0] = out_14; JAL = in_7; JALOut = out_17; MDIn[31:0] = in_8;
  //   MDOut[31:0] = out_18; MemToReg = in_6; MemToRegOut = out_16; PCin[31:0] = in_5; PCout[31:0] = out_15;
  //   RegWrite = in_10; RegWriteOut = out_20; Syscall = in_11; SyscallOut = out_21; W_num[4:0] = in_12;
  //   W_Out[4:0] = out_13
endmodule

module \原寄存器使用情况  (
  input  OP0,
  input  OP1,
  input  OP2,
  input  OP3,
  input  OP4,
  input  OP5,
  input  F0,
  input  F1,
  input  F2,
  input  F3,
  input  F4,
  input  F5,
  output R1used,
  output R2used
);

  wire and_1_out, and_2_out, and_3_out, and_4_out, and_5_out, and_6_out, and_7_out, and_8_out, and_9_out,
       and_10_out, and_11_out, and_12_out, and_13_out, and_14_out, and_15_out, and_16_out, and_17_out,
       and_18_out, and_19_out, and_20_out, and_21_out, and_22_out, and_23_out, and_24_out, and_25_out,
       and_26_out, and_27_out, and_28_out, and_29_out, and_30_out, and_31_out, and_32_out, and_33_out,
       and_34_out, and_35_out, and_36_out, and_37_out, and_38_out, and_39_out, and_40_out, and_41_out,
       and_42_out, not_1_out, not_2_out, not_3_out, not_4_out, not_5_out, not_6_out, not_7_out, not_8_out,
       not_9_out, not_10_out, not_11_out, not_12_out, not_13_out, not_14_out, not_15_out, not_16_out,
       not_17_out, not_18_out, not_19_out, not_20_out, not_21_out, not_22_out, not_23_out, not_24_out,
       not_25_out, not_26_out, not_27_out, not_28_out, not_29_out, not_30_out, not_31_out, not_32_out,
       not_33_out, not_34_out, not_35_out, not_36_out, not_37_out, not_38_out, not_39_out, not_40_out,
       not_41_out, not_42_out, not_43_out, not_44_out, not_45_out, not_46_out, not_47_out, not_48_out,
       not_49_out, not_50_out, not_51_out, not_52_out, not_53_out, not_54_out, not_55_out, not_56_out,
       not_57_out, not_58_out, not_59_out, not_60_out, not_61_out, not_62_out, not_63_out, not_64_out,
       not_65_out, not_66_out, not_67_out, not_68_out, not_69_out, not_70_out, not_71_out, not_72_out,
       not_73_out, not_74_out, not_75_out, not_76_out, not_77_out, not_78_out, not_79_out, not_80_out,
       not_81_out, not_82_out, not_83_out, not_84_out, not_85_out, not_86_out, not_87_out, not_88_out,
       not_89_out, not_90_out, not_91_out, not_92_out, not_93_out, not_94_out, not_95_out, not_96_out,
       not_97_out, not_98_out, not_99_out, not_100_out, not_101_out, not_102_out, not_103_out, not_104_out,
       not_105_out, not_106_out, not_107_out, not_108_out, not_109_out, not_110_out, not_111_out,
       not_112_out, not_113_out, not_114_out, not_115_out, not_116_out, not_117_out, not_118_out,
       not_119_out, not_120_out, not_121_out, not_122_out, not_123_out, not_124_out, not_125_out,
       not_126_out, not_127_out, not_128_out, not_129_out, not_130_out, not_131_out, not_132_out,
       not_133_out, not_134_out, not_135_out, not_136_out, not_137_out, not_138_out, not_139_out,
       not_140_out, not_141_out, not_142_out, not_143_out, not_144_out, not_145_out, not_146_out,
       not_147_out, not_148_out, not_149_out, not_150_out, not_151_out, not_152_out, not_153_out,
       not_154_out, not_155_out, not_156_out, not_157_out, not_158_out, not_159_out, not_160_out,
       not_161_out, not_162_out, not_163_out, not_164_out, not_165_out, not_166_out, not_167_out,
       not_168_out, not_169_out, not_170_out, not_171_out, not_172_out, not_173_out, not_174_out,
       not_175_out, not_176_out, not_177_out, not_178_out, not_179_out, not_180_out, not_181_out,
       not_182_out, not_183_out, not_184_out, not_185_out, not_186_out, not_187_out, not_188_out,
       not_189_out, not_190_out, not_191_out, not_192_out, not_193_out, not_194_out, not_195_out,
       not_196_out, not_197_out, not_198_out, not_199_out, not_200_out, not_201_out, not_202_out,
       not_203_out, not_204_out, not_205_out, not_206_out, not_207_out, not_208_out, not_209_out,
       not_210_out, not_211_out, not_212_out, not_213_out, not_214_out, not_215_out, not_216_out,
       not_217_out, not_218_out, not_219_out, not_220_out, not_221_out, not_222_out, not_223_out,
       not_224_out, not_225_out, not_226_out, not_227_out, not_228_out, not_229_out, not_230_out,
       not_231_out, not_232_out, not_233_out, not_234_out, not_235_out, not_236_out, not_237_out,
       not_238_out, not_239_out, not_240_out, not_241_out, not_242_out, not_243_out, not_244_out,
       not_245_out, not_246_out, not_247_out, not_248_out, not_249_out, not_250_out, not_251_out,
       not_252_out, not_253_out, not_254_out, not_255_out, not_256_out, not_257_out, not_258_out,
       not_259_out, not_260_out, not_261_out, not_262_out, not_263_out, not_264_out, not_265_out,
       not_266_out, not_267_out, not_268_out, not_269_out, not_270_out, not_271_out, not_272_out,
       not_273_out, not_274_out, not_275_out, not_276_out, not_277_out, not_278_out, not_279_out,
       not_280_out, not_281_out, not_282_out, not_283_out, not_284_out, not_285_out, not_286_out,
       not_287_out, not_288_out, not_289_out, not_290_out, not_291_out, not_292_out, not_293_out,
       not_294_out, not_295_out, not_296_out, not_297_out, not_298_out, not_299_out, not_300_out,
       not_301_out, not_302_out, not_303_out, not_304_out, not_305_out, not_306_out, not_307_out,
       not_308_out, not_309_out, not_310_out, not_311_out, not_312_out, not_313_out, not_314_out,
       not_315_out, not_316_out, not_317_out, not_318_out, not_319_out, not_320_out, not_321_out;

  not not_1 (not_1_out, OP5);
  not not_2 (not_2_out, OP4);
  not not_3 (not_3_out, OP3);
  not not_4 (not_4_out, OP2);
  not not_5 (not_5_out, OP1);
  not not_6 (not_6_out, OP0);
  not not_7 (not_7_out, F5);
  not not_8 (not_8_out, F4);
  not not_9 (not_9_out, F3);
  not not_10 (not_10_out, F2);
  not not_11 (not_11_out, F1);
  not not_12 (not_12_out, F0);
  not not_13 (not_13_out, OP5);
  not not_14 (not_14_out, OP4);
  not not_15 (not_15_out, OP3);
  not not_16 (not_16_out, OP2);
  not not_17 (not_17_out, OP1);
  not not_18 (not_18_out, OP0);
  not not_19 (not_19_out, F5);
  not not_20 (not_20_out, F4);
  not not_21 (not_21_out, F3);
  not not_22 (not_22_out, F2);
  not not_23 (not_23_out, OP5);
  not not_24 (not_24_out, OP4);
  not not_25 (not_25_out, OP3);
  not not_26 (not_26_out, OP2);
  not not_27 (not_27_out, OP1);
  not not_28 (not_28_out, OP0);
  not not_29 (not_29_out, F5);
  not not_30 (not_30_out, F4);
  not not_31 (not_31_out, F3);
  not not_32 (not_32_out, F2);
  not not_33 (not_33_out, F0);
  not not_34 (not_34_out, OP5);
  not not_35 (not_35_out, OP4);
  not not_36 (not_36_out, OP3);
  not not_37 (not_37_out, OP2);
  not not_38 (not_38_out, OP1);
  not not_39 (not_39_out, OP0);
  not not_40 (not_40_out, F4);
  not not_41 (not_41_out, F3);
  not not_42 (not_42_out, F2);
  not not_43 (not_43_out, F1);
  not not_44 (not_44_out, F0);
  not not_45 (not_45_out, OP5);
  not not_46 (not_46_out, OP4);
  not not_47 (not_47_out, OP3);
  not not_48 (not_48_out, OP2);
  not not_49 (not_49_out, OP1);
  not not_50 (not_50_out, OP0);
  not not_51 (not_51_out, F4);
  not not_52 (not_52_out, F3);
  not not_53 (not_53_out, F2);
  not not_54 (not_54_out, F1);
  not not_55 (not_55_out, OP5);
  not not_56 (not_56_out, OP4);
  not not_57 (not_57_out, OP3);
  not not_58 (not_58_out, OP2);
  not not_59 (not_59_out, OP1);
  not not_60 (not_60_out, OP0);
  not not_61 (not_61_out, F4);
  not not_62 (not_62_out, F3);
  not not_63 (not_63_out, F2);
  not not_64 (not_64_out, F0);
  not not_65 (not_65_out, OP5);
  not not_66 (not_66_out, OP4);
  not not_67 (not_67_out, OP3);
  not not_68 (not_68_out, OP2);
  not not_69 (not_69_out, OP1);
  not not_70 (not_70_out, OP0);
  not not_71 (not_71_out, F4);
  not not_72 (not_72_out, F3);
  not not_73 (not_73_out, F1);
  not not_74 (not_74_out, F0);
  not not_75 (not_75_out, OP5);
  not not_76 (not_76_out, OP4);
  not not_77 (not_77_out, OP3);
  not not_78 (not_78_out, OP2);
  not not_79 (not_79_out, OP1);
  not not_80 (not_80_out, OP0);
  not not_81 (not_81_out, F4);
  not not_82 (not_82_out, F3);
  not not_83 (not_83_out, F1);
  not not_84 (not_84_out, OP5);
  not not_85 (not_85_out, OP4);
  not not_86 (not_86_out, OP3);
  not not_87 (not_87_out, OP2);
  not not_88 (not_88_out, OP1);
  not not_89 (not_89_out, OP0);
  not not_90 (not_90_out, F4);
  not not_91 (not_91_out, F3);
  not not_92 (not_92_out, OP5);
  not not_93 (not_93_out, OP4);
  not not_94 (not_94_out, OP3);
  not not_95 (not_95_out, OP2);
  not not_96 (not_96_out, OP1);
  not not_97 (not_97_out, OP0);
  not not_98 (not_98_out, F4);
  not not_99 (not_99_out, F2);
  not not_100 (not_100_out, F0);
  not not_101 (not_101_out, OP5);
  not not_102 (not_102_out, OP4);
  not not_103 (not_103_out, OP3);
  not not_104 (not_104_out, OP2);
  not not_105 (not_105_out, OP1);
  not not_106 (not_106_out, OP0);
  not not_107 (not_107_out, F4);
  not not_108 (not_108_out, F2);
  not not_109 (not_109_out, OP5);
  not not_110 (not_110_out, OP4);
  not not_111 (not_111_out, OP3);
  not not_112 (not_112_out, OP2);
  not not_113 (not_113_out, OP1);
  not not_114 (not_114_out, OP0);
  not not_115 (not_115_out, F5);
  not not_116 (not_116_out, F4);
  not not_117 (not_117_out, F2);
  not not_118 (not_118_out, F1);
  not not_119 (not_119_out, F0);
  not not_120 (not_120_out, OP5);
  not not_121 (not_121_out, OP4);
  not not_122 (not_122_out, OP3);
  not not_123 (not_123_out, OP2);
  not not_124 (not_124_out, OP1);
  not not_125 (not_125_out, OP0);
  not not_126 (not_126_out, F5);
  not not_127 (not_127_out, F4);
  not not_128 (not_128_out, F1);
  not not_129 (not_129_out, F0);
  not not_130 (not_130_out, OP5);
  not not_131 (not_131_out, OP4);
  not not_132 (not_132_out, OP3);
  not not_133 (not_133_out, OP1);
  not not_134 (not_134_out, OP0);
  not not_135 (not_135_out, OP5);
  not not_136 (not_136_out, OP4);
  not not_137 (not_137_out, OP3);
  not not_138 (not_138_out, OP1);
  not not_139 (not_139_out, OP5);
  not not_140 (not_140_out, OP4);
  not not_141 (not_141_out, OP2);
  not not_142 (not_142_out, OP1);
  not not_143 (not_143_out, OP0);
  not not_144 (not_144_out, OP5);
  not not_145 (not_145_out, OP4);
  not not_146 (not_146_out, OP1);
  not not_147 (not_147_out, OP0);
  not not_148 (not_148_out, OP5);
  not not_149 (not_149_out, OP4);
  not not_150 (not_150_out, OP2);
  not not_151 (not_151_out, OP1);
  not not_152 (not_152_out, OP5);
  not not_153 (not_153_out, OP4);
  not not_154 (not_154_out, OP2);
  not not_155 (not_155_out, OP0);
  not not_156 (not_156_out, OP5);
  not not_157 (not_157_out, OP4);
  not not_158 (not_158_out, OP1);
  not not_159 (not_159_out, OP4);
  not not_160 (not_160_out, OP3);
  not not_161 (not_161_out, OP2);
  not not_162 (not_162_out, OP4);
  not not_163 (not_163_out, OP2);
  not not_164 (not_164_out, OP5);
  not not_165 (not_165_out, OP4);
  not not_166 (not_166_out, OP3);
  not not_167 (not_167_out, OP2);
  not not_168 (not_168_out, OP1);
  not not_169 (not_169_out, OP0);
  not not_170 (not_170_out, F5);
  not not_171 (not_171_out, F4);
  not not_172 (not_172_out, F3);
  not not_173 (not_173_out, OP5);
  not not_174 (not_174_out, OP4);
  not not_175 (not_175_out, OP2);
  not not_176 (not_176_out, OP4);
  not not_177 (not_177_out, OP2);
  not not_178 (not_178_out, OP1);
  not not_179 (not_179_out, OP0);
  not not_180 (not_180_out, OP5);
  not not_181 (not_181_out, OP4);
  not not_182 (not_182_out, OP3);
  not not_183 (not_183_out, OP0);
  not not_184 (not_184_out, OP5);
  not not_185 (not_185_out, OP4);
  not not_186 (not_186_out, OP3);
  not not_187 (not_187_out, OP2);
  not not_188 (not_188_out, OP1);
  not not_189 (not_189_out, OP0);
  not not_190 (not_190_out, F5);
  not not_191 (not_191_out, F4);
  not not_192 (not_192_out, F3);
  not not_193 (not_193_out, F2);
  not not_194 (not_194_out, F1);
  not not_195 (not_195_out, F0);
  not not_196 (not_196_out, OP5);
  not not_197 (not_197_out, OP4);
  not not_198 (not_198_out, OP3);
  not not_199 (not_199_out, OP2);
  not not_200 (not_200_out, OP1);
  not not_201 (not_201_out, OP0);
  not not_202 (not_202_out, F5);
  not not_203 (not_203_out, F4);
  not not_204 (not_204_out, F3);
  not not_205 (not_205_out, F2);
  not not_206 (not_206_out, OP5);
  not not_207 (not_207_out, OP4);
  not not_208 (not_208_out, OP3);
  not not_209 (not_209_out, OP2);
  not not_210 (not_210_out, OP1);
  not not_211 (not_211_out, OP0);
  not not_212 (not_212_out, F5);
  not not_213 (not_213_out, F4);
  not not_214 (not_214_out, F3);
  not not_215 (not_215_out, F2);
  not not_216 (not_216_out, F0);
  not not_217 (not_217_out, OP5);
  not not_218 (not_218_out, OP4);
  not not_219 (not_219_out, OP3);
  not not_220 (not_220_out, OP2);
  not not_221 (not_221_out, OP1);
  not not_222 (not_222_out, OP0);
  not not_223 (not_223_out, F4);
  not not_224 (not_224_out, F3);
  not not_225 (not_225_out, F2);
  not not_226 (not_226_out, F1);
  not not_227 (not_227_out, F0);
  not not_228 (not_228_out, OP5);
  not not_229 (not_229_out, OP4);
  not not_230 (not_230_out, OP3);
  not not_231 (not_231_out, OP2);
  not not_232 (not_232_out, OP1);
  not not_233 (not_233_out, OP0);
  not not_234 (not_234_out, F4);
  not not_235 (not_235_out, F3);
  not not_236 (not_236_out, F2);
  not not_237 (not_237_out, F1);
  not not_238 (not_238_out, OP5);
  not not_239 (not_239_out, OP4);
  not not_240 (not_240_out, OP3);
  not not_241 (not_241_out, OP2);
  not not_242 (not_242_out, OP1);
  not not_243 (not_243_out, OP0);
  not not_244 (not_244_out, F4);
  not not_245 (not_245_out, F3);
  not not_246 (not_246_out, F2);
  not not_247 (not_247_out, F0);
  not not_248 (not_248_out, OP5);
  not not_249 (not_249_out, OP4);
  not not_250 (not_250_out, OP3);
  not not_251 (not_251_out, OP2);
  not not_252 (not_252_out, OP1);
  not not_253 (not_253_out, OP0);
  not not_254 (not_254_out, F4);
  not not_255 (not_255_out, F3);
  not not_256 (not_256_out, F1);
  not not_257 (not_257_out, F0);
  not not_258 (not_258_out, OP5);
  not not_259 (not_259_out, OP4);
  not not_260 (not_260_out, OP3);
  not not_261 (not_261_out, OP2);
  not not_262 (not_262_out, OP1);
  not not_263 (not_263_out, OP0);
  not not_264 (not_264_out, F4);
  not not_265 (not_265_out, F3);
  not not_266 (not_266_out, F1);
  not not_267 (not_267_out, OP5);
  not not_268 (not_268_out, OP4);
  not not_269 (not_269_out, OP3);
  not not_270 (not_270_out, OP2);
  not not_271 (not_271_out, OP1);
  not not_272 (not_272_out, OP0);
  not not_273 (not_273_out, F4);
  not not_274 (not_274_out, F3);
  not not_275 (not_275_out, OP5);
  not not_276 (not_276_out, OP4);
  not not_277 (not_277_out, OP3);
  not not_278 (not_278_out, OP2);
  not not_279 (not_279_out, OP1);
  not not_280 (not_280_out, OP0);
  not not_281 (not_281_out, F4);
  not not_282 (not_282_out, F2);
  not not_283 (not_283_out, F0);
  not not_284 (not_284_out, OP5);
  not not_285 (not_285_out, OP4);
  not not_286 (not_286_out, OP3);
  not not_287 (not_287_out, OP2);
  not not_288 (not_288_out, OP1);
  not not_289 (not_289_out, OP0);
  not not_290 (not_290_out, F4);
  not not_291 (not_291_out, F2);
  not not_292 (not_292_out, OP5);
  not not_293 (not_293_out, OP4);
  not not_294 (not_294_out, OP3);
  not not_295 (not_295_out, OP2);
  not not_296 (not_296_out, OP1);
  not not_297 (not_297_out, OP0);
  not not_298 (not_298_out, F5);
  not not_299 (not_299_out, F4);
  not not_300 (not_300_out, F1);
  not not_301 (not_301_out, F0);
  not not_302 (not_302_out, OP5);
  not not_303 (not_303_out, OP4);
  not not_304 (not_304_out, OP3);
  not not_305 (not_305_out, OP1);
  not not_306 (not_306_out, OP0);
  not not_307 (not_307_out, OP5);
  not not_308 (not_308_out, OP4);
  not not_309 (not_309_out, OP3);
  not not_310 (not_310_out, OP1);
  not not_311 (not_311_out, OP4);
  not not_312 (not_312_out, OP2);
  not not_313 (not_313_out, OP5);
  not not_314 (not_314_out, OP4);
  not not_315 (not_315_out, OP3);
  not not_316 (not_316_out, OP2);
  not not_317 (not_317_out, OP1);
  not not_318 (not_318_out, OP0);
  not not_319 (not_319_out, F5);
  not not_320 (not_320_out, F4);
  not not_321 (not_321_out, F3);
  and and_1 (and_1_out, not_1_out, not_2_out, not_3_out, not_4_out, not_5_out, not_6_out, not_7_out, not_8_out, not_9_out, not_10_out, not_11_out, not_12_out);
  and and_2 (and_2_out, not_13_out, not_14_out, not_15_out, not_16_out, not_17_out, not_18_out, not_19_out, not_20_out, not_21_out, not_22_out, F1, F0);
  and and_3 (and_3_out, not_23_out, not_24_out, not_25_out, not_26_out, not_27_out, not_28_out, not_29_out, not_30_out, not_31_out, not_32_out, F1, not_33_out);
  and and_4 (and_4_out, not_34_out, not_35_out, not_36_out, not_37_out, not_38_out, not_39_out, F5, not_40_out, not_41_out, not_42_out, not_43_out, not_44_out);
  and and_5 (and_5_out, not_45_out, not_46_out, not_47_out, not_48_out, not_49_out, not_50_out, F5, not_51_out, not_52_out, not_53_out, not_54_out, F0);
  and and_6 (and_6_out, not_55_out, not_56_out, not_57_out, not_58_out, not_59_out, not_60_out, F5, not_61_out, not_62_out, not_63_out, F1, not_64_out);
  and and_7 (and_7_out, not_65_out, not_66_out, not_67_out, not_68_out, not_69_out, not_70_out, F5, not_71_out, not_72_out, F2, not_73_out, not_74_out);
  and and_8 (and_8_out, not_75_out, not_76_out, not_77_out, not_78_out, not_79_out, not_80_out, F5, not_81_out, not_82_out, F2, not_83_out, F0);
  and and_9 (and_9_out, not_84_out, not_85_out, not_86_out, not_87_out, not_88_out, not_89_out, F5, not_90_out, not_91_out, F2, F1, F0);
  and and_10 (and_10_out, not_92_out, not_93_out, not_94_out, not_95_out, not_96_out, not_97_out, F5, not_98_out, F3, not_99_out, F1, not_100_out);
  and and_11 (and_11_out, not_101_out, not_102_out, not_103_out, not_104_out, not_105_out, not_106_out, F5, not_107_out, F3, not_108_out, F1, F0);
  and and_12 (and_12_out, not_109_out, not_110_out, not_111_out, not_112_out, not_113_out, not_114_out, not_115_out, not_116_out, F3, not_117_out, not_118_out, not_119_out);
  and and_13 (and_13_out, not_120_out, not_121_out, not_122_out, not_123_out, not_124_out, not_125_out, not_126_out, not_127_out, F3, F2, not_128_out, not_129_out);
  and and_14 (and_14_out, not_130_out, not_131_out, not_132_out, OP2, not_133_out, not_134_out);
  and and_15 (and_15_out, not_135_out, not_136_out, not_137_out, OP2, not_138_out, OP0);
  and and_16 (and_16_out, not_139_out, not_140_out, OP3, not_141_out, not_142_out, not_143_out);
  and and_17 (and_17_out, not_144_out, not_145_out, OP3, OP2, not_146_out, not_147_out);
  and and_18 (and_18_out, not_148_out, not_149_out, OP3, not_150_out, not_151_out, OP0);
  and and_19 (and_19_out, not_152_out, not_153_out, OP3, not_154_out, OP1, not_155_out);
  and and_20 (and_20_out, not_156_out, not_157_out, OP3, OP2, not_158_out, OP0);
  and and_21 (and_21_out, OP5, not_159_out, not_160_out, not_161_out, OP1, OP0);
  and and_22 (and_22_out, OP5, not_162_out, OP3, not_163_out, OP1, OP0);
  and and_23 (and_23_out, not_164_out, not_165_out, not_166_out, not_167_out, not_168_out, not_169_out, not_170_out, not_171_out, not_172_out, F2, F1, F0);
  and and_24 (and_24_out, not_173_out, not_174_out, OP3, not_175_out, OP1, OP0);
  and and_25 (and_25_out, OP5, not_176_out, OP3, not_177_out, not_178_out, not_179_out);
  and and_26 (and_26_out, not_180_out, not_181_out, not_182_out, OP2, OP1, not_183_out);
  and and_27 (and_27_out, not_184_out, not_185_out, not_186_out, not_187_out, not_188_out, not_189_out, not_190_out, not_191_out, not_192_out, not_193_out, not_194_out, not_195_out);
  and and_28 (and_28_out, not_196_out, not_197_out, not_198_out, not_199_out, not_200_out, not_201_out, not_202_out, not_203_out, not_204_out, not_205_out, F1, F0);
  and and_29 (and_29_out, not_206_out, not_207_out, not_208_out, not_209_out, not_210_out, not_211_out, not_212_out, not_213_out, not_214_out, not_215_out, F1, not_216_out);
  and and_30 (and_30_out, not_217_out, not_218_out, not_219_out, not_220_out, not_221_out, not_222_out, F5, not_223_out, not_224_out, not_225_out, not_226_out, not_227_out);
  and and_31 (and_31_out, not_228_out, not_229_out, not_230_out, not_231_out, not_232_out, not_233_out, F5, not_234_out, not_235_out, not_236_out, not_237_out, F0);
  and and_32 (and_32_out, not_238_out, not_239_out, not_240_out, not_241_out, not_242_out, not_243_out, F5, not_244_out, not_245_out, not_246_out, F1, not_247_out);
  and and_33 (and_33_out, not_248_out, not_249_out, not_250_out, not_251_out, not_252_out, not_253_out, F5, not_254_out, not_255_out, F2, not_256_out, not_257_out);
  and and_34 (and_34_out, not_258_out, not_259_out, not_260_out, not_261_out, not_262_out, not_263_out, F5, not_264_out, not_265_out, F2, not_266_out, F0);
  and and_35 (and_35_out, not_267_out, not_268_out, not_269_out, not_270_out, not_271_out, not_272_out, F5, not_273_out, not_274_out, F2, F1, F0);
  and and_36 (and_36_out, not_275_out, not_276_out, not_277_out, not_278_out, not_279_out, not_280_out, F5, not_281_out, F3, not_282_out, F1, not_283_out);
  and and_37 (and_37_out, not_284_out, not_285_out, not_286_out, not_287_out, not_288_out, not_289_out, F5, not_290_out, F3, not_291_out, F1, F0);
  and and_38 (and_38_out, not_292_out, not_293_out, not_294_out, not_295_out, not_296_out, not_297_out, not_298_out, not_299_out, F3, F2, not_300_out, not_301_out);
  and and_39 (and_39_out, not_302_out, not_303_out, not_304_out, OP2, not_305_out, not_306_out);
  and and_40 (and_40_out, not_307_out, not_308_out, not_309_out, OP2, not_310_out, OP0);
  and and_41 (and_41_out, OP5, not_311_out, OP3, not_312_out, OP1, OP0);
  and and_42 (and_42_out, not_313_out, not_314_out, not_315_out, not_316_out, not_317_out, not_318_out, not_319_out, not_320_out, not_321_out, F2, F1, F0);
  or or_1 (R1used, and_1_out, and_2_out, and_3_out, and_4_out, and_5_out, and_6_out, and_7_out, and_8_out, and_9_out, and_10_out, and_11_out, and_12_out, and_13_out, and_14_out, and_15_out, and_16_out, and_17_out, and_18_out, and_19_out, and_20_out, and_21_out, and_22_out, and_23_out, and_24_out, and_25_out, and_26_out);
  or or_2 (R2used, and_27_out, and_28_out, and_29_out, and_30_out, and_31_out, and_32_out, and_33_out, and_34_out, and_35_out, and_36_out, and_37_out, and_38_out, and_39_out, and_40_out, and_41_out, and_42_out);
endmodule

module \数据相关检测  (
  input  [5:0] OP,
  input  [4:0] EX_W_num,
  input  EX_regw,
  input  [4:0] MEM_W_num,
  input  MEM_regw,
  input  [5:0] Func,
  input  [4:0] ID_R1_num,
  input  [4:0] R2used,
  output \数据相关 
);

  wire and_1_out, and_2_out, and_3_out, and_4_out, and_5_out, and_6_out, comparator_1_eq, comparator_2_eq,
       comparator_3_eq, comparator_4_eq, comparator_5_eq, comparator_6_eq, not_1_out, not_2_out, or_1_out,
       or_2_out, \原寄存器使用情况_1_r1used , \原寄存器使用情况_1_r2used ;

  Comparator #(.width(5), .mode("twosComplement")) comparator_1 (
    .a(ID_R1_num), .b(EX_W_num), .eq(comparator_1_eq));  // open: gt, lt
  Comparator #(.width(5), .mode("twosComplement")) comparator_2 (
    .a(ID_R1_num), .b(MEM_W_num), .eq(comparator_2_eq));  // open: gt, lt
  \原寄存器使用情况  \u_原寄存器使用情况_1  (
    .OP0(OP[0]), .OP1(OP[1]), .OP2(OP[2]), .OP3(OP[3]), .OP4(OP[4]), .OP5(OP[5]), .F0(Func[0]), .F1(Func[1]),
    .F2(Func[2]), .F3(Func[3]), .F4(Func[4]), .F5(Func[5]), .R1used(\原寄存器使用情况_1_r1used ),
    .R2used(\原寄存器使用情况_1_r2used ));
  Comparator #(.width(5), .mode("twosComplement")) comparator_3 (
    .a(R2used), .b(EX_W_num), .eq(comparator_3_eq));  // open: gt, lt
  Comparator #(.width(5), .mode("twosComplement")) comparator_4 (
    .a(R2used), .b(MEM_W_num), .eq(comparator_4_eq));  // open: gt, lt
  Comparator #(.width(5), .mode("twosComplement")) comparator_5 (
    .a(ID_R1_num), .b({5{1'b0}}), .eq(comparator_5_eq));  // open: gt, lt
  not not_1 (not_1_out, comparator_5_eq);
  and and_1 (and_1_out, comparator_1_eq, EX_regw);
  and and_2 (and_2_out, comparator_2_eq, MEM_regw);
  and and_3 (and_3_out, comparator_3_eq, EX_regw);
  and and_4 (and_4_out, comparator_4_eq, MEM_regw);
  Comparator #(.width(5), .mode("twosComplement")) comparator_6 (
    .a(R2used), .b({5{1'b0}}), .eq(comparator_6_eq));  // open: gt, lt
  not not_2 (not_2_out, comparator_6_eq);
  or or_1 (or_1_out, and_1_out, and_2_out);
  or or_2 (or_2_out, and_3_out, and_4_out);
  and and_5 (and_5_out, not_1_out, or_1_out, \原寄存器使用情况_1_r1used );
  and and_6 (and_6_out, \原寄存器使用情况_1_r2used , or_2_out, not_2_out);
  or or_3 (\数据相关 , and_5_out, and_6_out);

  // Other names for the same wires on the sheet: OP_CODE[5:0] = OP; R1used[4:0] = ID_R1_num
endmodule

module \重定向检测  (
  input  EX_RegWrite,
  input  EX_MemToReg,
  input  [4:0] EX_WriteReg_num,
  input  [5:0] OP,
  input  [5:0] Func,
  input  MEM_RegWrite,
  input  MEM_MemToReg,
  input  [4:0] MEM_W_num,
  input  [4:0] R1_num,
  input  [4:0] R2_num,
  output Load_use,
  output [1:0] forwardR1,
  output [1:0] forwardR2
);

  wire and_4_out, and_5_out, case0_R1, case0_R2, case1_R1, case1_R2, case2_R1, case2_R2, case3_R1, case3_R2,
       comparator_1_eq, comparator_2_eq, comparator_3_eq, comparator_4_eq, comparator_5_eq, comparator_6_eq,
       comparator_7_eq, comparator_10_eq, comparator_11_eq, comparator_12_eq, not_1_out, not_2_out,
       not_3_out, not_4_out, or_1_out, R1_Used, R2_Used;
  wire [1:0] multiplexer_1_out, multiplexer_2_out, multiplexer_3_out, multiplexer_5_out, multiplexer_6_out,
       multiplexer_7_out;

  Multiplexer #(.select(1), .width(2), .disabled("Z"), .enable("false")) multiplexer_1 (
    .in0(2'b00), .in1(2'b01), .out(multiplexer_1_out), .sel(case1_R1));
  Comparator #(.width(5), .mode("twosComplement")) comparator_1 (
    .a(R1_num), .b(MEM_W_num), .eq(comparator_1_eq));  // open: gt, lt
  Comparator #(.width(5), .mode("twosComplement")) comparator_2 (
    .a(R1_num), .b(MEM_W_num), .eq(comparator_2_eq));  // open: gt, lt
  Comparator #(.width(5), .mode("twosComplement")) comparator_3 (
    .a(R1_num), .b(EX_WriteReg_num), .eq(comparator_3_eq));  // open: gt, lt
  \原寄存器使用情况  \u_原寄存器使用情况_1  (
    .OP0(OP[0]), .OP1(OP[1]), .OP2(OP[2]), .OP3(OP[3]), .OP4(OP[4]), .OP5(OP[5]), .F0(Func[0]), .F1(Func[1]),
    .F2(Func[2]), .F3(Func[3]), .F4(Func[4]), .F5(Func[5]), .R1used(R1_Used), .R2used(R2_Used));
  Multiplexer #(.select(1), .width(2), .disabled("Z"), .enable("false")) multiplexer_2 (
    .in0(multiplexer_1_out), .in1(2'b10), .out(multiplexer_2_out), .sel(case2_R1));
  and and_1 (case1_R1, comparator_1_eq, R1_Used, MEM_RegWrite, MEM_MemToReg);
  and and_2 (case2_R1, comparator_2_eq, R1_Used, MEM_RegWrite, not_1_out);
  not not_1 (not_1_out, MEM_MemToReg);
  and and_3 (case3_R1, comparator_3_eq, R1_Used, EX_RegWrite);
  Multiplexer #(.select(1), .width(2), .disabled("Z"), .enable("false")) multiplexer_3 (
    .in0(multiplexer_2_out), .in1(2'b11), .out(multiplexer_3_out), .sel(case3_R1));
  Comparator #(.width(5), .mode("twosComplement")) comparator_4 (
    .a(R1_num), .b({5{1'b0}}), .eq(comparator_4_eq));  // open: gt, lt
  Comparator #(.width(5), .mode("twosComplement")) comparator_5 (
    .a(R1_num), .b(EX_WriteReg_num), .eq(comparator_5_eq));  // open: gt, lt
  Comparator #(.width(5), .mode("twosComplement")) comparator_6 (
    .a(R2_num), .b({5{1'b0}}), .eq(comparator_6_eq));  // open: gt, lt
  Comparator #(.width(5), .mode("twosComplement")) comparator_7 (
    .a(R2_num), .b(EX_WriteReg_num), .eq(comparator_7_eq));  // open: gt, lt
  Comparator #(.width(5), .mode("twosComplement")) comparator_8 (
    .a(R1_num), .b({5{1'b0}}), .eq(case0_R1));  // open: gt, lt
  Comparator #(.width(5), .mode("twosComplement")) comparator_9 (
    .a(R2_num), .b({5{1'b0}}), .eq(case0_R2));  // open: gt, lt
  Multiplexer #(.select(1), .width(2), .disabled("Z"), .enable("false")) multiplexer_4 (
    .in0(multiplexer_3_out), .in1(2'b00), .out(forwardR1), .sel(case0_R1));
  not not_2 (not_2_out, comparator_4_eq);
  not not_3 (not_3_out, comparator_6_eq);
  and and_4 (and_4_out, not_2_out, comparator_5_eq, EX_RegWrite, R1_Used);
  and and_5 (and_5_out, not_3_out, comparator_7_eq, EX_RegWrite, R2_Used);
  or or_1 (or_1_out, and_4_out, and_5_out);
  Comparator #(.width(5), .mode("twosComplement")) comparator_10 (
    .a(R2_num), .b(MEM_W_num), .eq(comparator_10_eq));  // open: gt, lt
  Comparator #(.width(5), .mode("twosComplement")) comparator_11 (
    .a(R2_num), .b(MEM_W_num), .eq(comparator_11_eq));  // open: gt, lt
  Comparator #(.width(5), .mode("twosComplement")) comparator_12 (
    .a(R2_num), .b(EX_WriteReg_num), .eq(comparator_12_eq));  // open: gt, lt
  Multiplexer #(.select(1), .width(2), .disabled("Z"), .enable("false")) multiplexer_5 (
    .in0(2'b00), .in1(2'b01), .out(multiplexer_5_out), .sel(case1_R2));
  Multiplexer #(.select(1), .width(2), .disabled("Z"), .enable("false")) multiplexer_6 (
    .in0(multiplexer_5_out), .in1(2'b10), .out(multiplexer_6_out), .sel(case2_R2));
  and and_6 (Load_use, or_1_out, EX_MemToReg);
  not not_4 (not_4_out, MEM_MemToReg);
  Multiplexer #(.select(1), .width(2), .disabled("Z"), .enable("false")) multiplexer_7 (
    .in0(multiplexer_6_out), .in1(2'b11), .out(multiplexer_7_out), .sel(case3_R2));
  and and_7 (case1_R2, comparator_10_eq, R2_Used, MEM_RegWrite, MEM_MemToReg);
  and and_8 (case2_R2, comparator_11_eq, R2_Used, MEM_RegWrite, not_4_out);
  and and_9 (case3_R2, comparator_12_eq, R2_Used, EX_RegWrite);
  Multiplexer #(.select(1), .width(2), .disabled("Z"), .enable("false")) multiplexer_8 (
    .in0(multiplexer_7_out), .in1(2'b00), .out(forwardR2), .sel(case0_R2));

  // Other names for the same wires on the sheet: EX_W_num[4:0] = EX_WriteReg_num; OP_CODE[5:0] = OP

  // Notes on the sheet:
  //   重定向WB.ALUR
  //   重定向WB.Mem
  //   重定向MEM.ALUR
  //   0号寄存器直接使用
  //   0号寄存器直接使用
  //   判断是否为load指令
  //   重定向WB.ALUR
  //   重定向WB.Mem
  //   重定向MEM.ALUR
endmodule
